// Logisim project 单周期_ccab上板.circ as structural Verilog: 6 circuits, main circuit SingleCycleRiscv  
module SingleCycleRiscv (
  input  Go,
  input  RST,
  output [7:0] SEG,
  output [7:0] NA
);

  wire alu_1_equal, alu_1_out_6, and_1_out, and_2_out, and_3_out, and_4_out, Auipc, Branch, CLK,
       comparator_1_eq, Ecall, halt, JAL, JALR, Lhu, MemToReg, MemWrite, not_1_out, not_2_out, not_3_out,
       not_4_out, not_5_out, or_2_out, RegWrite, singlecyclehardwiredcontroller_1_alu_src,
       singlecyclehardwiredcontroller_1_beq, singlecyclehardwiredcontroller_1_bltu,
       singlecyclehardwiredcontroller_1_bne, singlecyclehardwiredcontroller_1_s_type, URET;
  wire [0:0] bit_extender_4_out;
  wire [1:0] MemStartByte;
  wire [3:0] singlecyclehardwiredcontroller_1_alu_op;
  wire [4:0] multiplexer_3_out, multiplexer_4_out;
  wire [9:0] alu_1_result;
  wire [11:0] multiplexer_5_out;
  wire [15:0] TotalTNum;
  wire [31:0] adder_2_out, adder_3_out, adder_4_out, adder_5_out, bit_extender_1_out, bit_extender_3_out,
       bit_extender_5_out, bit_extender_6_out, bit_extender_7_out, bit_extender_8_out, BranchAddress,
       IorSImme, IR, JalImme, LedData, MDin, memoword, multiplexer_1_out, multiplexer_2_out,
       multiplexer_7_out, multiplexer_8_out, multiplexer_9_out, Next_PC, OrderPc, PC, R_rs1, RandomRAM_data,
       RDin, signmemo, UImme;
  wire [31:1] JalrImme;
  wire [31:12] alu_1_result_2;

  not not_1 (not_1_out, halt);
  Clock #(.highDuration(1), .lowDuration(1)) clock_1 (.out(CLK));
  Register #(.width(32), .trigger("rising"), .Select("low")) u_PC (
    .D(Next_PC), .en(not_1_out), .Q(PC), .clk(CLK), .clr(RST));
  // FPGADigit #(.trigger("rising")) fpgadigit_1: pin names not known; wires that end beside it: LedData, CLK, SEG, NA
  Adder #(.width(32)) adder_1 (.a(PC), .b(32'h4), .out(OrderPc));  // open: cin, cout
  Adder #(.width(32)) adder_2 (.a(PC), .b(BranchAddress), .out(adder_2_out));  // open: cin, cout
  Adder #(.width(32)) adder_3 (.a(PC), .b(JalImme), .out(adder_3_out));  // open: cin, cout
  Adder #(.width(32)) adder_4 (.a(R_rs1), .b({JalrImme, 1'b0}), .out(adder_4_out));  // open: cin, cout
  ROM #(.addrWidth(10), .dataWidth(32)) OnlyReadRom (.addr(PC[11:2]), .data(IR));
  Multiplexer #(.select(1), .width(32), .disabled(0), .enable("false")) multiplexer_1 (
    .in0(OrderPc), .in1(adder_2_out), .out(multiplexer_1_out), .sel(Branch));
  Multiplexer #(.select(1), .width(32), .disabled(0), .enable("false")) multiplexer_2 (
    .in0(multiplexer_1_out), .in1(adder_3_out), .out(multiplexer_2_out), .sel(JAL));
  SingleCycleHardwiredController singlecyclehardwiredcontroller_1 (
    .Funct({IR[30], IR[25], IR[14:12]}), .OP(IR[6:2]), .ALU_OP(singlecyclehardwiredcontroller_1_alu_op),
    .MemToReg(MemToReg), .MemWrite(MemWrite), .ALU_SRC(singlecyclehardwiredcontroller_1_alu_src),
    .RegWrite(RegWrite), .ecall(Ecall), .S_type(singlecyclehardwiredcontroller_1_s_type), .Jalr(JALR),
    .Beq(singlecyclehardwiredcontroller_1_beq), .JAL(JAL), .Bne(singlecyclehardwiredcontroller_1_bne),
    .IR21(IR[21]), .uret(URET), .Bltu(singlecyclehardwiredcontroller_1_bltu), .Lhu(Lhu), .Auipc(Auipc));
  Multiplexer #(.select(1), .width(5), .disabled(0), .enable("false")) multiplexer_3 (
    .in0(IR[19:15]), .in1(5'b10001), .out(multiplexer_3_out), .sel(Ecall));
  Multiplexer #(.select(1), .width(5), .disabled(0), .enable("false")) multiplexer_4 (
    .in0(IR[24:20]), .in1(5'b01010), .out(multiplexer_4_out), .sel(Ecall));
  Multiplexer #(.select(1), .width(12), .disabled(0), .enable("false")) multiplexer_5 (
    .in0(IR[31:20]), .in1({IR[31:25], IR[11:7]}), .out(multiplexer_5_out),
    .sel(singlecyclehardwiredcontroller_1_s_type));
  assign bit_extender_1_out = {{12{IR[31]}}, IR[31:12]};  // Bit_Extender bit_extender_1
  Multiplexer #(.select(1), .width(32), .disabled(0), .enable("false")) multiplexer_6 (
    .in0(multiplexer_2_out), .in1(adder_4_out), .out(Next_PC), .sel(JALR));
  assign IorSImme = {{20{multiplexer_5_out[11]}}, multiplexer_5_out};  // Bit_Extender bit_extender_2
  Regifile regifile_1 (
    .R1Adr(multiplexer_3_out), .R2Adr(multiplexer_4_out), .Din(RDin), .Clk(CLK), .WE(RegWrite),
    .WAdr(IR[11:7]), .R1(R_rs1), .R2(MDin));
  Shifter #(.width(32), .shift("ll")) shifter_1 (.in(bit_extender_1_out), .\dist (5'b01100), .out(UImme));
  assign bit_extender_3_out = {{20{IR[31]}}, {IR[31], IR[7], IR[30:25], IR[11:8]}};  // Bit_Extender bit_extender_3
  not not_2 (not_2_out, alu_1_equal);
  // Probe on singlecyclehardwiredcontroller_1_alu_op
  Multiplexer #(.select(1), .width(32), .disabled(0), .enable("false")) multiplexer_7 (
    .in0(MDin), .in1(IorSImme), .out(multiplexer_7_out), .sel(singlecyclehardwiredcontroller_1_alu_src));
  Shifter #(.width(32), .shift("ll")) shifter_2 (.in(bit_extender_3_out), .\dist (5'b00001), .out(BranchAddress));
  and and_1 (and_1_out, singlecyclehardwiredcontroller_1_bltu, alu_1_out_6);
  and and_2 (and_2_out, singlecyclehardwiredcontroller_1_bne, not_2_out);
  ALU alu_1 (
    .X(R_rs1), .Y(multiplexer_7_out), .AluOP(singlecyclehardwiredcontroller_1_alu_op), .Equal(alu_1_equal),
    .Result({alu_1_result_2, alu_1_result, MemStartByte}), .out_6(alu_1_out_6));  // open: Result_2, out_4
  assign {JalrImme, bit_extender_4_out[0]} = {{20{IR[31]}}, IR[31:20]};  // Bit_Extender bit_extender_4
  and and_3 (and_3_out, singlecyclehardwiredcontroller_1_beq, alu_1_equal);
  assign bit_extender_5_out = {{12{IR[31]}}, {IR[31], IR[19:12], IR[20], IR[30:21]}};  // Bit_Extender bit_extender_5
  or or_1 (Branch, and_3_out, and_1_out, and_2_out);
  RAM #(.addrWidth(10), .dataWidth(32), .bus("separate"), .Select("high")) RandomRAM (
    .addr(alu_1_result), .din(MDin), .data(RandomRAM_data), .str(MemWrite), .clk(CLK), .ld(MemToReg),
    .clr(RST));  // open: sel
  Shifter #(.width(32), .shift("ll")) shifter_3 (.in(bit_extender_5_out), .\dist (5'b00001), .out(JalImme));
  Multiplexer #(.select(1), .width(32), .disabled(0), .enable("false")) multiplexer_8 (
    .in0({alu_1_result_2, alu_1_result, MemStartByte}), .in1(RandomRAM_data), .out(multiplexer_8_out),
    .sel(MemToReg));
  not not_3 (not_3_out, halt);
  Comparator #(.width(32), .mode("twosComplement")) comparator_1 (
    .a(R_rs1), .b(32'h22), .eq(comparator_1_eq));  // open: gt, lt
  not not_4 (not_4_out, Go);
  Counter #(.width(16), .max('hffff), .ongoal("wrap"), .trigger("rising"), .behavior("new")) counter_1 (
    .D(16'h1), .count(not_3_out), .Q(TotalTNum), .clk(CLK));  // open: load, carry, clr, preset, down
  // Probe on TotalTNum
  or or_2 (or_2_out, JAL, JALR);
  Multiplexer #(.select(1), .width(32), .disabled(0), .enable("false")) multiplexer_9 (
    .in0(multiplexer_8_out), .in1(OrderPc), .out(multiplexer_9_out), .sel(or_2_out));
  and and_4 (and_4_out, comparator_1_eq, Ecall);
  not not_5 (not_5_out, comparator_1_eq);
  and and_5 (halt, not_5_out, not_4_out, Ecall);
  Multiplexer #(.select(1), .width(32), .disabled(0), .enable("false")) multiplexer_10 (
    .in0(multiplexer_9_out), .in1(adder_5_out), .out(memoword), .sel(Auipc));
  Adder #(.width(32)) adder_5 (.a(PC), .b(UImme), .out(adder_5_out));  // open: cin, cout
  Register #(.width(32), .trigger("rising"), .Select("low")) register_1 (
    .D(MDin), .en(and_4_out), .Q(LedData), .clk(CLK), .clr(RST));
  Multiplexer #(.select(1), .width(32), .disabled(0), .enable("false")) multiplexer_11 (
    .in0(memoword), .in1(signmemo), .out(RDin), .sel(Lhu));
  assign bit_extender_6_out = {{16{1'b0}}, memoword[15:0]};  // Bit_Extender bit_extender_6
  assign bit_extender_7_out = {{16{1'b0}}, memoword[23:8]};  // Bit_Extender bit_extender_7
  assign bit_extender_8_out = {{16{1'b0}}, memoword[31:16]};  // Bit_Extender bit_extender_8
  Multiplexer #(.select(2), .width(32), .disabled(0), .enable("false")) multiplexer_12 (
    .in0(bit_extender_6_out), .in1(bit_extender_7_out), .in2(bit_extender_8_out), .out(signmemo),
    .sel(MemStartByte));  // open: in3

  // Other names for the same wires on the sheet: R_rs2[31:0] = MDin

  // Notes on the sheet:
  //   contents of OnlyReadRom (hex, n*v repeats v):
  //   100493 100006f 100493 200913 300993 100006f 100493 200913 300993 100006f 100493 200913 300993
  //   100006f 100493 200913 300993 414000ef 100413 100493 1f49493 900533 2200893 73 24d493 48463 fedff06f
  //   900533 2200893 73 100493 249493 900533 2200893 73 48463 fedff06f 100493 1f49493 900533 2200893 73
  //   4034d493 900533 2200893 73 4044d493 900533 2200893 73 4044d493 900533 2200893 73 4044d493 900533
  //   2200893 73 4044d493 900533 2200893 73 4044d493 900533 2200893 73 4044d493 900533 2200893 73 4044d493
  //   900533 2200893 73 100413 1f41993 41f9d993 433 c00913 300b13 140413 f47413 800293 100313 499993
  //   89e9b3 1300533 2200893 73 406282b3 fe0294e3 140413 f00f93 1f47433 1c41413 800293 100313 49d993
  //   89e9b3 1300533 2200893 73 406282b3 fe0294e3 1c45413 406b0b33 b0463 f95ff06f 2b3 fff2c293 829293
  //   ff2e293 500533 2200893 73 fff00413 493 84a023 140413 448493 84a023 140413 448493 84a023 140413
  //   448493 84a023 140413 448493 84a023 140413 448493 84a023 140413 448493 84a023 140413 448493 84a023
  //   140413 448493 84a023 140413 448493 84a023 140413 448493 84a023 140413 448493 84a023 140413 448493
  //   84a023 140413 448493 84a023 140413 448493 84a023 140413 448493 84a023 140413 448493 140413 433
  //   3c00493 42983 4aa03 149a2b3 28663 134a023 1442023 ffc48493 fe9412e3 800533 2200893 73 440413 3c00493
  //   fc9416e3 3200893 73 fff00293 7700493 849493 7748493 900533 2200893 73 1000e13 54c4b3 900533 2200893
  //   73 fffe0e13 fe0e16e3 a00893 73 13 430497 900533 2200893 73 430497 900533 2200893 73 430497 900533
  //   2200893 73 430497 900533 2200893 73 430497 900533 2200893 73 430497 900533 2200893 73 430497 900533
  //   2200893 73 430497 900533 2200893 73 a00893 73 313 1000e13 8400493 849493 8348493 400913 891913
  //   490913 849493 8248493 849493 8148493 891913 490913 891913 490913 932023 12484b3 430313 fffe0e13
  //   fe0e18e3 2000e13 313 35483 900533 2200893 73 230313 fffe0e13 fe0e14e3 a00893 73 ff100493 900533
  //   2200893 73 148493 fe9068e3 900533 2200893 73 a00893 73 413 140413 800533 2200893 73 240413 800533
  //   2200893 73 340413 800533 2200893 73 440413 800533 2200893 73 540413 800533 2200893 73 640413 800533
  //   2200893 73 740413 800533 2200893 73 840413 800533 2200893 2200893 73 8067
endmodule

module SingleCycleHardwiredController (
  input  [4:0] OP,
  input  [4:0] Funct,
  input  IR21,
  output [3:0] ALU_OP,
  output uret,
  output MemToReg,
  output ecall,
  output MemWrite,
  output Bltu,
  output Lhu,
  output Auipc,
  output ALU_SRC,
  output RegWrite,
  output S_type,
  output Beq,
  output Bne,
  output Jalr,
  output JAL
);

  wire controlsignal_1_ecall;

  OperationController operationcontroller_1 (
    .OP2(OP[0]), .OP3(OP[1]), .OP4(OP[2]), .OP5(OP[3]), .OP6(OP[4]), .F12(Funct[0]), .F13(Funct[1]),
    .F14(Funct[2]), .F25(Funct[3]), .F30(Funct[4]), .S0(ALU_OP[0]), .S1(ALU_OP[1]), .S2(ALU_OP[2]),
    .S3(ALU_OP[3]));
  ControlSignal controlsignal_1 (
    .OP2(OP[0]), .OP3(OP[1]), .OP4(OP[2]), .OP5(OP[3]), .OP6(OP[4]), .MemToReg(MemToReg), .F12(Funct[0]),
    .F13(Funct[1]), .F14(Funct[2]), .F25(Funct[3]), .F30(Funct[4]), .MemWrite(MemWrite), .BLTU(Bltu),
    .LHU(Lhu), .AUIPC(Auipc), .ALU_SRC(ALU_SRC), .RegWrite(RegWrite), .ecall(controlsignal_1_ecall),
    .S_Type(S_type), .BEQ(Beq), .BNE(Bne), .JALR(Jalr), .JAL(JAL));
  and and_1 (uret, IR21, controlsignal_1_ecall);
  and and_2 (ecall, ~IR21, controlsignal_1_ecall);  // AND_Gate

  // Other names for the same wires on the sheet: OP_CODE[4:0] = OP
endmodule

module OperationController (
  input  OP2,
  input  OP3,
  input  OP4,
  input  OP5,
  input  OP6,
  input  F12,
  input  F13,
  input  F14,
  input  F25,
  input  F30,
  output S0,
  output S1,
  output S2,
  output S3
);

  wire and_1_out, and_2_out, and_3_out, and_4_out, and_5_out, and_6_out, and_7_out, and_8_out, and_9_out,
       and_10_out, and_11_out, and_12_out, and_13_out, and_14_out, and_15_out, and_16_out, and_17_out,
       and_18_out, and_19_out, and_20_out, and_21_out, and_22_out, and_23_out, and_24_out, and_25_out,
       and_26_out, and_27_out, and_28_out, and_29_out, and_30_out, and_31_out, and_32_out, and_33_out,
       and_34_out, not_1_out, not_2_out, not_3_out, not_4_out, not_5_out, not_6_out, not_7_out, not_8_out,
       not_9_out, not_10_out, not_11_out, not_12_out, not_13_out, not_14_out, not_15_out, not_16_out,
       not_17_out, not_18_out, not_19_out, not_20_out, not_21_out, not_22_out, not_23_out, not_24_out,
       not_25_out, not_26_out, not_27_out, not_28_out, not_29_out, not_30_out, not_31_out, not_32_out,
       not_33_out, not_34_out, not_35_out, not_36_out, not_37_out, not_38_out, not_39_out, not_40_out,
       not_41_out, not_42_out, not_43_out, not_44_out, not_45_out, not_46_out, not_47_out, not_48_out,
       not_49_out, not_50_out, not_51_out, not_52_out, not_53_out, not_54_out, not_55_out, not_56_out,
       not_57_out, not_58_out, not_59_out, not_60_out, not_61_out, not_62_out, not_63_out, not_64_out,
       not_65_out, not_66_out, not_67_out, not_68_out, not_69_out, not_70_out, not_71_out, not_72_out,
       not_73_out, not_74_out, not_75_out, not_76_out, not_77_out, not_78_out, not_79_out, not_80_out,
       not_81_out, not_82_out, not_83_out, not_84_out, not_85_out, not_86_out, not_87_out, not_88_out,
       not_89_out, not_90_out, not_91_out, not_92_out, not_93_out, not_94_out, not_95_out, not_96_out,
       not_97_out, not_98_out, not_99_out, not_100_out, not_101_out, not_102_out, not_103_out, not_104_out,
       not_105_out, not_106_out, not_107_out, not_108_out, not_109_out, not_110_out, not_111_out,
       not_112_out, not_113_out, not_114_out, not_115_out, not_116_out, not_117_out, not_118_out,
       not_119_out, not_120_out, not_121_out, not_122_out, not_123_out, not_124_out, not_125_out,
       not_126_out, not_127_out, not_128_out, not_129_out, not_130_out, not_131_out, not_132_out,
       not_133_out, not_134_out, not_135_out, not_136_out, not_137_out, not_138_out, not_139_out,
       not_140_out, not_141_out, not_142_out, not_143_out, not_144_out, not_145_out, not_146_out,
       not_147_out, not_148_out, not_149_out, not_150_out, not_151_out, not_152_out, not_153_out,
       not_154_out, not_155_out, not_156_out, not_157_out, not_158_out, not_159_out, not_160_out,
       not_161_out, not_162_out, not_163_out, not_164_out, not_165_out, not_166_out, not_167_out,
       not_168_out, not_169_out, not_170_out, not_171_out, not_172_out, not_173_out, not_174_out,
       not_175_out, not_176_out, not_177_out, not_178_out, not_179_out, not_180_out, not_181_out,
       not_182_out, not_183_out, not_184_out, not_185_out, not_186_out, not_187_out, not_188_out,
       not_189_out, not_190_out, not_191_out, not_192_out, not_193_out, not_194_out, not_195_out,
       not_196_out, not_197_out, not_198_out, not_199_out, not_200_out, not_201_out, not_202_out,
       not_203_out, not_204_out, not_205_out, not_206_out;

  not not_1 (not_1_out, F30);
  not not_2 (not_2_out, F25);
  not not_3 (not_3_out, F14);
  not not_4 (not_4_out, F13);
  not not_5 (not_5_out, F12);
  not not_6 (not_6_out, OP6);
  not not_7 (not_7_out, OP3);
  not not_8 (not_8_out, OP2);
  not not_9 (not_9_out, F30);
  not not_10 (not_10_out, F25);
  not not_11 (not_11_out, OP6);
  not not_12 (not_12_out, OP3);
  not not_13 (not_13_out, OP2);
  not not_14 (not_14_out, F30);
  not not_15 (not_15_out, F25);
  not not_16 (not_16_out, F14);
  not not_17 (not_17_out, F12);
  not not_18 (not_18_out, OP6);
  not not_19 (not_19_out, OP3);
  not not_20 (not_20_out, OP2);
  not not_21 (not_21_out, F14);
  not not_22 (not_22_out, F13);
  not not_23 (not_23_out, F12);
  not not_24 (not_24_out, OP6);
  not not_25 (not_25_out, OP5);
  not not_26 (not_26_out, OP3);
  not not_27 (not_27_out, OP2);
  not not_28 (not_28_out, OP6);
  not not_29 (not_29_out, OP5);
  not not_30 (not_30_out, OP3);
  not not_31 (not_31_out, OP2);
  not not_32 (not_32_out, F13);
  not not_33 (not_33_out, F12);
  not not_34 (not_34_out, OP6);
  not not_35 (not_35_out, OP5);
  not not_36 (not_36_out, OP3);
  not not_37 (not_37_out, OP2);
  not not_38 (not_38_out, F14);
  not not_39 (not_39_out, F12);
  not not_40 (not_40_out, OP6);
  not not_41 (not_41_out, OP5);
  not not_42 (not_42_out, OP3);
  not not_43 (not_43_out, OP2);
  not not_44 (not_44_out, F25);
  not not_45 (not_45_out, F13);
  not not_46 (not_46_out, OP6);
  not not_47 (not_47_out, OP5);
  not not_48 (not_48_out, OP3);
  not not_49 (not_49_out, OP2);
  not not_50 (not_50_out, F14);
  not not_51 (not_51_out, F12);
  not not_52 (not_52_out, OP6);
  not not_53 (not_53_out, OP5);
  not not_54 (not_54_out, OP4);
  not not_55 (not_55_out, OP3);
  not not_56 (not_56_out, OP2);
  not not_57 (not_57_out, F14);
  not not_58 (not_58_out, F12);
  not not_59 (not_59_out, OP6);
  not not_60 (not_60_out, OP4);
  not not_61 (not_61_out, OP3);
  not not_62 (not_62_out, OP2);
  not not_63 (not_63_out, F30);
  not not_64 (not_64_out, F25);
  not not_65 (not_65_out, F13);
  not not_66 (not_66_out, F12);
  not not_67 (not_67_out, OP6);
  not not_68 (not_68_out, OP3);
  not not_69 (not_69_out, OP2);
  not not_70 (not_70_out, F25);
  not not_71 (not_71_out, F14);
  not not_72 (not_72_out, F13);
  not not_73 (not_73_out, F12);
  not not_74 (not_74_out, OP6);
  not not_75 (not_75_out, OP3);
  not not_76 (not_76_out, OP2);
  not not_77 (not_77_out, F30);
  not not_78 (not_78_out, F25);
  not not_79 (not_79_out, OP6);
  not not_80 (not_80_out, OP3);
  not not_81 (not_81_out, OP2);
  not not_82 (not_82_out, F30);
  not not_83 (not_83_out, F25);
  not not_84 (not_84_out, F14);
  not not_85 (not_85_out, F12);
  not not_86 (not_86_out, OP6);
  not not_87 (not_87_out, OP3);
  not not_88 (not_88_out, OP2);
  not not_89 (not_89_out, OP6);
  not not_90 (not_90_out, OP5);
  not not_91 (not_91_out, OP3);
  not not_92 (not_92_out, OP2);
  not not_93 (not_93_out, F14);
  not not_94 (not_94_out, F12);
  not not_95 (not_95_out, OP6);
  not not_96 (not_96_out, OP5);
  not not_97 (not_97_out, OP3);
  not not_98 (not_98_out, OP2);
  not not_99 (not_99_out, F30);
  not not_100 (not_100_out, F25);
  not not_101 (not_101_out, F13);
  not not_102 (not_102_out, OP6);
  not not_103 (not_103_out, OP5);
  not not_104 (not_104_out, OP3);
  not not_105 (not_105_out, OP2);
  not not_106 (not_106_out, F30);
  not not_107 (not_107_out, F25);
  not not_108 (not_108_out, F14);
  not not_109 (not_109_out, F13);
  not not_110 (not_110_out, F12);
  not not_111 (not_111_out, OP6);
  not not_112 (not_112_out, OP3);
  not not_113 (not_113_out, OP2);
  not not_114 (not_114_out, F25);
  not not_115 (not_115_out, F14);
  not not_116 (not_116_out, F13);
  not not_117 (not_117_out, F12);
  not not_118 (not_118_out, OP6);
  not not_119 (not_119_out, OP3);
  not not_120 (not_120_out, OP2);
  not not_121 (not_121_out, F30);
  not not_122 (not_122_out, F25);
  not not_123 (not_123_out, OP6);
  not not_124 (not_124_out, OP3);
  not not_125 (not_125_out, OP2);
  not not_126 (not_126_out, F30);
  not not_127 (not_127_out, F25);
  not not_128 (not_128_out, F14);
  not not_129 (not_129_out, OP6);
  not not_130 (not_130_out, OP3);
  not not_131 (not_131_out, OP2);
  not not_132 (not_132_out, F14);
  not not_133 (not_133_out, F13);
  not not_134 (not_134_out, F12);
  not not_135 (not_135_out, OP6);
  not not_136 (not_136_out, OP5);
  not not_137 (not_137_out, OP3);
  not not_138 (not_138_out, OP2);
  not not_139 (not_139_out, OP6);
  not not_140 (not_140_out, OP5);
  not not_141 (not_141_out, OP3);
  not not_142 (not_142_out, OP2);
  not not_143 (not_143_out, F14);
  not not_144 (not_144_out, F12);
  not not_145 (not_145_out, OP6);
  not not_146 (not_146_out, OP5);
  not not_147 (not_147_out, OP4);
  not not_148 (not_148_out, OP3);
  not not_149 (not_149_out, OP2);
  not not_150 (not_150_out, F14);
  not not_151 (not_151_out, F12);
  not not_152 (not_152_out, OP6);
  not not_153 (not_153_out, OP4);
  not not_154 (not_154_out, OP3);
  not not_155 (not_155_out, OP2);
  not not_156 (not_156_out, F12);
  not not_157 (not_157_out, OP4);
  not not_158 (not_158_out, OP3);
  not not_159 (not_159_out, OP2);
  not not_160 (not_160_out, F30);
  not not_161 (not_161_out, F25);
  not not_162 (not_162_out, F12);
  not not_163 (not_163_out, OP6);
  not not_164 (not_164_out, OP3);
  not not_165 (not_165_out, OP2);
  not not_166 (not_166_out, F30);
  not not_167 (not_167_out, F25);
  not not_168 (not_168_out, F14);
  not not_169 (not_169_out, F12);
  not not_170 (not_170_out, OP6);
  not not_171 (not_171_out, OP3);
  not not_172 (not_172_out, OP2);
  not not_173 (not_173_out, F30);
  not not_174 (not_174_out, F25);
  not not_175 (not_175_out, F14);
  not not_176 (not_176_out, OP6);
  not not_177 (not_177_out, OP3);
  not not_178 (not_178_out, OP2);
  not not_179 (not_179_out, F12);
  not not_180 (not_180_out, OP6);
  not not_181 (not_181_out, OP5);
  not not_182 (not_182_out, OP3);
  not not_183 (not_183_out, OP2);
  not not_184 (not_184_out, F13);
  not not_185 (not_185_out, F12);
  not not_186 (not_186_out, OP6);
  not not_187 (not_187_out, OP5);
  not not_188 (not_188_out, OP3);
  not not_189 (not_189_out, OP2);
  not not_190 (not_190_out, F14);
  not not_191 (not_191_out, F12);
  not not_192 (not_192_out, OP6);
  not not_193 (not_193_out, OP5);
  not not_194 (not_194_out, OP3);
  not not_195 (not_195_out, OP2);
  not not_196 (not_196_out, F30);
  not not_197 (not_197_out, F25);
  not not_198 (not_198_out, F13);
  not not_199 (not_199_out, F12);
  not not_200 (not_200_out, OP6);
  not not_201 (not_201_out, OP3);
  not not_202 (not_202_out, OP2);
  not not_203 (not_203_out, F12);
  not not_204 (not_204_out, OP4);
  not not_205 (not_205_out, OP3);
  not not_206 (not_206_out, OP2);
  and and_1 (and_1_out, not_1_out, not_2_out, not_3_out, not_4_out, not_5_out, not_6_out, OP5, OP4, not_7_out, not_8_out);
  and and_2 (and_2_out, not_9_out, not_10_out, F14, F13, F12, not_11_out, OP5, OP4, not_12_out, not_13_out);
  and and_3 (and_3_out, not_14_out, not_15_out, not_16_out, F13, not_17_out, not_18_out, OP5, OP4, not_19_out, not_20_out);
  and and_4 (and_4_out, not_21_out, not_22_out, not_23_out, not_24_out, not_25_out, OP4, not_26_out, not_27_out);
  and and_5 (and_5_out, F14, F13, F12, not_28_out, not_29_out, OP4, not_30_out, not_31_out);
  and and_6 (and_6_out, F14, not_32_out, not_33_out, not_34_out, not_35_out, OP4, not_36_out, not_37_out);
  and and_7 (and_7_out, not_38_out, F13, not_39_out, not_40_out, not_41_out, OP4, not_42_out, not_43_out);
  and and_8 (and_8_out, F30, not_44_out, F14, not_45_out, F12, not_46_out, not_47_out, OP4, not_48_out, not_49_out);
  and and_9 (and_9_out, not_50_out, F13, not_51_out, not_52_out, not_53_out, not_54_out, not_55_out, not_56_out);
  and and_10 (and_10_out, not_57_out, F13, not_58_out, not_59_out, OP5, not_60_out, not_61_out, not_62_out);
  and and_11 (and_11_out, not_63_out, not_64_out, F14, not_65_out, not_66_out, not_67_out, OP5, OP4, not_68_out, not_69_out);
  and and_12 (and_12_out, F30, not_70_out, not_71_out, not_72_out, not_73_out, not_74_out, OP5, OP4, not_75_out, not_76_out);
  and and_13 (and_13_out, not_77_out, not_78_out, F14, F13, F12, not_79_out, OP5, OP4, not_80_out, not_81_out);
  and and_14 (and_14_out, not_82_out, not_83_out, not_84_out, F13, not_85_out, not_86_out, OP5, OP4, not_87_out, not_88_out);
  and and_15 (and_15_out, F14, F13, F12, not_89_out, not_90_out, OP4, not_91_out, not_92_out);
  and and_16 (and_16_out, not_93_out, F13, not_94_out, not_95_out, not_96_out, OP4, not_97_out, not_98_out);
  and and_17 (and_17_out, not_99_out, not_100_out, F14, not_101_out, F12, not_102_out, not_103_out, OP4, not_104_out, not_105_out);
  and and_18 (and_18_out, not_106_out, not_107_out, not_108_out, not_109_out, not_110_out, not_111_out, OP5, OP4, not_112_out, not_113_out);
  and and_19 (and_19_out, F30, not_114_out, not_115_out, not_116_out, not_117_out, not_118_out, OP5, OP4, not_119_out, not_120_out);
  and and_20 (and_20_out, not_121_out, not_122_out, F14, F13, F12, not_123_out, OP5, OP4, not_124_out, not_125_out);
  and and_21 (and_21_out, not_126_out, not_127_out, not_128_out, F13, F12, not_129_out, OP5, OP4, not_130_out, not_131_out);
  and and_22 (and_22_out, not_132_out, not_133_out, not_134_out, not_135_out, not_136_out, OP4, not_137_out, not_138_out);
  and and_23 (and_23_out, F14, F13, F12, not_139_out, not_140_out, OP4, not_141_out, not_142_out);
  and and_24 (and_24_out, not_143_out, F13, not_144_out, not_145_out, not_146_out, not_147_out, not_148_out, not_149_out);
  and and_25 (and_25_out, not_150_out, F13, not_151_out, not_152_out, OP5, not_153_out, not_154_out, not_155_out);
  and and_26 (and_26_out, F14, F13, not_156_out, OP6, OP5, not_157_out, not_158_out, not_159_out);
  and and_27 (and_27_out, not_160_out, not_161_out, F14, F13, not_162_out, not_163_out, OP5, OP4, not_164_out, not_165_out);
  and and_28 (and_28_out, not_166_out, not_167_out, not_168_out, F13, not_169_out, not_170_out, OP5, OP4, not_171_out, not_172_out);
  and and_29 (and_29_out, not_173_out, not_174_out, not_175_out, F13, F12, not_176_out, OP5, OP4, not_177_out, not_178_out);
  and and_30 (and_30_out, F14, F13, not_179_out, not_180_out, not_181_out, OP4, not_182_out, not_183_out);
  and and_31 (and_31_out, F14, not_184_out, not_185_out, not_186_out, not_187_out, OP4, not_188_out, not_189_out);
  and and_32 (and_32_out, not_190_out, F13, not_191_out, not_192_out, not_193_out, OP4, not_194_out, not_195_out);
  and and_33 (and_33_out, not_196_out, not_197_out, F14, not_198_out, not_199_out, not_200_out, OP5, OP4, not_201_out, not_202_out);
  and and_34 (and_34_out, F14, F13, not_203_out, OP6, OP5, not_204_out, not_205_out, not_206_out);
  or or_1 (S0, and_1_out, and_2_out, and_3_out, and_4_out, and_5_out, and_6_out, and_7_out, and_8_out, and_9_out, and_10_out, and_11_out);
  or or_2 (S1, and_12_out, and_13_out, and_14_out, and_15_out, and_16_out, and_17_out);
  or or_3 (S2, and_18_out, and_19_out, and_20_out, and_21_out, and_22_out, and_23_out, and_24_out, and_25_out, and_26_out);
  or or_4 (S3, and_27_out, and_28_out, and_29_out, and_30_out, and_31_out, and_32_out, and_33_out, and_34_out);
endmodule

module ControlSignal (
  input  OP2,
  input  OP3,
  input  OP4,
  input  OP5,
  input  OP6,
  input  F12,
  input  F13,
  input  F14,
  input  F25,
  input  F30,
  output MemToReg,
  output MemWrite,
  output BLTU,
  output LHU,
  output AUIPC,
  output ALU_SRC,
  output RegWrite,
  output ecall,
  output S_Type,
  output BEQ,
  output BNE,
  output JALR,
  output JAL
);

  wire and_1_out, and_2_out, and_7_out, and_8_out, and_9_out, and_10_out, and_11_out, and_12_out, and_13_out,
       and_14_out, and_15_out, and_16_out, and_17_out, and_18_out, and_19_out, and_20_out, and_21_out,
       and_22_out, and_23_out, and_24_out, not_1_out, not_2_out, not_3_out, not_4_out, not_5_out, not_6_out,
       not_7_out, not_8_out, not_9_out, not_10_out, not_11_out, not_12_out, not_13_out, not_14_out,
       not_15_out, not_16_out, not_17_out, not_18_out, not_19_out, not_20_out, not_21_out, not_22_out,
       not_23_out, not_24_out, not_25_out, not_26_out, not_27_out, not_28_out, not_29_out, not_30_out,
       not_31_out, not_32_out, not_33_out, not_34_out, not_35_out, not_36_out, not_37_out, not_38_out,
       not_39_out, not_40_out, not_41_out, not_42_out, not_43_out, not_44_out, not_45_out, not_46_out,
       not_47_out, not_48_out, not_49_out, not_50_out, not_51_out, not_52_out, not_53_out, not_54_out,
       not_55_out, not_56_out, not_57_out, not_58_out, not_59_out, not_60_out, not_61_out, not_62_out,
       not_63_out, not_64_out, not_65_out, not_66_out, not_67_out, not_68_out, not_69_out, not_70_out,
       not_71_out, not_72_out, not_73_out, not_74_out, not_75_out, not_76_out, not_77_out, not_78_out,
       not_79_out, not_80_out, not_81_out, not_82_out, not_83_out, not_84_out, not_85_out, not_86_out,
       not_87_out, not_88_out, not_89_out, not_90_out, not_91_out, not_92_out, not_93_out, not_94_out,
       not_95_out, not_96_out, not_97_out, not_98_out, not_99_out, not_100_out, not_101_out, not_102_out,
       not_103_out, not_104_out, not_105_out, not_106_out, not_107_out, not_108_out, not_109_out,
       not_110_out, not_111_out, not_112_out, not_113_out, not_114_out, not_115_out, not_116_out,
       not_117_out, not_118_out, not_119_out, not_120_out, not_121_out, not_122_out, not_123_out,
       not_124_out, not_125_out, not_126_out, not_127_out, not_128_out, not_129_out, not_130_out,
       not_131_out, not_132_out, not_133_out, not_134_out, not_135_out, not_136_out, not_137_out,
       not_138_out, not_139_out, not_140_out, not_141_out, not_142_out, not_143_out, not_144_out,
       not_145_out, not_146_out, not_147_out, not_148_out, not_149_out, not_150_out;

  not not_1 (not_1_out, OP2);
  not not_2 (not_2_out, OP3);
  not not_3 (not_3_out, OP4);
  not not_4 (not_4_out, OP5);
  not not_5 (not_5_out, OP6);
  not not_6 (not_6_out, F12);
  not not_7 (not_7_out, F14);
  not not_8 (not_8_out, OP2);
  not not_9 (not_9_out, OP3);
  not not_10 (not_10_out, OP4);
  not not_11 (not_11_out, OP5);
  not not_12 (not_12_out, OP6);
  not not_13 (not_13_out, F13);
  not not_14 (not_14_out, OP2);
  not not_15 (not_15_out, OP3);
  not not_16 (not_16_out, OP4);
  not not_17 (not_17_out, OP6);
  not not_18 (not_18_out, F12);
  not not_19 (not_19_out, F14);
  not not_20 (not_20_out, OP2);
  not not_21 (not_21_out, OP3);
  not not_22 (not_22_out, OP4);
  not not_23 (not_23_out, F12);
  not not_24 (not_24_out, OP2);
  not not_25 (not_25_out, OP3);
  not not_26 (not_26_out, OP4);
  not not_27 (not_27_out, OP5);
  not not_28 (not_28_out, OP6);
  not not_29 (not_29_out, F13);
  not not_30 (not_30_out, OP3);
  not not_31 (not_31_out, OP5);
  not not_32 (not_32_out, OP6);
  not not_33 (not_33_out, OP2);
  not not_34 (not_34_out, OP3);
  not not_35 (not_35_out, OP4);
  not not_36 (not_36_out, OP6);
  not not_37 (not_37_out, F12);
  not not_38 (not_38_out, F14);
  not not_39 (not_39_out, OP2);
  not not_40 (not_40_out, OP3);
  not not_41 (not_41_out, OP4);
  not not_42 (not_42_out, OP5);
  not not_43 (not_43_out, OP6);
  not not_44 (not_44_out, F13);
  not not_45 (not_45_out, OP2);
  not not_46 (not_46_out, OP3);
  not not_47 (not_47_out, OP5);
  not not_48 (not_48_out, OP6);
  not not_49 (not_49_out, F12);
  not not_50 (not_50_out, OP2);
  not not_51 (not_51_out, OP3);
  not not_52 (not_52_out, OP5);
  not not_53 (not_53_out, OP6);
  not not_54 (not_54_out, F13);
  not not_55 (not_55_out, F25);
  not not_56 (not_56_out, F30);
  not not_57 (not_57_out, OP2);
  not not_58 (not_58_out, OP3);
  not not_59 (not_59_out, OP5);
  not not_60 (not_60_out, OP6);
  not not_61 (not_61_out, F25);
  not not_62 (not_62_out, OP2);
  not not_63 (not_63_out, OP3);
  not not_64 (not_64_out, OP5);
  not not_65 (not_65_out, OP6);
  not not_66 (not_66_out, OP2);
  not not_67 (not_67_out, OP3);
  not not_68 (not_68_out, OP5);
  not not_69 (not_69_out, OP6);
  not not_70 (not_70_out, F12);
  not not_71 (not_71_out, F14);
  not not_72 (not_72_out, OP2);
  not not_73 (not_73_out, OP3);
  not not_74 (not_74_out, OP4);
  not not_75 (not_75_out, OP5);
  not not_76 (not_76_out, OP6);
  not not_77 (not_77_out, F13);
  not not_78 (not_78_out, OP2);
  not not_79 (not_79_out, OP3);
  not not_80 (not_80_out, OP6);
  not not_81 (not_81_out, F12);
  not not_82 (not_82_out, F13);
  not not_83 (not_83_out, F14);
  not not_84 (not_84_out, F25);
  not not_85 (not_85_out, OP2);
  not not_86 (not_86_out, OP3);
  not not_87 (not_87_out, OP6);
  not not_88 (not_88_out, F12);
  not not_89 (not_89_out, F25);
  not not_90 (not_90_out, F30);
  not not_91 (not_91_out, OP3);
  not not_92 (not_92_out, OP5);
  not not_93 (not_93_out, OP6);
  not not_94 (not_94_out, F12);
  not not_95 (not_95_out, OP3);
  not not_96 (not_96_out, OP5);
  not not_97 (not_97_out, OP6);
  not not_98 (not_98_out, F13);
  not not_99 (not_99_out, F25);
  not not_100 (not_100_out, F30);
  not not_101 (not_101_out, OP3);
  not not_102 (not_102_out, OP5);
  not not_103 (not_103_out, OP6);
  not not_104 (not_104_out, F25);
  not not_105 (not_105_out, OP3);
  not not_106 (not_106_out, OP5);
  not not_107 (not_107_out, OP6);
  not not_108 (not_108_out, OP2);
  not not_109 (not_109_out, OP3);
  not not_110 (not_110_out, OP6);
  not not_111 (not_111_out, F25);
  not not_112 (not_112_out, F30);
  not not_113 (not_113_out, OP4);
  not not_114 (not_114_out, F12);
  not not_115 (not_115_out, F13);
  not not_116 (not_116_out, F14);
  not not_117 (not_117_out, OP3);
  not not_118 (not_118_out, OP5);
  not not_119 (not_119_out, OP6);
  not not_120 (not_120_out, OP4);
  not not_121 (not_121_out, OP2);
  not not_122 (not_122_out, OP3);
  not not_123 (not_123_out, F12);
  not not_124 (not_124_out, F13);
  not not_125 (not_125_out, F14);
  not not_126 (not_126_out, F25);
  not not_127 (not_127_out, F30);
  not not_128 (not_128_out, OP2);
  not not_129 (not_129_out, OP3);
  not not_130 (not_130_out, OP4);
  not not_131 (not_131_out, OP6);
  not not_132 (not_132_out, F12);
  not not_133 (not_133_out, F14);
  not not_134 (not_134_out, OP2);
  not not_135 (not_135_out, OP3);
  not not_136 (not_136_out, OP4);
  not not_137 (not_137_out, F12);
  not not_138 (not_138_out, F13);
  not not_139 (not_139_out, F14);
  not not_140 (not_140_out, OP2);
  not not_141 (not_141_out, OP3);
  not not_142 (not_142_out, OP4);
  not not_143 (not_143_out, F13);
  not not_144 (not_144_out, F14);
  not not_145 (not_145_out, OP3);
  not not_146 (not_146_out, OP4);
  not not_147 (not_147_out, F12);
  not not_148 (not_148_out, F13);
  not not_149 (not_149_out, F14);
  not not_150 (not_150_out, OP4);
  and and_1 (and_1_out, not_1_out, not_2_out, not_3_out, not_4_out, not_5_out, not_6_out, F13, not_7_out);
  and and_2 (and_2_out, not_8_out, not_9_out, not_10_out, not_11_out, not_12_out, F12, not_13_out, F14);
  and and_3 (MemWrite, not_14_out, not_15_out, not_16_out, OP5, not_17_out, not_18_out, F13, not_19_out);
  and and_4 (BLTU, not_20_out, not_21_out, not_22_out, OP5, OP6, not_23_out, F13, F14);
  and and_5 (LHU, not_24_out, not_25_out, not_26_out, not_27_out, not_28_out, F12, not_29_out, F14);
  and and_6 (AUIPC, OP2, not_30_out, OP4, not_31_out, not_32_out);
  and and_7 (and_7_out, not_33_out, not_34_out, not_35_out, not_36_out, not_37_out, F13, not_38_out);
  and and_8 (and_8_out, not_39_out, not_40_out, not_41_out, not_42_out, not_43_out, F12, not_44_out, F14);
  and and_9 (and_9_out, not_45_out, not_46_out, OP4, not_47_out, not_48_out, not_49_out);
  and and_10 (and_10_out, not_50_out, not_51_out, OP4, not_52_out, not_53_out, not_54_out, not_55_out, not_56_out);
  and and_11 (and_11_out, not_57_out, not_58_out, OP4, not_59_out, not_60_out, F14, not_61_out);
  and and_12 (and_12_out, not_62_out, not_63_out, OP4, not_64_out, not_65_out, F13, F14);
  and and_13 (and_13_out, not_66_out, not_67_out, not_68_out, not_69_out, not_70_out, F13, not_71_out);
  and and_14 (and_14_out, not_72_out, not_73_out, not_74_out, not_75_out, not_76_out, F12, not_77_out, F14);
  and and_15 (and_15_out, not_78_out, not_79_out, OP4, not_80_out, not_81_out, not_82_out, not_83_out, not_84_out);
  and and_16 (and_16_out, not_85_out, not_86_out, OP4, not_87_out, not_88_out, not_89_out, not_90_out);
  and and_17 (and_17_out, not_91_out, OP4, not_92_out, not_93_out, not_94_out);
  and and_18 (and_18_out, not_95_out, OP4, not_96_out, not_97_out, not_98_out, not_99_out, not_100_out);
  and and_19 (and_19_out, not_101_out, OP4, not_102_out, not_103_out, F14, not_104_out);
  and and_20 (and_20_out, not_105_out, OP4, not_106_out, not_107_out, F13, F14);
  and and_21 (and_21_out, not_108_out, not_109_out, OP4, OP5, not_110_out, F13, not_111_out, not_112_out);
  and and_22 (and_22_out, OP2, not_113_out, OP5, OP6, not_114_out, not_115_out, not_116_out);
  and and_23 (and_23_out, OP2, not_117_out, OP4, not_118_out, not_119_out);
  and and_24 (and_24_out, OP2, OP3, not_120_out, OP5, OP6);
  and and_25 (ecall, not_121_out, not_122_out, OP4, OP5, OP6, not_123_out, not_124_out, not_125_out, not_126_out, not_127_out);
  and and_26 (S_Type, not_128_out, not_129_out, not_130_out, OP5, not_131_out, not_132_out, F13, not_133_out);
  and and_27 (BEQ, not_134_out, not_135_out, not_136_out, OP5, OP6, not_137_out, not_138_out, not_139_out);
  and and_28 (BNE, not_140_out, not_141_out, not_142_out, OP5, OP6, F12, not_143_out, not_144_out);
  and and_29 (JALR, OP2, not_145_out, not_146_out, OP5, OP6, not_147_out, not_148_out, not_149_out);
  and and_30 (JAL, OP2, OP3, not_150_out, OP5, OP6);
  or or_1 (MemToReg, and_1_out, and_2_out);
  or or_2 (ALU_SRC, and_7_out, and_8_out, and_9_out, and_10_out, and_11_out, and_12_out);
  or or_3 (RegWrite, and_13_out, and_14_out, and_15_out, and_16_out, and_17_out, and_18_out, and_19_out, and_20_out, and_21_out, and_22_out, and_23_out, and_24_out);
endmodule

module Regifile (
  input  [4:0] R1Adr,
  input  [4:0] R2Adr,
  input  [31:0] Din,
  input  Clk,
  input  WE,
  input  [4:0] WAdr,
  output [31:0] R1,
  output [31:0] R2
);

  wire and_1_out, and_2_out, and_3_out, and_4_out, and_5_out, and_6_out, and_7_out, and_8_out, and_9_out,
       and_10_out, and_11_out, and_12_out, and_13_out, and_14_out, and_15_out, and_16_out, and_17_out,
       and_18_out, and_19_out, and_20_out, and_21_out, and_22_out, and_23_out, and_24_out, and_25_out,
       and_26_out, and_27_out, and_28_out, and_29_out, and_30_out, and_31_out;
  wire [31:0] Dout00, Dout01, Dout02, Dout03, Dout04, Dout05, Dout06, Dout07, Dout08, Dout09, Dout10, Dout11,
       Dout12, Dout13, Dout14, Dout15, Dout16, Dout17, Dout18, Dout19, Dout20, Dout21, Dout22, Dout23,
       Dout24, Dout25, Dout26, Dout27, Dout28, Dout29, Dout30, Dout31;

  and and_1 (and_1_out, WE, ~WAdr[0], ~WAdr[1], WAdr[2], ~WAdr[3], ~WAdr[4]);  // AND_Gate
  and and_2 (and_2_out, WE, ~WAdr[0], ~WAdr[1], ~WAdr[2], WAdr[3], ~WAdr[4]);  // AND_Gate
  and and_3 (and_3_out, WE, ~WAdr[0], ~WAdr[1], WAdr[2], WAdr[3], ~WAdr[4]);  // AND_Gate
  and and_4 (and_4_out, WE, ~WAdr[0], ~WAdr[1], ~WAdr[2], ~WAdr[3], WAdr[4]);  // AND_Gate
  and and_5 (and_5_out, WE, ~WAdr[0], ~WAdr[1], WAdr[2], ~WAdr[3], WAdr[4]);  // AND_Gate
  and and_6 (and_6_out, WE, ~WAdr[0], ~WAdr[1], ~WAdr[2], WAdr[3], WAdr[4]);  // AND_Gate
  and and_7 (and_7_out, WE, ~WAdr[0], ~WAdr[1], WAdr[2], WAdr[3], WAdr[4]);  // AND_Gate
  Register #(.width(32), .trigger("rising"), .Select("low")) register_1 (
    .D(Din), .en(1'b0), .Q(Dout00), .clk(Clk));  // open: clr
  Register #(.width(32), .trigger("rising"), .Select("low")) register_2 (
    .D(Din), .en(and_1_out), .Q(Dout04), .clk(Clk));  // open: clr
  Register #(.width(32), .trigger("rising"), .Select("low")) register_3 (
    .D(Din), .en(and_2_out), .Q(Dout08), .clk(Clk));  // open: clr
  Register #(.width(32), .trigger("rising"), .Select("low")) register_4 (
    .D(Din), .en(and_3_out), .Q(Dout12), .clk(Clk));  // open: clr
  Register #(.width(32), .trigger("rising"), .Select("low")) register_5 (
    .D(Din), .en(and_4_out), .Q(Dout16), .clk(Clk));  // open: clr
  Register #(.width(32), .trigger("rising"), .Select("low")) register_6 (
    .D(Din), .en(and_5_out), .Q(Dout20), .clk(Clk));  // open: clr
  Register #(.width(32), .trigger("rising"), .Select("low")) register_7 (
    .D(Din), .en(and_6_out), .Q(Dout24), .clk(Clk));  // open: clr
  Register #(.width(32), .trigger("rising"), .Select("low")) register_8 (
    .D(Din), .en(and_7_out), .Q(Dout28), .clk(Clk));  // open: clr
  and and_8 (and_8_out, WE, WAdr[0], ~WAdr[1], ~WAdr[2], ~WAdr[3], ~WAdr[4]);  // AND_Gate
  and and_9 (and_9_out, WE, WAdr[0], ~WAdr[1], WAdr[2], ~WAdr[3], ~WAdr[4]);  // AND_Gate
  and and_10 (and_10_out, WE, WAdr[0], ~WAdr[1], ~WAdr[2], WAdr[3], ~WAdr[4]);  // AND_Gate
  and and_11 (and_11_out, WE, WAdr[0], ~WAdr[1], WAdr[2], WAdr[3], ~WAdr[4]);  // AND_Gate
  and and_12 (and_12_out, WE, WAdr[0], ~WAdr[1], ~WAdr[2], ~WAdr[3], WAdr[4]);  // AND_Gate
  and and_13 (and_13_out, WE, WAdr[0], ~WAdr[1], WAdr[2], ~WAdr[3], WAdr[4]);  // AND_Gate
  and and_14 (and_14_out, WE, WAdr[0], ~WAdr[1], ~WAdr[2], WAdr[3], WAdr[4]);  // AND_Gate
  and and_15 (and_15_out, WE, WAdr[0], ~WAdr[1], WAdr[2], WAdr[3], WAdr[4]);  // AND_Gate
  Register #(.width(32), .trigger("rising"), .Select("low")) register_9 (
    .D(Din), .en(and_8_out), .Q(Dout01), .clk(Clk));  // open: clr
  Register #(.width(32), .trigger("rising"), .Select("low")) register_10 (
    .D(Din), .en(and_9_out), .Q(Dout05), .clk(Clk));  // open: clr
  Register #(.width(32), .trigger("rising"), .Select("low")) register_11 (
    .D(Din), .en(and_10_out), .Q(Dout09), .clk(Clk));  // open: clr
  Register #(.width(32), .trigger("rising"), .Select("low")) register_12 (
    .D(Din), .en(and_11_out), .Q(Dout13), .clk(Clk));  // open: clr
  Register #(.width(32), .trigger("rising"), .Select("low")) register_13 (
    .D(Din), .en(and_12_out), .Q(Dout17), .clk(Clk));  // open: clr
  Register #(.width(32), .trigger("rising"), .Select("low")) register_14 (
    .D(Din), .en(and_13_out), .Q(Dout21), .clk(Clk));  // open: clr
  Register #(.width(32), .trigger("rising"), .Select("low")) register_15 (
    .D(Din), .en(and_14_out), .Q(Dout25), .clk(Clk));  // open: clr
  Register #(.width(32), .trigger("rising"), .Select("low")) register_16 (
    .D(Din), .en(and_15_out), .Q(Dout29), .clk(Clk));  // open: clr
  and and_16 (and_16_out, WE, ~WAdr[0], WAdr[1], ~WAdr[2], ~WAdr[3], ~WAdr[4]);  // AND_Gate
  and and_17 (and_17_out, WE, ~WAdr[0], WAdr[1], WAdr[2], ~WAdr[3], ~WAdr[4]);  // AND_Gate
  and and_18 (and_18_out, WE, ~WAdr[0], WAdr[1], ~WAdr[2], WAdr[3], ~WAdr[4]);  // AND_Gate
  and and_19 (and_19_out, WE, ~WAdr[0], WAdr[1], WAdr[2], WAdr[3], ~WAdr[4]);  // AND_Gate
  and and_20 (and_20_out, WE, ~WAdr[0], WAdr[1], ~WAdr[2], ~WAdr[3], WAdr[4]);  // AND_Gate
  and and_21 (and_21_out, WE, ~WAdr[0], WAdr[1], WAdr[2], ~WAdr[3], WAdr[4]);  // AND_Gate
  and and_22 (and_22_out, WE, ~WAdr[0], WAdr[1], ~WAdr[2], WAdr[3], WAdr[4]);  // AND_Gate
  and and_23 (and_23_out, WE, ~WAdr[0], WAdr[1], WAdr[2], WAdr[3], WAdr[4]);  // AND_Gate
  Multiplexer #(.select(5), .width(32), .disabled(0), .enable("false")) multiplexer_1 (
    .in0(Dout00), .in1(Dout01), .in2(Dout02), .in3(Dout03), .in4(Dout04), .in5(Dout05), .in6(Dout06),
    .in7(Dout07), .in8(Dout08), .in9(Dout09), .in10(Dout10), .in11(Dout11), .in12(Dout12), .in13(Dout13),
    .in14(Dout14), .in15(Dout15), .in16(Dout16), .in17(Dout17), .in18(Dout18), .in19(Dout19), .in20(Dout20),
    .in21(Dout21), .in22(Dout22), .in23(Dout23), .in24(Dout24), .in25(Dout25), .in26(Dout26), .in27(Dout27),
    .in28(Dout28), .in29(Dout29), .in30(Dout30), .in31(Dout31), .out(R1), .sel(R1Adr));
  Register #(.width(32), .trigger("rising"), .Select("low")) register_17 (
    .D(Din), .en(and_16_out), .Q(Dout02), .clk(Clk));  // open: clr
  Register #(.width(32), .trigger("rising"), .Select("low")) register_18 (
    .D(Din), .en(and_17_out), .Q(Dout06), .clk(Clk));  // open: clr
  Register #(.width(32), .trigger("rising"), .Select("low")) register_19 (
    .D(Din), .en(and_18_out), .Q(Dout10), .clk(Clk));  // open: clr
  Register #(.width(32), .trigger("rising"), .Select("low")) register_20 (
    .D(Din), .en(and_19_out), .Q(Dout14), .clk(Clk));  // open: clr
  Register #(.width(32), .trigger("rising"), .Select("low")) register_21 (
    .D(Din), .en(and_20_out), .Q(Dout18), .clk(Clk));  // open: clr
  Register #(.width(32), .trigger("rising"), .Select("low")) register_22 (
    .D(Din), .en(and_21_out), .Q(Dout22), .clk(Clk));  // open: clr
  Register #(.width(32), .trigger("rising"), .Select("low")) register_23 (
    .D(Din), .en(and_22_out), .Q(Dout26), .clk(Clk));  // open: clr
  Register #(.width(32), .trigger("rising"), .Select("low")) register_24 (
    .D(Din), .en(and_23_out), .Q(Dout30), .clk(Clk));  // open: clr
  and and_24 (and_24_out, WE, WAdr[0], WAdr[1], ~WAdr[2], ~WAdr[3], ~WAdr[4]);  // AND_Gate
  and and_25 (and_25_out, WE, WAdr[0], WAdr[1], WAdr[2], ~WAdr[3], ~WAdr[4]);  // AND_Gate
  and and_26 (and_26_out, WE, WAdr[0], WAdr[1], ~WAdr[2], WAdr[3], ~WAdr[4]);  // AND_Gate
  and and_27 (and_27_out, WE, WAdr[0], WAdr[1], WAdr[2], WAdr[3], ~WAdr[4]);  // AND_Gate
  and and_28 (and_28_out, WE, WAdr[0], WAdr[1], ~WAdr[2], ~WAdr[3], WAdr[4]);  // AND_Gate
  and and_29 (and_29_out, WE, WAdr[0], WAdr[1], WAdr[2], ~WAdr[3], WAdr[4]);  // AND_Gate
  and and_30 (and_30_out, WE, WAdr[0], WAdr[1], ~WAdr[2], WAdr[3], WAdr[4]);  // AND_Gate
  and and_31 (and_31_out, WE, WAdr[0], WAdr[1], WAdr[2], WAdr[3], WAdr[4]);
  Multiplexer #(.select(5), .width(32), .disabled(0), .enable("false")) multiplexer_2 (
    .in0(Dout00), .in1(Dout01), .in2(Dout02), .in3(Dout03), .in4(Dout04), .in5(Dout05), .in6(Dout06),
    .in7(Dout07), .in8(Dout08), .in9(Dout09), .in10(Dout10), .in11(Dout11), .in12(Dout12), .in13(Dout13),
    .in14(Dout14), .in15(Dout15), .in16(Dout16), .in17(Dout17), .in18(Dout18), .in19(Dout19), .in20(Dout20),
    .in21(Dout21), .in22(Dout22), .in23(Dout23), .in24(Dout24), .in25(Dout25), .in26(Dout26), .in27(Dout27),
    .in28(Dout28), .in29(Dout29), .in30(Dout30), .in31(Dout31), .out(R2), .sel(R2Adr));
  Register #(.width(32), .trigger("rising"), .Select("low")) register_25 (
    .D(Din), .en(and_24_out), .Q(Dout03), .clk(Clk));  // open: clr
  Register #(.width(32), .trigger("rising"), .Select("low")) register_26 (
    .D(Din), .en(and_25_out), .Q(Dout07), .clk(Clk));  // open: clr
  Register #(.width(32), .trigger("rising"), .Select("low")) register_27 (
    .D(Din), .en(and_26_out), .Q(Dout11), .clk(Clk));  // open: clr
  Register #(.width(32), .trigger("rising"), .Select("low")) register_28 (
    .D(Din), .en(and_27_out), .Q(Dout15), .clk(Clk));  // open: clr
  Register #(.width(32), .trigger("rising"), .Select("low")) register_29 (
    .D(Din), .en(and_28_out), .Q(Dout19), .clk(Clk));  // open: clr
  Register #(.width(32), .trigger("rising"), .Select("low")) register_30 (
    .D(Din), .en(and_29_out), .Q(Dout23), .clk(Clk));  // open: clr
  Register #(.width(32), .trigger("rising"), .Select("low")) register_31 (
    .D(Din), .en(and_30_out), .Q(Dout27), .clk(Clk));  // open: clr
  Register #(.width(32), .trigger("rising"), .Select("low")) register_32 (
    .D(Din), .en(and_31_out), .Q(Dout31), .clk(Clk));  // open: clr

  // Other names for the same wires on the sheet: W0 = WAdr[0]; W1 = WAdr[1]; W2 = WAdr[2]; W3 = WAdr[3]; W4 = WAdr[4]
endmodule

module ALU (
  input  [31:0] X,
  input  [31:0] Y,
  input  [3:0] AluOP,
  output out_4,
  output Equal,
  output out_6,
  output [31:0] Result,
  output [31:0] Result_2
);

  wire [0:0] comparator_1_lt, comparator_2_lt;
  wire [31:0] adder_1_out, AND_out, NOR_out, OR_out, shifter_1_out, shifter_2_out, shifter_3_out,
       subtractor_1_out, XOR_out;

  assign AND_out = X & Y;  // AND_Gate AND, 32 bits wide
  assign OR_out = X | Y;  // OR_Gate OR, 32 bits wide
  Shifter #(.width(32), .shift("ll")) shifter_1 (.in(X), .\dist (Y[4:0]), .out(shifter_1_out));
  Shifter #(.width(32), .shift("ar")) shifter_2 (.in(X), .\dist (Y[4:0]), .out(shifter_2_out));
  Shifter #(.width(32), .shift("lr")) shifter_3 (.in(X), .\dist (Y[4:0]), .out(shifter_3_out));
  Adder #(.width(32)) adder_1 (.a(X), .b(Y), .out(adder_1_out));  // open: cin, cout
  Subtractor #(.width(32)) subtractor_1 (.a(X), .b(Y), .out(subtractor_1_out));  // open: bin, bout
  assign XOR_out = X ^ Y;  // XOR_Gate XOR, 32 bits wide
  assign NOR_out = ~(X | Y);  // NOR_Gate NOR, 32 bits wide
  Comparator #(.width(32), .mode("twosComplement")) comparator_1 (
    .a(X), .b(Y), .eq(Equal), .lt(comparator_1_lt[0]));  // open: gt
  Comparator #(.width(32), .mode("unsigned")) comparator_2 (.a(X), .b(Y), .lt(comparator_2_lt[0]));  // open: gt, eq
  Multiplexer #(.select(4), .width(32), .disabled(0), .enable("false")) multiplexer_1 (
    .in0(shifter_1_out), .in1(shifter_2_out), .in2(shifter_3_out), .in3({32{1'b0}}), .in4({32{1'b0}}),
    .in5(adder_1_out), .in6(subtractor_1_out), .in7(AND_out), .in8(OR_out), .in9(XOR_out), .in10(NOR_out),
    .in11({{31{1'b0}}, comparator_1_lt[0]}), .in12({{31{1'b0}}, comparator_2_lt[0]}), .in13({32{1'b0}}),
    .in14({32{1'b0}}), .in15({32{1'b0}}), .out(Result), .sel(AluOP));
  Multiplexer #(.select(4), .width(32), .disabled(0), .enable("false")) multiplexer_2 (
    .in0({32{1'b0}}), .in1({32{1'b0}}), .in2({32{1'b0}}), .in3({32{1'b0}}), .in4({32{1'b0}}),
    .in5({32{1'b0}}), .in6({32{1'b0}}), .in7({32{1'b0}}), .in8({32{1'b0}}), .in9({32{1'b0}}),
    .in10({32{1'b0}}), .in11({32{1'b0}}), .in12({32{1'b0}}), .in13({32{1'b0}}), .in14({32{1'b0}}),
    .in15({32{1'b0}}), .out(Result_2), .sel(AluOP));
  Multiplexer #(.select(4), .width(1), .disabled(0), .enable("false")) multiplexer_3 (
    .in0(1'b0), .in1(1'b0), .in2(1'b0), .in3(1'b0), .in4(1'b0), .in5(1'b0), .in6(1'b0), .in7(1'b0),
    .in8(1'b0), .in9(1'b0), .in10(1'b0), .in11(comparator_1_lt[0]), .in12(comparator_2_lt[0]), .in13(1'b0),
    .in14(1'b0), .in15(1'b0), .out(out_6), .sel(AluOP));
  not not_1 (out_4, out_6);

  // Other names for the same wires on the sheet: Result2[31:0] = Result_2; S[3:0] = AluOP; tunnel = out_6;
  //   tunnel_t = out_4
endmodule
