// Logisim project 重定向流水线动态分支预测.circ as structural Verilog: 21 circuits, main circuit ◇单周期RISC-V
module \单周期RISC_V  (
  input  IR1,
  input  IR2,
  input  IR3,
  output RegWrite,
  output MemWrite,
  output [31:0] PC,
  output [31:0] IR,
  output [31:0] RDin,
  output [31:0] MDin,
  output [31:0] LedData
);

  wire alu_1_equal, and_1_out, and_2_out, and_3_out, Branch, CLK, clock_1_out, comparator_1_eq,
       comparator_2_eq, comparator_2_lt, d_ff_1_q, Ecall, Go, halt, IR1_t, IR2_t, IR3_t, IRA, IRB, IRC, JAL,
       JALR, MemToReg, nand_1_out, not_1_out, not_2_out, not_3_out, not_4_out, not_5_out, or_5_out, RST,
       URET, W1, W2, W3, \单周期硬布线控制器_1_alu_src , \单周期硬布线控制器_1_beq , \单周期硬布线控制器_1_bne , \单周期硬布线控制器_1_s_type ;
  wire [0:0] bit_extender_3_out;
  wire [3:0] \单周期硬布线控制器_1_alu_op ;
  wire [4:0] multiplexer_3_out, multiplexer_4_out;
  wire [9:0] alu_1_result_2;
  wire [11:0] multiplexer_5_out;
  wire [12:0] CNT_num;
  wire [15:0] \总周期数 ;
  wire [31:0] adder_2_out, adder_3_out, adder_4_out, alu_1_result, bit_extender_2_out, bit_extender_4_out,
       \BranchAddress_B型指令的立即数 , \I型或S型指令的立即数 , \Jal的立即数 , multiplexer_1_out, multiplexer_2_out,
       multiplexer_7_out, multiplexer_8_out, Next_PC, PC_4, R_rs1, ram_1_data;
  wire [31:1] \Jalr的立即数 ;

  Button \u_继续运行  (.out(Go));
  Button _1 (.out(IRA));
  Button _2 (.out(IRB));
  Button _3 (.out(IRC));
  LED #(.active("true")) led_1 (.in(W1));
  LED #(.active("true")) led_2 (.in(W2));
  LED #(.active("true")) led_3 (.in(W3));
  not not_1 (not_1_out, halt);
  Hex_Digit_Display hex_digit_display_1 (.value(LedData[31:28]));  // open: dp
  // Probe on Next_PC[11:2]
  Register #(.width(32), .trigger("rising"), .Select("low")) u_PC (
    .D(Next_PC), .en(not_1_out), .Q(PC), .clk(CLK), .clr(RST));
  Hex_Digit_Display hex_digit_display_2 (.value(LedData[23:20]));  // open: dp
  Hex_Digit_Display hex_digit_display_3 (.value(LedData[27:24]));  // open: dp
  // Probe on PC[11:2]
  Adder #(.width(32)) adder_1 (.a(PC), .b(32'h4), .out(PC_4));  // open: cin, cout
  Hex_Digit_Display hex_digit_display_4 (.value(LedData[15:12]));  // open: dp
  Hex_Digit_Display hex_digit_display_5 (.value(LedData[19:16]));  // open: dp
  // RiscV_Probe riscv_probe_1: pin names not known; wires that end beside it: IR
  Adder #(.width(32)) adder_2 (.a(PC), .b(\BranchAddress_B型指令的立即数 ), .out(adder_2_out));  // open: cin, cout
  Adder #(.width(32)) adder_3 (.a(PC), .b(\Jal的立即数 ), .out(adder_3_out));  // open: cin, cout
  Adder #(.width(32)) adder_4 (.a(R_rs1), .b({\Jalr的立即数 , 1'b0}), .out(adder_4_out));  // open: cin, cout
  Hex_Digit_Display hex_digit_display_6 (.value(LedData[11:8]));  // open: dp
  Hex_Digit_Display hex_digit_display_7 (.value(LedData[7:4]));  // open: dp
  // Probe on \总周期数 
  ROM #(.addrWidth(10), .dataWidth(32), .Select("high")) rom_1 (.addr(PC[11:2]), .data(IR));
  Multiplexer #(.select(1), .width(32), .disabled("Z"), .enable("false")) multiplexer_1 (
    .in0(PC_4), .in1(adder_2_out), .out(multiplexer_1_out), .sel(Branch));
  Hex_Digit_Display hex_digit_display_8 (.value(LedData[3:0]));  // open: dp
  Multiplexer #(.select(1), .width(32), .disabled("Z"), .enable("false")) multiplexer_2 (
    .in0(multiplexer_1_out), .in1(adder_3_out), .out(multiplexer_2_out), .sel(JAL));
  \单周期硬布线控制器  \u_单周期硬布线控制器_1  (
    .Funct({IR[30], IR[25], IR[14:12]}), .OP(IR[6:2]), .ALU_OP(\单周期硬布线控制器_1_alu_op ), .MemToReg(MemToReg),
    .MemWrite(MemWrite), .ALU_SRC(\单周期硬布线控制器_1_alu_src ), .RegWrite(RegWrite), .ecall(Ecall),
    .S_type(\单周期硬布线控制器_1_s_type ), .Jalr(JALR), .Beq(\单周期硬布线控制器_1_beq ), .JAL(JAL), .Bne(\单周期硬布线控制器_1_bne ),
    .in_3(IR[21]), .uret(URET));  // open: Readrs1, Readrs2
  Multiplexer #(.select(1), .width(5), .disabled("Z"), .enable("false")) multiplexer_3 (
    .in0(IR[19:15]), .in1(5'b10001), .out(multiplexer_3_out), .sel(Ecall));
  Multiplexer #(.select(1), .width(5), .disabled("Z"), .enable("false")) multiplexer_4 (
    .in0(IR[24:20]), .in1(5'b01010), .out(multiplexer_4_out), .sel(Ecall));
  Multiplexer #(.select(1), .width(12), .disabled("Z"), .enable("false")) multiplexer_5 (
    .in0(IR[31:20]), .in1({IR[31:25], IR[11:7]}), .out(multiplexer_5_out), .sel(\单周期硬布线控制器_1_s_type ));
  Multiplexer #(.select(1), .width(32), .disabled("Z"), .enable("false")) multiplexer_6 (
    .in0(multiplexer_2_out), .in1(adder_4_out), .out(Next_PC), .sel(JALR));
  or or_1 (IR1_t, IR1, IRA);
  assign \I型或S型指令的立即数  = {{20{multiplexer_5_out[11]}}, multiplexer_5_out};  // Bit_Extender bit_extender_1
  or or_2 (IR2_t, IR2, IRB);
  Regifile regifile_1 (
    .Din(RDin), .Clk(CLK), .R1(R_rs1), .R2(MDin), .WE(RegWrite), .W_num(IR[11:7]),
    .R1_num(multiplexer_3_out), .R2_num(multiplexer_4_out));
  assign bit_extender_2_out = {{20{IR[31]}}, {IR[31], IR[7], IR[30:25], IR[11:8]}};  // Bit_Extender bit_extender_2
  or or_3 (IR3_t, IR3, IRC);
  not not_2 (not_2_out, alu_1_equal);
  Multiplexer #(.select(1), .width(32), .disabled("Z"), .enable("false")) multiplexer_7 (
    .in0(MDin), .in1(\I型或S型指令的立即数 ), .out(multiplexer_7_out), .sel(\单周期硬布线控制器_1_alu_src ));
  Shifter #(.width(32), .shift("ll")) shifter_1 (
    .in(bit_extender_2_out), .\dist (5'b00001), .out(\BranchAddress_B型指令的立即数 ));
  and and_1 (and_1_out, \单周期硬布线控制器_1_bne , not_2_out);
  ALU alu_1 (
    .X(R_rs1), .Y(multiplexer_7_out), .AluOP(\单周期硬布线控制器_1_alu_op ), .Equal(alu_1_equal),
    .Result({alu_1_result[31:12], alu_1_result_2, alu_1_result[1:0]}));  // open: Result_2, out_4, out_6
  assign {\Jalr的立即数 , bit_extender_3_out[0]} = {{20{IR[31]}}, IR[31:20]};  // Bit_Extender bit_extender_3
  and and_2 (and_2_out, \单周期硬布线控制器_1_beq , alu_1_equal);
  assign bit_extender_4_out = {{12{IR[31]}}, {IR[31], IR[19:12], IR[20], IR[30:21]}};  // Bit_Extender bit_extender_4
  or or_4 (Branch, and_2_out, and_1_out);
  RAM #(.addrWidth(10), .dataWidth(32), .bus("separate"), .Select("high")) ram_1 (
    .addr(alu_1_result_2), .din(MDin), .data(ram_1_data), .str(MemWrite), .clk(CLK), .ld(MemToReg), .clr(RST));  // open: sel
  Shifter #(.width(32), .shift("ll")) shifter_2 (.in(bit_extender_4_out), .\dist (5'b00001), .out(\Jal的立即数 ));
  Multiplexer #(.select(1), .width(32), .disabled("Z"), .enable("false")) multiplexer_8 (
    .in0({alu_1_result[31:12], alu_1_result_2, alu_1_result[1:0]}), .in1(ram_1_data),
    .out(multiplexer_8_out), .sel(MemToReg));
  not not_3 (not_3_out, halt);
  Comparator #(.width(32), .mode("twosComplement")) comparator_1 (
    .a(R_rs1), .b(32'h22), .eq(comparator_1_eq));  // open: gt, lt
  not not_4 (not_4_out, Go);
  Counter #(.width(16), .max('hffff), .ongoal("wrap"), .trigger("rising"), .behavior("new")) counter_1 (
    .D(16'h1), .count(not_3_out), .Q(\总周期数 ), .clk(CLK));  // open: load, carry, clr, preset, down
  or or_5 (or_5_out, JAL, JALR);
  Multiplexer #(.select(1), .width(32), .disabled("Z"), .enable("false")) multiplexer_9 (
    .in0(multiplexer_8_out), .in1(PC_4), .out(RDin), .sel(or_5_out));
  and and_3 (and_3_out, comparator_1_eq, Ecall);
  not not_5 (not_5_out, comparator_1_eq);
  and and_4 (halt, not_5_out, not_4_out, Ecall);
  D_Flip_Flop #(.trigger("high"), .Pre_Clr_Positions("LEGACY"), .NegatePresetClear("false"), .enable("true"), .NewFFLayout("false")) d_ff_1 (.Q(d_ff_1_q));  // open: clk, D, Qn, preset, en, reset
  // Probe on 13'hc
  Register #(.width(32), .trigger("rising"), .Select("low")) register_1 (
    .D(MDin), .en(and_3_out), .Q(LedData), .clk(CLK), .clr(RST));
  Comparator #(.width(13), .mode("twosComplement")) comparator_2 (
    .a(CNT_num), .b(13'hc), .eq(comparator_2_eq), .lt(comparator_2_lt));  // open: gt
  Clock #(.highDuration(1), .lowDuration(1)) clock_1 (.out(clock_1_out));
  Counter #(.width(13), .max('h1fff), .ongoal("stay"), .trigger("rising"), .behavior("old")) counter_2 (
    .count(comparator_2_lt), .Q(CNT_num), .clk(clock_1_out));  // open: load, D, carry, clr, preset
  nand nand_1 (nand_1_out, d_ff_1_q, comparator_2_eq);
  assign CLK = nand_1_out ? clock_1_out : 1'bz;  // Controlled_Buffer controlled_buffer_1
  Pull_Resistor #(.pull(1)) pull_resistor_1 (.node(CLK));

  // Other names for the same wires on the sheet: R_rs2[31:0] = MDin

  // Notes on the sheet:
  //   中断源
  //   中断等待指示
  //   数码管输出应该用寄存器锁存，否则显示数据只能一闪而过
  //   数码管输出
  //   指令探针
  //   指令存储器
  //   指令字
  //   contents of rom_1 (hex, n*v repeats v):
  //   100493 100006f 100493 200913 300993 100006f 100493 200913 300993 100006f 100493 200913 300993
  //   100006f 100493 200913 300993 29c000ef 100413 100493 1f49493 900533 2200893 73 24d493 48463 fedff06f
  //   900533 2200893 73 100493 249493 900533 2200893 73 48463 fedff06f 100493 1f49493 900533 2200893 73
  //   4034d493 900533 2200893 73 4044d493 900533 2200893 73 4044d493 900533 2200893 73 4044d493 900533
  //   2200893 73 4044d493 900533 2200893 73 4044d493 900533 2200893 73 4044d493 900533 2200893 73 4044d493
  //   900533 2200893 73 100413 1f41993 41f9d993 433 c00913 300b13 140413 f47413 800293 100313 499993
  //   89e9b3 1300533 2200893 73 406282b3 fe0294e3 140413 f00f93 1f47433 1c41413 800293 100313 49d993
  //   89e9b3 1300533 2200893 73 406282b3 fe0294e3 1c45413 406b0b33 b0463 f95ff06f 2b3 fff2c293 829293
  //   ff2e293 500533 2200893 73 fff00413 493 84a023 140413 448493 84a023 140413 448493 84a023 140413
  //   448493 84a023 140413 448493 84a023 140413 448493 84a023 140413 448493 84a023 140413 448493 84a023
  //   140413 448493 84a023 140413 448493 84a023 140413 448493 84a023 140413 448493 84a023 140413 448493
  //   84a023 140413 448493 84a023 140413 448493 84a023 140413 448493 84a023 140413 448493 140413 433
  //   3c00493 42983 4aa03 149a2b3 28663 134a023 1442023 ffc48493 fe9412e3 800533 2200893 73 440413 3c00493
  //   fc9416e3 a00893 73 413 140413 800533 2200893 73 240413 800533 2200893 73 340413 800533 2200893 73
  //   440413 800533 2200893 73 540413 800533 2200893 73 640413 800533 2200893 73 740413 800533 2200893 73
  //   840413 800533 2200893 2200893 73 8067
  //   JAL
  //   JALR
  //   URET
  //   Beq
  //   Bne
  //   AluOP
  //   MemWrite(数据存储器的写使能控制信号)
  //   AluSrcB(运算器B输入选择 )
  //   RegWrite(寄存器堆的写使能控制信号）
  //   MemToReg(为1时将数据存储器读出的数据写回寄存器堆，否则将运算结果写回寄存器堆)
  //   数据存储器
  //   为方便自动评测，需要输出PC，IR，寄存器堆写如数据RDin
  //   RAM写使能MemWrite、RAM写入数据MDin等信号
  //   控制位
  //   暂停节拍，不能为0
  //   戳工具置1进入计数暂停模式，ctrl+k时钟自动运行到对应节拍暂停
  //   ctrl+k关闭时钟连续运行，将控制位置零，进入单步调试模式调试
  //   用这个时钟源需要去掉电路中的其他时钟源
  //   可计数暂停的时钟源
endmodule

// 单周期硬布线控制器
module \单周期硬布线控制器  (
  input  [4:0] OP,
  input  [4:0] Funct,
  input  in_3,
  output [3:0] ALU_OP,
  output uret,
  output MemToReg,
  output ecall,
  output MemWrite,
  output ALU_SRC,
  output RegWrite,
  output S_type,
  output Beq,
  output Bne,
  output Jalr,
  output JAL,
  output Readrs1,
  output Readrs2
);

  wire \控制信号自动生成_1_ecall ;

  \运算控制器自动生成  \u_运算控制器自动生成_1  (
    .OP2(OP[0]), .OP3(OP[1]), .OP4(OP[2]), .OP5(OP[3]), .OP6(OP[4]), .F12(Funct[0]), .F13(Funct[1]),
    .F14(Funct[2]), .F25(Funct[3]), .F30(Funct[4]), .S0(ALU_OP[0]), .S1(ALU_OP[1]), .S2(ALU_OP[2]),
    .S3(ALU_OP[3]));
  \控制信号自动生成  \u_控制信号自动生成_1  (
    .OP2(OP[0]), .OP3(OP[1]), .MemToReg(MemToReg), .OP4(OP[2]), .OP5(OP[3]), .OP6(OP[4]), .F12(Funct[0]),
    .F13(Funct[1]), .MemWrite(MemWrite), .F14(Funct[2]), .F25(Funct[3]), .F30(Funct[4]), .ALU_SRC(ALU_SRC),
    .RegWrite(RegWrite), .ecall(\控制信号自动生成_1_ecall ), .S_Type(S_type), .BEQ(Beq), .BNE(Bne), .JALR(Jalr),
    .JAL(JAL), .Readrs1(Readrs1), .Readrs2(Readrs2));
  and and_1 (uret, in_3, \控制信号自动生成_1_ecall );
  and and_2 (ecall, ~in_3, \控制信号自动生成_1_ecall );  // AND_Gate

  // Other names for the same wires on the sheet: IR21 = in_3; OP_CODE[4:0] = OP

  // Notes on the sheet:
  //   运算器控制器，根据指令生成运算器功能选择信号
  //   控制信号生成，产生数据通路需要的其他控制信号
endmodule

// 运算器控制器
module \运算控制器自动生成  (
  input  OP2,
  input  OP3,
  input  OP4,
  input  OP5,
  input  OP6,
  input  F12,
  input  F13,
  input  F14,
  input  F25,
  input  F30,
  output S0,
  output S1,
  output S2,
  output S3
);

  wire and_1_out, and_2_out, and_3_out, and_4_out, and_5_out, and_6_out, and_7_out, and_8_out, and_9_out,
       and_10_out, and_11_out, and_12_out, and_13_out, and_14_out, and_15_out, and_16_out, and_17_out,
       and_18_out, and_19_out, and_20_out, and_21_out, and_22_out, and_23_out, and_24_out, and_25_out,
       and_26_out, and_27_out, and_28_out, and_29_out, and_30_out, not_1_out, not_2_out, not_3_out,
       not_4_out, not_5_out, not_6_out, not_7_out, not_8_out, not_9_out, not_10_out, not_11_out, not_12_out,
       not_13_out, not_14_out, not_15_out, not_16_out, not_17_out, not_18_out, not_19_out, not_20_out,
       not_21_out, not_22_out, not_23_out, not_24_out, not_25_out, not_26_out, not_27_out, not_28_out,
       not_29_out, not_30_out, not_31_out, not_32_out, not_33_out, not_34_out, not_35_out, not_36_out,
       not_37_out, not_38_out, not_39_out, not_40_out, not_41_out, not_42_out, not_43_out, not_44_out,
       not_45_out, not_46_out, not_47_out, not_48_out, not_49_out, not_50_out, not_51_out, not_52_out,
       not_53_out, not_54_out, not_55_out, not_56_out, not_57_out, not_58_out, not_59_out, not_60_out,
       not_61_out, not_62_out, not_63_out, not_64_out, not_65_out, not_66_out, not_67_out, not_68_out,
       not_69_out, not_70_out, not_71_out, not_72_out, not_73_out, not_74_out, not_75_out, not_76_out,
       not_77_out, not_78_out, not_79_out, not_80_out, not_81_out, not_82_out, not_83_out, not_84_out,
       not_85_out, not_86_out, not_87_out, not_88_out, not_89_out, not_90_out, not_91_out, not_92_out,
       not_93_out, not_94_out, not_95_out, not_96_out, not_97_out, not_98_out, not_99_out, not_100_out,
       not_101_out, not_102_out, not_103_out, not_104_out, not_105_out, not_106_out, not_107_out,
       not_108_out, not_109_out, not_110_out, not_111_out, not_112_out, not_113_out, not_114_out,
       not_115_out, not_116_out, not_117_out, not_118_out, not_119_out, not_120_out, not_121_out,
       not_122_out, not_123_out, not_124_out, not_125_out, not_126_out, not_127_out, not_128_out,
       not_129_out, not_130_out, not_131_out, not_132_out, not_133_out, not_134_out, not_135_out,
       not_136_out, not_137_out, not_138_out, not_139_out, not_140_out, not_141_out, not_142_out,
       not_143_out, not_144_out, not_145_out, not_146_out, not_147_out, not_148_out, not_149_out,
       not_150_out, not_151_out, not_152_out, not_153_out, not_154_out, not_155_out, not_156_out,
       not_157_out, not_158_out, not_159_out, not_160_out, not_161_out, not_162_out, not_163_out,
       not_164_out, not_165_out, not_166_out, not_167_out, not_168_out, not_169_out, not_170_out,
       not_171_out, not_172_out, not_173_out, not_174_out, not_175_out, not_176_out, not_177_out,
       not_178_out, not_179_out, not_180_out, not_181_out, not_182_out, not_183_out, not_184_out;

  not not_1 (not_1_out, F30);
  not not_2 (not_2_out, F25);
  not not_3 (not_3_out, F14);
  not not_4 (not_4_out, F13);
  not not_5 (not_5_out, F12);
  not not_6 (not_6_out, OP6);
  not not_7 (not_7_out, OP3);
  not not_8 (not_8_out, OP2);
  not not_9 (not_9_out, F30);
  not not_10 (not_10_out, F25);
  not not_11 (not_11_out, OP6);
  not not_12 (not_12_out, OP3);
  not not_13 (not_13_out, OP2);
  not not_14 (not_14_out, F30);
  not not_15 (not_15_out, F25);
  not not_16 (not_16_out, F14);
  not not_17 (not_17_out, F12);
  not not_18 (not_18_out, OP6);
  not not_19 (not_19_out, OP3);
  not not_20 (not_20_out, OP2);
  not not_21 (not_21_out, F14);
  not not_22 (not_22_out, F13);
  not not_23 (not_23_out, F12);
  not not_24 (not_24_out, OP6);
  not not_25 (not_25_out, OP5);
  not not_26 (not_26_out, OP3);
  not not_27 (not_27_out, OP2);
  not not_28 (not_28_out, OP6);
  not not_29 (not_29_out, OP5);
  not not_30 (not_30_out, OP3);
  not not_31 (not_31_out, OP2);
  not not_32 (not_32_out, F13);
  not not_33 (not_33_out, F12);
  not not_34 (not_34_out, OP6);
  not not_35 (not_35_out, OP5);
  not not_36 (not_36_out, OP3);
  not not_37 (not_37_out, OP2);
  not not_38 (not_38_out, F14);
  not not_39 (not_39_out, F12);
  not not_40 (not_40_out, OP6);
  not not_41 (not_41_out, OP5);
  not not_42 (not_42_out, OP3);
  not not_43 (not_43_out, OP2);
  not not_44 (not_44_out, F25);
  not not_45 (not_45_out, F13);
  not not_46 (not_46_out, OP6);
  not not_47 (not_47_out, OP5);
  not not_48 (not_48_out, OP3);
  not not_49 (not_49_out, OP2);
  not not_50 (not_50_out, F14);
  not not_51 (not_51_out, F12);
  not not_52 (not_52_out, OP6);
  not not_53 (not_53_out, OP5);
  not not_54 (not_54_out, OP4);
  not not_55 (not_55_out, OP3);
  not not_56 (not_56_out, OP2);
  not not_57 (not_57_out, F14);
  not not_58 (not_58_out, F12);
  not not_59 (not_59_out, OP6);
  not not_60 (not_60_out, OP4);
  not not_61 (not_61_out, OP3);
  not not_62 (not_62_out, OP2);
  not not_63 (not_63_out, F25);
  not not_64 (not_64_out, F14);
  not not_65 (not_65_out, F13);
  not not_66 (not_66_out, F12);
  not not_67 (not_67_out, OP6);
  not not_68 (not_68_out, OP3);
  not not_69 (not_69_out, OP2);
  not not_70 (not_70_out, F30);
  not not_71 (not_71_out, F25);
  not not_72 (not_72_out, OP6);
  not not_73 (not_73_out, OP3);
  not not_74 (not_74_out, OP2);
  not not_75 (not_75_out, F30);
  not not_76 (not_76_out, F25);
  not not_77 (not_77_out, F14);
  not not_78 (not_78_out, F12);
  not not_79 (not_79_out, OP6);
  not not_80 (not_80_out, OP3);
  not not_81 (not_81_out, OP2);
  not not_82 (not_82_out, OP6);
  not not_83 (not_83_out, OP5);
  not not_84 (not_84_out, OP3);
  not not_85 (not_85_out, OP2);
  not not_86 (not_86_out, F14);
  not not_87 (not_87_out, F12);
  not not_88 (not_88_out, OP6);
  not not_89 (not_89_out, OP5);
  not not_90 (not_90_out, OP3);
  not not_91 (not_91_out, OP2);
  not not_92 (not_92_out, F30);
  not not_93 (not_93_out, F25);
  not not_94 (not_94_out, F13);
  not not_95 (not_95_out, OP6);
  not not_96 (not_96_out, OP5);
  not not_97 (not_97_out, OP3);
  not not_98 (not_98_out, OP2);
  not not_99 (not_99_out, F30);
  not not_100 (not_100_out, F25);
  not not_101 (not_101_out, F14);
  not not_102 (not_102_out, F13);
  not not_103 (not_103_out, F12);
  not not_104 (not_104_out, OP6);
  not not_105 (not_105_out, OP3);
  not not_106 (not_106_out, OP2);
  not not_107 (not_107_out, F25);
  not not_108 (not_108_out, F14);
  not not_109 (not_109_out, F13);
  not not_110 (not_110_out, F12);
  not not_111 (not_111_out, OP6);
  not not_112 (not_112_out, OP3);
  not not_113 (not_113_out, OP2);
  not not_114 (not_114_out, F30);
  not not_115 (not_115_out, F25);
  not not_116 (not_116_out, OP6);
  not not_117 (not_117_out, OP3);
  not not_118 (not_118_out, OP2);
  not not_119 (not_119_out, F30);
  not not_120 (not_120_out, F25);
  not not_121 (not_121_out, F14);
  not not_122 (not_122_out, OP6);
  not not_123 (not_123_out, OP3);
  not not_124 (not_124_out, OP2);
  not not_125 (not_125_out, F14);
  not not_126 (not_126_out, F13);
  not not_127 (not_127_out, F12);
  not not_128 (not_128_out, OP6);
  not not_129 (not_129_out, OP5);
  not not_130 (not_130_out, OP3);
  not not_131 (not_131_out, OP2);
  not not_132 (not_132_out, OP6);
  not not_133 (not_133_out, OP5);
  not not_134 (not_134_out, OP3);
  not not_135 (not_135_out, OP2);
  not not_136 (not_136_out, F14);
  not not_137 (not_137_out, F12);
  not not_138 (not_138_out, OP6);
  not not_139 (not_139_out, OP5);
  not not_140 (not_140_out, OP4);
  not not_141 (not_141_out, OP3);
  not not_142 (not_142_out, OP2);
  not not_143 (not_143_out, F14);
  not not_144 (not_144_out, F12);
  not not_145 (not_145_out, OP6);
  not not_146 (not_146_out, OP4);
  not not_147 (not_147_out, OP3);
  not not_148 (not_148_out, OP2);
  not not_149 (not_149_out, F30);
  not not_150 (not_150_out, F25);
  not not_151 (not_151_out, F12);
  not not_152 (not_152_out, OP6);
  not not_153 (not_153_out, OP3);
  not not_154 (not_154_out, OP2);
  not not_155 (not_155_out, F30);
  not not_156 (not_156_out, F25);
  not not_157 (not_157_out, F14);
  not not_158 (not_158_out, F12);
  not not_159 (not_159_out, OP6);
  not not_160 (not_160_out, OP3);
  not not_161 (not_161_out, OP2);
  not not_162 (not_162_out, F30);
  not not_163 (not_163_out, F25);
  not not_164 (not_164_out, F14);
  not not_165 (not_165_out, OP6);
  not not_166 (not_166_out, OP3);
  not not_167 (not_167_out, OP2);
  not not_168 (not_168_out, F12);
  not not_169 (not_169_out, OP6);
  not not_170 (not_170_out, OP5);
  not not_171 (not_171_out, OP3);
  not not_172 (not_172_out, OP2);
  not not_173 (not_173_out, F13);
  not not_174 (not_174_out, F12);
  not not_175 (not_175_out, OP6);
  not not_176 (not_176_out, OP5);
  not not_177 (not_177_out, OP3);
  not not_178 (not_178_out, OP2);
  not not_179 (not_179_out, F14);
  not not_180 (not_180_out, F12);
  not not_181 (not_181_out, OP6);
  not not_182 (not_182_out, OP5);
  not not_183 (not_183_out, OP3);
  not not_184 (not_184_out, OP2);
  and and_1 (and_1_out, not_1_out, not_2_out, not_3_out, not_4_out, not_5_out, not_6_out, OP5, OP4, not_7_out, not_8_out);
  and and_2 (and_2_out, not_9_out, not_10_out, F14, F13, F12, not_11_out, OP5, OP4, not_12_out, not_13_out);
  and and_3 (and_3_out, not_14_out, not_15_out, not_16_out, F13, not_17_out, not_18_out, OP5, OP4, not_19_out, not_20_out);
  and and_4 (and_4_out, not_21_out, not_22_out, not_23_out, not_24_out, not_25_out, OP4, not_26_out, not_27_out);
  and and_5 (and_5_out, F14, F13, F12, not_28_out, not_29_out, OP4, not_30_out, not_31_out);
  and and_6 (and_6_out, F14, not_32_out, not_33_out, not_34_out, not_35_out, OP4, not_36_out, not_37_out);
  and and_7 (and_7_out, not_38_out, F13, not_39_out, not_40_out, not_41_out, OP4, not_42_out, not_43_out);
  and and_8 (and_8_out, F30, not_44_out, F14, not_45_out, F12, not_46_out, not_47_out, OP4, not_48_out, not_49_out);
  and and_9 (and_9_out, not_50_out, F13, not_51_out, not_52_out, not_53_out, not_54_out, not_55_out, not_56_out);
  and and_10 (and_10_out, not_57_out, F13, not_58_out, not_59_out, OP5, not_60_out, not_61_out, not_62_out);
  and and_11 (and_11_out, F30, not_63_out, not_64_out, not_65_out, not_66_out, not_67_out, OP5, OP4, not_68_out, not_69_out);
  and and_12 (and_12_out, not_70_out, not_71_out, F14, F13, F12, not_72_out, OP5, OP4, not_73_out, not_74_out);
  and and_13 (and_13_out, not_75_out, not_76_out, not_77_out, F13, not_78_out, not_79_out, OP5, OP4, not_80_out, not_81_out);
  and and_14 (and_14_out, F14, F13, F12, not_82_out, not_83_out, OP4, not_84_out, not_85_out);
  and and_15 (and_15_out, not_86_out, F13, not_87_out, not_88_out, not_89_out, OP4, not_90_out, not_91_out);
  and and_16 (and_16_out, not_92_out, not_93_out, F14, not_94_out, F12, not_95_out, not_96_out, OP4, not_97_out, not_98_out);
  and and_17 (and_17_out, not_99_out, not_100_out, not_101_out, not_102_out, not_103_out, not_104_out, OP5, OP4, not_105_out, not_106_out);
  and and_18 (and_18_out, F30, not_107_out, not_108_out, not_109_out, not_110_out, not_111_out, OP5, OP4, not_112_out, not_113_out);
  and and_19 (and_19_out, not_114_out, not_115_out, F14, F13, F12, not_116_out, OP5, OP4, not_117_out, not_118_out);
  and and_20 (and_20_out, not_119_out, not_120_out, not_121_out, F13, F12, not_122_out, OP5, OP4, not_123_out, not_124_out);
  and and_21 (and_21_out, not_125_out, not_126_out, not_127_out, not_128_out, not_129_out, OP4, not_130_out, not_131_out);
  and and_22 (and_22_out, F14, F13, F12, not_132_out, not_133_out, OP4, not_134_out, not_135_out);
  and and_23 (and_23_out, not_136_out, F13, not_137_out, not_138_out, not_139_out, not_140_out, not_141_out, not_142_out);
  and and_24 (and_24_out, not_143_out, F13, not_144_out, not_145_out, OP5, not_146_out, not_147_out, not_148_out);
  and and_25 (and_25_out, not_149_out, not_150_out, F14, F13, not_151_out, not_152_out, OP5, OP4, not_153_out, not_154_out);
  and and_26 (and_26_out, not_155_out, not_156_out, not_157_out, F13, not_158_out, not_159_out, OP5, OP4, not_160_out, not_161_out);
  and and_27 (and_27_out, not_162_out, not_163_out, not_164_out, F13, F12, not_165_out, OP5, OP4, not_166_out, not_167_out);
  and and_28 (and_28_out, F14, F13, not_168_out, not_169_out, not_170_out, OP4, not_171_out, not_172_out);
  and and_29 (and_29_out, F14, not_173_out, not_174_out, not_175_out, not_176_out, OP4, not_177_out, not_178_out);
  and and_30 (and_30_out, not_179_out, F13, not_180_out, not_181_out, not_182_out, OP4, not_183_out, not_184_out);
  or or_1 (S0, and_1_out, and_2_out, and_3_out, and_4_out, and_5_out, and_6_out, and_7_out, and_8_out, and_9_out, and_10_out);
  or or_2 (S1, and_11_out, and_12_out, and_13_out, and_14_out, and_15_out, and_16_out);
  or or_3 (S2, and_17_out, and_18_out, and_19_out, and_20_out, and_21_out, and_22_out, and_23_out, and_24_out);
  or or_4 (S3, and_25_out, and_26_out, and_27_out, and_28_out, and_29_out, and_30_out);
endmodule

// 控制信号生成
module \控制信号自动生成  (
  input  OP2,
  input  OP3,
  input  OP4,
  input  OP5,
  input  OP6,
  input  F12,
  input  F13,
  input  F14,
  input  F25,
  input  F30,
  output MemToReg,
  output MemWrite,
  output ALU_SRC,
  output RegWrite,
  output ecall,
  output S_Type,
  output BEQ,
  output BNE,
  output JALR,
  output JAL,
  output Readrs1,
  output Readrs2
);

  wire and_3_out, and_4_out, and_5_out, and_6_out, and_7_out, and_8_out, and_9_out, and_10_out, and_11_out,
       and_12_out, and_13_out, and_14_out, and_15_out, and_16_out, and_23_out, and_24_out, and_25_out,
       and_26_out, and_27_out, and_28_out, and_29_out, and_30_out, and_31_out, and_32_out, and_33_out,
       and_34_out, and_35_out, and_36_out, and_37_out, and_38_out, and_39_out, and_40_out, and_41_out,
       and_42_out, and_43_out, and_44_out, and_45_out, and_46_out, and_47_out, not_1_out, not_2_out,
       not_3_out, not_4_out, not_5_out, not_6_out, not_7_out, not_8_out, not_9_out, not_10_out, not_11_out,
       not_12_out, not_13_out, not_14_out, not_15_out, not_16_out, not_17_out, not_18_out, not_19_out,
       not_20_out, not_21_out, not_22_out, not_23_out, not_24_out, not_25_out, not_26_out, not_27_out,
       not_28_out, not_29_out, not_30_out, not_31_out, not_32_out, not_33_out, not_34_out, not_35_out,
       not_36_out, not_37_out, not_38_out, not_39_out, not_40_out, not_41_out, not_42_out, not_43_out,
       not_44_out, not_45_out, not_46_out, not_47_out, not_48_out, not_49_out, not_50_out, not_51_out,
       not_52_out, not_53_out, not_54_out, not_55_out, not_56_out, not_57_out, not_58_out, not_59_out,
       not_60_out, not_61_out, not_62_out, not_63_out, not_64_out, not_65_out, not_66_out, not_67_out,
       not_68_out, not_69_out, not_70_out, not_71_out, not_72_out, not_73_out, not_74_out, not_75_out,
       not_76_out, not_77_out, not_78_out, not_79_out, not_80_out, not_81_out, not_82_out, not_83_out,
       not_84_out, not_85_out, not_86_out, not_87_out, not_88_out, not_89_out, not_90_out, not_91_out,
       not_92_out, not_93_out, not_94_out, not_95_out, not_96_out, not_97_out, not_98_out, not_99_out,
       not_100_out, not_101_out, not_102_out, not_103_out, not_104_out, not_105_out, not_106_out,
       not_107_out, not_108_out, not_109_out, not_110_out, not_111_out, not_112_out, not_113_out,
       not_114_out, not_115_out, not_116_out, not_117_out, not_118_out, not_119_out, not_120_out,
       not_121_out, not_122_out, not_123_out, not_124_out, not_125_out, not_126_out, not_127_out,
       not_128_out, not_129_out, not_130_out, not_131_out, not_132_out, not_133_out, not_134_out,
       not_135_out, not_136_out, not_137_out, not_138_out, not_139_out, not_140_out, not_141_out,
       not_142_out, not_143_out, not_144_out, not_145_out, not_146_out, not_147_out, not_148_out,
       not_149_out, not_150_out, not_151_out, not_152_out, not_153_out, not_154_out, not_155_out,
       not_156_out, not_157_out, not_158_out, not_159_out, not_160_out, not_161_out, not_162_out,
       not_163_out, not_164_out, not_165_out, not_166_out, not_167_out, not_168_out, not_169_out,
       not_170_out, not_171_out, not_172_out, not_173_out, not_174_out, not_175_out, not_176_out,
       not_177_out, not_178_out, not_179_out, not_180_out, not_181_out, not_182_out, not_183_out,
       not_184_out, not_185_out, not_186_out, not_187_out, not_188_out, not_189_out, not_190_out,
       not_191_out, not_192_out, not_193_out, not_194_out, not_195_out, not_196_out, not_197_out,
       not_198_out, not_199_out, not_200_out, not_201_out, not_202_out, not_203_out, not_204_out,
       not_205_out, not_206_out, not_207_out, not_208_out, not_209_out, not_210_out, not_211_out,
       not_212_out, not_213_out, not_214_out, not_215_out, not_216_out, not_217_out, not_218_out,
       not_219_out, not_220_out, not_221_out, not_222_out, not_223_out, not_224_out, not_225_out,
       not_226_out, not_227_out, not_228_out, not_229_out, not_230_out, not_231_out, not_232_out,
       not_233_out, not_234_out, not_235_out, not_236_out, not_237_out, not_238_out, not_239_out,
       not_240_out, not_241_out, not_242_out, not_243_out, not_244_out, not_245_out, not_246_out,
       not_247_out, not_248_out, not_249_out, not_250_out, not_251_out, not_252_out, not_253_out,
       not_254_out, not_255_out, not_256_out, not_257_out, not_258_out, not_259_out, not_260_out,
       not_261_out, not_262_out;

  not not_1 (not_1_out, OP2);
  not not_2 (not_2_out, OP3);
  not not_3 (not_3_out, OP4);
  not not_4 (not_4_out, OP5);
  not not_5 (not_5_out, OP6);
  not not_6 (not_6_out, F12);
  not not_7 (not_7_out, F14);
  not not_8 (not_8_out, OP2);
  not not_9 (not_9_out, OP3);
  not not_10 (not_10_out, OP4);
  not not_11 (not_11_out, OP6);
  not not_12 (not_12_out, F12);
  not not_13 (not_13_out, F14);
  not not_14 (not_14_out, OP2);
  not not_15 (not_15_out, OP3);
  not not_16 (not_16_out, OP4);
  not not_17 (not_17_out, OP6);
  not not_18 (not_18_out, F12);
  not not_19 (not_19_out, F14);
  not not_20 (not_20_out, OP2);
  not not_21 (not_21_out, OP3);
  not not_22 (not_22_out, OP5);
  not not_23 (not_23_out, OP6);
  not not_24 (not_24_out, F12);
  not not_25 (not_25_out, OP2);
  not not_26 (not_26_out, OP3);
  not not_27 (not_27_out, OP5);
  not not_28 (not_28_out, OP6);
  not not_29 (not_29_out, F13);
  not not_30 (not_30_out, F25);
  not not_31 (not_31_out, F30);
  not not_32 (not_32_out, OP2);
  not not_33 (not_33_out, OP3);
  not not_34 (not_34_out, OP5);
  not not_35 (not_35_out, OP6);
  not not_36 (not_36_out, F25);
  not not_37 (not_37_out, OP2);
  not not_38 (not_38_out, OP3);
  not not_39 (not_39_out, OP5);
  not not_40 (not_40_out, OP6);
  not not_41 (not_41_out, OP2);
  not not_42 (not_42_out, OP3);
  not not_43 (not_43_out, OP5);
  not not_44 (not_44_out, OP6);
  not not_45 (not_45_out, F12);
  not not_46 (not_46_out, F14);
  not not_47 (not_47_out, OP2);
  not not_48 (not_48_out, OP3);
  not not_49 (not_49_out, OP5);
  not not_50 (not_50_out, OP6);
  not not_51 (not_51_out, F13);
  not not_52 (not_52_out, OP2);
  not not_53 (not_53_out, OP3);
  not not_54 (not_54_out, OP6);
  not not_55 (not_55_out, F12);
  not not_56 (not_56_out, F13);
  not not_57 (not_57_out, F14);
  not not_58 (not_58_out, F25);
  not not_59 (not_59_out, OP2);
  not not_60 (not_60_out, OP3);
  not not_61 (not_61_out, OP5);
  not not_62 (not_62_out, OP6);
  not not_63 (not_63_out, OP2);
  not not_64 (not_64_out, OP3);
  not not_65 (not_65_out, OP6);
  not not_66 (not_66_out, F25);
  not not_67 (not_67_out, F30);
  not not_68 (not_68_out, OP2);
  not not_69 (not_69_out, OP3);
  not not_70 (not_70_out, F25);
  not not_71 (not_71_out, F30);
  not not_72 (not_72_out, OP2);
  not not_73 (not_73_out, OP3);
  not not_74 (not_74_out, OP4);
  not not_75 (not_75_out, F12);
  not not_76 (not_76_out, F13);
  not not_77 (not_77_out, F14);
  not not_78 (not_78_out, OP4);
  not not_79 (not_79_out, OP2);
  not not_80 (not_80_out, OP3);
  not not_81 (not_81_out, F12);
  not not_82 (not_82_out, F13);
  not not_83 (not_83_out, F14);
  not not_84 (not_84_out, F25);
  not not_85 (not_85_out, F30);
  not not_86 (not_86_out, OP2);
  not not_87 (not_87_out, OP3);
  not not_88 (not_88_out, OP4);
  not not_89 (not_89_out, OP6);
  not not_90 (not_90_out, F12);
  not not_91 (not_91_out, F14);
  not not_92 (not_92_out, OP2);
  not not_93 (not_93_out, OP3);
  not not_94 (not_94_out, OP4);
  not not_95 (not_95_out, F12);
  not not_96 (not_96_out, F13);
  not not_97 (not_97_out, F14);
  not not_98 (not_98_out, OP2);
  not not_99 (not_99_out, OP3);
  not not_100 (not_100_out, OP4);
  not not_101 (not_101_out, F13);
  not not_102 (not_102_out, F14);
  not not_103 (not_103_out, OP3);
  not not_104 (not_104_out, OP4);
  not not_105 (not_105_out, F12);
  not not_106 (not_106_out, F13);
  not not_107 (not_107_out, F14);
  not not_108 (not_108_out, OP4);
  not not_109 (not_109_out, F30);
  not not_110 (not_110_out, F25);
  not not_111 (not_111_out, F14);
  not not_112 (not_112_out, F13);
  not not_113 (not_113_out, F12);
  not not_114 (not_114_out, OP6);
  not not_115 (not_115_out, OP3);
  not not_116 (not_116_out, OP2);
  not not_117 (not_117_out, F25);
  not not_118 (not_118_out, F14);
  not not_119 (not_119_out, F13);
  not not_120 (not_120_out, F12);
  not not_121 (not_121_out, OP6);
  not not_122 (not_122_out, OP3);
  not not_123 (not_123_out, OP2);
  not not_124 (not_124_out, F30);
  not not_125 (not_125_out, F25);
  not not_126 (not_126_out, OP6);
  not not_127 (not_127_out, OP3);
  not not_128 (not_128_out, OP2);
  not not_129 (not_129_out, F30);
  not not_130 (not_130_out, F25);
  not not_131 (not_131_out, F12);
  not not_132 (not_132_out, OP6);
  not not_133 (not_133_out, OP3);
  not not_134 (not_134_out, OP2);
  not not_135 (not_135_out, F30);
  not not_136 (not_136_out, F25);
  not not_137 (not_137_out, F14);
  not not_138 (not_138_out, F12);
  not not_139 (not_139_out, OP6);
  not not_140 (not_140_out, OP3);
  not not_141 (not_141_out, OP2);
  not not_142 (not_142_out, F30);
  not not_143 (not_143_out, F25);
  not not_144 (not_144_out, F14);
  not not_145 (not_145_out, OP6);
  not not_146 (not_146_out, OP3);
  not not_147 (not_147_out, OP2);
  not not_148 (not_148_out, F14);
  not not_149 (not_149_out, F13);
  not not_150 (not_150_out, F12);
  not not_151 (not_151_out, OP6);
  not not_152 (not_152_out, OP5);
  not not_153 (not_153_out, OP3);
  not not_154 (not_154_out, OP2);
  not not_155 (not_155_out, OP6);
  not not_156 (not_156_out, OP5);
  not not_157 (not_157_out, OP3);
  not not_158 (not_158_out, OP2);
  not not_159 (not_159_out, F12);
  not not_160 (not_160_out, OP6);
  not not_161 (not_161_out, OP5);
  not not_162 (not_162_out, OP3);
  not not_163 (not_163_out, OP2);
  not not_164 (not_164_out, F13);
  not not_165 (not_165_out, F12);
  not not_166 (not_166_out, OP6);
  not not_167 (not_167_out, OP5);
  not not_168 (not_168_out, OP3);
  not not_169 (not_169_out, OP2);
  not not_170 (not_170_out, F14);
  not not_171 (not_171_out, F12);
  not not_172 (not_172_out, OP6);
  not not_173 (not_173_out, OP5);
  not not_174 (not_174_out, OP3);
  not not_175 (not_175_out, OP2);
  not not_176 (not_176_out, F30);
  not not_177 (not_177_out, F25);
  not not_178 (not_178_out, F14);
  not not_179 (not_179_out, F13);
  not not_180 (not_180_out, OP6);
  not not_181 (not_181_out, OP5);
  not not_182 (not_182_out, OP3);
  not not_183 (not_183_out, OP2);
  not not_184 (not_184_out, F30);
  not not_185 (not_185_out, F25);
  not not_186 (not_186_out, F13);
  not not_187 (not_187_out, OP6);
  not not_188 (not_188_out, OP5);
  not not_189 (not_189_out, OP3);
  not not_190 (not_190_out, OP2);
  not not_191 (not_191_out, F25);
  not not_192 (not_192_out, F13);
  not not_193 (not_193_out, OP6);
  not not_194 (not_194_out, OP5);
  not not_195 (not_195_out, OP3);
  not not_196 (not_196_out, OP2);
  not not_197 (not_197_out, F14);
  not not_198 (not_198_out, F12);
  not not_199 (not_199_out, OP6);
  not not_200 (not_200_out, OP5);
  not not_201 (not_201_out, OP4);
  not not_202 (not_202_out, OP3);
  not not_203 (not_203_out, OP2);
  not not_204 (not_204_out, F14);
  not not_205 (not_205_out, F12);
  not not_206 (not_206_out, OP6);
  not not_207 (not_207_out, OP4);
  not not_208 (not_208_out, OP3);
  not not_209 (not_209_out, OP2);
  not not_210 (not_210_out, F30);
  not not_211 (not_211_out, F25);
  not not_212 (not_212_out, F14);
  not not_213 (not_213_out, F13);
  not not_214 (not_214_out, F12);
  not not_215 (not_215_out, OP3);
  not not_216 (not_216_out, OP2);
  not not_217 (not_217_out, F14);
  not not_218 (not_218_out, F13);
  not not_219 (not_219_out, F12);
  not not_220 (not_220_out, OP4);
  not not_221 (not_221_out, OP3);
  not not_222 (not_222_out, OP2);
  not not_223 (not_223_out, F14);
  not not_224 (not_224_out, F13);
  not not_225 (not_225_out, OP4);
  not not_226 (not_226_out, OP3);
  not not_227 (not_227_out, OP2);
  not not_228 (not_228_out, F14);
  not not_229 (not_229_out, F13);
  not not_230 (not_230_out, F12);
  not not_231 (not_231_out, OP4);
  not not_232 (not_232_out, OP3);
  not not_233 (not_233_out, OP2);
  not not_234 (not_234_out, OP3);
  not not_235 (not_235_out, OP4);
  not not_236 (not_236_out, OP6);
  not not_237 (not_237_out, F12);
  not not_238 (not_238_out, F14);
  not not_239 (not_239_out, OP2);
  not not_240 (not_240_out, OP3);
  not not_241 (not_241_out, OP4);
  not not_242 (not_242_out, F13);
  not not_243 (not_243_out, F14);
  not not_244 (not_244_out, OP2);
  not not_245 (not_245_out, OP3);
  not not_246 (not_246_out, OP6);
  not not_247 (not_247_out, F12);
  not not_248 (not_248_out, F13);
  not not_249 (not_249_out, F14);
  not not_250 (not_250_out, F25);
  not not_251 (not_251_out, OP2);
  not not_252 (not_252_out, OP3);
  not not_253 (not_253_out, F12);
  not not_254 (not_254_out, F13);
  not not_255 (not_255_out, F14);
  not not_256 (not_256_out, F25);
  not not_257 (not_257_out, F30);
  not not_258 (not_258_out, OP2);
  not not_259 (not_259_out, OP3);
  not not_260 (not_260_out, OP6);
  not not_261 (not_261_out, F25);
  not not_262 (not_262_out, F30);
  and and_1 (MemToReg, not_1_out, not_2_out, not_3_out, not_4_out, not_5_out, not_6_out, F13, not_7_out);
  and and_2 (MemWrite, not_8_out, not_9_out, not_10_out, OP5, not_11_out, not_12_out, F13, not_13_out);
  and and_3 (and_3_out, not_14_out, not_15_out, not_16_out, not_17_out, not_18_out, F13, not_19_out);
  and and_4 (and_4_out, not_20_out, not_21_out, OP4, not_22_out, not_23_out, not_24_out);
  and and_5 (and_5_out, not_25_out, not_26_out, OP4, not_27_out, not_28_out, not_29_out, not_30_out, not_31_out);
  and and_6 (and_6_out, not_32_out, not_33_out, OP4, not_34_out, not_35_out, F14, not_36_out);
  and and_7 (and_7_out, not_37_out, not_38_out, OP4, not_39_out, not_40_out, F13, F14);
  and and_8 (and_8_out, not_41_out, not_42_out, not_43_out, not_44_out, not_45_out, F13, not_46_out);
  and and_9 (and_9_out, not_47_out, not_48_out, OP4, not_49_out, not_50_out, not_51_out);
  and and_10 (and_10_out, not_52_out, not_53_out, OP4, not_54_out, not_55_out, not_56_out, not_57_out, not_58_out);
  and and_11 (and_11_out, not_59_out, not_60_out, OP4, not_61_out, not_62_out, F14);
  and and_12 (and_12_out, not_63_out, not_64_out, OP4, OP5, not_65_out, F13, not_66_out, not_67_out);
  and and_13 (and_13_out, not_68_out, not_69_out, OP4, OP5, F13, F14, not_70_out, not_71_out);
  and and_14 (and_14_out, not_72_out, not_73_out, OP4, OP5, OP6, F12, F13, F14);
  and and_15 (and_15_out, OP2, not_74_out, OP5, OP6, not_75_out, not_76_out, not_77_out);
  and and_16 (and_16_out, OP2, OP3, not_78_out, OP5, OP6);
  and and_17 (ecall, not_79_out, not_80_out, OP4, OP5, OP6, not_81_out, not_82_out, not_83_out, not_84_out, not_85_out);
  and and_18 (S_Type, not_86_out, not_87_out, not_88_out, OP5, not_89_out, not_90_out, F13, not_91_out);
  and and_19 (BEQ, not_92_out, not_93_out, not_94_out, OP5, OP6, not_95_out, not_96_out, not_97_out);
  and and_20 (BNE, not_98_out, not_99_out, not_100_out, OP5, OP6, F12, not_101_out, not_102_out);
  and and_21 (JALR, OP2, not_103_out, not_104_out, OP5, OP6, not_105_out, not_106_out, not_107_out);
  and and_22 (JAL, OP2, OP3, not_108_out, OP5, OP6);
  and and_23 (and_23_out, not_109_out, not_110_out, not_111_out, not_112_out, not_113_out, not_114_out, OP5, OP4, not_115_out, not_116_out);
  and and_24 (and_24_out, F30, not_117_out, not_118_out, not_119_out, not_120_out, not_121_out, OP5, OP4, not_122_out, not_123_out);
  and and_25 (and_25_out, not_124_out, not_125_out, F14, F13, F12, not_126_out, OP5, OP4, not_127_out, not_128_out);
  and and_26 (and_26_out, not_129_out, not_130_out, F14, F13, not_131_out, not_132_out, OP5, OP4, not_133_out, not_134_out);
  and and_27 (and_27_out, not_135_out, not_136_out, not_137_out, F13, not_138_out, not_139_out, OP5, OP4, not_140_out, not_141_out);
  and and_28 (and_28_out, not_142_out, not_143_out, not_144_out, F13, F12, not_145_out, OP5, OP4, not_146_out, not_147_out);
  and and_29 (and_29_out, not_148_out, not_149_out, not_150_out, not_151_out, not_152_out, OP4, not_153_out, not_154_out);
  and and_30 (and_30_out, F14, F13, F12, not_155_out, not_156_out, OP4, not_157_out, not_158_out);
  and and_31 (and_31_out, F14, F13, not_159_out, not_160_out, not_161_out, OP4, not_162_out, not_163_out);
  and and_32 (and_32_out, F14, not_164_out, not_165_out, not_166_out, not_167_out, OP4, not_168_out, not_169_out);
  and and_33 (and_33_out, not_170_out, F13, not_171_out, not_172_out, not_173_out, OP4, not_174_out, not_175_out);
  and and_34 (and_34_out, not_176_out, not_177_out, not_178_out, not_179_out, F12, not_180_out, not_181_out, OP4, not_182_out, not_183_out);
  and and_35 (and_35_out, not_184_out, not_185_out, F14, not_186_out, F12, not_187_out, not_188_out, OP4, not_189_out, not_190_out);
  and and_36 (and_36_out, F30, not_191_out, F14, not_192_out, F12, not_193_out, not_194_out, OP4, not_195_out, not_196_out);
  and and_37 (and_37_out, not_197_out, F13, not_198_out, not_199_out, not_200_out, not_201_out, not_202_out, not_203_out);
  and and_38 (and_38_out, not_204_out, F13, not_205_out, not_206_out, OP5, not_207_out, not_208_out, not_209_out);
  and and_39 (and_39_out, not_210_out, not_211_out, not_212_out, not_213_out, not_214_out, OP6, OP5, OP4, not_215_out, not_216_out);
  and and_40 (and_40_out, not_217_out, not_218_out, not_219_out, OP6, OP5, not_220_out, not_221_out, not_222_out);
  and and_41 (and_41_out, not_223_out, not_224_out, F12, OP6, OP5, not_225_out, not_226_out, not_227_out);
  and and_42 (and_42_out, not_228_out, not_229_out, not_230_out, OP6, OP5, not_231_out, not_232_out, OP2);
  and and_43 (and_43_out, not_233_out, not_234_out, not_235_out, OP5, not_236_out, not_237_out, F13, not_238_out);
  and and_44 (and_44_out, not_239_out, not_240_out, not_241_out, OP5, OP6, not_242_out, not_243_out);
  and and_45 (and_45_out, not_244_out, not_245_out, OP4, OP5, not_246_out, not_247_out, not_248_out, not_249_out, not_250_out);
  and and_46 (and_46_out, not_251_out, not_252_out, OP4, OP5, not_253_out, not_254_out, not_255_out, not_256_out, not_257_out);
  and and_47 (and_47_out, not_258_out, not_259_out, OP4, OP5, not_260_out, F13, not_261_out, not_262_out);
  or or_1 (ALU_SRC, and_3_out, and_4_out, and_5_out, and_6_out, and_7_out);
  or or_2 (Readrs2, and_43_out, and_44_out, and_45_out, and_46_out, and_47_out);
  or or_3 (RegWrite, and_8_out, and_9_out, and_10_out, and_11_out, and_12_out, and_13_out, and_14_out, and_15_out, and_16_out);
  or or_4 (Readrs1, and_23_out, and_24_out, and_25_out, and_26_out, and_27_out, and_28_out, and_29_out, and_30_out, and_31_out, and_32_out, and_33_out, and_34_out, and_35_out, and_36_out, and_37_out, and_38_out, and_39_out, and_40_out, and_41_out, and_42_out);
endmodule

// ALU
module ALU (
  input  [31:0] X,
  input  [31:0] Y,
  input  [3:0] AluOP,
  output out_4,
  output Equal,
  output out_6,
  output [31:0] Result,
  output [31:0] Result_2
);

  wire [0:0] comparator_1_lt, comparator_2_lt;
  wire [31:0] adder_1_out, AND_out, divider_1_out, divider_1_rem, multiplier_1_cout, multiplier_1_out,
       NOR_out, OR_out, shifter_1_out, shifter_2_out, shifter_3_out, subtractor_1_out, XOR_out;

  assign AND_out = X & Y;  // AND_Gate AND, 32 bits wide
  assign OR_out = X | Y;  // OR_Gate OR, 32 bits wide
  Shifter #(.width(32), .shift("ll")) shifter_1 (.in(X), .\dist (Y[4:0]), .out(shifter_1_out));
  Shifter #(.width(32), .shift("ar")) shifter_2 (.in(X), .\dist (Y[4:0]), .out(shifter_2_out));
  Shifter #(.width(32), .shift("lr")) shifter_3 (.in(X), .\dist (Y[4:0]), .out(shifter_3_out));
  Multiplier #(.width(32)) multiplier_1 (.a(X), .b(Y), .out(multiplier_1_out), .cout(multiplier_1_cout));  // open: cin
  Divider #(.width(32)) divider_1 (.a(X), .b(Y), .out(divider_1_out), .rem(divider_1_rem));  // open: upper
  Adder #(.width(32)) adder_1 (.a(X), .b(Y), .out(adder_1_out));  // open: cin, cout
  Subtractor #(.width(32)) subtractor_1 (.a(X), .b(Y), .out(subtractor_1_out));  // open: bin, bout
  assign XOR_out = X ^ Y;  // XOR_Gate XOR, 32 bits wide
  assign NOR_out = ~(X | Y);  // NOR_Gate NOR, 32 bits wide
  Comparator #(.width(32), .mode("twosComplement")) comparator_1 (
    .a(X), .b(Y), .eq(Equal), .lt(comparator_1_lt[0]));  // open: gt
  Comparator #(.width(32), .mode("unsigned")) comparator_2 (.a(X), .b(Y), .lt(comparator_2_lt[0]));  // open: gt, eq
  Multiplexer #(.select(4), .width(32), .disabled("Z"), .enable("false")) multiplexer_1 (
    .in0(shifter_1_out), .in1(shifter_2_out), .in2(shifter_3_out), .in3(multiplier_1_out),
    .in4(divider_1_out), .in5(adder_1_out), .in6(subtractor_1_out), .in7(AND_out), .in8(OR_out),
    .in9(XOR_out), .in10(NOR_out), .in11({{31{1'b0}}, comparator_1_lt[0]}),
    .in12({{31{1'b0}}, comparator_2_lt[0]}), .in13({32{1'b0}}), .in14({32{1'b0}}), .in15({32{1'b0}}),
    .out(Result), .sel(AluOP));
  Multiplexer #(.select(4), .width(32), .disabled("Z"), .enable("false")) multiplexer_2 (
    .in0({32{1'b0}}), .in1({32{1'b0}}), .in2({32{1'b0}}), .in3(multiplier_1_cout), .in4(divider_1_rem),
    .in5({32{1'b0}}), .in6({32{1'b0}}), .in7({32{1'b0}}), .in8({32{1'b0}}), .in9({32{1'b0}}),
    .in10({32{1'b0}}), .in11({32{1'b0}}), .in12({32{1'b0}}), .in13({32{1'b0}}), .in14({32{1'b0}}),
    .in15({32{1'b0}}), .out(Result_2), .sel(AluOP));
  Multiplexer #(.select(4), .width(1), .disabled("Z"), .enable("false")) multiplexer_3 (
    .in0(1'b0), .in1(1'b0), .in2(1'b0), .in3(1'b0), .in4(1'b0), .in5(1'b0), .in6(1'b0), .in7(1'b0),
    .in8(1'b0), .in9(1'b0), .in10(1'b0), .in11(comparator_1_lt[0]), .in12(comparator_2_lt[0]), .in13(1'b0),
    .in14(1'b0), .in15(1'b0), .out(out_6), .sel(AluOP));
  not not_1 (out_4, out_6);

  // Other names for the same wires on the sheet: Result2[31:0] = Result_2; S[3:0] = AluOP; tunnel = out_6;
  //   tunnel_t = out_4

  // Notes on the sheet:
  //   不要改变此引脚区域内容，也不要改变ALU封装形式
  //   输入引脚
  //   输出引脚
endmodule

module Regifile (
  input  [31:0] Din,
  input  Clk,
  input  WE,
  input  [4:0] R1_num,
  input  [4:0] W_num,
  input  [4:0] R2_num,
  output [31:0] R1,
  output [31:0] R2
);

  wire not_1_out;

  not not_1 (not_1_out, Clk);
  // RegisterFile registerfile_1: pin names not known; wires that end beside it: Din, not_1_out, WE, W_num, R1_num, R2_num, R1, R2
endmodule

module \理想流水线  (
  output RegWrite,
  output MemWrite,
  output [31:0] IF_PC,
  output [31:0] ID_PC,
  output [31:0] EX_PC,
  output [31:0] M_PC,
  output [31:0] WB_PC,
  output [31:0] RDin,
  output [31:0] MDin,
  output [31:0] LedData
);

  wire alu_1_equal, and_1_out, and_2_out, and_3_out, Branch_EX, CLK, clock_1_out, comparator_1_eq,
       comparator_1_lt, comparator_2_eq, d_ff_1_q, Ecall_EX, Ecall_IF, Ecall_MEM, Ecall_WB, Go, halt,
       ID_EX_alusrcb_2, ID_EX_beq_2, ID_EX_bne_2, IR1, IR2, IR3, JAL, JALR, MemToReg_EX, MemToReg_MEM,
       MemToReg_WB, MemWrite_EX, nand_1_out, not_1_out, not_2_out, not_3_out, not_4_out, not_5_out,
       RegWrite_EX, RegWrite_MEM, RST, URET, W1, W2, W3, \单周期硬布线控制器_1_alu_src , \单周期硬布线控制器_1_beq ,
       \单周期硬布线控制器_1_bne , \单周期硬布线控制器_1_memtoreg , \单周期硬布线控制器_1_memwrite , \单周期硬布线控制器_1_regwrite ,
       \单周期硬布线控制器_1_s_type ;
  wire [0:0] bit_extender_1_out;
  wire [3:0] ID_EX_aluop_2, \单周期硬布线控制器_1_alu_op ;
  wire [4:0] W__EX, W__MEM, W__WB;
  wire [11:0] multiplexer_1_out;
  wire [12:0] CNT_num;
  wire [15:0] \LoadUse次数 , \总周期数 , \插入气泡数 , \无条件分支数 , \条件分支成功数 ;
  wire [31:0] adder_1_out, alu_1_result, bit_extender_2_out, bit_extender_4_out,
       \BranchAddress_B型指令的立即数__ID , EX_IR, EX_MEM_aluresult_2, \ID_EX_i型或s型指令的立即数_2 , ID_EX_r_rs2_2, ID_IR,
       IF_IR, \I型或S型指令的立即数_EX , \I型或S型指令的立即数_ID , \Jalr的立即数_EX , \Jal的立即数_EX , \Jal的立即数_ID , MEM_IR,
       MEM_WB_aluresult_2, MEM_WB_rd_2, multiplexer_2_out, PC_4_EX, PC_4_ID, R_rs1__EX, R_rs1__ID,
       R_rs1__MEM, R_rs1__WB, R_rs2__ID, R_rs2__WB, ram_1_data, WB_IR;
  wire [31:1] \Jalr的立即数_ID ;

  Button \u_总复位  (.out(RST));
  Button _1 (.out(IR1));
  Button _2 (.out(IR2));
  Button _3 (.out(IR3));
  // Probe on \总周期数 
  // Probe on \总周期数 
  Button \u_继续运行  (.out(Go));
  LED #(.active("true")) led_1 (.in(W1));
  LED #(.active("true")) led_2 (.in(W2));
  LED #(.active("true")) led_3 (.in(W3));
  Hex_Digit_Display hex_digit_display_1 (.value(LedData[31:28]));  // open: dp
  // Probe on IF_PC[19:0]
  // RiscV_Probe riscv_probe_1: pin names not known; wires that end beside it: IF_IR
  // Probe on adder_1_out[11:2]
  not not_1 (not_1_out, halt);
  Hex_Digit_Display hex_digit_display_2 (.value(LedData[23:20]));  // open: dp
  Hex_Digit_Display hex_digit_display_3 (.value(LedData[27:24]));  // open: dp
  // Probe on ID_PC[19:0]
  // RiscV_Probe riscv_probe_2: pin names not known; wires that end beside it: ID_IR
  Register #(.width(32), .trigger("rising"), .Select("low")) PC (
    .D(adder_1_out), .en(not_1_out), .Q(IF_PC), .clk(CLK), .clr(RST));
  Hex_Digit_Display hex_digit_display_4 (.value(LedData[15:12]));  // open: dp
  Hex_Digit_Display hex_digit_display_5 (.value(LedData[19:16]));  // open: dp
  // Probe on IF_PC[11:2]
  Adder #(.width(32)) adder_1 (.a(IF_PC), .b(32'h4), .out(adder_1_out));  // open: cin, cout
  Hex_Digit_Display hex_digit_display_6 (.value(LedData[7:4]));  // open: dp
  Hex_Digit_Display hex_digit_display_7 (.value(LedData[11:8]));  // open: dp
  // Probe on EX_PC[19:0]
  // RiscV_Probe riscv_probe_3: pin names not known; wires that end beside it: EX_IR
  Hex_Digit_Display hex_digit_display_8 (.value(LedData[3:0]));  // open: dp
  ROM #(.addrWidth(10), .dataWidth(32), .Select("high")) rom_1 (.addr(IF_PC[11:2]), .data(IF_IR));
  // Probe on \总周期数 
  // Probe on M_PC[19:0]
  // RiscV_Probe riscv_probe_4: pin names not known; wires that end beside it: MEM_IR
  IF_ID IF_ID (
    .CLK(CLK), .\同步清零 (RST), .\指令字 (IF_IR), .PC_4(adder_1_out), .\指令字_2 (ID_IR), .PC_4_2(PC_4_ID),
    .PC(IF_PC), .PC_2(ID_PC));  // open: 使能_为1时时钟有效, PredictJump, PredictJump_2
  // Probe on \总周期数 
  // Probe on \无条件分支数 
  // Probe on \条件分支成功数 
  // Probe on \插入气泡数 
  // Probe on \LoadUse次数 
  // RiscV_Probe riscv_probe_5: pin names not known; wires that end beside it: IF_IR, IF_PC, adder_1_out, ID_IR
  // Probe on IF_PC[11:0]
  // Probe on WB_PC[19:0]
  // RiscV_Probe riscv_probe_6: pin names not known; wires that end beside it: WB_IR
  // Probe on ID_PC[11:0]
  // Probe on EX_PC[11:0]
  \单周期硬布线控制器  \u_单周期硬布线控制器_1  (
    .Funct({ID_IR[30], ID_IR[25], ID_IR[14:12]}), .OP(ID_IR[6:2]), .ALU_OP(\单周期硬布线控制器_1_alu_op ),
    .MemToReg(\单周期硬布线控制器_1_memtoreg ), .MemWrite(\单周期硬布线控制器_1_memwrite ), .ALU_SRC(\单周期硬布线控制器_1_alu_src ),
    .RegWrite(\单周期硬布线控制器_1_regwrite ), .ecall(Ecall_IF), .S_type(\单周期硬布线控制器_1_s_type ), .Jalr(JALR),
    .Beq(\单周期硬布线控制器_1_beq ), .JAL(JAL), .Bne(\单周期硬布线控制器_1_bne ), .in_3(ID_IR[21]), .uret(URET));  // open: Readrs1, Readrs2
  Multiplexer #(.select(1), .width(12), .disabled("Z"), .enable("false")) multiplexer_1 (
    .in0(ID_IR[31:20]), .in1({ID_IR[31:25], ID_IR[11:7]}), .out(multiplexer_1_out), .sel(\单周期硬布线控制器_1_s_type ));
  assign {\Jalr的立即数_ID , bit_extender_1_out[0]} = {{20{ID_IR[31]}}, ID_IR[31:20]};  // Bit_Extender bit_extender_1
  assign bit_extender_2_out = {{12{ID_IR[31]}}, {ID_IR[31], ID_IR[19:12], ID_IR[20], ID_IR[30:21]}};  // Bit_Extender bit_extender_2
  // Probe on M_PC[11:0]
  D_Flip_Flop #(.trigger("high"), .Pre_Clr_Positions("LEGACY"), .NegatePresetClear("false"), .enable("true"), .NewFFLayout("false")) d_ff_1 (.Q(d_ff_1_q));  // open: clk, D, Qn, preset, en, reset
  // Probe on 13'hc
  assign \I型或S型指令的立即数_ID  = {{20{multiplexer_1_out[11]}}, multiplexer_1_out};  // Bit_Extender bit_extender_3
  assign bit_extender_4_out = {{20{ID_IR[31]}}, {ID_IR[31], ID_IR[7], ID_IR[30:25], ID_IR[11:8]}};  // Bit_Extender bit_extender_4
  Shifter #(.width(32), .shift("ll")) shifter_1 (.in(bit_extender_2_out), .\dist (5'b00001), .out(\Jal的立即数_ID ));
  // Probe on WB_PC[11:0]
  Comparator #(.width(13), .mode("twosComplement")) comparator_1 (
    .a(CNT_num), .b(13'hc), .eq(comparator_1_eq), .lt(comparator_1_lt));  // open: gt
  Clock #(.highDuration(1), .lowDuration(1)) clock_1 (.out(clock_1_out));
  Regifile regifile_1 (
    .Din(RDin), .Clk(CLK), .R1(R_rs1__ID), .R2(R_rs2__ID), .WE(RegWrite), .W_num(W__WB),
    .R1_num(ID_IR[19:15]), .R2_num(ID_IR[24:20]));
  Shifter #(.width(32), .shift("ll")) shifter_2 (
    .in(bit_extender_4_out), .\dist (5'b00001), .out(\BranchAddress_B型指令的立即数__ID ));
  nand nand_1 (nand_1_out, d_ff_1_q, comparator_1_eq);
  Counter #(.width(13), .max('h1fff), .ongoal("stay"), .trigger("rising"), .behavior("old")) counter_1 (
    .count(comparator_1_lt), .Q(CNT_num), .clk(clock_1_out));  // open: load, D, carry, clr, preset
  assign CLK = nand_1_out ? clock_1_out : 1'bz;  // Controlled_Buffer controlled_buffer_1
  Pull_Resistor #(.pull(1)) pull_resistor_1 (.node(CLK));
  ID_EX ID_EX (
    .CLK(CLK), .\同步清零 (RST), .R_rs1(R_rs1__ID), .W_num(ID_IR[11:7]), .R_rs2(R_rs2__ID),
    .\I型或S型指令的立即数 (\I型或S型指令的立即数_ID ), .\B型指令的立即数 (\BranchAddress_B型指令的立即数__ID ), .BEQ(\单周期硬布线控制器_1_beq ),
    .\JAL的立即数 (\Jal的立即数_ID ), .MEMTOREG(\单周期硬布线控制器_1_memtoreg ), .MEMWRITE(\单周期硬布线控制器_1_memwrite ),
    .\JALR的立即数 ({\Jalr的立即数_ID , 1'b0}), .ALUOP(\单周期硬布线控制器_1_alu_op ), .ALUSRCB(\单周期硬布线控制器_1_alu_src ),
    .REGWRITE(\单周期硬布线控制器_1_regwrite ), .ECALL(Ecall_IF), .R_rs1_2(R_rs1__EX), .W_num_2(W__EX),
    .R_rs2_2(ID_EX_r_rs2_2), .\I型或S型指令的立即数_2 (\ID_EX_i型或s型指令的立即数_2 ), .\B型指令的立即数_2 (\I型或S型指令的立即数_EX ),
    .BEQ_2(ID_EX_beq_2), .\JAL的立即数_2 (\Jal的立即数_EX ), .MEMTOREG_2(MemToReg_EX), .MEMWRITE_2(MemWrite_EX),
    .\JALR的立即数_2 (\Jalr的立即数_EX ), .ALUOP_2(ID_EX_aluop_2), .ALUSRCB_2(ID_EX_alusrcb_2),
    .REGWRITE_2(RegWrite_EX), .ECALL_2(Ecall_EX), .PC(ID_PC), .PC_2(EX_PC), .BNE(\单周期硬布线控制器_1_bne ),
    .BNE_2(ID_EX_bne_2), .PC_4(PC_4_ID), .PC_4_2(PC_4_EX), .\指令字 (ID_IR), .\指令字_2 (EX_IR));  // open: 使能_为1时时钟有效, JAL, JALR, URET, JAL_2, JALR_2, URET_2, rs1forward, rs1forward_2, rs2forward, rs2forward_2, PredictJump, PredictJump_2
  Multiplexer #(.select(1), .width(32), .disabled("Z"), .enable("false")) multiplexer_2 (
    .in0(ID_EX_r_rs2_2), .in1(\ID_EX_i型或s型指令的立即数_2 ), .out(multiplexer_2_out), .sel(ID_EX_alusrcb_2));
  not not_2 (not_2_out, alu_1_equal);
  ALU alu_1 (
    .X(R_rs1__EX), .Y(multiplexer_2_out), .AluOP(ID_EX_aluop_2), .Equal(alu_1_equal), .Result(alu_1_result));  // open: Result_2, out_4, out_6
  and and_1 (and_1_out, ID_EX_beq_2, alu_1_equal);
  or or_1 (Branch_EX, and_1_out, and_2_out);
  and and_2 (and_2_out, ID_EX_bne_2, not_2_out);
  EX_MEM EX_MEM (
    .CLK(CLK), .\同步清零 (RST), .W_num(W__EX), .R_rs2(ID_EX_r_rs2_2), .ALURESULT(alu_1_result),
    .MEMTOREG(MemToReg_EX), .MEMWRITE(MemWrite_EX), .REGWRITE(RegWrite_EX), .ECALL(Ecall_EX),
    .W_num_2(W__MEM), .R_rs2_2(MDin), .ALURESULT_2(EX_MEM_aluresult_2), .MEMTOREG_2(MemToReg_MEM),
    .MEMWRITE_2(MemWrite), .REGWRITE_2(RegWrite_MEM), .ECALL_2(Ecall_MEM), .PC(EX_PC), .PC_2(M_PC),
    .\指令字 (EX_IR), .\指令字_2 (MEM_IR), .R_rs1(R_rs1__EX), .R_rs1_2(R_rs1__MEM));  // open: 使能_为1时时钟有效, URET, URET_2, PC_4, PC_4_2, JAL, JAL_2, JALR, JALR_2
  Comparator #(.width(32), .mode("twosComplement")) comparator_2 (
    .a(R_rs1__WB), .b(32'h22), .eq(comparator_2_eq));  // open: gt, lt
  not not_3 (not_3_out, halt);
  RAM #(.addrWidth(10), .dataWidth(32), .bus("separate"), .Select("high")) ram_1 (
    .addr(EX_MEM_aluresult_2[11:2]), .din(MDin), .data(ram_1_data), .str(MemWrite), .clk(CLK),
    .ld(MemToReg_MEM), .clr(RST));  // open: sel
  not not_4 (not_4_out, comparator_2_eq);
  not not_5 (not_5_out, Go);
  Counter #(.width(16), .max('hffff), .ongoal("wrap"), .trigger("rising"), .behavior("new")) counter_2 (
    .D(16'h1), .count(not_3_out), .Q(\总周期数 ), .clk(CLK));  // open: load, carry, clr, preset, down
  and and_3 (and_3_out, comparator_2_eq, Ecall_WB);
  and and_4 (halt, not_4_out, not_5_out, Ecall_WB);
  MEM_WB MEM_WB (
    .CLK(CLK), .\同步清零 (RST), .W_num(W__MEM), .RD(ram_1_data), .ALURESULT(EX_MEM_aluresult_2),
    .MEMTOREG(MemToReg_MEM), .REGWRITE(RegWrite_MEM), .ECALL(Ecall_MEM), .W_num_2(W__WB), .RD_2(MEM_WB_rd_2),
    .ALURESULT_2(MEM_WB_aluresult_2), .MEMTOREG_2(MemToReg_WB), .REGWRITE_2(RegWrite), .ECALL_2(Ecall_WB),
    .PC(M_PC), .PC_2(WB_PC), .\指令字 (MEM_IR), .\指令字_2 (WB_IR), .R_rs1(R_rs1__MEM), .R_rs1_2(R_rs1__WB),
    .R_rs2(MDin), .R_rs2_2(R_rs2__WB));  // open: 使能_为1时时钟有效, URET, URET_2, PC_4, PC_4_2, JAL, JAL_2, JALR, JALR_2
  Register #(.width(32), .trigger("rising"), .Select("low")) register_1 (
    .D(R_rs2__WB), .en(and_3_out), .Q(LedData), .clk(CLK), .clr(RST));
  Multiplexer #(.select(1), .width(32), .disabled("Z"), .enable("false")) multiplexer_3 (
    .in0(MEM_WB_aluresult_2), .in1(MEM_WB_rd_2), .out(RDin), .sel(MemToReg_WB));

  // Other names for the same wires on the sheet: IR[31:0] = ID_IR; W__ID[4:0] = ID_IR[11:7]; MEM_PC[31:0] = M_PC;
  //   R_rs2__MEM[31:0] = MDin; RegWrite_WB = RegWrite

  // Notes on the sheet:
  //   中断源
  //   时空图监测，可删除
  //   中断等待指示
  //   数码管输出
  //   指令存储器
  //   contents of rom_1 (hex, n*v repeats v):
  //   413 493 913 993 46413 14e493 296913 39e993 842023 942223 1242423 1342623 a00893 493 913 993 73
  //   指令探针
  //   指令字
  //   JALR
  //   URET
  //   控制位
  //   Beq
  //   Bne
  //   AluOP
  //   流水调试日志用
  //   暂停节拍，不能为0
  //   MemWrite(数据存储器的写使能控制信号)
  //   AluSrcB(运算器B输入选择 )
  //   RegWrite(寄存器堆的写使能控制信号）
  //   戳工具置1进入计数暂停模式，ctrl+k时钟自动运行到对应节拍暂停
  //   ctrl+k关闭时钟连续运行，将控制位置零，进入单步调试模式调试
  //   用这个时钟源需要去掉电路中的其他时钟源
  //   MemToReg(为1时将数据存储器读出的数据写回寄存器堆，否则将运算结果写回寄存器堆)
  //   可计数暂停的时钟源
  //   为方便自动评测，需要输出流水线各段保存的PC值，注意是PC不是PC+4，另外ID段寄存器写入信息，Mem段内存写入信息也要输出
  //   数据存储器
endmodule

module \重定向流水线  (
  output RegWrite,
  output MemWrite,
  output [31:0] IF_PC,
  output [31:0] ID_PC,
  output [31:0] EX_PC,
  output [31:0] M_PC,
  output [31:0] WB_PC,
  output [31:0] RDin,
  output [31:0] MDin,
  output [31:0] LedData
);

  wire alu_1_equal, and_1_out, and_2_out, and_3_out, and_4_out, and_5_out, and_6_out, Branch_EX,
       Branchtaken_EX, CLK, clock_1_out, comparator_1_eq, comparator_2_eq, comparator_3_eq, comparator_4_eq,
       comparator_5_eq, comparator_6_eq, comparator_7_eq, comparator_8_eq, comparator_9_eq, comparator_9_lt,
       comparator_10_eq, comparator_11_eq, comparator_12_eq, comparator_13_eq, comparator_14_eq, d_ff_1_q,
       Ecall_EX, Ecall_IF, Ecall_MEM, Ecall_WB, Go, halt, ID_EX_alusrcb_2, ID_EX_beq_2, ID_EX_bne_2, IR1,
       IR2, IR3, JAL_EX, JAL_ID, JAL_MEM, JAL_WB, JALR_EX, JALR_ID, JALR_MEM, JALR_WB, LoadUse, MemToReg_EX,
       MemToReg_MEM, MemToReg_WB, MemWrite_EX, nand_1_out, not_1_out, not_2_out, not_3_out, not_4_out,
       not_5_out, not_6_out, not_7_out, not_8_out, not_9_out, not_10_out, not_11_out, not_12_out, not_13_out,
       or_1_out, or_2_out, or_6_out, Readrs1_ID, Readrs2_ID, RegWrite_EX, RegWrite_MEM, RST, URET_ID, W1, W2,
       W3, \单周期硬布线控制器_1_alu_src , \单周期硬布线控制器_1_beq , \单周期硬布线控制器_1_bne , \单周期硬布线控制器_1_memtoreg ,
       \单周期硬布线控制器_1_memwrite , \单周期硬布线控制器_1_regwrite , \单周期硬布线控制器_1_s_type ;
  wire [0:0] bit_extender_1_out;
  wire [1:0] B_2_out, B_out, rs1forward_EX, rs1forward_ID, rs2forward_EX, rs2forward_ID;
  wire [3:0] ID_EX_aluop_2, \单周期硬布线控制器_1_alu_op ;
  wire [4:0] rs1_ID, rs2_ID, W__EX, W__MEM, W__WB;
  wire [11:0] multiplexer_8_out;
  wire [12:0] CNT_num;
  wire [15:0] \LoadUse次数 , \总周期数 , \插入气泡数 , \无条件分支数 , \条件分支成功数 ;
  wire [31:0] adder_1_out, adder_3_out, adder_4_out, adder_5_out, alu_1_result, bit_extender_2_out,
       bit_extender_4_out, \BranchAddress_B型指令的立即数__EX , \BranchAddress_B型指令的立即数__ID , EX_IR,
       EX_MEM_aluresult_2, ID_EX_r_rs2_2, ID_IR, IF_IR, \I型或S型指令的立即数_EX , \I型或S型指令的立即数_ID , \Jalr的立即数_EX ,
       \Jal的立即数_EX , \Jal的立即数_ID , MEM_IR, MEM_WB_aluresult_2, MEM_WB_rd_2, multiplexer_1_out,
       multiplexer_2_out, multiplexer_11_out, multiplexer_12_out, Nextpc, PC_4, PC_4_EX, PC_4_ID, PC_4_MEM,
       PC_4_WB, R_rs1__EX, \R_rs1__EX重定向后 , R_rs1__ID, R_rs1__MEM, R_rs1__WB, \R_rs2__EX重定向后 , R_rs2__ID,
       R_rs2__WB, ram_1_data, WB_IR;
  wire [31:1] \Jalr的立即数_ID ;

  Button \u_总复位  (.out(RST));
  Button _1 (.out(IR1));
  Button _2 (.out(IR2));
  Button _3 (.out(IR3));
  // Probe on \总周期数 
  // Probe on \总周期数 
  Button \u_继续运行  (.out(Go));
  LED #(.active("true")) led_1 (.in(W1));
  LED #(.active("true")) led_2 (.in(W2));
  LED #(.active("true")) led_3 (.in(W3));
  not not_1 (not_1_out, halt);
  Hex_Digit_Display hex_digit_display_1 (.value(LedData[31:28]));  // open: dp
  // Probe on IF_PC[19:0]
  // RiscV_Probe riscv_probe_1: pin names not known; wires that end beside it: IF_IR
  // Probe on Nextpc[11:2]
  and and_1 (and_1_out, not_1_out, not_2_out);
  not not_2 (not_2_out, LoadUse);
  Hex_Digit_Display hex_digit_display_2 (.value(LedData[27:24]));  // open: dp
  Hex_Digit_Display hex_digit_display_3 (.value(LedData[23:20]));  // open: dp
  // Probe on ID_PC[19:0]
  // RiscV_Probe riscv_probe_2: pin names not known; wires that end beside it: ID_IR
  Register #(.width(32), .trigger("rising"), .Select("low")) PC (
    .D(Nextpc), .en(and_1_out), .Q(IF_PC), .clk(CLK), .clr(RST));
  Comparator #(.width(5), .mode("twosComplement")) comparator_1 (
    .a(rs1_ID), .b({5{1'b0}}), .eq(comparator_1_eq));  // open: gt, lt
  Comparator #(.width(5), .mode("twosComplement")) comparator_2 (
    .a(rs1_ID), .b(W__EX), .eq(comparator_2_eq));  // open: gt, lt
  Comparator #(.width(5), .mode("twosComplement")) comparator_3 (
    .a(rs1_ID), .b({5{1'b0}}), .eq(comparator_3_eq));  // open: gt, lt
  Comparator #(.width(5), .mode("twosComplement")) comparator_4 (
    .a(rs1_ID), .b(W__MEM), .eq(comparator_4_eq));  // open: gt, lt
  Comparator #(.width(5), .mode("twosComplement")) comparator_5 (
    .a(rs2_ID), .b({5{1'b0}}), .eq(comparator_5_eq));  // open: gt, lt
  Comparator #(.width(5), .mode("twosComplement")) comparator_6 (
    .a(rs2_ID), .b(W__EX), .eq(comparator_6_eq));  // open: gt, lt
  Comparator #(.width(5), .mode("twosComplement")) comparator_7 (
    .a(rs2_ID), .b({5{1'b0}}), .eq(comparator_7_eq));  // open: gt, lt
  Comparator #(.width(5), .mode("twosComplement")) comparator_8 (
    .a(rs2_ID), .b(W__MEM), .eq(comparator_8_eq));  // open: gt, lt
  Hex_Digit_Display hex_digit_display_4 (.value(LedData[19:16]));  // open: dp
  Hex_Digit_Display hex_digit_display_5 (.value(LedData[15:12]));  // open: dp
  // Probe on IF_PC[11:2]
  Adder #(.width(32)) adder_1 (.a(IF_PC), .b(32'h4), .out(adder_1_out));  // open: cin, cout
  Adder #(.width(32)) adder_2 (.a(IF_PC), .b(32'h4), .out(PC_4));  // open: cin, cout
  Adder #(.width(32)) adder_3 (.a(EX_PC), .b(\BranchAddress_B型指令的立即数__EX ), .out(adder_3_out));  // open: cin, cout
  Adder #(.width(32)) adder_4 (.a(EX_PC), .b(\Jal的立即数_EX ), .out(adder_4_out));  // open: cin, cout
  not not_3 (not_3_out, comparator_1_eq);
  not not_4 (not_4_out, comparator_3_eq);
  not not_5 (not_5_out, comparator_5_eq);
  not not_6 (not_6_out, comparator_7_eq);
  Hex_Digit_Display hex_digit_display_6 (.value(LedData[11:8]));  // open: dp
  Hex_Digit_Display hex_digit_display_7 (.value(LedData[7:4]));  // open: dp
  // Probe on EX_PC[19:0]
  // RiscV_Probe riscv_probe_3: pin names not known; wires that end beside it: EX_IR
  Multiplexer #(.select(1), .width(32), .disabled("Z"), .enable("false")) multiplexer_1 (
    .in0(PC_4), .in1(adder_3_out), .out(multiplexer_1_out), .sel(Branch_EX));
  Adder #(.width(32)) adder_5 (.a(\R_rs1__EX重定向后 ), .b(\Jalr的立即数_EX ), .out(adder_5_out));  // open: cin, cout
  and A (B_out[1], Readrs1_ID, not_3_out, RegWrite_EX, comparator_2_eq);
  and B (B_out[0], Readrs1_ID, not_4_out, RegWrite_MEM, comparator_4_eq);
  and A_2 (B_2_out[1], Readrs2_ID, not_5_out, RegWrite_EX, comparator_6_eq);
  and B_2 (B_2_out[0], Readrs2_ID, not_6_out, RegWrite_MEM, comparator_8_eq);
  Hex_Digit_Display hex_digit_display_8 (.value(LedData[3:0]));  // open: dp
  ROM #(.addrWidth(10), .dataWidth(32), .Select("high")) rom_1 (.addr(IF_PC[11:2]), .data(IF_IR));
  not not_7 (not_7_out, LoadUse);
  Multiplexer #(.select(1), .width(32), .disabled("Z"), .enable("false")) multiplexer_2 (
    .in0(multiplexer_1_out), .in1(adder_4_out), .out(multiplexer_2_out), .sel(JAL_EX));
  // Probe on \总周期数 
  // Probe on M_PC[19:0]
  // RiscV_Probe riscv_probe_4: pin names not known; wires that end beside it: MEM_IR
  IF_ID IF_ID (
    .CLK(CLK), .\同步清零 (or_1_out), .\使能_为1时时钟有效 (not_7_out), .\指令字 (IF_IR), .PC_4(adder_1_out),
    .\指令字_2 (ID_IR), .PC_4_2(PC_4_ID), .PC(IF_PC), .PC_2(ID_PC));  // open: PredictJump, PredictJump_2
  or or_1 (or_1_out, Branchtaken_EX, RST);
  // Probe on \总周期数 
  // Probe on \无条件分支数 
  // Probe on \条件分支成功数 
  // Probe on \插入气泡数 
  // Probe on \LoadUse次数 
  // RiscV_Probe riscv_probe_5: pin names not known; wires that end beside it: IF_IR, IF_PC, adder_1_out, ID_IR
  Multiplexer #(.select(1), .width(32), .disabled("Z"), .enable("false")) multiplexer_3 (
    .in0(multiplexer_2_out), .in1(adder_5_out), .out(Nextpc), .sel(JALR_EX));
  // Probe on Nextpc
  // Probe on IF_PC[11:0]
  // Probe on WB_PC[19:0]
  // RiscV_Probe riscv_probe_6: pin names not known; wires that end beside it: WB_IR
  Multiplexer #(.select(2), .width(2), .disabled("Z"), .enable("false")) multiplexer_4 (
    .in0(2'b00), .in1(2'b01), .in2(2'b10), .in3(2'b10), .out(rs1forward_ID), .sel(B_out));
  Multiplexer #(.select(2), .width(2), .disabled("Z"), .enable("false")) multiplexer_5 (
    .in0(2'b00), .in1(2'b01), .in2(2'b10), .in3(2'b10), .out(rs2forward_ID), .sel(B_2_out));
  // Probe on ID_PC[11:0]
  // Probe on EX_PC[11:0]
  \单周期硬布线控制器  \u_单周期硬布线控制器_1  (
    .Funct({ID_IR[30], ID_IR[25], ID_IR[14:12]}), .OP(ID_IR[6:2]), .ALU_OP(\单周期硬布线控制器_1_alu_op ),
    .MemToReg(\单周期硬布线控制器_1_memtoreg ), .MemWrite(\单周期硬布线控制器_1_memwrite ), .ALU_SRC(\单周期硬布线控制器_1_alu_src ),
    .RegWrite(\单周期硬布线控制器_1_regwrite ), .ecall(Ecall_IF), .S_type(\单周期硬布线控制器_1_s_type ), .Jalr(JALR_ID),
    .Beq(\单周期硬布线控制器_1_beq ), .JAL(JAL_ID), .Bne(\单周期硬布线控制器_1_bne ), .in_3(ID_IR[21]), .uret(URET_ID),
    .Readrs1(Readrs1_ID), .Readrs2(Readrs2_ID));
  Multiplexer #(.select(1), .width(5), .disabled("Z"), .enable("false")) multiplexer_6 (
    .in0(ID_IR[19:15]), .in1(5'b10001), .out(rs1_ID), .sel(Ecall_IF));
  Multiplexer #(.select(1), .width(5), .disabled("Z"), .enable("false")) multiplexer_7 (
    .in0(ID_IR[24:20]), .in1(5'b01010), .out(rs2_ID), .sel(Ecall_IF));
  Multiplexer #(.select(1), .width(12), .disabled("Z"), .enable("false")) multiplexer_8 (
    .in0(ID_IR[31:20]), .in1({ID_IR[31:25], ID_IR[11:7]}), .out(multiplexer_8_out), .sel(\单周期硬布线控制器_1_s_type ));
  assign {\Jalr的立即数_ID , bit_extender_1_out[0]} = {{20{ID_IR[31]}}, ID_IR[31:20]};  // Bit_Extender bit_extender_1
  assign bit_extender_2_out = {{12{ID_IR[31]}}, {ID_IR[31], ID_IR[19:12], ID_IR[20], ID_IR[30:21]}};  // Bit_Extender bit_extender_2
  // Probe on M_PC[11:0]
  D_Flip_Flop #(.trigger("high"), .Pre_Clr_Positions("LEGACY"), .NegatePresetClear("false"), .enable("true"), .NewFFLayout("false")) d_ff_1 (.Q(d_ff_1_q));  // open: clk, D, Qn, preset, en, reset
  // Probe on 13'hc
  assign \I型或S型指令的立即数_ID  = {{20{multiplexer_8_out[11]}}, multiplexer_8_out};  // Bit_Extender bit_extender_3
  assign bit_extender_4_out = {{20{ID_IR[31]}}, {ID_IR[31], ID_IR[7], ID_IR[30:25], ID_IR[11:8]}};  // Bit_Extender bit_extender_4
  Shifter #(.width(32), .shift("ll")) shifter_1 (.in(bit_extender_2_out), .\dist (5'b00001), .out(\Jal的立即数_ID ));
  // Probe on WB_PC[11:0]
  Comparator #(.width(13), .mode("twosComplement")) comparator_9 (
    .a(CNT_num), .b(13'hc), .eq(comparator_9_eq), .lt(comparator_9_lt));  // open: gt
  Clock #(.highDuration(1), .lowDuration(1)) clock_1 (.out(clock_1_out));
  Regifile regifile_1 (
    .Din(RDin), .Clk(CLK), .R1(R_rs1__ID), .R2(R_rs2__ID), .WE(RegWrite), .W_num(W__WB), .R1_num(rs1_ID),
    .R2_num(rs2_ID));
  Shifter #(.width(32), .shift("ll")) shifter_2 (
    .in(bit_extender_4_out), .\dist (5'b00001), .out(\BranchAddress_B型指令的立即数__ID ));
  Comparator #(.width(5), .mode("twosComplement")) comparator_10 (
    .a(rs1_ID), .b({5{1'b0}}), .eq(comparator_10_eq));  // open: gt, lt
  Comparator #(.width(5), .mode("twosComplement")) comparator_11 (
    .a(rs1_ID), .b(W__EX), .eq(comparator_11_eq));  // open: gt, lt
  Comparator #(.width(5), .mode("twosComplement")) comparator_12 (
    .a(rs2_ID), .b({5{1'b0}}), .eq(comparator_12_eq));  // open: gt, lt
  Comparator #(.width(5), .mode("twosComplement")) comparator_13 (
    .a(rs2_ID), .b(W__EX), .eq(comparator_13_eq));  // open: gt, lt
  nand nand_1 (nand_1_out, d_ff_1_q, comparator_9_eq);
  Counter #(.width(13), .max('h1fff), .ongoal("stay"), .trigger("rising"), .behavior("old")) counter_1 (
    .count(comparator_9_lt), .Q(CNT_num), .clk(clock_1_out));  // open: load, D, carry, clr, preset
  not not_8 (not_8_out, comparator_10_eq);
  not not_9 (not_9_out, comparator_12_eq);
  assign CLK = nand_1_out ? clock_1_out : 1'bz;  // Controlled_Buffer controlled_buffer_1
  and and_2 (and_2_out, Readrs1_ID, not_8_out, MemToReg_EX, comparator_11_eq);
  and and_3 (and_3_out, Readrs2_ID, not_9_out, MemToReg_EX, comparator_13_eq);
  Pull_Resistor #(.pull(1)) pull_resistor_1 (.node(CLK));
  ID_EX ID_EX (
    .CLK(CLK), .\同步清零 (or_2_out), .R_rs1(R_rs1__ID), .W_num(ID_IR[11:7]), .R_rs2(R_rs2__ID), .JAL(JAL_ID),
    .JALR(JALR_ID), .\I型或S型指令的立即数 (\I型或S型指令的立即数_ID ), .\B型指令的立即数 (\BranchAddress_B型指令的立即数__ID ),
    .BEQ(\单周期硬布线控制器_1_beq ), .\JAL的立即数 (\Jal的立即数_ID ), .MEMTOREG(\单周期硬布线控制器_1_memtoreg ),
    .MEMWRITE(\单周期硬布线控制器_1_memwrite ), .\JALR的立即数 ({\Jalr的立即数_ID , 1'b0}), .ALUOP(\单周期硬布线控制器_1_alu_op ),
    .ALUSRCB(\单周期硬布线控制器_1_alu_src ), .REGWRITE(\单周期硬布线控制器_1_regwrite ), .ECALL(Ecall_IF),
    .R_rs1_2(R_rs1__EX), .W_num_2(W__EX), .R_rs2_2(ID_EX_r_rs2_2), .JAL_2(JAL_EX), .JALR_2(JALR_EX),
    .\I型或S型指令的立即数_2 (\I型或S型指令的立即数_EX ), .\B型指令的立即数_2 (\BranchAddress_B型指令的立即数__EX ), .BEQ_2(ID_EX_beq_2),
    .\JAL的立即数_2 (\Jal的立即数_EX ), .MEMTOREG_2(MemToReg_EX), .MEMWRITE_2(MemWrite_EX),
    .\JALR的立即数_2 (\Jalr的立即数_EX ), .ALUOP_2(ID_EX_aluop_2), .ALUSRCB_2(ID_EX_alusrcb_2),
    .REGWRITE_2(RegWrite_EX), .ECALL_2(Ecall_EX), .PC(ID_PC), .PC_2(EX_PC), .BNE(\单周期硬布线控制器_1_bne ),
    .BNE_2(ID_EX_bne_2), .PC_4(PC_4_ID), .PC_4_2(PC_4_EX), .\指令字 (ID_IR), .\指令字_2 (EX_IR),
    .rs1forward(rs1forward_ID), .rs1forward_2(rs1forward_EX), .rs2forward(rs2forward_ID),
    .rs2forward_2(rs2forward_EX));  // open: 使能_为1时时钟有效, URET, URET_2, PredictJump, PredictJump_2
  or or_2 (or_2_out, Branchtaken_EX, LoadUse);
  or or_3 (LoadUse, and_2_out, and_3_out);
  Multiplexer #(.select(2), .width(32), .disabled("Z"), .enable("false")) multiplexer_9 (
    .in0(ID_EX_r_rs2_2), .in1(RDin), .in2(EX_MEM_aluresult_2), .out(\R_rs2__EX重定向后 ), .sel(rs2forward_EX));  // open: in3
  Multiplexer #(.select(2), .width(32), .disabled("Z"), .enable("false")) multiplexer_10 (
    .in0(R_rs1__EX), .in1(RDin), .in2(EX_MEM_aluresult_2), .out(\R_rs1__EX重定向后 ), .sel(rs1forward_EX));  // open: in3
  or or_4 (Branchtaken_EX, JAL_EX, JALR_EX, Branch_EX);
  Multiplexer #(.select(1), .width(32), .disabled("Z"), .enable("false")) multiplexer_11 (
    .in0(\R_rs2__EX重定向后 ), .in1(\I型或S型指令的立即数_EX ), .out(multiplexer_11_out), .sel(ID_EX_alusrcb_2));
  and and_4 (and_4_out, ID_EX_beq_2, alu_1_equal);
  and and_5 (and_5_out, ID_EX_bne_2, not_10_out);
  not not_10 (not_10_out, alu_1_equal);
  ALU alu_1 (
    .X(\R_rs1__EX重定向后 ), .Y(multiplexer_11_out), .AluOP(ID_EX_aluop_2), .Equal(alu_1_equal),
    .Result(alu_1_result));  // open: Result_2, out_4, out_6
  or or_5 (Branch_EX, and_4_out, and_5_out);
  EX_MEM EX_MEM (
    .CLK(CLK), .\同步清零 (RST), .W_num(W__EX), .R_rs2(\R_rs2__EX重定向后 ), .ALURESULT(alu_1_result),
    .MEMTOREG(MemToReg_EX), .MEMWRITE(MemWrite_EX), .REGWRITE(RegWrite_EX), .ECALL(Ecall_EX),
    .W_num_2(W__MEM), .R_rs2_2(MDin), .ALURESULT_2(EX_MEM_aluresult_2), .MEMTOREG_2(MemToReg_MEM),
    .MEMWRITE_2(MemWrite), .REGWRITE_2(RegWrite_MEM), .ECALL_2(Ecall_MEM), .PC(EX_PC), .PC_2(M_PC),
    .\指令字 (EX_IR), .\指令字_2 (MEM_IR), .R_rs1(\R_rs1__EX重定向后 ), .R_rs1_2(R_rs1__MEM), .PC_4(PC_4_EX),
    .PC_4_2(PC_4_MEM), .JAL(JAL_EX), .JAL_2(JAL_MEM), .JALR(JALR_EX), .JALR_2(JALR_MEM));  // open: 使能_为1时时钟有效, URET, URET_2
  Comparator #(.width(32), .mode("twosComplement")) comparator_14 (
    .a(R_rs1__WB), .b(32'h22), .eq(comparator_14_eq));  // open: gt, lt
  not not_11 (not_11_out, halt);
  not not_12 (not_12_out, comparator_14_eq);
  not not_13 (not_13_out, Go);
  Counter #(.width(16), .max('hffff), .ongoal("wrap"), .trigger("rising"), .behavior("new")) counter_2 (
    .D(16'h1), .count(not_11_out), .Q(\总周期数 ), .clk(CLK));  // open: load, carry, clr, preset, down
  and and_6 (and_6_out, comparator_14_eq, Ecall_WB);
  and and_7 (halt, not_12_out, not_13_out, Ecall_WB);
  RAM #(.addrWidth(10), .dataWidth(32), .bus("separate"), .Select("high")) ram_1 (
    .addr(EX_MEM_aluresult_2[11:2]), .din(MDin), .data(ram_1_data), .str(MemWrite), .clk(CLK),
    .ld(MemToReg_MEM), .clr(RST));  // open: sel
  Register #(.width(32), .trigger("rising"), .Select("low")) register_1 (
    .D(R_rs2__WB), .en(and_6_out), .Q(LedData), .clk(CLK), .clr(RST));
  MEM_WB MEM_WB (
    .CLK(CLK), .\同步清零 (RST), .W_num(W__MEM), .RD(ram_1_data), .ALURESULT(EX_MEM_aluresult_2),
    .MEMTOREG(MemToReg_MEM), .REGWRITE(RegWrite_MEM), .ECALL(Ecall_MEM), .W_num_2(W__WB), .RD_2(MEM_WB_rd_2),
    .ALURESULT_2(MEM_WB_aluresult_2), .MEMTOREG_2(MemToReg_WB), .REGWRITE_2(RegWrite), .ECALL_2(Ecall_WB),
    .PC(M_PC), .PC_2(WB_PC), .\指令字 (MEM_IR), .\指令字_2 (WB_IR), .R_rs1(R_rs1__MEM), .R_rs1_2(R_rs1__WB),
    .R_rs2(MDin), .R_rs2_2(R_rs2__WB), .PC_4(PC_4_MEM), .PC_4_2(PC_4_WB), .JAL(JAL_MEM), .JAL_2(JAL_WB),
    .JALR(JALR_MEM), .JALR_2(JALR_WB));  // open: 使能_为1时时钟有效, URET, URET_2
  Multiplexer #(.select(1), .width(32), .disabled("Z"), .enable("false")) multiplexer_12 (
    .in0(MEM_WB_aluresult_2), .in1(MEM_WB_rd_2), .out(multiplexer_12_out), .sel(MemToReg_WB));
  or or_6 (or_6_out, JAL_WB, JALR_WB);
  Multiplexer #(.select(1), .width(32), .disabled("Z"), .enable("false")) multiplexer_13 (
    .in0(multiplexer_12_out), .in1(PC_4_WB), .out(RDin), .sel(or_6_out));

  // Other names for the same wires on the sheet: W__ID[4:0] = ID_IR[11:7]; MEM_PC[31:0] = M_PC;
  //   R_rs2__MEM[31:0] = MDin; RegWrite_WB = RegWrite

  // Notes on the sheet:
  //   中断源
  //   时空图监测，可删除
  //   中断等待指示
  //   数码管输出
  //   指令存储器
  //   contents of rom_1 (hex, n*v repeats v):
  //   100493 100006f 100493 200913 300993 100006f 100493 200913 300993 100006f 100493 200913 300993
  //   100006f 100493 200913 300993 29c000ef 100413 100493 1f49493 900533 2200893 73 24d493 48463 fedff06f
  //   900533 2200893 73 100493 249493 900533 2200893 73 48463 fedff06f 100493 1f49493 900533 2200893 73
  //   4034d493 900533 2200893 73 4044d493 900533 2200893 73 4044d493 900533 2200893 73 4044d493 900533
  //   2200893 73 4044d493 900533 2200893 73 4044d493 900533 2200893 73 4044d493 900533 2200893 73 4044d493
  //   900533 2200893 73 100413 1f41993 41f9d993 433 c00913 300b13 140413 f47413 800293 100313 499993
  //   89e9b3 1300533 2200893 73 406282b3 fe0294e3 140413 f00f93 1f47433 1c41413 800293 100313 49d993
  //   89e9b3 1300533 2200893 73 406282b3 fe0294e3 1c45413 406b0b33 b0463 f95ff06f 2b3 fff2c293 829293
  //   ff2e293 500533 2200893 73 fff00413 493 84a023 140413 448493 84a023 140413 448493 84a023 140413
  //   448493 84a023 140413 448493 84a023 140413 448493 84a023 140413 448493 84a023 140413 448493 84a023
  //   140413 448493 84a023 140413 448493 84a023 140413 448493 84a023 140413 448493 84a023 140413 448493
  //   84a023 140413 448493 84a023 140413 448493 84a023 140413 448493 84a023 140413 448493 140413 433
  //   3c00493 42983 4aa03 149a2b3 28663 134a023 1442023 ffc48493 fe9412e3 800533 2200893 73 440413 3c00493
  //   fc9416e3 a00893 73 413 140413 800533 2200893 73 240413 800533 2200893 73 340413 800533 2200893 73
  //   440413 800533 2200893 73 540413 800533 2200893 73 640413 800533 2200893 73 740413 800533 2200893 73
  //   840413 800533 2200893 2200893 73 8067
  //   指令探针
  //   指令字
  //   JALR
  //   URET
  //   控制位
  //   Beq
  //   Bne
  //   AluOP
  //   流水调试日志用
  //   暂停节拍，不能为0
  //   MemWrite(数据存储器的写使能控制信号)
  //   AluSrcB(运算器B输入选择 )
  //   RegWrite(寄存器堆的写使能控制信号）
  //   戳工具置1进入计数暂停模式，ctrl+k时钟自动运行到对应节拍暂停
  //   ctrl+k关闭时钟连续运行，将控制位置零，进入单步调试模式调试
  //   MemToReg(为1时将数据存储器读出的数据写回寄存器堆，否则将运算结果写回寄存器堆)
  //   可计数暂停的时钟源
  //   为方便自动评测，需要输出流水线各段保存的PC值，注意是PC不是PC+4，另外ID段寄存器写入信息，Mem段内存写入信息也要输出
  //   数据存储器
endmodule

module \气泡流水线  (
  output RegWrite,
  output MemWrite,
  output [31:0] IF_PC,
  output [31:0] ID_PC,
  output [31:0] EX_PC,
  output [31:0] M_PC,
  output [31:0] WB_PC,
  output [31:0] RDin,
  output [31:0] MDin,
  output [31:0] LedData
);

  wire alu_1_equal, and_1_out, and_2_out, and_3_out, and_4_out, and_5_out, and_6_out, and_7_out, and_8_out,
       and_9_out, and_10_out, Branch_EX, Branchtaken_EX, CLK, clock_1_out, comparator_1_eq, comparator_2_eq,
       comparator_2_lt, comparator_3_eq, comparator_4_eq, comparator_5_eq, comparator_6_eq, comparator_7_eq,
       comparator_8_eq, comparator_9_eq, comparator_10_eq, comparator_11_eq, comparator_12_eq,
       comparator_13_eq, d_ff_1_q, DataHazzard, Ecall_EX, Ecall_IF, Ecall_MEM, Ecall_WB, Go, halt,
       ID_EX_alusrcb_2, ID_EX_beq_2, ID_EX_bne_2, IR1, IR2, IR3, JAL_EX, JAL_ID, JAL_MEM, JAL_WB, JALR_EX,
       JALR_ID, JALR_MEM, JALR_WB, LoadUse, MemToReg_EX, MemToReg_MEM, MemToReg_WB, MemWrite_EX, nand_1_out,
       not_1_out, not_2_out, not_3_out, not_4_out, not_5_out, not_6_out, not_7_out, not_8_out, not_9_out,
       not_10_out, not_11_out, or_3_out, or_4_out, or_9_out, Readrs1_ID, Readrs2_ID, RegWrite_EX,
       RegWrite_MEM, RST, URET_ID, W1, W2, W3, \单周期硬布线控制器_1_alu_src , \单周期硬布线控制器_1_beq , \单周期硬布线控制器_1_bne ,
       \单周期硬布线控制器_1_memtoreg , \单周期硬布线控制器_1_memwrite , \单周期硬布线控制器_1_readrs1 , \单周期硬布线控制器_1_readrs2 ,
       \单周期硬布线控制器_1_regwrite , \单周期硬布线控制器_1_s_type ;
  wire [0:0] bit_extender_1_out;
  wire [3:0] ID_EX_aluop_2, \单周期硬布线控制器_1_alu_op ;
  wire [4:0] rs1_ID, rs2_ID, W__EX, W__MEM, W__WB;
  wire [11:0] multiplexer_6_out;
  wire [12:0] CNT_num;
  wire [15:0] \LoadUse次数 , \总周期数 , \插入气泡数 , \无条件分支数 , \条件分支成功数 ;
  wire [31:0] adder_1_out, adder_3_out, adder_4_out, adder_5_out, alu_1_result, bit_extender_2_out,
       bit_extender_4_out, \BranchAddress_B型指令的立即数__EX , \BranchAddress_B型指令的立即数__ID , EX_IR,
       EX_MEM_aluresult_2, ID_EX_r_rs2_2, ID_IR, IF_IR, \I型或S型指令的立即数_EX , \I型或S型指令的立即数_ID , \Jalr的立即数_EX ,
       \Jal的立即数_EX , \Jal的立即数_ID , MEM_IR, MEM_WB_aluresult_2, MEM_WB_rd_2, multiplexer_1_out,
       multiplexer_2_out, multiplexer_7_out, multiplexer_8_out, Nextpc, PC_4, PC_4_EX, PC_4_ID, PC_4_MEM,
       PC_4_WB, R_rs1__EX, R_rs1__ID, R_rs1__MEM, R_rs1__WB, R_rs2__ID, R_rs2__WB, ram_1_data, WB_IR;
  wire [31:1] \Jalr的立即数_ID ;

  Button \u_总复位  (.out(RST));
  Button _1 (.out(IR1));
  Button _2 (.out(IR2));
  Button _3 (.out(IR3));
  // Probe on \总周期数 
  // Probe on \总周期数 
  Button \u_继续运行  (.out(Go));
  LED #(.active("true")) led_1 (.in(W1));
  LED #(.active("true")) led_2 (.in(W2));
  LED #(.active("true")) led_3 (.in(W3));
  not not_1 (not_1_out, halt);
  Hex_Digit_Display hex_digit_display_1 (.value(LedData[31:28]));  // open: dp
  // Probe on IF_PC[19:0]
  // RiscV_Probe riscv_probe_1: pin names not known; wires that end beside it: IF_IR
  // Probe on Nextpc[11:2]
  and and_1 (and_1_out, not_1_out, not_2_out);
  not not_2 (not_2_out, DataHazzard);
  Hex_Digit_Display hex_digit_display_2 (.value(LedData[23:20]));  // open: dp
  Hex_Digit_Display hex_digit_display_3 (.value(LedData[27:24]));  // open: dp
  // Probe on ID_PC[19:0]
  // RiscV_Probe riscv_probe_2: pin names not known; wires that end beside it: ID_IR
  Register #(.width(32), .trigger("rising"), .Select("low")) PC (
    .D(Nextpc), .en(and_1_out), .Q(IF_PC), .clk(CLK), .clr(RST));
  Hex_Digit_Display hex_digit_display_4 (.value(LedData[15:12]));  // open: dp
  Hex_Digit_Display hex_digit_display_5 (.value(LedData[19:16]));  // open: dp
  // Probe on IF_PC[11:2]
  Adder #(.width(32)) adder_1 (.a(IF_PC), .b(32'h4), .out(adder_1_out));  // open: cin, cout
  Adder #(.width(32)) adder_2 (.a(IF_PC), .b(32'h4), .out(PC_4));  // open: cin, cout
  Adder #(.width(32)) adder_3 (.a(EX_PC), .b(\BranchAddress_B型指令的立即数__EX ), .out(adder_3_out));  // open: cin, cout
  Adder #(.width(32)) adder_4 (.a(EX_PC), .b(\Jal的立即数_EX ), .out(adder_4_out));  // open: cin, cout
  Hex_Digit_Display hex_digit_display_6 (.value(LedData[11:8]));  // open: dp
  Hex_Digit_Display hex_digit_display_7 (.value(LedData[7:4]));  // open: dp
  // Probe on EX_PC[19:0]
  // RiscV_Probe riscv_probe_3: pin names not known; wires that end beside it: EX_IR
  Multiplexer #(.select(1), .width(32), .disabled("Z"), .enable("false")) multiplexer_1 (
    .in0(PC_4), .in1(adder_3_out), .out(multiplexer_1_out), .sel(Branch_EX));
  Adder #(.width(32)) adder_5 (.a(R_rs1__EX), .b(\Jalr的立即数_EX ), .out(adder_5_out));  // open: cin, cout
  Hex_Digit_Display hex_digit_display_8 (.value(LedData[3:0]));  // open: dp
  ROM #(.addrWidth(10), .dataWidth(32), .Select("high")) rom_1 (.addr(IF_PC[11:2]), .data(IF_IR));
  not not_3 (not_3_out, DataHazzard);
  Multiplexer #(.select(1), .width(32), .disabled("Z"), .enable("false")) multiplexer_2 (
    .in0(multiplexer_1_out), .in1(adder_4_out), .out(multiplexer_2_out), .sel(JAL_EX));
  // Probe on \总周期数 
  // Probe on M_PC[19:0]
  // RiscV_Probe riscv_probe_4: pin names not known; wires that end beside it: MEM_IR
  or or_1 (Readrs2_ID, \单周期硬布线控制器_1_readrs2 , comparator_1_eq);
  or or_2 (Readrs1_ID, \单周期硬布线控制器_1_readrs1 , comparator_1_eq);
  IF_ID IF_ID (
    .CLK(CLK), .\同步清零 (or_3_out), .\使能_为1时时钟有效 (not_3_out), .\指令字 (IF_IR), .PC_4(adder_1_out),
    .\指令字_2 (ID_IR), .PC_4_2(PC_4_ID), .PC(IF_PC), .PC_2(ID_PC));  // open: PredictJump, PredictJump_2
  or or_3 (or_3_out, Branchtaken_EX, RST);
  // Probe on \总周期数 
  // Probe on \无条件分支数 
  // Probe on \条件分支成功数 
  // Probe on \插入气泡数 
  // Probe on \LoadUse次数 
  // RiscV_Probe riscv_probe_5: pin names not known; wires that end beside it: IF_IR, IF_PC, adder_1_out, ID_IR
  Multiplexer #(.select(1), .width(32), .disabled("Z"), .enable("false")) multiplexer_3 (
    .in0(multiplexer_2_out), .in1(adder_5_out), .out(Nextpc), .sel(JALR_EX));
  // Probe on IF_PC[11:0]
  // Probe on WB_PC[19:0]
  // RiscV_Probe riscv_probe_6: pin names not known; wires that end beside it: WB_IR
  // Probe on ID_PC[11:0]
  // Probe on EX_PC[11:0]
  \单周期硬布线控制器  \u_单周期硬布线控制器_1  (
    .Funct({ID_IR[30], ID_IR[25], ID_IR[14:12]}), .OP(ID_IR[6:2]), .ALU_OP(\单周期硬布线控制器_1_alu_op ),
    .MemToReg(\单周期硬布线控制器_1_memtoreg ), .MemWrite(\单周期硬布线控制器_1_memwrite ), .ALU_SRC(\单周期硬布线控制器_1_alu_src ),
    .RegWrite(\单周期硬布线控制器_1_regwrite ), .ecall(Ecall_IF), .S_type(\单周期硬布线控制器_1_s_type ), .Jalr(JALR_ID),
    .Beq(\单周期硬布线控制器_1_beq ), .JAL(JAL_ID), .Bne(\单周期硬布线控制器_1_bne ), .in_3(ID_IR[21]), .uret(URET_ID),
    .Readrs1(\单周期硬布线控制器_1_readrs1 ), .Readrs2(\单周期硬布线控制器_1_readrs2 ));
  Multiplexer #(.select(1), .width(5), .disabled("Z"), .enable("false")) multiplexer_4 (
    .in0(ID_IR[19:15]), .in1(5'b10001), .out(rs1_ID), .sel(Ecall_IF));
  Multiplexer #(.select(1), .width(5), .disabled("Z"), .enable("false")) multiplexer_5 (
    .in0(ID_IR[24:20]), .in1(5'b01010), .out(rs2_ID), .sel(Ecall_IF));
  Multiplexer #(.select(1), .width(12), .disabled("Z"), .enable("false")) multiplexer_6 (
    .in0(ID_IR[31:20]), .in1({ID_IR[31:25], ID_IR[11:7]}), .out(multiplexer_6_out), .sel(\单周期硬布线控制器_1_s_type ));
  assign {\Jalr的立即数_ID , bit_extender_1_out[0]} = {{20{ID_IR[31]}}, ID_IR[31:20]};  // Bit_Extender bit_extender_1
  assign bit_extender_2_out = {{12{ID_IR[31]}}, {ID_IR[31], ID_IR[19:12], ID_IR[20], ID_IR[30:21]}};  // Bit_Extender bit_extender_2
  // Probe on M_PC[11:0]
  D_Flip_Flop #(.trigger("high"), .Pre_Clr_Positions("LEGACY"), .NegatePresetClear("false"), .enable("true"), .NewFFLayout("false")) d_ff_1 (.Q(d_ff_1_q));  // open: clk, D, Qn, preset, en, reset
  // Probe on 13'hc
  Comparator #(.width(32), .mode("twosComplement")) comparator_1 (
    .a(ID_IR), .b({32{1'b0}}), .eq(comparator_1_eq));  // open: gt, lt
  assign \I型或S型指令的立即数_ID  = {{20{multiplexer_6_out[11]}}, multiplexer_6_out};  // Bit_Extender bit_extender_3
  assign bit_extender_4_out = {{20{ID_IR[31]}}, {ID_IR[31], ID_IR[7], ID_IR[30:25], ID_IR[11:8]}};  // Bit_Extender bit_extender_4
  Shifter #(.width(32), .shift("ll")) shifter_1 (.in(bit_extender_2_out), .\dist (5'b00001), .out(\Jal的立即数_ID ));
  // Probe on WB_PC[11:0]
  Comparator #(.width(13), .mode("twosComplement")) comparator_2 (
    .a(CNT_num), .b(13'hc), .eq(comparator_2_eq), .lt(comparator_2_lt));  // open: gt
  Clock #(.highDuration(1), .lowDuration(1)) clock_1 (.out(clock_1_out));
  Regifile regifile_1 (
    .Din(RDin), .Clk(CLK), .R1(R_rs1__ID), .R2(R_rs2__ID), .WE(RegWrite), .W_num(W__WB), .R1_num(rs1_ID),
    .R2_num(rs2_ID));
  Shifter #(.width(32), .shift("ll")) shifter_2 (
    .in(bit_extender_4_out), .\dist (5'b00001), .out(\BranchAddress_B型指令的立即数__ID ));
  nand nand_1 (nand_1_out, d_ff_1_q, comparator_2_eq);
  Counter #(.width(13), .max('h1fff), .ongoal("stay"), .trigger("rising"), .behavior("old")) counter_1 (
    .count(comparator_2_lt), .Q(CNT_num), .clk(clock_1_out));  // open: load, D, carry, clr, preset
  assign CLK = nand_1_out ? clock_1_out : 1'bz;  // Controlled_Buffer controlled_buffer_1
  Comparator #(.width(5), .mode("twosComplement")) comparator_3 (
    .a(rs1_ID), .b({5{1'b0}}), .eq(comparator_3_eq));  // open: gt, lt
  Comparator #(.width(5), .mode("twosComplement")) comparator_4 (
    .a(rs1_ID), .b(W__EX), .eq(comparator_4_eq));  // open: gt, lt
  Comparator #(.width(5), .mode("twosComplement")) comparator_5 (
    .a(rs1_ID), .b({5{1'b0}}), .eq(comparator_5_eq));  // open: gt, lt
  Comparator #(.width(5), .mode("twosComplement")) comparator_6 (
    .a(rs1_ID), .b(W__EX), .eq(comparator_6_eq));  // open: gt, lt
  Pull_Resistor #(.pull(1)) pull_resistor_1 (.node(CLK));
  ID_EX ID_EX (
    .CLK(CLK), .\同步清零 (or_4_out), .R_rs1(R_rs1__ID), .W_num(ID_IR[11:7]), .R_rs2(R_rs2__ID), .JAL(JAL_ID),
    .JALR(JALR_ID), .\I型或S型指令的立即数 (\I型或S型指令的立即数_ID ), .\B型指令的立即数 (\BranchAddress_B型指令的立即数__ID ),
    .BEQ(\单周期硬布线控制器_1_beq ), .\JAL的立即数 (\Jal的立即数_ID ), .MEMTOREG(\单周期硬布线控制器_1_memtoreg ),
    .MEMWRITE(\单周期硬布线控制器_1_memwrite ), .\JALR的立即数 ({\Jalr的立即数_ID , 1'b0}), .ALUOP(\单周期硬布线控制器_1_alu_op ),
    .ALUSRCB(\单周期硬布线控制器_1_alu_src ), .REGWRITE(\单周期硬布线控制器_1_regwrite ), .ECALL(Ecall_IF),
    .R_rs1_2(R_rs1__EX), .W_num_2(W__EX), .R_rs2_2(ID_EX_r_rs2_2), .JAL_2(JAL_EX), .JALR_2(JALR_EX),
    .\I型或S型指令的立即数_2 (\I型或S型指令的立即数_EX ), .\B型指令的立即数_2 (\BranchAddress_B型指令的立即数__EX ), .BEQ_2(ID_EX_beq_2),
    .\JAL的立即数_2 (\Jal的立即数_EX ), .MEMTOREG_2(MemToReg_EX), .MEMWRITE_2(MemWrite_EX),
    .\JALR的立即数_2 (\Jalr的立即数_EX ), .ALUOP_2(ID_EX_aluop_2), .ALUSRCB_2(ID_EX_alusrcb_2),
    .REGWRITE_2(RegWrite_EX), .ECALL_2(Ecall_EX), .PC(ID_PC), .PC_2(EX_PC), .BNE(\单周期硬布线控制器_1_bne ),
    .BNE_2(ID_EX_bne_2), .PC_4(PC_4_ID), .PC_4_2(PC_4_EX), .\指令字 (ID_IR), .\指令字_2 (EX_IR));  // open: 使能_为1时时钟有效, URET, URET_2, rs1forward, rs1forward_2, rs2forward, rs2forward_2, PredictJump, PredictJump_2
  or or_4 (or_4_out, Branchtaken_EX, DataHazzard);
  not not_4 (not_4_out, comparator_3_eq);
  not not_5 (not_5_out, comparator_5_eq);
  and and_2 (and_2_out, Readrs1_ID, not_4_out, MemToReg_EX, comparator_4_eq);
  and and_3 (and_3_out, Readrs1_ID, not_5_out, MemToReg_EX, comparator_6_eq);
  Multiplexer #(.select(1), .width(32), .disabled("Z"), .enable("false")) multiplexer_7 (
    .in0(ID_EX_r_rs2_2), .in1(\I型或S型指令的立即数_EX ), .out(multiplexer_7_out), .sel(ID_EX_alusrcb_2));
  or or_5 (LoadUse, and_2_out, and_3_out);
  or or_6 (Branchtaken_EX, JAL_EX, JALR_EX, Branch_EX);
  not not_6 (not_6_out, alu_1_equal);
  ALU alu_1 (
    .X(R_rs1__EX), .Y(multiplexer_7_out), .AluOP(ID_EX_aluop_2), .Equal(alu_1_equal), .Result(alu_1_result));  // open: Result_2, out_4, out_6
  and and_4 (and_4_out, ID_EX_beq_2, alu_1_equal);
  or or_7 (Branch_EX, and_4_out, and_5_out);
  and and_5 (and_5_out, ID_EX_bne_2, not_6_out);
  EX_MEM EX_MEM (
    .CLK(CLK), .\同步清零 (RST), .W_num(W__EX), .R_rs2(ID_EX_r_rs2_2), .ALURESULT(alu_1_result),
    .MEMTOREG(MemToReg_EX), .MEMWRITE(MemWrite_EX), .REGWRITE(RegWrite_EX), .ECALL(Ecall_EX),
    .W_num_2(W__MEM), .R_rs2_2(MDin), .ALURESULT_2(EX_MEM_aluresult_2), .MEMTOREG_2(MemToReg_MEM),
    .MEMWRITE_2(MemWrite), .REGWRITE_2(RegWrite_MEM), .ECALL_2(Ecall_MEM), .PC(EX_PC), .PC_2(M_PC),
    .\指令字 (EX_IR), .\指令字_2 (MEM_IR), .R_rs1(R_rs1__EX), .R_rs1_2(R_rs1__MEM), .PC_4(PC_4_EX),
    .PC_4_2(PC_4_MEM), .JAL(JAL_EX), .JAL_2(JAL_MEM), .JALR(JALR_EX), .JALR_2(JALR_MEM));  // open: 使能_为1时时钟有效, URET, URET_2
  Comparator #(.width(32), .mode("twosComplement")) comparator_7 (
    .a(R_rs1__WB), .b(32'h22), .eq(comparator_7_eq));  // open: gt, lt
  not not_7 (not_7_out, halt);
  Comparator #(.width(5), .mode("twosComplement")) comparator_8 (
    .a(rs1_ID), .b(W__EX), .eq(comparator_8_eq));  // open: gt, lt
  Comparator #(.width(5), .mode("twosComplement")) comparator_9 (
    .a(rs2_ID), .b(W__EX), .eq(comparator_9_eq));  // open: gt, lt
  Comparator #(.width(5), .mode("twosComplement")) comparator_10 (
    .a(rs1_ID), .b(W__MEM), .eq(comparator_10_eq));  // open: gt, lt
  Comparator #(.width(5), .mode("twosComplement")) comparator_11 (
    .a(rs2_ID), .b(W__MEM), .eq(comparator_11_eq));  // open: gt, lt
  not not_8 (not_8_out, comparator_12_eq);
  Comparator #(.width(5), .mode("twosComplement")) comparator_12 (
    .a(rs1_ID), .b({5{1'b0}}), .eq(comparator_12_eq));  // open: gt, lt
  Comparator #(.width(5), .mode("twosComplement")) comparator_13 (
    .a(rs2_ID), .b({5{1'b0}}), .eq(comparator_13_eq));  // open: gt, lt
  not not_9 (not_9_out, comparator_13_eq);
  RAM #(.addrWidth(10), .dataWidth(32), .bus("separate"), .Select("high")) ram_1 (
    .addr(EX_MEM_aluresult_2[11:2]), .din(MDin), .data(ram_1_data), .str(MemWrite), .clk(CLK),
    .ld(MemToReg_MEM), .clr(RST));  // open: sel
  not not_10 (not_10_out, comparator_7_eq);
  not not_11 (not_11_out, Go);
  Counter #(.width(16), .max('hffff), .ongoal("wrap"), .trigger("rising"), .behavior("new")) counter_2 (
    .D(16'h1), .count(not_7_out), .Q(\总周期数 ), .clk(CLK));  // open: load, carry, clr, preset, down
  and and_6 (and_6_out, Readrs1_ID, RegWrite_EX, comparator_8_eq, not_8_out);
  and and_7 (and_7_out, Readrs2_ID, RegWrite_EX, comparator_9_eq, not_9_out);
  and and_8 (and_8_out, Readrs1_ID, RegWrite_MEM, comparator_10_eq, not_8_out);
  and and_9 (and_9_out, Readrs2_ID, RegWrite_MEM, comparator_11_eq, not_9_out);
  and and_10 (and_10_out, comparator_7_eq, Ecall_WB);
  and and_11 (halt, not_10_out, not_11_out, Ecall_WB);
  MEM_WB MEM_WB (
    .CLK(CLK), .\同步清零 (RST), .W_num(W__MEM), .RD(ram_1_data), .ALURESULT(EX_MEM_aluresult_2),
    .MEMTOREG(MemToReg_MEM), .REGWRITE(RegWrite_MEM), .ECALL(Ecall_MEM), .W_num_2(W__WB), .RD_2(MEM_WB_rd_2),
    .ALURESULT_2(MEM_WB_aluresult_2), .MEMTOREG_2(MemToReg_WB), .REGWRITE_2(RegWrite), .ECALL_2(Ecall_WB),
    .PC(M_PC), .PC_2(WB_PC), .\指令字 (MEM_IR), .\指令字_2 (WB_IR), .R_rs1(R_rs1__MEM), .R_rs1_2(R_rs1__WB),
    .R_rs2(MDin), .R_rs2_2(R_rs2__WB), .PC_4(PC_4_MEM), .PC_4_2(PC_4_WB), .JAL(JAL_MEM), .JAL_2(JAL_WB),
    .JALR(JALR_MEM), .JALR_2(JALR_WB));  // open: 使能_为1时时钟有效, URET, URET_2
  Register #(.width(32), .trigger("rising"), .Select("low")) register_1 (
    .D(R_rs2__WB), .en(and_10_out), .Q(LedData), .clk(CLK), .clr(RST));
  or or_8 (DataHazzard, and_6_out, and_7_out, and_8_out, and_9_out);
  Multiplexer #(.select(1), .width(32), .disabled("Z"), .enable("false")) multiplexer_8 (
    .in0(MEM_WB_aluresult_2), .in1(MEM_WB_rd_2), .out(multiplexer_8_out), .sel(MemToReg_WB));
  or or_9 (or_9_out, JAL_WB, JALR_WB);
  Multiplexer #(.select(1), .width(32), .disabled("Z"), .enable("false")) multiplexer_9 (
    .in0(multiplexer_8_out), .in1(PC_4_WB), .out(RDin), .sel(or_9_out));

  // Other names for the same wires on the sheet: IR[31:0] = ID_IR; W__ID[4:0] = ID_IR[11:7]; MEM_PC[31:0] = M_PC;
  //   R_rs2__MEM[31:0] = MDin; RegWrite_WB = RegWrite

  // Notes on the sheet:
  //   中断源
  //   时空图监测，可删除
  //   中断等待指示
  //   数码管输出
  //   指令存储器
  //   contents of rom_1 (hex, n*v repeats v):
  //   100493 100006f 100493 200913 300993 100006f 100493 200913 300993 100006f 100493 200913 300993
  //   100006f 100493 200913 300993 29c000ef 100413 100493 1f49493 900533 2200893 73 24d493 48463 fedff06f
  //   900533 2200893 73 100493 249493 900533 2200893 73 48463 fedff06f 100493 1f49493 900533 2200893 73
  //   4034d493 900533 2200893 73 4044d493 900533 2200893 73 4044d493 900533 2200893 73 4044d493 900533
  //   2200893 73 4044d493 900533 2200893 73 4044d493 900533 2200893 73 4044d493 900533 2200893 73 4044d493
  //   900533 2200893 73 100413 1f41993 41f9d993 433 c00913 300b13 140413 f47413 800293 100313 499993
  //   89e9b3 1300533 2200893 73 406282b3 fe0294e3 140413 f00f93 1f47433 1c41413 800293 100313 49d993
  //   89e9b3 1300533 2200893 73 406282b3 fe0294e3 1c45413 406b0b33 b0463 f95ff06f 2b3 fff2c293 829293
  //   ff2e293 500533 2200893 73 fff00413 493 84a023 140413 448493 84a023 140413 448493 84a023 140413
  //   448493 84a023 140413 448493 84a023 140413 448493 84a023 140413 448493 84a023 140413 448493 84a023
  //   140413 448493 84a023 140413 448493 84a023 140413 448493 84a023 140413 448493 84a023 140413 448493
  //   84a023 140413 448493 84a023 140413 448493 84a023 140413 448493 84a023 140413 448493 140413 433
  //   3c00493 42983 4aa03 149a2b3 28663 134a023 1442023 ffc48493 fe9412e3 800533 2200893 73 440413 3c00493
  //   fc9416e3 a00893 73 413 140413 800533 2200893 73 240413 800533 2200893 73 340413 800533 2200893 73
  //   440413 800533 2200893 73 540413 800533 2200893 73 640413 800533 2200893 73 740413 800533 2200893 73
  //   840413 800533 2200893 2200893 73 8067
  //   指令探针
  //   指令字
  //   JALR
  //   URET
  //   控制位
  //   Beq
  //   Bne
  //   AluOP
  //   流水调试日志用
  //   暂停节拍，不能为0
  //   MemWrite(数据存储器的写使能控制信号)
  //   AluSrcB(运算器B输入选择 )
  //   RegWrite(寄存器堆的写使能控制信号）
  //   戳工具置1进入计数暂停模式，ctrl+k时钟自动运行到对应节拍暂停
  //   ctrl+k关闭时钟连续运行，将控制位置零，进入单步调试模式调试
  //   MemToReg(为1时将数据存储器读出的数据写回寄存器堆，否则将运算结果写回寄存器堆)
  //   可计数暂停的时钟源
  //   为方便自动评测，需要输出流水线各段保存的PC值，注意是PC不是PC+4，另外ID段寄存器写入信息，Mem段内存写入信息也要输出
  //   数据存储器
endmodule

module \中断按键参考电路  (
  input  \同步清零信号 ,
  output \与中断屏蔽位与 
);

  wire \_1号中断_out , and_1_out, clock_1_out, d_ff_1_q, or_1_out, or_2_out;

  Clock #(.highDuration(1), .lowDuration(1)) clock_1 (.out(clock_1_out));
  Button \_1号中断  (.out(\_1号中断_out ));
  or or_1 (or_1_out, \与中断屏蔽位与 , d_ff_1_q);
  LED #(.active("true")) \_1号中断等待指示灯  (.in(or_1_out));
  D_Flip_Flop #(.trigger("rising"), .Pre_Clr_Positions("LEGACY"), .NegatePresetClear("false"), .enable("true"), .NewFFLayout("false")) d_ff_1 (
    .clk(\_1号中断_out ), .D(1'b1), .Q(d_ff_1_q), .reset(\与中断屏蔽位与 ));  // open: Qn, preset, en
  or or_2 (or_2_out, d_ff_1_q, \与中断屏蔽位与 );
  and and_1 (and_1_out, or_2_out, ~\同步清零信号 );  // AND_Gate
  D_Flip_Flop #(.trigger("rising"), .Pre_Clr_Positions("LEGACY"), .NegatePresetClear("false"), .enable("true"), .NewFFLayout("false")) IR1 (
    .clk(clock_1_out), .D(and_1_out), .Q(\与中断屏蔽位与 ));  // open: Qn, preset, en, reset

  // Notes on the sheet:
  //   中断信号采样参考电路
  //   Reset 
endmodule

module \单周期_单级中断  (
  input  IR1,
  input  IR2,
  input  IR3,
  output RegWrite,
  output MemWrite,
  output [31:0] PC,
  output [31:0] IR,
  output [31:0] RDin,
  output [31:0] MDin,
  output [31:0] LedData
);

  wire CLK, clock_1_out, comparator_1_eq, comparator_2_eq, comparator_3_eq, comparator_4_eq, comparator_5_eq,
       comparator_5_lt, d_ff_1_q, Go, IR1_t, IR2_t, IR3_t, IRA, IRB, IRC, nand_1_out, or_1_out, W1, W2, W3;
  wire [12:0] CNT_num;
  wire [15:0] \总周期数 ;

  Button \u_继续运行  (.out(Go));
  Button _1 ();  // open: out
  Button _2 ();  // open: out
  Button _3 ();  // open: out
  LED #(.active("true")) led_1 (.in(W1));
  LED #(.active("true")) led_2 (.in(W2));
  LED #(.active("true")) led_3 (.in(W3));
  Hex_Digit_Display hex_digit_display_1 (.value(LedData[31:28]));  // open: dp
  Comparator #(.width(16), .mode("twosComplement")) comparator_1 (
    .a(16'h23b), .b(\总周期数 ), .eq(comparator_1_eq));  // open: gt, lt
  Comparator #(.width(16), .mode("twosComplement")) comparator_2 (
    .a(\总周期数 ), .b(16'h1), .eq(comparator_2_eq));  // open: gt, lt
  Comparator #(.width(16), .mode("twosComplement")) comparator_3 (
    .a(\总周期数 ), .b(16'h4), .eq(comparator_3_eq));  // open: gt, lt
  Comparator #(.width(16), .mode("twosComplement")) comparator_4 (
    .a(\总周期数 ), .b(16'h7), .eq(comparator_4_eq));  // open: gt, lt
  Hex_Digit_Display hex_digit_display_2 (.value(LedData[23:20]));  // open: dp
  Hex_Digit_Display hex_digit_display_3 (.value(LedData[27:24]));  // open: dp
  or or_1 (or_1_out, comparator_1_eq, comparator_2_eq);
  assign IRA = or_1_out ? ~CLK : 1'bz;  // Controlled_Inverter controlled_inverter_1
  assign IRB = comparator_3_eq ? ~CLK : 1'bz;  // Controlled_Inverter controlled_inverter_2
  assign IRC = comparator_4_eq ? ~CLK : 1'bz;  // Controlled_Inverter controlled_inverter_3
  Hex_Digit_Display hex_digit_display_4 (.value(LedData[15:12]));  // open: dp
  Hex_Digit_Display hex_digit_display_5 (.value(LedData[19:16]));  // open: dp
  Pull_Resistor #(.pull(0)) pull_resistor_1 (.node(IRA));
  Pull_Resistor #(.pull(0)) pull_resistor_2 (.node(IRB));
  Pull_Resistor #(.pull(0)) pull_resistor_3 (.node(IRC));
  Hex_Digit_Display hex_digit_display_6 (.value(LedData[11:8]));  // open: dp
  Hex_Digit_Display hex_digit_display_7 (.value(LedData[7:4]));  // open: dp
  // Probe on \总周期数 
  Hex_Digit_Display hex_digit_display_8 (.value(LedData[3:0]));  // open: dp
  or or_2 (IR1_t, IR1, IRA);
  or or_3 (IR2_t, IR2, IRB);
  or or_4 (IR3_t, IR3, IRC);
  D_Flip_Flop #(.trigger("high"), .Pre_Clr_Positions("LEGACY"), .NegatePresetClear("false"), .enable("true"), .NewFFLayout("false")) d_ff_1 (.Q(d_ff_1_q));  // open: clk, D, Qn, preset, en, reset
  // Probe on 13'hc
  Comparator #(.width(13), .mode("twosComplement")) comparator_5 (
    .a(CNT_num), .b(13'hc), .eq(comparator_5_eq), .lt(comparator_5_lt));  // open: gt
  Clock #(.highDuration(1), .lowDuration(1)) clock_1 (.out(clock_1_out));
  Counter #(.width(13), .max('h1fff), .ongoal("stay"), .trigger("rising"), .behavior("old")) counter_1 (
    .count(comparator_5_lt), .Q(CNT_num), .clk(clock_1_out));  // open: load, D, carry, clr, preset
  nand nand_1 (nand_1_out, d_ff_1_q, comparator_5_eq);
  assign CLK = nand_1_out ? clock_1_out : 1'bz;  // Controlled_Buffer controlled_buffer_1
  Pull_Resistor #(.pull(1)) pull_resistor_4 (.node(CLK));

  // Notes on the sheet:
  //   中断源
  //   中断等待指示
  //   总复位信号应将除ROM以外所有存储组件全部清零
  //   单级中断测试信号模拟器
  //   数码管输出
  //   数码管输出应该用寄存器锁存，否则显示数据只能一闪而过
  //   为方便自动评测，需要输出PC，IR，寄存器堆写如数据RDin
  //   RAM写使能MemWrite、RAM写入数据MDin等信号
  //   控制位
  //   暂停节拍，不能为0
  //   戳工具置1进入计数暂停模式，ctrl+k时钟自动运行到对应节拍暂停
  //   ctrl+k关闭时钟连续运行，将控制位置零，进入单步调试模式调试
  //   可计数暂停的时钟源
endmodule
module \单周期_多级中断  (
  input  IR1,
  input  IR2,
  input  IR3,
  output RegWrite,
  output MemWrite,
  output [31:0] PC,
  output [31:0] IR,
  output [31:0] RDin,
  output [31:0] MDin,
  output [31:0] LedData
);

  wire CLK, clock_1_out, comparator_1_eq, comparator_2_eq, comparator_3_eq, comparator_4_eq, comparator_5_eq,
       comparator_6_eq, comparator_6_lt, d_ff_1_q, Go, IR1_t, IR2_t, IR3_t, IRA, IRB, IRC, nand_1_out,
       or_1_out, or_2_out, W1, W2, W3;
  wire [12:0] CNT_num;
  wire [15:0] \总周期数 ;

  Button \u_继续运行  (.out(Go));
  Button _1 ();  // open: out
  Button _2 ();  // open: out
  Button _3 ();  // open: out
  LED #(.active("true")) led_1 (.in(W1));
  LED #(.active("true")) led_2 (.in(W2));
  LED #(.active("true")) led_3 (.in(W3));
  Hex_Digit_Display hex_digit_display_1 (.value(LedData[31:28]));  // open: dp
  Comparator #(.width(16), .mode("twosComplement")) comparator_1 (
    .a(\总周期数 ), .b(16'h7), .eq(comparator_1_eq));  // open: gt, lt
  Comparator #(.width(16), .mode("twosComplement")) comparator_2 (
    .a(\总周期数 ), .b(16'h241), .eq(comparator_2_eq));  // open: gt, lt
  Hex_Digit_Display hex_digit_display_2 (.value(LedData[23:20]));  // open: dp
  Hex_Digit_Display hex_digit_display_3 (.value(LedData[27:24]));  // open: dp
  Comparator #(.width(16), .mode("twosComplement")) comparator_3 (
    .a(16'h258), .b(\总周期数 ), .eq(comparator_3_eq));  // open: gt, lt
  or or_1 (or_1_out, comparator_3_eq, comparator_4_eq);
  Comparator #(.width(16), .mode("twosComplement")) comparator_4 (
    .a(\总周期数 ), .b(16'h1), .eq(comparator_4_eq));  // open: gt, lt
  Comparator #(.width(16), .mode("twosComplement")) comparator_5 (
    .a(\总周期数 ), .b(16'h4), .eq(comparator_5_eq));  // open: gt, lt
  or or_2 (or_2_out, comparator_1_eq, comparator_2_eq);
  Hex_Digit_Display hex_digit_display_4 (.value(LedData[19:16]));  // open: dp
  Hex_Digit_Display hex_digit_display_5 (.value(LedData[15:12]));  // open: dp
  Pull_Resistor #(.pull(0)) pull_resistor_1 (.node(IRA));
  assign IRA = or_1_out ? ~CLK : 1'bz;  // Controlled_Inverter controlled_inverter_1
  Pull_Resistor #(.pull(0)) pull_resistor_2 (.node(IRB));
  assign IRB = comparator_5_eq ? ~CLK : 1'bz;  // Controlled_Inverter controlled_inverter_2
  Pull_Resistor #(.pull(0)) pull_resistor_3 (.node(IRC));
  assign IRC = or_2_out ? ~CLK : 1'bz;  // Controlled_Inverter controlled_inverter_3
  Hex_Digit_Display hex_digit_display_6 (.value(LedData[7:4]));  // open: dp
  Hex_Digit_Display hex_digit_display_7 (.value(LedData[11:8]));  // open: dp
  // Probe on \总周期数 
  Hex_Digit_Display hex_digit_display_8 (.value(LedData[3:0]));  // open: dp
  or or_3 (IR1_t, IR1, IRA);
  or or_4 (IR2_t, IR2, IRB);
  or or_5 (IR3_t, IR3, IRC);
  D_Flip_Flop #(.trigger("high"), .Pre_Clr_Positions("LEGACY"), .NegatePresetClear("false"), .enable("true"), .NewFFLayout("false")) d_ff_1 (.Q(d_ff_1_q));  // open: clk, D, Qn, preset, en, reset
  // Probe on 13'hc
  Comparator #(.width(13), .mode("twosComplement")) comparator_6 (
    .a(CNT_num), .b(13'hc), .eq(comparator_6_eq), .lt(comparator_6_lt));  // open: gt
  Clock #(.highDuration(1), .lowDuration(1)) clock_1 (.out(clock_1_out));
  Counter #(.width(13), .max('h1fff), .ongoal("stay"), .trigger("rising"), .behavior("old")) counter_1 (
    .count(comparator_6_lt), .Q(CNT_num), .clk(clock_1_out));  // open: load, D, carry, clr, preset
  nand nand_1 (nand_1_out, d_ff_1_q, comparator_6_eq);
  assign CLK = nand_1_out ? clock_1_out : 1'bz;  // Controlled_Buffer controlled_buffer_1
  Pull_Resistor #(.pull(1)) pull_resistor_4 (.node(CLK));

  // Notes on the sheet:
  //   中断源
  //   中断等待指示
  //   总复位信号应将除ROM以外所有存储组件全部清零
  //   多级中断测试信号模拟器
  //   数码管输出
  //   数码管输出应该用寄存器锁存，否则显示数据只能一闪而过
  //   为方便自动评测，需要输出PC，IR，寄存器堆写如数据RDin
  //   RAM写使能MemWrite、RAM写入数据MDin等信号
  //   控制位
  //   暂停节拍，不能为0
  //   戳工具置1进入计数暂停模式，ctrl+k时钟自动运行到对应节拍暂停
  //   ctrl+k关闭时钟连续运行，将控制位置零，进入单步调试模式调试
  //   可计数暂停的时钟源
endmodule

module \封装正确性测试  (
);

  wire IR1, IR2, IR3, MemW, RegW;
  wire [31:0] EX_PC, ID_PC, IF_PC, IR, LED, MDin, MDinr, MEM_PC, PC, RDin, RDinr, WB_PC;

  \单周期RISC_V  \u_单周期risc_v_1  (
    .IR1(IR1), .IR2(IR2), .IR3(IR3), .RegWrite(RegW), .MemWrite(MemW), .PC(PC), .IR(IR), .RDin(RDin),
    .MDin(MDin), .LedData(LED));
  \气泡流水线  \u_气泡流水线_1  (
    .RegWrite(RegW), .MemWrite(MemW), .IF_PC(IF_PC), .ID_PC(ID_PC), .EX_PC(EX_PC), .M_PC(MEM_PC),
    .WB_PC(WB_PC), .RDin(RDinr), .MDin(MDinr), .LedData(LED));
  \单周期_单级中断  \u_单周期_单级中断_1  (
    .IR1(IR1), .IR2(IR2), .IR3(IR3), .RegWrite(RegW), .MemWrite(MemW), .PC(PC), .IR(IR), .RDin(RDin),
    .MDin(MDin), .LedData(LED));
  \理想流水线  \u_理想流水线_1  (
    .RegWrite(RegW), .MemWrite(MemW), .IF_PC(IF_PC), .ID_PC(ID_PC), .EX_PC(EX_PC), .M_PC(MEM_PC),
    .WB_PC(WB_PC), .RDin(RDinr), .MDin(MDinr), .LedData(LED));
  \重定向流水线  \u_重定向流水线_1  (
    .RegWrite(RegW), .MemWrite(MemW), .IF_PC(IF_PC), .ID_PC(ID_PC), .EX_PC(EX_PC), .M_PC(MEM_PC),
    .WB_PC(WB_PC), .RDin(RDinr), .MDin(MDinr), .LedData(LED));
  \单周期_多级中断  \u_单周期_多级中断_1  (
    .IR1(IR1), .IR2(IR2), .IR3(IR3), .RegWrite(RegW), .MemWrite(MemW), .PC(PC), .IR(IR), .RDin(RDin),
    .MDin(MDin), .LedData(LED));

  // Notes on the sheet:
  //   单周期封装测试
  //   气泡流水封装测试
  //   单周期+单级中断封装测试
  //   请检查上面封装有无位宽不匹配，引脚标签是否和连接的标签相对应，否则无法在educoder平台上正确测试
  //   理想流水封装测试
  //   重定向流水封装测试
  //   单周期+多级中断封装测试
endmodule

module IF_ID (
  input  CLK,
  input  \同步清零 ,
  input  \使能_为1时时钟有效 ,
  input  [31:0] \指令字 ,
  input  [31:0] PC_4,
  input  [31:0] PC,
  input  PredictJump,
  output [31:0] \指令字_2 ,
  output [31:0] PC_4_2,
  output [31:0] PC_2,
  output PredictJump_2
);

  wire multiplexer_4_out;
  wire [31:0] multiplexer_1_out, multiplexer_2_out, multiplexer_3_out;

  Multiplexer #(.select(1), .width(32), .disabled("Z"), .enable("false")) multiplexer_1 (
    .in0(\指令字 ), .in1({32{1'b0}}), .out(multiplexer_1_out), .sel(\同步清零 ));
  Multiplexer #(.select(1), .width(32), .disabled("Z"), .enable("false")) multiplexer_2 (
    .in0(PC_4), .in1({32{1'b0}}), .out(multiplexer_2_out), .sel(\同步清零 ));
  Multiplexer #(.select(1), .width(32), .disabled("Z"), .enable("false")) multiplexer_3 (
    .in0(PC), .in1({32{1'b0}}), .out(multiplexer_3_out), .sel(\同步清零 ));
  Multiplexer #(.select(1), .width(1), .disabled("Z"), .enable("false")) multiplexer_4 (
    .in0(PredictJump), .in1(1'b0), .out(multiplexer_4_out), .sel(\同步清零 ));
  Register #(.width(32), .trigger("rising"), .Select("low")) register_1 (
    .D(multiplexer_1_out), .en(\使能_为1时时钟有效 ), .Q(\指令字_2 ), .clk(CLK));  // open: clr
  Register #(.width(32), .trigger("rising"), .Select("low")) register_2 (
    .D(multiplexer_2_out), .en(\使能_为1时时钟有效 ), .Q(PC_4_2), .clk(CLK));  // open: clr
  Register #(.width(32), .trigger("rising"), .Select("low")) register_3 (
    .D(multiplexer_3_out), .en(\使能_为1时时钟有效 ), .Q(PC_2), .clk(CLK));  // open: clr
  Register #(.width(1), .trigger("rising"), .Select("low")) register_4 (
    .D(multiplexer_4_out), .en(\使能_为1时时钟有效 ), .Q(PredictJump_2), .clk(CLK));  // open: clr
endmodule

module ID_EX (
  input  CLK,
  input  \同步清零 ,
  input  \使能_为1时时钟有效 ,
  input  [31:0] R_rs1,
  input  [4:0] W_num,
  input  [31:0] R_rs2,
  input  JAL,
  input  JALR,
  input  [31:0] \I型或S型指令的立即数 ,
  input  URET,
  input  [31:0] \B型指令的立即数 ,
  input  BEQ,
  input  [31:0] \JAL的立即数 ,
  input  MEMTOREG,
  input  MEMWRITE,
  input  [31:0] \JALR的立即数 ,
  input  [3:0] ALUOP,
  input  ALUSRCB,
  input  [31:0] PC,
  input  REGWRITE,
  input  [31:0] PC_4,
  input  ECALL,
  input  [31:0] \指令字 ,
  input  BNE,
  input  [1:0] rs1forward,
  input  PredictJump,
  input  [1:0] rs2forward,
  output [31:0] R_rs1_2,
  output [4:0] W_num_2,
  output [31:0] R_rs2_2,
  output JAL_2,
  output JALR_2,
  output [31:0] \I型或S型指令的立即数_2 ,
  output URET_2,
  output [31:0] \B型指令的立即数_2 ,
  output BEQ_2,
  output [31:0] \JAL的立即数_2 ,
  output MEMTOREG_2,
  output MEMWRITE_2,
  output [31:0] \JALR的立即数_2 ,
  output [3:0] ALUOP_2,
  output ALUSRCB_2,
  output [31:0] PC_2,
  output REGWRITE_2,
  output [31:0] PC_4_2,
  output ECALL_2,
  output [31:0] \指令字_2 ,
  output BNE_2,
  output [1:0] rs1forward_2,
  output PredictJump_2,
  output [1:0] rs2forward_2
);

  wire multiplexer_10_out, multiplexer_12_out, multiplexer_13_out, multiplexer_14_out, multiplexer_15_out,
       multiplexer_16_out, multiplexer_17_out, multiplexer_19_out, multiplexer_20_out, multiplexer_21_out,
       multiplexer_22_out;
  wire [1:0] multiplexer_23_out, multiplexer_24_out;
  wire [3:0] multiplexer_18_out;
  wire [4:0] multiplexer_11_out;
  wire [31:0] multiplexer_1_out, multiplexer_2_out, multiplexer_3_out, multiplexer_4_out, multiplexer_5_out,
       multiplexer_6_out, multiplexer_7_out, multiplexer_8_out, multiplexer_9_out;

  Multiplexer #(.select(1), .width(32), .disabled("Z"), .enable("false")) multiplexer_1 (
    .in0(R_rs1), .in1({32{1'b0}}), .out(multiplexer_1_out), .sel(\同步清零 ));
  Multiplexer #(.select(1), .width(32), .disabled("Z"), .enable("false")) multiplexer_2 (
    .in0(R_rs2), .in1({32{1'b0}}), .out(multiplexer_2_out), .sel(\同步清零 ));
  Multiplexer #(.select(1), .width(32), .disabled("Z"), .enable("false")) multiplexer_3 (
    .in0(\I型或S型指令的立即数 ), .in1({32{1'b0}}), .out(multiplexer_3_out), .sel(\同步清零 ));
  Multiplexer #(.select(1), .width(32), .disabled("Z"), .enable("false")) multiplexer_4 (
    .in0(\B型指令的立即数 ), .in1({32{1'b0}}), .out(multiplexer_4_out), .sel(\同步清零 ));
  Multiplexer #(.select(1), .width(32), .disabled("Z"), .enable("false")) multiplexer_5 (
    .in0(\JAL的立即数 ), .in1({32{1'b0}}), .out(multiplexer_5_out), .sel(\同步清零 ));
  Multiplexer #(.select(1), .width(32), .disabled("Z"), .enable("false")) multiplexer_6 (
    .in0(\JALR的立即数 ), .in1({32{1'b0}}), .out(multiplexer_6_out), .sel(\同步清零 ));
  Multiplexer #(.select(1), .width(32), .disabled("Z"), .enable("false")) multiplexer_7 (
    .in0(PC), .in1({32{1'b0}}), .out(multiplexer_7_out), .sel(\同步清零 ));
  Multiplexer #(.select(1), .width(32), .disabled("Z"), .enable("false")) multiplexer_8 (
    .in0(PC_4), .in1({32{1'b0}}), .out(multiplexer_8_out), .sel(\同步清零 ));
  Multiplexer #(.select(1), .width(32), .disabled("Z"), .enable("false")) multiplexer_9 (
    .in0(\指令字 ), .in1({32{1'b0}}), .out(multiplexer_9_out), .sel(\同步清零 ));
  Multiplexer #(.select(1), .width(1), .disabled("Z"), .enable("false")) multiplexer_10 (
    .in0(PredictJump), .in1(1'b0), .out(multiplexer_10_out), .sel(\同步清零 ));
  Register #(.width(32), .trigger("rising"), .Select("low")) register_1 (
    .D(multiplexer_1_out), .en(\使能_为1时时钟有效 ), .Q(R_rs1_2), .clk(CLK));  // open: clr
  Register #(.width(32), .trigger("rising"), .Select("low")) register_2 (
    .D(multiplexer_2_out), .en(\使能_为1时时钟有效 ), .Q(R_rs2_2), .clk(CLK));  // open: clr
  Register #(.width(32), .trigger("rising"), .Select("low")) register_3 (
    .D(multiplexer_3_out), .en(\使能_为1时时钟有效 ), .Q(\I型或S型指令的立即数_2 ), .clk(CLK));  // open: clr
  Register #(.width(32), .trigger("rising"), .Select("low")) register_4 (
    .D(multiplexer_4_out), .en(\使能_为1时时钟有效 ), .Q(\B型指令的立即数_2 ), .clk(CLK));  // open: clr
  Register #(.width(32), .trigger("rising"), .Select("low")) register_5 (
    .D(multiplexer_5_out), .en(\使能_为1时时钟有效 ), .Q(\JAL的立即数_2 ), .clk(CLK));  // open: clr
  Register #(.width(32), .trigger("rising"), .Select("low")) register_6 (
    .D(multiplexer_6_out), .en(\使能_为1时时钟有效 ), .Q(\JALR的立即数_2 ), .clk(CLK));  // open: clr
  Register #(.width(32), .trigger("rising"), .Select("low")) register_7 (
    .D(multiplexer_7_out), .en(\使能_为1时时钟有效 ), .Q(PC_2), .clk(CLK));  // open: clr
  Register #(.width(32), .trigger("rising"), .Select("low")) register_8 (
    .D(multiplexer_8_out), .en(\使能_为1时时钟有效 ), .Q(PC_4_2), .clk(CLK));  // open: clr
  Register #(.width(32), .trigger("rising"), .Select("low")) register_9 (
    .D(multiplexer_9_out), .en(\使能_为1时时钟有效 ), .Q(\指令字_2 ), .clk(CLK));  // open: clr
  Register #(.width(1), .trigger("rising"), .Select("low")) register_10 (
    .D(multiplexer_10_out), .en(\使能_为1时时钟有效 ), .Q(PredictJump_2), .clk(CLK));  // open: clr
  Multiplexer #(.select(1), .width(5), .disabled("Z"), .enable("false")) multiplexer_11 (
    .in0(W_num), .in1({5{1'b0}}), .out(multiplexer_11_out), .sel(\同步清零 ));
  Multiplexer #(.select(1), .width(1), .disabled("Z"), .enable("false")) multiplexer_12 (
    .in0(JAL), .in1(1'b0), .out(multiplexer_12_out), .sel(\同步清零 ));
  Multiplexer #(.select(1), .width(1), .disabled("Z"), .enable("false")) multiplexer_13 (
    .in0(JALR), .in1(1'b0), .out(multiplexer_13_out), .sel(\同步清零 ));
  Multiplexer #(.select(1), .width(1), .disabled("Z"), .enable("false")) multiplexer_14 (
    .in0(URET), .in1(1'b0), .out(multiplexer_14_out), .sel(\同步清零 ));
  Multiplexer #(.select(1), .width(1), .disabled("Z"), .enable("false")) multiplexer_15 (
    .in0(BEQ), .in1(1'b0), .out(multiplexer_15_out), .sel(\同步清零 ));
  Multiplexer #(.select(1), .width(1), .disabled("Z"), .enable("false")) multiplexer_16 (
    .in0(MEMTOREG), .in1(1'b0), .out(multiplexer_16_out), .sel(\同步清零 ));
  Multiplexer #(.select(1), .width(1), .disabled("Z"), .enable("false")) multiplexer_17 (
    .in0(MEMWRITE), .in1(1'b0), .out(multiplexer_17_out), .sel(\同步清零 ));
  Multiplexer #(.select(1), .width(4), .disabled("Z"), .enable("false")) multiplexer_18 (
    .in0(ALUOP), .in1(4'b0000), .out(multiplexer_18_out), .sel(\同步清零 ));
  Multiplexer #(.select(1), .width(1), .disabled("Z"), .enable("false")) multiplexer_19 (
    .in0(ALUSRCB), .in1(1'b0), .out(multiplexer_19_out), .sel(\同步清零 ));
  Multiplexer #(.select(1), .width(1), .disabled("Z"), .enable("false")) multiplexer_20 (
    .in0(REGWRITE), .in1(1'b0), .out(multiplexer_20_out), .sel(\同步清零 ));
  Multiplexer #(.select(1), .width(1), .disabled("Z"), .enable("false")) multiplexer_21 (
    .in0(ECALL), .in1(1'b0), .out(multiplexer_21_out), .sel(\同步清零 ));
  Multiplexer #(.select(1), .width(1), .disabled("Z"), .enable("false")) multiplexer_22 (
    .in0(BNE), .in1(1'b0), .out(multiplexer_22_out), .sel(\同步清零 ));
  Multiplexer #(.select(1), .width(2), .disabled("Z"), .enable("false")) multiplexer_23 (
    .in0(rs1forward), .in1(2'b00), .out(multiplexer_23_out), .sel(\同步清零 ));
  Multiplexer #(.select(1), .width(2), .disabled("Z"), .enable("false")) multiplexer_24 (
    .in0(rs2forward), .in1(2'b00), .out(multiplexer_24_out), .sel(\同步清零 ));
  Register #(.width(5), .trigger("rising"), .Select("low")) register_11 (
    .D(multiplexer_11_out), .en(\使能_为1时时钟有效 ), .Q(W_num_2), .clk(CLK));  // open: clr
  Register #(.width(1), .trigger("rising"), .Select("low")) register_12 (
    .D(multiplexer_12_out), .en(\使能_为1时时钟有效 ), .Q(JAL_2), .clk(CLK));  // open: clr
  Register #(.width(1), .trigger("rising"), .Select("low")) register_13 (
    .D(multiplexer_13_out), .en(\使能_为1时时钟有效 ), .Q(JALR_2), .clk(CLK));  // open: clr
  Register #(.width(1), .trigger("rising"), .Select("low")) register_14 (
    .D(multiplexer_14_out), .en(\使能_为1时时钟有效 ), .Q(URET_2), .clk(CLK));  // open: clr
  Register #(.width(1), .trigger("rising"), .Select("low")) register_15 (
    .D(multiplexer_15_out), .en(\使能_为1时时钟有效 ), .Q(BEQ_2), .clk(CLK));  // open: clr
  Register #(.width(1), .trigger("rising"), .Select("low")) register_16 (
    .D(multiplexer_16_out), .en(\使能_为1时时钟有效 ), .Q(MEMTOREG_2), .clk(CLK));  // open: clr
  Register #(.width(1), .trigger("rising"), .Select("low")) register_17 (
    .D(multiplexer_17_out), .en(\使能_为1时时钟有效 ), .Q(MEMWRITE_2), .clk(CLK));  // open: clr
  Register #(.width(4), .trigger("rising"), .Select("low")) register_18 (
    .D(multiplexer_18_out), .en(\使能_为1时时钟有效 ), .Q(ALUOP_2), .clk(CLK));  // open: clr
  Register #(.width(1), .trigger("rising"), .Select("low")) register_19 (
    .D(multiplexer_19_out), .en(\使能_为1时时钟有效 ), .Q(ALUSRCB_2), .clk(CLK));  // open: clr
  Register #(.width(1), .trigger("rising"), .Select("low")) register_20 (
    .D(multiplexer_20_out), .en(\使能_为1时时钟有效 ), .Q(REGWRITE_2), .clk(CLK));  // open: clr
  Register #(.width(1), .trigger("rising"), .Select("low")) register_21 (
    .D(multiplexer_21_out), .en(\使能_为1时时钟有效 ), .Q(ECALL_2), .clk(CLK));  // open: clr
  Register #(.width(1), .trigger("rising"), .Select("low")) register_22 (
    .D(multiplexer_22_out), .en(\使能_为1时时钟有效 ), .Q(BNE_2), .clk(CLK));  // open: clr
  Register #(.width(2), .trigger("rising"), .Select("low")) register_23 (
    .D(multiplexer_23_out), .en(\使能_为1时时钟有效 ), .Q(rs1forward_2), .clk(CLK));  // open: clr
  Register #(.width(2), .trigger("rising"), .Select("low")) register_24 (
    .D(multiplexer_24_out), .en(\使能_为1时时钟有效 ), .Q(rs2forward_2), .clk(CLK));  // open: clr
endmodule

module EX_MEM (
  input  CLK,
  input  \同步清零 ,
  input  \使能_为1时时钟有效 ,
  input  [31:0] R_rs1,
  input  [4:0] W_num,
  input  JAL,
  input  [31:0] R_rs2,
  input  JALR,
  input  [31:0] ALURESULT,
  input  URET,
  input  [31:0] PC,
  input  MEMTOREG,
  input  [31:0] \指令字 ,
  input  MEMWRITE,
  input  [31:0] PC_4,
  input  REGWRITE,
  input  ECALL,
  output [31:0] R_rs1_2,
  output [4:0] W_num_2,
  output JAL_2,
  output [31:0] R_rs2_2,
  output JALR_2,
  output [31:0] ALURESULT_2,
  output URET_2,
  output [31:0] PC_2,
  output MEMTOREG_2,
  output [31:0] \指令字_2 ,
  output MEMWRITE_2,
  output [31:0] PC_4_2,
  output REGWRITE_2,
  output ECALL_2
);

  wire multiplexer_8_out, multiplexer_9_out, multiplexer_10_out, multiplexer_11_out, multiplexer_12_out,
       multiplexer_13_out, multiplexer_14_out;
  wire [4:0] multiplexer_7_out;
  wire [31:0] multiplexer_1_out, multiplexer_2_out, multiplexer_3_out, multiplexer_4_out, multiplexer_5_out,
       multiplexer_6_out;

  Multiplexer #(.select(1), .width(32), .disabled("Z"), .enable("false")) multiplexer_1 (
    .in0(R_rs1), .in1({32{1'b0}}), .out(multiplexer_1_out), .sel(\同步清零 ));
  Multiplexer #(.select(1), .width(32), .disabled("Z"), .enable("false")) multiplexer_2 (
    .in0(R_rs2), .in1({32{1'b0}}), .out(multiplexer_2_out), .sel(\同步清零 ));
  Multiplexer #(.select(1), .width(32), .disabled("Z"), .enable("false")) multiplexer_3 (
    .in0(ALURESULT), .in1({32{1'b0}}), .out(multiplexer_3_out), .sel(\同步清零 ));
  Multiplexer #(.select(1), .width(32), .disabled("Z"), .enable("false")) multiplexer_4 (
    .in0(PC), .in1({32{1'b0}}), .out(multiplexer_4_out), .sel(\同步清零 ));
  Multiplexer #(.select(1), .width(32), .disabled("Z"), .enable("false")) multiplexer_5 (
    .in0(\指令字 ), .in1({32{1'b0}}), .out(multiplexer_5_out), .sel(\同步清零 ));
  Multiplexer #(.select(1), .width(32), .disabled("Z"), .enable("false")) multiplexer_6 (
    .in0(PC_4), .in1({32{1'b0}}), .out(multiplexer_6_out), .sel(\同步清零 ));
  Register #(.width(32), .trigger("rising"), .Select("low")) register_1 (
    .D(multiplexer_1_out), .en(\使能_为1时时钟有效 ), .Q(R_rs1_2), .clk(CLK));  // open: clr
  Register #(.width(32), .trigger("rising"), .Select("low")) register_2 (
    .D(multiplexer_2_out), .en(\使能_为1时时钟有效 ), .Q(R_rs2_2), .clk(CLK));  // open: clr
  Register #(.width(32), .trigger("rising"), .Select("low")) register_3 (
    .D(multiplexer_3_out), .en(\使能_为1时时钟有效 ), .Q(ALURESULT_2), .clk(CLK));  // open: clr
  Register #(.width(32), .trigger("rising"), .Select("low")) register_4 (
    .D(multiplexer_4_out), .en(\使能_为1时时钟有效 ), .Q(PC_2), .clk(CLK));  // open: clr
  Register #(.width(32), .trigger("rising"), .Select("low")) register_5 (
    .D(multiplexer_5_out), .en(\使能_为1时时钟有效 ), .Q(\指令字_2 ), .clk(CLK));  // open: clr
  Register #(.width(32), .trigger("rising"), .Select("low")) register_6 (
    .D(multiplexer_6_out), .en(\使能_为1时时钟有效 ), .Q(PC_4_2), .clk(CLK));  // open: clr
  Multiplexer #(.select(1), .width(5), .disabled("Z"), .enable("false")) multiplexer_7 (
    .in0(W_num), .in1({5{1'b0}}), .out(multiplexer_7_out), .sel(\同步清零 ));
  Multiplexer #(.select(1), .width(1), .disabled("Z"), .enable("false")) multiplexer_8 (
    .in0(JAL), .in1(1'b0), .out(multiplexer_8_out), .sel(\同步清零 ));
  Multiplexer #(.select(1), .width(1), .disabled("Z"), .enable("false")) multiplexer_9 (
    .in0(JALR), .in1(1'b0), .out(multiplexer_9_out), .sel(\同步清零 ));
  Multiplexer #(.select(1), .width(1), .disabled("Z"), .enable("false")) multiplexer_10 (
    .in0(URET), .in1(1'b0), .out(multiplexer_10_out), .sel(\同步清零 ));
  Multiplexer #(.select(1), .width(1), .disabled("Z"), .enable("false")) multiplexer_11 (
    .in0(MEMTOREG), .in1(1'b0), .out(multiplexer_11_out), .sel(\同步清零 ));
  Multiplexer #(.select(1), .width(1), .disabled("Z"), .enable("false")) multiplexer_12 (
    .in0(MEMWRITE), .in1(1'b0), .out(multiplexer_12_out), .sel(\同步清零 ));
  Multiplexer #(.select(1), .width(1), .disabled("Z"), .enable("false")) multiplexer_13 (
    .in0(REGWRITE), .in1(1'b0), .out(multiplexer_13_out), .sel(\同步清零 ));
  Multiplexer #(.select(1), .width(1), .disabled("Z"), .enable("false")) multiplexer_14 (
    .in0(ECALL), .in1(1'b0), .out(multiplexer_14_out), .sel(\同步清零 ));
  Register #(.width(5), .trigger("rising"), .Select("low")) register_7 (
    .D(multiplexer_7_out), .en(\使能_为1时时钟有效 ), .Q(W_num_2), .clk(CLK));  // open: clr
  Register #(.width(1), .trigger("rising"), .Select("low")) register_8 (
    .D(multiplexer_8_out), .en(\使能_为1时时钟有效 ), .Q(JAL_2), .clk(CLK));  // open: clr
  Register #(.width(1), .trigger("rising"), .Select("low")) register_9 (
    .D(multiplexer_9_out), .en(\使能_为1时时钟有效 ), .Q(JALR_2), .clk(CLK));  // open: clr
  Register #(.width(1), .trigger("rising"), .Select("low")) register_10 (
    .D(multiplexer_10_out), .en(\使能_为1时时钟有效 ), .Q(URET_2), .clk(CLK));  // open: clr
  Register #(.width(1), .trigger("rising"), .Select("low")) register_11 (
    .D(multiplexer_11_out), .en(\使能_为1时时钟有效 ), .Q(MEMTOREG_2), .clk(CLK));  // open: clr
  Register #(.width(1), .trigger("rising"), .Select("low")) register_12 (
    .D(multiplexer_12_out), .en(\使能_为1时时钟有效 ), .Q(MEMWRITE_2), .clk(CLK));  // open: clr
  Register #(.width(1), .trigger("rising"), .Select("low")) register_13 (
    .D(multiplexer_13_out), .en(\使能_为1时时钟有效 ), .Q(REGWRITE_2), .clk(CLK));  // open: clr
  Register #(.width(1), .trigger("rising"), .Select("low")) register_14 (
    .D(multiplexer_14_out), .en(\使能_为1时时钟有效 ), .Q(ECALL_2), .clk(CLK));  // open: clr
endmodule

module MEM_WB (
  input  CLK,
  input  \同步清零 ,
  input  \使能_为1时时钟有效 ,
  input  [31:0] R_rs1,
  input  [4:0] W_num,
  input  [31:0] RD,
  input  JAL,
  input  JALR,
  input  [31:0] ALURESULT,
  input  URET,
  input  [31:0] \指令字 ,
  input  MEMTOREG,
  input  [31:0] R_rs2,
  input  [31:0] PC,
  input  REGWRITE,
  input  [31:0] PC_4,
  input  ECALL,
  output [31:0] R_rs1_2,
  output [4:0] W_num_2,
  output [31:0] RD_2,
  output JAL_2,
  output JALR_2,
  output [31:0] ALURESULT_2,
  output URET_2,
  output [31:0] \指令字_2 ,
  output MEMTOREG_2,
  output [31:0] R_rs2_2,
  output [31:0] PC_2,
  output REGWRITE_2,
  output [31:0] PC_4_2,
  output ECALL_2
);

  wire multiplexer_9_out, multiplexer_10_out, multiplexer_11_out, multiplexer_12_out, multiplexer_13_out,
       multiplexer_14_out;
  wire [4:0] multiplexer_8_out;
  wire [31:0] multiplexer_1_out, multiplexer_2_out, multiplexer_3_out, multiplexer_4_out, multiplexer_5_out,
       multiplexer_6_out, multiplexer_7_out;

  Multiplexer #(.select(1), .width(32), .disabled("Z"), .enable("false")) multiplexer_1 (
    .in0(R_rs1), .in1({32{1'b0}}), .out(multiplexer_1_out), .sel(\同步清零 ));
  Multiplexer #(.select(1), .width(32), .disabled("Z"), .enable("false")) multiplexer_2 (
    .in0(RD), .in1({32{1'b0}}), .out(multiplexer_2_out), .sel(\同步清零 ));
  Multiplexer #(.select(1), .width(32), .disabled("Z"), .enable("false")) multiplexer_3 (
    .in0(ALURESULT), .in1({32{1'b0}}), .out(multiplexer_3_out), .sel(\同步清零 ));
  Multiplexer #(.select(1), .width(32), .disabled("Z"), .enable("false")) multiplexer_4 (
    .in0(\指令字 ), .in1({32{1'b0}}), .out(multiplexer_4_out), .sel(\同步清零 ));
  Multiplexer #(.select(1), .width(32), .disabled("Z"), .enable("false")) multiplexer_5 (
    .in0(R_rs2), .in1({32{1'b0}}), .out(multiplexer_5_out), .sel(\同步清零 ));
  Multiplexer #(.select(1), .width(32), .disabled("Z"), .enable("false")) multiplexer_6 (
    .in0(PC), .in1({32{1'b0}}), .out(multiplexer_6_out), .sel(\同步清零 ));
  Multiplexer #(.select(1), .width(32), .disabled("Z"), .enable("false")) multiplexer_7 (
    .in0(PC_4), .in1({32{1'b0}}), .out(multiplexer_7_out), .sel(\同步清零 ));
  Register #(.width(32), .trigger("rising"), .Select("low")) register_1 (
    .D(multiplexer_1_out), .en(\使能_为1时时钟有效 ), .Q(R_rs1_2), .clk(CLK));  // open: clr
  Register #(.width(32), .trigger("rising"), .Select("low")) register_2 (
    .D(multiplexer_2_out), .en(\使能_为1时时钟有效 ), .Q(RD_2), .clk(CLK));  // open: clr
  Register #(.width(32), .trigger("rising"), .Select("low")) register_3 (
    .D(multiplexer_3_out), .en(\使能_为1时时钟有效 ), .Q(ALURESULT_2), .clk(CLK));  // open: clr
  Register #(.width(32), .trigger("rising"), .Select("low")) register_4 (
    .D(multiplexer_5_out), .en(\使能_为1时时钟有效 ), .Q(R_rs2_2), .clk(CLK));  // open: clr
  Register #(.width(32), .trigger("rising"), .Select("low")) register_5 (
    .D(multiplexer_4_out), .en(\使能_为1时时钟有效 ), .Q(\指令字_2 ), .clk(CLK));  // open: clr
  Register #(.width(32), .trigger("rising"), .Select("low")) register_6 (
    .D(multiplexer_6_out), .en(\使能_为1时时钟有效 ), .Q(PC_2), .clk(CLK));  // open: clr
  Register #(.width(32), .trigger("rising"), .Select("low")) register_7 (
    .D(multiplexer_7_out), .en(\使能_为1时时钟有效 ), .Q(PC_4_2), .clk(CLK));  // open: clr
  Multiplexer #(.select(1), .width(5), .disabled("Z"), .enable("false")) multiplexer_8 (
    .in0(W_num), .in1({5{1'b0}}), .out(multiplexer_8_out), .sel(\同步清零 ));
  Multiplexer #(.select(1), .width(1), .disabled("Z"), .enable("false")) multiplexer_9 (
    .in0(JAL), .in1(1'b0), .out(multiplexer_9_out), .sel(\同步清零 ));
  Multiplexer #(.select(1), .width(1), .disabled("Z"), .enable("false")) multiplexer_10 (
    .in0(JALR), .in1(1'b0), .out(multiplexer_10_out), .sel(\同步清零 ));
  Multiplexer #(.select(1), .width(1), .disabled("Z"), .enable("false")) multiplexer_11 (
    .in0(URET), .in1(1'b0), .out(multiplexer_11_out), .sel(\同步清零 ));
  Multiplexer #(.select(1), .width(1), .disabled("Z"), .enable("false")) multiplexer_12 (
    .in0(MEMTOREG), .in1(1'b0), .out(multiplexer_12_out), .sel(\同步清零 ));
  Multiplexer #(.select(1), .width(1), .disabled("Z"), .enable("false")) multiplexer_13 (
    .in0(REGWRITE), .in1(1'b0), .out(multiplexer_13_out), .sel(\同步清零 ));
  Multiplexer #(.select(1), .width(1), .disabled("Z"), .enable("false")) multiplexer_14 (
    .in0(ECALL), .in1(1'b0), .out(multiplexer_14_out), .sel(\同步清零 ));
  Register #(.width(5), .trigger("rising"), .Select("low")) register_8 (
    .D(multiplexer_8_out), .en(\使能_为1时时钟有效 ), .Q(W_num_2), .clk(CLK));  // open: clr
  Register #(.width(1), .trigger("rising"), .Select("low")) register_9 (
    .D(multiplexer_9_out), .en(\使能_为1时时钟有效 ), .Q(JAL_2), .clk(CLK));  // open: clr
  Register #(.width(1), .trigger("rising"), .Select("low")) register_10 (
    .D(multiplexer_10_out), .en(\使能_为1时时钟有效 ), .Q(JALR_2), .clk(CLK));  // open: clr
  Register #(.width(1), .trigger("rising"), .Select("low")) register_11 (
    .D(multiplexer_11_out), .en(\使能_为1时时钟有效 ), .Q(URET_2), .clk(CLK));  // open: clr
  Register #(.width(1), .trigger("rising"), .Select("low")) register_12 (
    .D(multiplexer_12_out), .en(\使能_为1时时钟有效 ), .Q(MEMTOREG_2), .clk(CLK));  // open: clr
  Register #(.width(1), .trigger("rising"), .Select("low")) register_13 (
    .D(multiplexer_13_out), .en(\使能_为1时时钟有效 ), .Q(REGWRITE_2), .clk(CLK));  // open: clr
  Register #(.width(1), .trigger("rising"), .Select("low")) register_14 (
    .D(multiplexer_14_out), .en(\使能_为1时时钟有效 ), .Q(ECALL_2), .clk(CLK));  // open: clr
endmodule

module \重定向流水线_动态分支预测  (
  output RegWrite,
  output MemWrite,
  output [31:0] IF_PC,
  output [31:0] ID_PC,
  output [31:0] EX_PC,
  output [31:0] M_PC,
  output [31:0] WB_PC,
  output [31:0] RDin,
  output [31:0] MDin,
  output [31:0] LedData
);

  wire alu_1_equal, and_1_out, and_2_out, and_3_out, and_4_out, and_5_out, and_7_out, and_8_out, Beq_EX,
       Bne_EX, Branch_EX, Branchtaken_EX, \B型Branch_EX , CLK, clock_1_out, comparator_1_eq, comparator_2_eq,
       comparator_3_eq, comparator_4_eq, comparator_5_eq, comparator_6_eq, comparator_7_eq, comparator_8_eq,
       comparator_9_eq, comparator_9_lt, comparator_10_eq, comparator_11_eq, comparator_12_eq,
       comparator_13_eq, comparator_14_eq, comparator_15_eq, d_ff_1_q, Ecall_EX, Ecall_IF, Ecall_MEM,
       Ecall_WB, Go, halt, ID_EX_alusrcb_2, IR1, IR2, IR3, JAL_EX, JAL_ID, JAL_MEM, JAL_WB, JALR_EX, JALR_ID,
       JALR_MEM, JALR_WB, LoadUse, MemToReg_EX, MemToReg_MEM, MemToReg_WB, MemWrite_EX, nand_1_out,
       not_1_out, not_2_out, not_3_out, not_4_out, not_5_out, not_6_out, not_7_out, not_8_out, not_9_out,
       not_10_out, not_11_out, not_12_out, not_13_out, not_14_out, not_15_out, not_17_out, not_18_out,
       or_1_out, or_2_out, or_8_out, PredictJump, PredictJump_EX, PredictJump_ID, Readrs1_ID, Readrs2_ID,
       RegWrite_EX, RegWrite_MEM, RST, URET_ID, W1, W2, W3, \单周期硬布线控制器_1_alu_src , \单周期硬布线控制器_1_beq ,
       \单周期硬布线控制器_1_bne , \单周期硬布线控制器_1_memtoreg , \单周期硬布线控制器_1_memwrite , \单周期硬布线控制器_1_regwrite ,
       \单周期硬布线控制器_1_s_type , \预测失败 ;
  wire [0:0] bit_extender_1_out;
  wire [1:0] B_2_out, B_out, rs1forward_EX, rs1forward_ID, rs2forward_EX, rs2forward_ID;
  wire [2:2] or_6_out;
  wire [3:0] ID_EX_aluop_2, \单周期硬布线控制器_1_alu_op ;
  wire [4:0] rs1_ID, rs2_ID, W__EX, W__MEM, W__WB;
  wire [11:0] multiplexer_9_out;
  wire [12:0] CNT_num;
  wire [15:0] \LoadUse次数 , \总周期数 , \插入气泡数 , \无条件分支数 , \条件分支成功数 ;
  wire [31:0] adder_1_out, adder_2_out, alu_1_result, bit_extender_2_out, bit_extender_4_out, BranchAddr_EX,
       \BranchAddress_B型指令的立即数__EX , \BranchAddress_B型指令的立即数__ID , \B型指令跳转地址 , EX_IR, EX_MEM_aluresult_2,
       ID_EX_r_rs2_2, ID_IR, IF_IR, \I型或S型指令的立即数_EX , \I型或S型指令的立即数_ID , \Jalr指令跳转地址 , \Jalr的立即数_EX ,
       \Jal指令跳转地址 , \Jal的立即数_EX , \Jal的立即数_ID , JumpAddr, MEM_IR, MEM_WB_aluresult_2, MEM_WB_rd_2,
       multiplexer_1_out, multiplexer_2_out, multiplexer_3_out, multiplexer_12_out, multiplexer_15_out,
       Nextpc, PC_4, PC_4_EX, PC_4_ID, PC_4_MEM, PC_4_WB, R_rs1__EX, \R_rs1__EX重定向后 , R_rs1__ID, R_rs1__MEM,
       R_rs1__WB, \R_rs2__EX重定向后 , R_rs2__ID, R_rs2__WB, ram_1_data, WB_IR, \最终的预测跳转地址 ;
  wire [31:1] \Jalr的立即数_ID ;

  Button \u_总复位  (.out(RST));
  Button _1 (.out(IR1));
  Button _2 (.out(IR2));
  Button _3 (.out(IR3));
  // Probe on \总周期数 
  // Probe on \总周期数 
  Button \u_继续运行  (.out(Go));
  LED #(.active("true")) led_1 (.in(W1));
  LED #(.active("true")) led_2 (.in(W2));
  LED #(.active("true")) led_3 (.in(W3));
  not not_1 (not_1_out, halt);
  // Probe on EX_PC
  Hex_Digit_Display hex_digit_display_1 (.value(LedData[31:28]));  // open: dp
  // Probe on IF_PC[19:0]
  // RiscV_Probe riscv_probe_1: pin names not known; wires that end beside it: IF_IR
  // Probe on Nextpc[11:2]
  and and_1 (and_1_out, not_1_out, not_2_out);
  not not_2 (not_2_out, LoadUse);
  Hex_Digit_Display hex_digit_display_2 (.value(LedData[27:24]));  // open: dp
  Hex_Digit_Display hex_digit_display_3 (.value(LedData[23:20]));  // open: dp
  // Probe on ID_PC[19:0]
  // RiscV_Probe riscv_probe_2: pin names not known; wires that end beside it: ID_IR
  Register #(.width(32), .trigger("rising"), .Select("low")) PC (
    .D(Nextpc), .en(and_1_out), .Q(IF_PC), .clk(CLK), .clr(RST));
  Comparator #(.width(5), .mode("twosComplement")) comparator_1 (
    .a(rs1_ID), .b({5{1'b0}}), .eq(comparator_1_eq));  // open: gt, lt
  Comparator #(.width(5), .mode("twosComplement")) comparator_2 (
    .a(rs1_ID), .b(W__EX), .eq(comparator_2_eq));  // open: gt, lt
  Comparator #(.width(5), .mode("twosComplement")) comparator_3 (
    .a(rs1_ID), .b({5{1'b0}}), .eq(comparator_3_eq));  // open: gt, lt
  Comparator #(.width(5), .mode("twosComplement")) comparator_4 (
    .a(rs1_ID), .b(W__MEM), .eq(comparator_4_eq));  // open: gt, lt
  Comparator #(.width(5), .mode("twosComplement")) comparator_5 (
    .a(rs2_ID), .b({5{1'b0}}), .eq(comparator_5_eq));  // open: gt, lt
  Comparator #(.width(5), .mode("twosComplement")) comparator_6 (
    .a(rs2_ID), .b(W__EX), .eq(comparator_6_eq));  // open: gt, lt
  Comparator #(.width(5), .mode("twosComplement")) comparator_7 (
    .a(rs2_ID), .b({5{1'b0}}), .eq(comparator_7_eq));  // open: gt, lt
  Comparator #(.width(5), .mode("twosComplement")) comparator_8 (
    .a(rs2_ID), .b(W__MEM), .eq(comparator_8_eq));  // open: gt, lt
  Hex_Digit_Display hex_digit_display_4 (.value(LedData[19:16]));  // open: dp
  Hex_Digit_Display hex_digit_display_5 (.value(LedData[15:12]));  // open: dp
  // Probe on IF_PC[11:2]
  Adder #(.width(32)) adder_1 (.a(IF_PC), .b(32'h4), .out(adder_1_out));  // open: cin, cout
  Adder #(.width(32)) adder_2 (.a(EX_PC), .b(32'h4), .out(adder_2_out));  // open: cin, cout
  Adder #(.width(32)) adder_3 (.a(EX_PC), .b(\BranchAddress_B型指令的立即数__EX ), .out(\B型指令跳转地址 ));  // open: cin, cout
  Adder #(.width(32)) adder_4 (.a(EX_PC), .b(\Jal的立即数_EX ), .out(\Jal指令跳转地址 ));  // open: cin, cout
  not not_3 (not_3_out, comparator_1_eq);
  not not_4 (not_4_out, comparator_3_eq);
  not not_5 (not_5_out, comparator_5_eq);
  not not_6 (not_6_out, comparator_7_eq);
  Hex_Digit_Display hex_digit_display_6 (.value(LedData[7:4]));  // open: dp
  Hex_Digit_Display hex_digit_display_7 (.value(LedData[11:8]));  // open: dp
  // Probe on EX_PC[19:0]
  // RiscV_Probe riscv_probe_3: pin names not known; wires that end beside it: EX_IR
  Multiplexer #(.select(1), .width(32), .disabled("Z"), .enable("false")) multiplexer_1 (
    .in0(adder_2_out), .in1(\B型指令跳转地址 ), .out(multiplexer_1_out), .sel(\B型Branch_EX ));
  Adder #(.width(32)) adder_5 (.a(\R_rs1__EX重定向后 ), .b(\Jalr的立即数_EX ), .out(\Jalr指令跳转地址 ));  // open: cin, cout
  and A (B_out[1], Readrs1_ID, not_3_out, RegWrite_EX, comparator_2_eq);
  and B (B_out[0], Readrs1_ID, not_4_out, RegWrite_MEM, comparator_4_eq);
  and A_2 (B_2_out[1], Readrs2_ID, not_5_out, RegWrite_EX, comparator_6_eq);
  and B_2 (B_2_out[0], Readrs2_ID, not_6_out, RegWrite_MEM, comparator_8_eq);
  Hex_Digit_Display hex_digit_display_8 (.value(LedData[3:0]));  // open: dp
  ROM #(.addrWidth(10), .dataWidth(32), .Select("high")) rom_1 (.addr(IF_PC[11:2]), .data(IF_IR));
  not not_7 (not_7_out, halt);
  and and_2 (and_2_out, not_7_out, not_8_out);
  not not_8 (not_8_out, LoadUse);
  // Probe on IF_PC
  Multiplexer #(.select(1), .width(32), .disabled("Z"), .enable("false")) multiplexer_2 (
    .in0(multiplexer_1_out), .in1(\Jal指令跳转地址 ), .out(multiplexer_2_out), .sel(JAL_EX));
  // Probe on \总周期数 
  // Probe on M_PC[19:0]
  // RiscV_Probe riscv_probe_4: pin names not known; wires that end beside it: MEM_IR
  IF_ID IF_ID (
    .CLK(CLK), .\同步清零 (or_1_out), .\使能_为1时时钟有效 (and_2_out), .\指令字 (IF_IR), .PC_4(adder_1_out),
    .\指令字_2 (ID_IR), .PC_4_2(PC_4_ID), .PC(IF_PC), .PC_2(ID_PC), .PredictJump(PredictJump),
    .PredictJump_2(PredictJump_ID));
  or or_1 (or_1_out, \预测失败 , RST);
  // Probe on \总周期数 
  // Probe on \无条件分支数 
  // Probe on \条件分支成功数 
  // Probe on \插入气泡数 
  // Probe on \LoadUse次数 
  // RiscV_Probe riscv_probe_5: pin names not known; wires that end beside it: IF_IR, IF_PC, adder_1_out, ID_IR
  Adder #(.width(32)) adder_6 (.a(IF_PC), .b(32'h4), .out(PC_4));  // open: cin, cout
  Multiplexer #(.select(1), .width(32), .disabled("Z"), .enable("false")) multiplexer_3 (
    .in0(multiplexer_2_out), .in1(\Jalr指令跳转地址 ), .out(multiplexer_3_out), .sel(JALR_EX));
  Multiplexer #(.select(1), .width(32), .disabled("Z"), .enable("false")) multiplexer_4 (
    .in0(\最终的预测跳转地址 ), .in1(multiplexer_3_out), .out(Nextpc), .sel(\预测失败 ));
  // Probe on IF_PC[11:0]
  // Probe on WB_PC[19:0]
  // RiscV_Probe riscv_probe_6: pin names not known; wires that end beside it: WB_IR
  // Probe on Nextpc
  Multiplexer #(.select(2), .width(2), .disabled("Z"), .enable("false")) multiplexer_5 (
    .in0(2'b00), .in1(2'b01), .in2(2'b10), .in3(2'b10), .out(rs1forward_ID), .sel(B_out));
  Multiplexer #(.select(2), .width(2), .disabled("Z"), .enable("false")) multiplexer_6 (
    .in0(2'b00), .in1(2'b01), .in2(2'b10), .in3(2'b10), .out(rs2forward_ID), .sel(B_2_out));
  // Probe on ID_PC[11:0]
  // Probe on EX_PC[11:0]
  \单周期硬布线控制器  \u_单周期硬布线控制器_1  (
    .Funct({ID_IR[30], ID_IR[25], ID_IR[14:12]}), .OP(ID_IR[6:2]), .ALU_OP(\单周期硬布线控制器_1_alu_op ),
    .MemToReg(\单周期硬布线控制器_1_memtoreg ), .MemWrite(\单周期硬布线控制器_1_memwrite ), .ALU_SRC(\单周期硬布线控制器_1_alu_src ),
    .RegWrite(\单周期硬布线控制器_1_regwrite ), .ecall(Ecall_IF), .S_type(\单周期硬布线控制器_1_s_type ), .Jalr(JALR_ID),
    .Beq(\单周期硬布线控制器_1_beq ), .JAL(JAL_ID), .Bne(\单周期硬布线控制器_1_bne ), .in_3(ID_IR[21]), .uret(URET_ID),
    .Readrs1(Readrs1_ID), .Readrs2(Readrs2_ID));
  Multiplexer #(.select(1), .width(5), .disabled("Z"), .enable("false")) multiplexer_7 (
    .in0(ID_IR[19:15]), .in1(5'b10001), .out(rs1_ID), .sel(Ecall_IF));
  Multiplexer #(.select(1), .width(5), .disabled("Z"), .enable("false")) multiplexer_8 (
    .in0(ID_IR[24:20]), .in1(5'b01010), .out(rs2_ID), .sel(Ecall_IF));
  Multiplexer #(.select(1), .width(12), .disabled("Z"), .enable("false")) multiplexer_9 (
    .in0(ID_IR[31:20]), .in1({ID_IR[31:25], ID_IR[11:7]}), .out(multiplexer_9_out), .sel(\单周期硬布线控制器_1_s_type ));
  assign {\Jalr的立即数_ID , bit_extender_1_out[0]} = {{20{ID_IR[31]}}, ID_IR[31:20]};  // Bit_Extender bit_extender_1
  assign bit_extender_2_out = {{12{ID_IR[31]}}, {ID_IR[31], ID_IR[19:12], ID_IR[20], ID_IR[30:21]}};  // Bit_Extender bit_extender_2
  // Probe on M_PC[11:0]
  D_Flip_Flop #(.trigger("high"), .Pre_Clr_Positions("LEGACY"), .NegatePresetClear("false"), .enable("true"), .NewFFLayout("false")) d_ff_1 (.Q(d_ff_1_q));  // open: clk, D, Qn, preset, en, reset
  // Probe on 13'hc
  assign \I型或S型指令的立即数_ID  = {{20{multiplexer_9_out[11]}}, multiplexer_9_out};  // Bit_Extender bit_extender_3
  assign bit_extender_4_out = {{20{ID_IR[31]}}, {ID_IR[31], ID_IR[7], ID_IR[30:25], ID_IR[11:8]}};  // Bit_Extender bit_extender_4
  Shifter #(.width(32), .shift("ll")) shifter_1 (.in(bit_extender_2_out), .\dist (5'b00001), .out(\Jal的立即数_ID ));
  // Probe on WB_PC[11:0]
  Comparator #(.width(13), .mode("twosComplement")) comparator_9 (
    .a(CNT_num), .b(13'hc), .eq(comparator_9_eq), .lt(comparator_9_lt));  // open: gt
  Clock #(.highDuration(1), .lowDuration(1)) clock_1 (.out(clock_1_out));
  Regifile regifile_1 (
    .Din(RDin), .Clk(CLK), .R1(R_rs1__ID), .R2(R_rs2__ID), .WE(RegWrite), .W_num(W__WB), .R1_num(rs1_ID),
    .R2_num(rs2_ID));
  Shifter #(.width(32), .shift("ll")) shifter_2 (
    .in(bit_extender_4_out), .\dist (5'b00001), .out(\BranchAddress_B型指令的立即数__ID ));
  Comparator #(.width(5), .mode("twosComplement")) comparator_10 (
    .a(rs1_ID), .b({5{1'b0}}), .eq(comparator_10_eq));  // open: gt, lt
  Comparator #(.width(5), .mode("twosComplement")) comparator_11 (
    .a(rs1_ID), .b(W__EX), .eq(comparator_11_eq));  // open: gt, lt
  Comparator #(.width(5), .mode("twosComplement")) comparator_12 (
    .a(rs2_ID), .b({5{1'b0}}), .eq(comparator_12_eq));  // open: gt, lt
  Comparator #(.width(5), .mode("twosComplement")) comparator_13 (
    .a(rs2_ID), .b(W__EX), .eq(comparator_13_eq));  // open: gt, lt
  nand nand_1 (nand_1_out, d_ff_1_q, comparator_9_eq);
  Counter #(.width(13), .max('h1fff), .ongoal("stay"), .trigger("rising"), .behavior("old")) counter_1 (
    .count(comparator_9_lt), .Q(CNT_num), .clk(clock_1_out));  // open: load, D, carry, clr, preset
  not not_9 (not_9_out, comparator_10_eq);
  not not_10 (not_10_out, comparator_12_eq);
  assign CLK = nand_1_out ? clock_1_out : 1'bz;  // Controlled_Buffer controlled_buffer_1
  and and_3 (and_3_out, Readrs1_ID, not_9_out, MemToReg_EX, comparator_11_eq);
  and and_4 (and_4_out, Readrs2_ID, not_10_out, MemToReg_EX, comparator_13_eq);
  Pull_Resistor #(.pull(1)) pull_resistor_1 (.node(CLK));
  ID_EX ID_EX (
    .CLK(CLK), .\同步清零 (or_2_out), .\使能_为1时时钟有效 (not_11_out), .R_rs1(R_rs1__ID), .W_num(ID_IR[11:7]),
    .R_rs2(R_rs2__ID), .JAL(JAL_ID), .JALR(JALR_ID), .\I型或S型指令的立即数 (\I型或S型指令的立即数_ID ),
    .\B型指令的立即数 (\BranchAddress_B型指令的立即数__ID ), .BEQ(\单周期硬布线控制器_1_beq ), .\JAL的立即数 (\Jal的立即数_ID ),
    .MEMTOREG(\单周期硬布线控制器_1_memtoreg ), .MEMWRITE(\单周期硬布线控制器_1_memwrite ), .\JALR的立即数 ({\Jalr的立即数_ID , 1'b0}),
    .ALUOP(\单周期硬布线控制器_1_alu_op ), .ALUSRCB(\单周期硬布线控制器_1_alu_src ), .REGWRITE(\单周期硬布线控制器_1_regwrite ),
    .ECALL(Ecall_IF), .R_rs1_2(R_rs1__EX), .W_num_2(W__EX), .R_rs2_2(ID_EX_r_rs2_2), .JAL_2(JAL_EX),
    .JALR_2(JALR_EX), .\I型或S型指令的立即数_2 (\I型或S型指令的立即数_EX ), .\B型指令的立即数_2 (\BranchAddress_B型指令的立即数__EX ),
    .BEQ_2(Beq_EX), .\JAL的立即数_2 (\Jal的立即数_EX ), .MEMTOREG_2(MemToReg_EX), .MEMWRITE_2(MemWrite_EX),
    .\JALR的立即数_2 (\Jalr的立即数_EX ), .ALUOP_2(ID_EX_aluop_2), .ALUSRCB_2(ID_EX_alusrcb_2),
    .REGWRITE_2(RegWrite_EX), .ECALL_2(Ecall_EX), .PC(ID_PC), .PC_2(EX_PC), .BNE(\单周期硬布线控制器_1_bne ),
    .BNE_2(Bne_EX), .PC_4(PC_4_ID), .PC_4_2(PC_4_EX), .\指令字 (ID_IR), .\指令字_2 (EX_IR),
    .rs1forward(rs1forward_ID), .rs1forward_2(rs1forward_EX), .rs2forward(rs2forward_ID),
    .rs2forward_2(rs2forward_EX), .PredictJump(PredictJump_ID), .PredictJump_2(PredictJump_EX));  // open: URET, URET_2
  or or_2 (or_2_out, \预测失败 , LoadUse);
  not not_11 (not_11_out, halt);
  or or_3 (LoadUse, and_3_out, and_4_out);
  Comparator #(.width(32), .mode("twosComplement")) comparator_14 (
    .a(R_rs1__WB), .b(32'h22), .eq(comparator_14_eq));  // open: gt, lt
  not not_12 (not_12_out, halt);
  or or_4 (Branch_EX, JAL_EX, JALR_EX, Beq_EX, Bne_EX);
  not not_13 (not_13_out, Go);
  Counter #(.width(16), .max('hffff), .ongoal("wrap"), .trigger("rising"), .behavior("new")) counter_2 (
    .D(16'h1), .count(not_12_out), .Q(\总周期数 ), .clk(CLK));  // open: load, carry, clr, preset, down
  Multiplexer #(.select(2), .width(32), .disabled("Z"), .enable("false")) multiplexer_10 (
    .in0(ID_EX_r_rs2_2), .in1(RDin), .in2(EX_MEM_aluresult_2), .out(\R_rs2__EX重定向后 ), .sel(rs2forward_EX));  // open: in3
  and and_5 (and_5_out, comparator_14_eq, Ecall_WB);
  not not_14 (not_14_out, comparator_14_eq);
  and and_6 (halt, not_14_out, not_13_out, Ecall_WB);
  Multiplexer #(.select(2), .width(32), .disabled("Z"), .enable("false")) multiplexer_11 (
    .in0(R_rs1__EX), .in1(RDin), .in2(EX_MEM_aluresult_2), .out(\R_rs1__EX重定向后 ), .sel(rs1forward_EX));  // open: in3
  Register #(.width(32), .trigger("rising"), .Select("low")) register_1 (
    .D(R_rs2__WB), .en(and_5_out), .Q(LedData), .clk(CLK), .clr(RST));
  or or_5 (Branchtaken_EX, JAL_EX, JALR_EX, \B型Branch_EX );
  Multiplexer #(.select(1), .width(32), .disabled("Z"), .enable("false")) multiplexer_12 (
    .in0(\R_rs2__EX重定向后 ), .in1(\I型或S型指令的立即数_EX ), .out(multiplexer_12_out), .sel(ID_EX_alusrcb_2));
  BTB btb_1 (
    .PC(IF_PC), .EX_PC(EX_PC), .EX_BranchAddr(BranchAddr_EX), .JumpAddr(JumpAddr), .PredictJump(PredictJump),
    .CLK(CLK), .EX_Branch(Branch_EX), .EX_BranchTaken(Branchtaken_EX));
  and and_7 (and_7_out, Beq_EX, alu_1_equal);
  and and_8 (and_8_out, Bne_EX, not_15_out);
  not not_15 (not_15_out, alu_1_equal);
  ALU alu_1 (
    .X(\R_rs1__EX重定向后 ), .Y(multiplexer_12_out), .AluOP(ID_EX_aluop_2), .Equal(alu_1_equal),
    .Result(alu_1_result));  // open: Result_2, out_4, out_6
  or or_6 (or_6_out[2], Beq_EX, Bne_EX);
  Comparator #(.width(1), .mode("twosComplement")) comparator_15 (
    .a(Branchtaken_EX), .b(PredictJump_EX), .eq(comparator_15_eq));  // open: gt, lt
  or or_7 (\B型Branch_EX , and_7_out, and_8_out);
  Multiplexer #(.select(3), .width(32), .disabled("Z"), .enable("false")) multiplexer_13 (
    .in0(IF_PC), .in1(\Jalr指令跳转地址 ), .in2(\Jal指令跳转地址 ), .in4(\B型指令跳转地址 ), .out(BranchAddr_EX),
    .sel({or_6_out[2], JAL_EX, JALR_EX}));  // open: in3, in5, in6, in7
  not not_16 (\预测失败 , comparator_15_eq);
  not not_17 (not_17_out, halt);
  Multiplexer #(.select(1), .width(32), .disabled("Z"), .enable("false")) multiplexer_14 (
    .in0(PC_4), .in1(JumpAddr), .out(\最终的预测跳转地址 ), .sel(PredictJump));
  EX_MEM EX_MEM (
    .CLK(CLK), .\同步清零 (RST), .\使能_为1时时钟有效 (not_17_out), .W_num(W__EX), .R_rs2(\R_rs2__EX重定向后 ),
    .ALURESULT(alu_1_result), .MEMTOREG(MemToReg_EX), .MEMWRITE(MemWrite_EX), .REGWRITE(RegWrite_EX),
    .ECALL(Ecall_EX), .W_num_2(W__MEM), .R_rs2_2(MDin), .ALURESULT_2(EX_MEM_aluresult_2),
    .MEMTOREG_2(MemToReg_MEM), .MEMWRITE_2(MemWrite), .REGWRITE_2(RegWrite_MEM), .ECALL_2(Ecall_MEM),
    .PC(EX_PC), .PC_2(M_PC), .\指令字 (EX_IR), .\指令字_2 (MEM_IR), .R_rs1(\R_rs1__EX重定向后 ), .R_rs1_2(R_rs1__MEM),
    .PC_4(PC_4_EX), .PC_4_2(PC_4_MEM), .JAL(JAL_EX), .JAL_2(JAL_MEM), .JALR(JALR_EX), .JALR_2(JALR_MEM));  // open: URET, URET_2
  RAM #(.addrWidth(10), .dataWidth(32), .bus("separate"), .Select("high")) ram_1 (
    .addr(EX_MEM_aluresult_2[11:2]), .din(MDin), .data(ram_1_data), .str(MemWrite), .clk(CLK),
    .ld(MemToReg_MEM), .clr(RST));  // open: sel
  not not_18 (not_18_out, halt);
  MEM_WB MEM_WB (
    .CLK(CLK), .\同步清零 (RST), .\使能_为1时时钟有效 (not_18_out), .W_num(W__MEM), .RD(ram_1_data),
    .ALURESULT(EX_MEM_aluresult_2), .MEMTOREG(MemToReg_MEM), .REGWRITE(RegWrite_MEM), .ECALL(Ecall_MEM),
    .W_num_2(W__WB), .RD_2(MEM_WB_rd_2), .ALURESULT_2(MEM_WB_aluresult_2), .MEMTOREG_2(MemToReg_WB),
    .REGWRITE_2(RegWrite), .ECALL_2(Ecall_WB), .PC(M_PC), .PC_2(WB_PC), .\指令字 (MEM_IR), .\指令字_2 (WB_IR),
    .R_rs1(R_rs1__MEM), .R_rs1_2(R_rs1__WB), .R_rs2(MDin), .R_rs2_2(R_rs2__WB), .PC_4(PC_4_MEM),
    .PC_4_2(PC_4_WB), .JAL(JAL_MEM), .JAL_2(JAL_WB), .JALR(JALR_MEM), .JALR_2(JALR_WB));  // open: URET, URET_2
  Multiplexer #(.select(1), .width(32), .disabled("Z"), .enable("false")) multiplexer_15 (
    .in0(MEM_WB_aluresult_2), .in1(MEM_WB_rd_2), .out(multiplexer_15_out), .sel(MemToReg_WB));
  or or_8 (or_8_out, JAL_WB, JALR_WB);
  Multiplexer #(.select(1), .width(32), .disabled("Z"), .enable("false")) multiplexer_16 (
    .in0(multiplexer_15_out), .in1(PC_4_WB), .out(RDin), .sel(or_8_out));

  // Other names for the same wires on the sheet: W__ID[4:0] = ID_IR[11:7]; MEM_PC[31:0] = M_PC;
  //   R_rs2__MEM[31:0] = MDin; RegWrite_WB = RegWrite

  // Notes on the sheet:
  //   中断源
  //   时空图监测，可删除
  //   中断等待指示
  //   数码管输出
  //   指令存储器
  //   contents of rom_1 (hex, n*v repeats v):
  //   100493 100006f 100493 200913 300993 100006f 100493 200913 300993 100006f 100493 200913 300993
  //   100006f 100493 200913 300993 29c000ef 100413 100493 1f49493 900533 2200893 73 24d493 48463 fedff06f
  //   900533 2200893 73 100493 249493 900533 2200893 73 48463 fedff06f 100493 1f49493 900533 2200893 73
  //   4034d493 900533 2200893 73 4044d493 900533 2200893 73 4044d493 900533 2200893 73 4044d493 900533
  //   2200893 73 4044d493 900533 2200893 73 4044d493 900533 2200893 73 4044d493 900533 2200893 73 4044d493
  //   900533 2200893 73 100413 1f41993 41f9d993 433 c00913 300b13 140413 f47413 800293 100313 499993
  //   89e9b3 1300533 2200893 73 406282b3 fe0294e3 140413 f00f93 1f47433 1c41413 800293 100313 49d993
  //   89e9b3 1300533 2200893 73 406282b3 fe0294e3 1c45413 406b0b33 b0463 f95ff06f 2b3 fff2c293 829293
  //   ff2e293 500533 2200893 73 fff00413 493 84a023 140413 448493 84a023 140413 448493 84a023 140413
  //   448493 84a023 140413 448493 84a023 140413 448493 84a023 140413 448493 84a023 140413 448493 84a023
  //   140413 448493 84a023 140413 448493 84a023 140413 448493 84a023 140413 448493 84a023 140413 448493
  //   84a023 140413 448493 84a023 140413 448493 84a023 140413 448493 84a023 140413 448493 140413 433
  //   3c00493 42983 4aa03 149a2b3 28663 134a023 1442023 ffc48493 fe9412e3 800533 2200893 73 440413 3c00493
  //   fc9416e3 a00893 73 413 140413 800533 2200893 73 240413 800533 2200893 73 340413 800533 2200893 73
  //   440413 800533 2200893 73 540413 800533 2200893 73 640413 800533 2200893 73 740413 800533 2200893 73
  //   840413 800533 2200893 2200893 73 8067
  //   指令探针
  //   指令字
  //   JALR
  //   URET
  //   控制位
  //   Beq
  //   Bne
  //   AluOP
  //   流水调试日志用
  //   暂停节拍，不能为0
  //   MemWrite(数据存储器的写使能控制信号)
  //   AluSrcB(运算器B输入选择 )
  //   RegWrite(寄存器堆的写使能控制信号）
  //   戳工具置1进入计数暂停模式，ctrl+k时钟自动运行到对应节拍暂停
  //   ctrl+k关闭时钟连续运行，将控制位置零，进入单步调试模式调试
  //   MemToReg(为1时将数据存储器读出的数据写回寄存器堆，否则将运算结果写回寄存器堆)
  //   可计数暂停的时钟源
  //   为方便自动评测，需要输出流水线各段保存的PC值，注意是PC不是PC+4，另外ID段寄存器写入信息，Mem段内存写入信息也要输出
  //   数据存储器
endmodule

module BTB (
  input  [31:0] PC,
  input  [31:0] EX_PC,
  input  [31:0] EX_BranchAddr,
  input  CLK,
  input  EX_Branch,
  input  EX_BranchTaken,
  output [31:0] JumpAddr,
  output PredictJump
);

  wire and_1_out, and_2_out, and_3_out, and_4_out, and_21_out, and_22_out, and_23_out, and_24_out,
       and_25_out, and_26_out, and_27_out, and_28_out, and_29_out, and_30_out, and_31_out, and_32_out,
       comparator_1_eq, comparator_2_eq, comparator_3_eq, comparator_4_eq, comparator_5_eq, comparator_6_eq,
       comparator_7_eq, comparator_8_eq, comparator_9_eq, comparator_10_eq, comparator_11_eq,
       comparator_12_eq, comparator_13_eq, comparator_14_eq, comparator_15_eq, comparator_16_eq, d_ff_1_q,
       d_ff_2_q, d_ff_3_q, d_ff_4_q, d_ff_5_q, d_ff_6_q, d_ff_7_q, d_ff_8_q, decoder_1_out0, decoder_1_out1,
       decoder_1_out2, decoder_1_out3, decoder_1_out4, decoder_1_out5, decoder_1_out6, decoder_1_out7,
       decoder_2_out0, decoder_2_out1, decoder_2_out2, decoder_2_out3, decoder_2_out4, decoder_2_out5,
       decoder_2_out6, decoder_2_out7, not_1_out, not_2_out, not_3_out, not_4_out, not_5_out, not_6_out,
       not_7_out, not_8_out, not_10_out, or_1_out, or_2_out, or_3_out, or_4_out, or_5_out, or_6_out,
       or_7_out, or_8_out, or_11_out, or_12_out, or_13_out, or_14_out, or_15_out, or_16_out, or_17_out,
       or_18_out, valid0, valid1, valid2, valid3, valid4, valid5, valid6, valid7, write0, write1, write2,
       write3, write4, write5, write6, write7, \写命中0 , \写命中1 , \写命中2 , \写命中3 , \写命中4 , \写命中5 , \写命中6 ,
       \写命中7 , \写操作命中 , \写操作没命中 , \命中0 , \命中1 , \命中2 , \命中3 , \命中4 , \命中5 , \命中6 , \命中7 , \有还未占用的槽 ;
  wire [1:0] \分支预测历史位0 , \分支预测历史位1 , \分支预测历史位2 , \分支预测历史位3 , \分支预测历史位4 , \分支预测历史位5 , \分支预测历史位6 , \分支预测历史位7 ,
       \分支预测历史位状态机_1_低位2 , \分支预测历史位状态机_2_低位2 , \分支预测历史位状态机_3_低位2 , \分支预测历史位状态机_4_低位2 , \分支预测历史位状态机_5_低位2 ,
       \分支预测历史位状态机_6_低位2 , \分支预测历史位状态机_7_低位2 , \分支预测历史位状态机_8_低位2 ;
  wire [2:0] \max_1_较大的的值对应的编号 , \max_2_较大的的值对应的编号 , \max_3_较大的的值对应的编号 , \max_4_较大的的值对应的编号 ,
       \max_5_较大的的值对应的编号 , \max_6_较大的的值对应的编号 , \编号最大的还未占用的槽 , \被淘汰置换的槽的编号 ;
  wire [15:0] count0, count1, count2, count3, count4, count5, count6, count7, \max_1_较大的的值 , \max_2_较大的的值 ,
       \max_3_较大的的值 , \max_4_较大的的值 , \max_5_较大的的值 , \max_6_较大的的值 ;
  wire [31:0] register_17_q, register_18_q, register_19_q, register_20_q, register_21_q, register_22_q,
       register_23_q, register_24_q, tag0, tag1, tag2, tag3, tag4, tag5, tag6, tag7;

  LED #(.active("true")) led_1 (.in(valid0));
  Register #(.width(1), .trigger("rising"), .Select("low")) register_1 (
    .D(1'b1), .en(write0), .Q(valid0), .clk(CLK));  // open: clr
  LED #(.active("true")) led_2 (.in(valid1));
  Register #(.width(1), .trigger("rising"), .Select("low")) register_2 (
    .D(1'b1), .en(write1), .Q(valid1), .clk(CLK));  // open: clr
  LED #(.active("true")) led_3 (.in(valid2));
  Register #(.width(1), .trigger("rising"), .Select("low")) register_3 (
    .D(1'b1), .en(write2), .Q(valid2), .clk(CLK));  // open: clr
  LED #(.active("true")) led_4 (.in(valid3));
  Register #(.width(1), .trigger("rising"), .Select("low")) register_4 (
    .D(1'b1), .en(write3), .Q(valid3), .clk(CLK));  // open: clr
  LED #(.active("true")) led_5 (.in(valid4));
  Register #(.width(1), .trigger("rising"), .Select("low")) register_5 (
    .D(1'b1), .en(write4), .Q(valid4), .clk(CLK));  // open: clr
  LED #(.active("true")) led_6 (.in(valid5));
  Register #(.width(1), .trigger("rising"), .Select("low")) register_6 (
    .D(1'b1), .en(write5), .Q(valid5), .clk(CLK));  // open: clr
  LED #(.active("true")) led_7 (.in(valid6));
  Register #(.width(1), .trigger("rising"), .Select("low")) register_7 (
    .D(1'b1), .en(write6), .Q(valid6), .clk(CLK));  // open: clr
  LED #(.active("true")) led_8 (.in(valid7));
  Register #(.width(1), .trigger("rising"), .Select("low")) register_8 (
    .D(1'b1), .en(write7), .Q(valid7), .clk(CLK));  // open: clr
  Register #(.width(32), .trigger("rising"), .Select("low")) register_9 (
    .D(EX_PC), .en(write0), .Q(tag0), .clk(CLK));  // open: clr
  Register #(.width(32), .trigger("rising"), .Select("low")) register_10 (
    .D(EX_PC), .en(write1), .Q(tag1), .clk(CLK));  // open: clr
  Register #(.width(32), .trigger("rising"), .Select("low")) register_11 (
    .D(EX_PC), .en(write2), .Q(tag2), .clk(CLK));  // open: clr
  Register #(.width(32), .trigger("rising"), .Select("low")) register_12 (
    .D(EX_PC), .en(write3), .Q(tag3), .clk(CLK));  // open: clr
  Register #(.width(32), .trigger("rising"), .Select("low")) register_13 (
    .D(EX_PC), .en(write4), .Q(tag4), .clk(CLK));  // open: clr
  Register #(.width(32), .trigger("rising"), .Select("low")) register_14 (
    .D(EX_PC), .en(write5), .Q(tag5), .clk(CLK));  // open: clr
  Register #(.width(32), .trigger("rising"), .Select("low")) register_15 (
    .D(EX_PC), .en(write6), .Q(tag6), .clk(CLK));  // open: clr
  Register #(.width(32), .trigger("rising"), .Select("low")) register_16 (
    .D(EX_PC), .en(write7), .Q(tag7), .clk(CLK));  // open: clr
  Register #(.width(32), .trigger("rising"), .Select("low")) register_17 (
    .D(EX_BranchAddr), .en(write0), .Q(register_17_q), .clk(CLK));  // open: clr
  Register #(.width(32), .trigger("rising"), .Select("low")) register_18 (
    .D(EX_BranchAddr), .en(write1), .Q(register_18_q), .clk(CLK));  // open: clr
  Register #(.width(32), .trigger("rising"), .Select("low")) register_19 (
    .D(EX_BranchAddr), .en(write2), .Q(register_19_q), .clk(CLK));  // open: clr
  Register #(.width(32), .trigger("rising"), .Select("low")) register_20 (
    .D(EX_BranchAddr), .en(write3), .Q(register_20_q), .clk(CLK));  // open: clr
  Register #(.width(32), .trigger("rising"), .Select("low")) register_21 (
    .D(EX_BranchAddr), .en(write4), .Q(register_21_q), .clk(CLK));  // open: clr
  Register #(.width(32), .trigger("rising"), .Select("low")) register_22 (
    .D(EX_BranchAddr), .en(write5), .Q(register_22_q), .clk(CLK));  // open: clr
  Register #(.width(32), .trigger("rising"), .Select("low")) register_23 (
    .D(EX_BranchAddr), .en(write6), .Q(register_23_q), .clk(CLK));  // open: clr
  Register #(.width(32), .trigger("rising"), .Select("low")) register_24 (
    .D(EX_BranchAddr), .en(write7), .Q(register_24_q), .clk(CLK));  // open: clr
  assign JumpAddr = \命中0  ? register_17_q : 32'bz;  // Controlled_Buffer controlled_buffer_1
  assign JumpAddr = \命中1  ? register_18_q : 32'bz;  // Controlled_Buffer controlled_buffer_2
  assign JumpAddr = \命中2  ? register_19_q : 32'bz;  // Controlled_Buffer controlled_buffer_3
  assign JumpAddr = \命中3  ? register_20_q : 32'bz;  // Controlled_Buffer controlled_buffer_4
  assign JumpAddr = \命中4  ? register_21_q : 32'bz;  // Controlled_Buffer controlled_buffer_5
  assign JumpAddr = \命中5  ? register_22_q : 32'bz;  // Controlled_Buffer controlled_buffer_6
  assign JumpAddr = \命中6  ? register_23_q : 32'bz;  // Controlled_Buffer controlled_buffer_7
  assign JumpAddr = \命中7  ? register_24_q : 32'bz;  // Controlled_Buffer controlled_buffer_8
  or or_1 (or_1_out, \命中0 , write0);
  or or_2 (or_2_out, \命中1 , write1);
  or or_3 (or_3_out, \命中2 , write2);
  or or_4 (or_4_out, \命中3 , write3);
  or or_5 (or_5_out, \命中4 , write4);
  or or_6 (or_6_out, \命中5 , write5);
  or or_7 (or_7_out, \命中6 , write6);
  or or_8 (or_8_out, \命中7 , write7);
  Counter #(.width(16), .max('hffff), .ongoal("wrap"), .trigger("rising"), .behavior("new")) counter_1 (
    .Q(count0), .clk(CLK), .clr(d_ff_1_q));  // open: load, D, count, carry, preset, down
  D_Flip_Flop #(.trigger("rising"), .Pre_Clr_Positions("ABOVE_BELOW"), .NegatePresetClear("false"), .enable("false"), .NewFFLayout("true")) d_ff_1 (
    .clk(CLK), .D(or_1_out), .Q(d_ff_1_q));  // open: Qn, preset, reset
  Counter #(.width(16), .max('hffff), .ongoal("wrap"), .trigger("rising"), .behavior("new")) counter_2 (
    .Q(count1), .clk(CLK), .clr(d_ff_2_q));  // open: load, D, count, carry, preset, down
  D_Flip_Flop #(.trigger("rising"), .Pre_Clr_Positions("ABOVE_BELOW"), .NegatePresetClear("false"), .enable("false"), .NewFFLayout("true")) d_ff_2 (
    .clk(CLK), .D(or_2_out), .Q(d_ff_2_q));  // open: Qn, preset, reset
  Counter #(.width(16), .max('hffff), .ongoal("wrap"), .trigger("rising"), .behavior("new")) counter_3 (
    .Q(count2), .clk(CLK), .clr(d_ff_3_q));  // open: load, D, count, carry, preset, down
  D_Flip_Flop #(.trigger("rising"), .Pre_Clr_Positions("ABOVE_BELOW"), .NegatePresetClear("false"), .enable("false"), .NewFFLayout("true")) d_ff_3 (
    .clk(CLK), .D(or_3_out), .Q(d_ff_3_q));  // open: Qn, preset, reset
  Counter #(.width(16), .max('hffff), .ongoal("wrap"), .trigger("rising"), .behavior("new")) counter_4 (
    .Q(count3), .clk(CLK), .clr(d_ff_4_q));  // open: load, D, count, carry, preset, down
  D_Flip_Flop #(.trigger("rising"), .Pre_Clr_Positions("ABOVE_BELOW"), .NegatePresetClear("false"), .enable("false"), .NewFFLayout("true")) d_ff_4 (
    .clk(CLK), .D(or_4_out), .Q(d_ff_4_q));  // open: Qn, preset, reset
  Counter #(.width(16), .max('hffff), .ongoal("wrap"), .trigger("rising"), .behavior("new")) counter_5 (
    .Q(count4), .clk(CLK), .clr(d_ff_5_q));  // open: load, D, count, carry, preset, down
  D_Flip_Flop #(.trigger("rising"), .Pre_Clr_Positions("ABOVE_BELOW"), .NegatePresetClear("false"), .enable("false"), .NewFFLayout("true")) d_ff_5 (
    .clk(CLK), .D(or_5_out), .Q(d_ff_5_q));  // open: Qn, preset, reset
  Counter #(.width(16), .max('hffff), .ongoal("wrap"), .trigger("rising"), .behavior("new")) counter_6 (
    .Q(count5), .clk(CLK), .clr(d_ff_6_q));  // open: load, D, count, carry, preset, down
  D_Flip_Flop #(.trigger("rising"), .Pre_Clr_Positions("ABOVE_BELOW"), .NegatePresetClear("false"), .enable("false"), .NewFFLayout("true")) d_ff_6 (
    .clk(CLK), .D(or_6_out), .Q(d_ff_6_q));  // open: Qn, preset, reset
  Counter #(.width(16), .max('hffff), .ongoal("wrap"), .trigger("rising"), .behavior("new")) counter_7 (
    .Q(count6), .clk(CLK), .clr(d_ff_7_q));  // open: load, D, count, carry, preset, down
  D_Flip_Flop #(.trigger("rising"), .Pre_Clr_Positions("ABOVE_BELOW"), .NegatePresetClear("false"), .enable("false"), .NewFFLayout("true")) d_ff_7 (
    .clk(CLK), .D(or_7_out), .Q(d_ff_7_q));  // open: Qn, preset, reset
  Counter #(.width(16), .max('hffff), .ongoal("wrap"), .trigger("rising"), .behavior("new")) counter_8 (
    .Q(count7), .clk(CLK), .clr(d_ff_8_q));  // open: load, D, count, carry, preset, down
  D_Flip_Flop #(.trigger("rising"), .Pre_Clr_Positions("ABOVE_BELOW"), .NegatePresetClear("false"), .enable("false"), .NewFFLayout("true")) d_ff_8 (
    .clk(CLK), .D(or_8_out), .Q(d_ff_8_q));  // open: Qn, preset, reset
  \分支预测历史位状态机  \u_分支预测历史位状态机_1  (
    .\高位 (\分支预测历史位0 [1]), .\低位 (\分支预测历史位0 [0]), .JUMP(EX_BranchTaken), .\高位2 (\分支预测历史位状态机_1_低位2 [1]),
    .\低位2 (\分支预测历史位状态机_1_低位2 [0]));
  \分支预测历史位状态机  \u_分支预测历史位状态机_2  (
    .\高位 (\分支预测历史位1 [1]), .\低位 (\分支预测历史位1 [0]), .JUMP(EX_BranchTaken), .\高位2 (\分支预测历史位状态机_2_低位2 [1]),
    .\低位2 (\分支预测历史位状态机_2_低位2 [0]));
  \分支预测历史位状态机  \u_分支预测历史位状态机_3  (
    .\高位 (\分支预测历史位2 [1]), .\低位 (\分支预测历史位2 [0]), .JUMP(EX_BranchTaken), .\高位2 (\分支预测历史位状态机_3_低位2 [1]),
    .\低位2 (\分支预测历史位状态机_3_低位2 [0]));
  \分支预测历史位状态机  \u_分支预测历史位状态机_4  (
    .\高位 (\分支预测历史位3 [1]), .\低位 (\分支预测历史位3 [0]), .JUMP(EX_BranchTaken), .\高位2 (\分支预测历史位状态机_4_低位2 [1]),
    .\低位2 (\分支预测历史位状态机_4_低位2 [0]));
  Comparator #(.width(32), .mode("twosComplement")) comparator_1 (
    .a(tag0), .b(PC), .eq(comparator_1_eq));  // open: gt, lt
  Comparator #(.width(32), .mode("twosComplement")) comparator_2 (
    .a(tag1), .b(PC), .eq(comparator_2_eq));  // open: gt, lt
  Comparator #(.width(32), .mode("twosComplement")) comparator_3 (
    .a(tag2), .b(PC), .eq(comparator_3_eq));  // open: gt, lt
  Comparator #(.width(32), .mode("twosComplement")) comparator_4 (
    .a(tag3), .b(PC), .eq(comparator_4_eq));  // open: gt, lt
  Comparator #(.width(32), .mode("twosComplement")) comparator_5 (
    .a(tag4), .b(PC), .eq(comparator_5_eq));  // open: gt, lt
  Comparator #(.width(32), .mode("twosComplement")) comparator_6 (
    .a(tag5), .b(PC), .eq(comparator_6_eq));  // open: gt, lt
  Comparator #(.width(32), .mode("twosComplement")) comparator_7 (
    .a(tag6), .b(PC), .eq(comparator_7_eq));  // open: gt, lt
  Comparator #(.width(32), .mode("twosComplement")) comparator_8 (
    .a(tag7), .b(PC), .eq(comparator_8_eq));  // open: gt, lt
  and and_1 (and_1_out, \写命中0 , EX_Branch);
  and and_2 (and_2_out, \写命中1 , EX_Branch);
  and and_3 (and_3_out, \写命中2 , EX_Branch);
  and and_4 (and_4_out, \写命中3 , EX_Branch);
  and and_5 (\命中0 , valid0, comparator_1_eq);
  and and_6 (\命中1 , valid1, comparator_2_eq);
  and and_7 (\命中2 , valid2, comparator_3_eq);
  and and_8 (\命中3 , valid3, comparator_4_eq);
  and and_9 (\命中4 , valid4, comparator_5_eq);
  and and_10 (\命中5 , valid5, comparator_6_eq);
  and and_11 (\命中6 , valid6, comparator_7_eq);
  and and_12 (\命中7 , valid7, comparator_8_eq);
  Register #(.width(2), .trigger("rising"), .Select("low")) register_25 (
    .D(\分支预测历史位状态机_1_低位2 ), .en(and_1_out), .Q(\分支预测历史位0 ), .clk(CLK));  // open: clr
  Register #(.width(2), .trigger("rising"), .Select("low")) register_26 (
    .D(\分支预测历史位状态机_2_低位2 ), .en(and_2_out), .Q(\分支预测历史位1 ), .clk(CLK));  // open: clr
  Register #(.width(2), .trigger("rising"), .Select("low")) register_27 (
    .D(\分支预测历史位状态机_3_低位2 ), .en(and_3_out), .Q(\分支预测历史位2 ), .clk(CLK));  // open: clr
  Register #(.width(2), .trigger("rising"), .Select("low")) register_28 (
    .D(\分支预测历史位状态机_4_低位2 ), .en(and_4_out), .Q(\分支预测历史位3 ), .clk(CLK));  // open: clr
  Comparator #(.width(32), .mode("twosComplement")) comparator_9 (
    .a(tag0), .b(EX_PC), .eq(comparator_9_eq));  // open: gt, lt
  Comparator #(.width(32), .mode("twosComplement")) comparator_10 (
    .a(tag1), .b(EX_PC), .eq(comparator_10_eq));  // open: gt, lt
  Comparator #(.width(32), .mode("twosComplement")) comparator_11 (
    .a(tag2), .b(EX_PC), .eq(comparator_11_eq));  // open: gt, lt
  Comparator #(.width(32), .mode("twosComplement")) comparator_12 (
    .a(tag3), .b(EX_PC), .eq(comparator_12_eq));  // open: gt, lt
  Comparator #(.width(32), .mode("twosComplement")) comparator_13 (
    .a(tag4), .b(EX_PC), .eq(comparator_13_eq));  // open: gt, lt
  Comparator #(.width(32), .mode("twosComplement")) comparator_14 (
    .a(tag5), .b(EX_PC), .eq(comparator_14_eq));  // open: gt, lt
  Comparator #(.width(32), .mode("twosComplement")) comparator_15 (
    .a(tag6), .b(EX_PC), .eq(comparator_15_eq));  // open: gt, lt
  Comparator #(.width(32), .mode("twosComplement")) comparator_16 (
    .a(tag7), .b(EX_PC), .eq(comparator_16_eq));  // open: gt, lt
  and and_13 (\写命中0 , valid0, comparator_9_eq);
  and and_14 (\写命中1 , valid1, comparator_10_eq);
  and and_15 (\写命中2 , valid2, comparator_11_eq);
  and and_16 (\写命中3 , valid3, comparator_12_eq);
  and and_17 (\写命中4 , valid4, comparator_13_eq);
  and and_18 (\写命中5 , valid5, comparator_14_eq);
  and and_19 (\写命中6 , valid6, comparator_15_eq);
  and and_20 (\写命中7 , valid7, comparator_16_eq);
  \分支预测历史位状态机  \u_分支预测历史位状态机_5  (
    .\高位 (\分支预测历史位4 [1]), .\低位 (\分支预测历史位4 [0]), .JUMP(EX_BranchTaken), .\高位2 (\分支预测历史位状态机_5_低位2 [1]),
    .\低位2 (\分支预测历史位状态机_5_低位2 [0]));
  \分支预测历史位状态机  \u_分支预测历史位状态机_6  (
    .\高位 (\分支预测历史位5 [1]), .\低位 (\分支预测历史位5 [0]), .JUMP(EX_BranchTaken), .\高位2 (\分支预测历史位状态机_6_低位2 [1]),
    .\低位2 (\分支预测历史位状态机_6_低位2 [0]));
  \分支预测历史位状态机  \u_分支预测历史位状态机_7  (
    .\高位 (\分支预测历史位6 [1]), .\低位 (\分支预测历史位6 [0]), .JUMP(EX_BranchTaken), .\高位2 (\分支预测历史位状态机_7_低位2 [1]),
    .\低位2 (\分支预测历史位状态机_7_低位2 [0]));
  \分支预测历史位状态机  \u_分支预测历史位状态机_8  (
    .\高位 (\分支预测历史位7 [1]), .\低位 (\分支预测历史位7 [0]), .JUMP(EX_BranchTaken), .\高位2 (\分支预测历史位状态机_8_低位2 [1]),
    .\低位2 (\分支预测历史位状态机_8_低位2 [0]));
  MAX max_1 (
    .\X的值 (count0), .\Y的值 (count1), .\X的编号 (3'b000), .\Y的编号 (3'b001), .\较大的的值 (\max_1_较大的的值 ),
    .\较大的的值对应的编号 (\max_1_较大的的值对应的编号 ));
  MAX max_2 (
    .\X的值 (count2), .\Y的值 (count3), .\X的编号 (3'b010), .\Y的编号 (3'b011), .\较大的的值 (\max_2_较大的的值 ),
    .\较大的的值对应的编号 (\max_2_较大的的值对应的编号 ));
  MAX max_3 (
    .\X的值 (count4), .\Y的值 (count5), .\X的编号 (3'b100), .\Y的编号 (3'b101), .\较大的的值 (\max_3_较大的的值 ),
    .\较大的的值对应的编号 (\max_3_较大的的值对应的编号 ));
  MAX max_4 (
    .\X的值 (count6), .\Y的值 (count7), .\X的编号 (3'b110), .\Y的编号 (3'b111), .\较大的的值 (\max_4_较大的的值 ),
    .\较大的的值对应的编号 (\max_4_较大的的值对应的编号 ));
  and and_21 (and_21_out, \写命中4 , EX_Branch);
  Register #(.width(2), .trigger("rising"), .Select("low")) register_29 (
    .D(\分支预测历史位状态机_5_低位2 ), .en(and_21_out), .Q(\分支预测历史位4 ), .clk(CLK));  // open: clr
  and and_22 (and_22_out, \写命中5 , EX_Branch);
  Register #(.width(2), .trigger("rising"), .Select("low")) register_30 (
    .D(\分支预测历史位状态机_6_低位2 ), .en(and_22_out), .Q(\分支预测历史位5 ), .clk(CLK));  // open: clr
  and and_23 (and_23_out, \写命中6 , EX_Branch);
  Register #(.width(2), .trigger("rising"), .Select("low")) register_31 (
    .D(\分支预测历史位状态机_7_低位2 ), .en(and_23_out), .Q(\分支预测历史位6 ), .clk(CLK));  // open: clr
  and and_24 (and_24_out, \写命中7 , EX_Branch);
  Register #(.width(2), .trigger("rising"), .Select("low")) register_32 (
    .D(\分支预测历史位状态机_8_低位2 ), .en(and_24_out), .Q(\分支预测历史位7 ), .clk(CLK));  // open: clr
  not not_1 (not_1_out, valid0);
  not not_2 (not_2_out, valid1);
  not not_3 (not_3_out, valid2);
  not not_4 (not_4_out, valid3);
  not not_5 (not_5_out, valid4);
  not not_6 (not_6_out, valid5);
  not not_7 (not_7_out, valid6);
  not not_8 (not_8_out, valid7);
  MAX max_5 (
    .\X的值 (\max_1_较大的的值 ), .\Y的值 (\max_2_较大的的值 ), .\X的编号 (\max_1_较大的的值对应的编号 ), .\Y的编号 (\max_2_较大的的值对应的编号 ),
    .\较大的的值 (\max_5_较大的的值 ), .\较大的的值对应的编号 (\max_5_较大的的值对应的编号 ));
  MAX max_6 (
    .\X的值 (\max_3_较大的的值 ), .\Y的值 (\max_4_较大的的值 ), .\X的编号 (\max_3_较大的的值对应的编号 ), .\Y的编号 (\max_4_较大的的值对应的编号 ),
    .\较大的的值 (\max_6_较大的的值 ), .\较大的的值对应的编号 (\max_6_较大的的值对应的编号 ));
  or or_9 (\写操作命中 , \写命中0 , \写命中1 , \写命中2 , \写命中3 , \写命中4 , \写命中5 , \写命中6 , \写命中7 );
  MAX max_7 (
    .\X的值 (\max_5_较大的的值 ), .\Y的值 (\max_6_较大的的值 ), .\X的编号 (\max_5_较大的的值对应的编号 ), .\Y的编号 (\max_6_较大的的值对应的编号 ),
    .\较大的的值对应的编号 (\被淘汰置换的槽的编号 ));  // open: 较大的的值
  not not_9 (\写操作没命中 , \写操作命中 );
  Priority_Encoder #(.select(3), .disabled("Z")) priority_encoder_1 (
    .in0(not_1_out), .in1(not_2_out), .in2(not_3_out), .in3(not_4_out), .in4(not_5_out), .in5(not_6_out),
    .in6(not_7_out), .in7(not_8_out), .out(\编号最大的还未占用的槽 ), .gs(\有还未占用的槽 ));  // open: en_out, en_in
  Decoder #(.select(3), .tristate("false"), .disabled(0), .enable("true")) decoder_1 (
    .out0(decoder_1_out0), .out1(decoder_1_out1), .out2(decoder_1_out2), .out3(decoder_1_out3),
    .out4(decoder_1_out4), .out5(decoder_1_out5), .out6(decoder_1_out6), .out7(decoder_1_out7),
    .sel(\编号最大的还未占用的槽 ), .en(\有还未占用的槽 ));
  Decoder #(.select(3), .tristate("false"), .disabled(0), .enable("true")) decoder_2 (
    .out0(decoder_2_out0), .out1(decoder_2_out1), .out2(decoder_2_out2), .out3(decoder_2_out3),
    .out4(decoder_2_out4), .out5(decoder_2_out5), .out6(decoder_2_out6), .out7(decoder_2_out7),
    .sel(\被淘汰置换的槽的编号 ), .en(not_10_out));
  not not_10 (not_10_out, \有还未占用的槽 );
  and and_25 (and_25_out, \分支预测历史位0 [1], \命中0 );
  and and_26 (and_26_out, \分支预测历史位1 [1], \命中1 );
  and and_27 (and_27_out, \分支预测历史位2 [1], \命中2 );
  and and_28 (and_28_out, \分支预测历史位3 [1], \命中3 );
  and and_29 (and_29_out, \分支预测历史位4 [1], \命中4 );
  and and_30 (and_30_out, \分支预测历史位5 [1], \命中5 );
  and and_31 (and_31_out, \分支预测历史位6 [1], \命中6 );
  and and_32 (and_32_out, \分支预测历史位7 [1], \命中7 );
  or or_10 (PredictJump, and_25_out, and_26_out, and_27_out, and_28_out, and_29_out, and_30_out, and_31_out, and_32_out);
  or or_11 (or_11_out, decoder_1_out0, decoder_2_out0);
  or or_12 (or_12_out, decoder_1_out1, decoder_2_out1);
  or or_13 (or_13_out, decoder_1_out2, decoder_2_out2);
  or or_14 (or_14_out, decoder_1_out3, decoder_2_out3);
  or or_15 (or_15_out, decoder_1_out4, decoder_2_out4);
  or or_16 (or_16_out, decoder_1_out5, decoder_2_out5);
  or or_17 (or_17_out, decoder_1_out6, decoder_2_out6);
  or or_18 (or_18_out, decoder_1_out7, decoder_2_out7);
  and and_33 (write0, \写操作没命中 , EX_Branch, or_11_out);
  and and_34 (write1, \写操作没命中 , EX_Branch, or_12_out);
  and and_35 (write2, \写操作没命中 , EX_Branch, or_13_out);
  and and_36 (write3, \写操作没命中 , EX_Branch, or_14_out);
  and and_37 (write4, \写操作没命中 , EX_Branch, or_15_out);
  and and_38 (write5, \写操作没命中 , EX_Branch, or_16_out);
  and and_39 (write6, \写操作没命中 , EX_Branch, or_17_out);
  and and_40 (write7, \写操作没命中 , EX_Branch, or_18_out);

  // Notes on the sheet:
  //   输入引脚
  //   输出引脚
  //   count0是0号槽未被访问的次数，正比于冷置的时间长度
  //   这里的写操作没命中是指不能直接用EX的分支地址替换原分支地址
endmodule

module MAX (
  input  [15:0] \X的值 ,
  input  [15:0] \Y的值 ,
  input  [2:0] \X的编号 ,
  input  [2:0] \Y的编号 ,
  output [15:0] \较大的的值 ,
  output [2:0] \较大的的值对应的编号 
);

  wire comparator_1_eq, comparator_1_gt, or_1_out;

  Comparator #(.width(16), .mode("unsigned")) comparator_1 (
    .a(\X的值 ), .b(\Y的值 ), .gt(comparator_1_gt), .eq(comparator_1_eq));  // open: lt
  Multiplexer #(.select(1), .width(16), .disabled("Z"), .enable("false")) multiplexer_1 (
    .in0(\Y的值 ), .in1(\X的值 ), .out(\较大的的值 ), .sel(or_1_out));
  or or_1 (or_1_out, comparator_1_gt, comparator_1_eq);
  Multiplexer #(.select(1), .width(3), .disabled("Z"), .enable("false")) multiplexer_2 (
    .in0(\Y的编号 ), .in1(\X的编号 ), .out(\较大的的值对应的编号 ), .sel(or_1_out));
endmodule

module \分支预测历史位状态机  (
  input  \高位 ,
  input  \低位 ,
  input  JUMP,
  output \高位2 ,
  output \低位2 
);

  wire and_1_out, and_2_out, and_3_out, and_4_out, not_1_out, not_2_out, not_3_out, not_4_out, not_5_out;

  not not_1 (not_1_out, \低位 );
  not not_2 (not_2_out, \高位 );
  not not_3 (not_3_out, \低位 );
  not not_4 (not_4_out, \低位 );
  not not_5 (not_5_out, JUMP);
  and and_1 (and_1_out, \低位 , JUMP);
  and and_2 (and_2_out, \高位 , not_1_out);
  and and_3 (and_3_out, not_2_out, not_3_out, JUMP);
  and and_4 (and_4_out, \高位 , not_4_out, not_5_out);
  or or_1 (\高位2 , and_1_out, and_2_out);
  or or_2 (\低位2 , and_3_out, and_4_out);
endmodule
