// Logisim project cpu21-riscv-ans.circ as structural Verilog: 24 circuits, main circuit ◇单周期RISC-V
module \单周期RISC_V  (
  output RegWrite,
  output MemWrite,
  output [31:0] PC,
  output [31:0] IR,
  output [31:0] RDin,
  output [31:0] MDin,
  output [31:0] LedData
);

  wire and_1_out, and_2_out, and_3_out, and_4_out, AUIPC, Beq, BGEU, Bne, CLK, clock_1_out, comparator_1_eq,
       comparator_2_eq, comparator_2_lt, d_ff_1_q, ecall, equal, GE, Go, halt, IRA, IRB, IRC, jal, jalr,
       MemToReg, nand_1_out, not_1_out, not_2_out, or_1_out, or_2_out, riscv_probe_1_p3, RST, SB, W1, W2, W3,
       \单周期硬布线控制器_1_alu_src , \单周期硬布线控制器_1_s_type ;
  wire [1:0] priority_encoder_1_out, priority_encoder_2_out;
  wire [3:0] decoder_1_out0, multiplexer_7_out, \单周期硬布线控制器_1_alu_op ;
  wire [4:0] multiplexer_2_out, multiplexer_3_out;
  wire [12:0] CNT_num;
  wire [15:0] \总周期数 ;
  wire [31:0] adder_2_out, adder_3_out, bit_extender_1_out, bit_extender_2_out, bit_extender_3_out,
       bit_extender_4_out, bit_extender_5_out, mips_ram_1_p8, multiplexer_1_out, multiplexer_4_out,
       multiplexer_5_out, PC_4, PC_imm, regifile_1_r1, regifile_1_r2, result, shifter_1_out, shifter_2_out,
       shifter_3_out;

  Button \u_继续运行  (.out(Go));
  Button _1 (.out(IRA));
  Button _2 (.out(IRB));
  Button _3 (.out(IRC));
  LED #(.active("true")) led_1 (.in(W1));
  LED #(.active("true")) led_2 (.in(W2));
  LED #(.active("true")) led_3 (.in(W3));
  Priority_Encoder #(.select(2), .disabled("Z")) priority_encoder_1 (
    .in0(1'b1), .in1(jalr), .in2(jal), .in3(or_1_out), .out(priority_encoder_1_out));  // open: gs, en_out, en_in
  Multiplexer #(.select(2), .width(32), .disabled("Z"), .enable("false")) multiplexer_1 (
    .in0(PC_4), .in1(result), .in2(adder_3_out), .in3(adder_2_out), .out(multiplexer_1_out),
    .sel(priority_encoder_1_out));
  Hex_Digit_Display hex_digit_display_1 (.value(LedData[31:28]));  // open: dp
  or or_1 (or_1_out, and_2_out, and_3_out, and_1_out);
  and and_1 (and_1_out, ~equal, Bne);  // AND_Gate
  and and_2 (and_2_out, Beq, equal);
  Register #(.width(32), .trigger("rising"), .Select("low")) u_PC (
    .D(multiplexer_1_out), .en(not_1_out), .Q(PC), .clk(CLK), .clr(RST));
  not not_1 (not_1_out, halt);
  Hex_Digit_Display hex_digit_display_2 (.value(LedData[27:24]));  // open: dp
  Hex_Digit_Display hex_digit_display_3 (.value(LedData[23:20]));  // open: dp
  and and_3 (and_3_out, GE, BGEU);
  Hex_Digit_Display hex_digit_display_4 (.value(LedData[15:12]));  // open: dp
  Hex_Digit_Display hex_digit_display_5 (.value(LedData[19:16]));  // open: dp
  // RiscV_Probe riscv_probe_1: pin names not known; wires that end beside it: IR, IR, riscv_probe_1_p3
  Adder #(.width(32)) adder_1 (.a(PC), .b(32'h4), .out(PC_4));  // open: cin, cout
  Hex_Digit_Display hex_digit_display_6 (.value(LedData[7:4]));  // open: dp
  Hex_Digit_Display hex_digit_display_7 (.value(LedData[11:8]));  // open: dp
  // Probe on \总周期数 
  ROM #(.addrWidth(10), .dataWidth(32), .Select("high")) rom_1 (.addr(PC[11:2]), .data(IR));
  Hex_Digit_Display hex_digit_display_8 (.value(LedData[3:0]));  // open: dp
  \单周期硬布线控制器  \u_单周期硬布线控制器_1  (
    .Funct({IR[30], IR[25], IR[14:12]}), .OP(IR[6:2]), .ALU_OP(\单周期硬布线控制器_1_alu_op ), .MemToReg(MemToReg),
    .MemWrite(MemWrite), .ALU_SRC(\单周期硬布线控制器_1_alu_src ), .RegWrite(RegWrite), .ecall(ecall),
    .S_type(\单周期硬布线控制器_1_s_type ), .Jalr(jalr), .Beq(Beq), .JAL(jal), .Bne(Bne), .in_3(IR[21]),
    .uret(riscv_probe_1_p3), .AUIPC(AUIPC), .BGEU(BGEU), .SB(SB));  // open: Rs1used, Rs2used, CSRRSI, CSRRCI
  Multiplexer #(.select(1), .width(5), .disabled("Z"), .enable("false")) multiplexer_2 (
    .in0(IR[19:15]), .in1(5'b10001), .out(multiplexer_2_out), .sel(ecall));
  Multiplexer #(.select(1), .width(5), .disabled("Z"), .enable("false")) multiplexer_3 (
    .in0(IR[24:20]), .in1(5'b01010), .out(multiplexer_3_out), .sel(ecall));
  assign bit_extender_1_out = {{20{IR[31]}}, IR[31:20]};  // Bit_Extender bit_extender_1
  assign bit_extender_2_out = {{20{IR[31]}}, {IR[31:25], IR[11:7]}};  // Bit_Extender bit_extender_2
  Multiplexer #(.select(1), .width(32), .disabled("Z"), .enable("false")) multiplexer_4 (
    .in0(bit_extender_1_out), .in1(bit_extender_2_out), .out(multiplexer_4_out), .sel(\单周期硬布线控制器_1_s_type ));
  assign bit_extender_3_out = {{20{IR[31]}}, {IR[31], IR[7], IR[30:25], IR[11:8]}};  // Bit_Extender bit_extender_3
  Shifter #(.width(32), .shift("ll")) shifter_1 (.in(bit_extender_3_out), .\dist (5'b00001), .out(shifter_1_out));
  assign bit_extender_4_out = {{12{IR[31]}}, {IR[31], IR[19:12], IR[20], IR[30:21]}};  // Bit_Extender bit_extender_4
  Shifter #(.width(32), .shift("ll")) shifter_2 (.in(bit_extender_4_out), .\dist (5'b00001), .out(shifter_2_out));
  assign bit_extender_5_out = {{12{IR[31]}}, IR[31:12]};  // Bit_Extender bit_extender_5
  Shifter #(.width(32), .shift("ll")) shifter_3 (.in(bit_extender_5_out), .\dist (5'b01100), .out(shifter_3_out));
  Regifile regifile_1 (
    .Din(RDin), .Clk(CLK), .R1(regifile_1_r1), .R2(regifile_1_r2), .WE(RegWrite), .W_num(IR[11:7]),
    .R1_num(multiplexer_2_out), .R2_num(multiplexer_3_out));
  Adder #(.width(32)) adder_2 (.a(shifter_1_out), .b(PC), .out(adder_2_out));  // open: cin, cout
  Adder #(.width(32)) adder_3 (.a(shifter_2_out), .b(PC), .out(adder_3_out));  // open: cin, cout
  Adder #(.width(32)) adder_4 (.a(shifter_3_out), .b(PC), .out(PC_imm));  // open: cin, cout
  Multiplexer #(.select(1), .width(32), .disabled("Z"), .enable("false")) multiplexer_5 (
    .in0(regifile_1_r2), .in1(multiplexer_4_out), .out(multiplexer_5_out), .sel(\单周期硬布线控制器_1_alu_src ));
  Multiplexer #(.select(1), .width(32), .disabled("Z"), .enable("false")) multiplexer_6 (
    .in0(regifile_1_r2),
    .in1({regifile_1_r2[7:0], regifile_1_r2[7:0], regifile_1_r2[7:0], regifile_1_r2[7:0]}), .out(MDin),
    .sel(SB));
  ALU alu_1 (
    .X(regifile_1_r1), .Y(multiplexer_5_out), .AluOP(\单周期硬布线控制器_1_alu_op ), .Equal(equal), .Result(result),
    .out_4(GE));  // open: Result_2, out_6
  not not_2 (not_2_out, halt);
  Button button_1 (.out(RST));
  Decoder #(.select(2), .tristate("false"), .disabled("Z"), .enable("false")) decoder_1 (
    .out0(decoder_1_out0[0]), .out1(decoder_1_out0[1]), .out2(decoder_1_out0[2]), .out3(decoder_1_out0[3]),
    .sel(result[1:0]));
  and and_4 (and_4_out, comparator_1_eq, ecall);
  Comparator #(.width(32), .mode("twosComplement")) comparator_1 (
    .a(32'h22), .b(regifile_1_r1), .eq(comparator_1_eq));  // open: gt, lt
  Counter #(.width(16), .max('hffff), .ongoal("wrap"), .trigger("rising"), .behavior("new")) counter_1 (
    .count(not_2_out), .Q(\总周期数 ), .clk(CLK), .clr(RST));  // open: load, D, carry, preset, down
  Register #(.width(32), .trigger("rising"), .Select("low")) register_1 (
    .D(regifile_1_r2), .en(and_4_out), .Q(LedData), .clk(CLK), .clr(RST));
  and and_5 (halt, ~comparator_1_eq, ~Go, ecall);  // AND_Gate
  // MIPS_RAM mips_ram_1: pin names not known; wires that end beside it: result[21:2], MDin, MemWrite, CLK, LedData, 1'b1, RST, mips_ram_1_p8
  Multiplexer #(.select(1), .width(4), .disabled("Z"), .enable("false")) multiplexer_7 (
    .in0(4'b1111), .in1(decoder_1_out0), .out(multiplexer_7_out), .sel(SB));
  Priority_Encoder #(.select(2), .disabled("Z")) priority_encoder_2 (
    .in0(1'b1), .in1(MemToReg), .in2(or_2_out), .in3(AUIPC), .out(priority_encoder_2_out));  // open: gs, en_out, en_in
  Multiplexer #(.select(2), .width(32), .disabled("Z"), .enable("false")) multiplexer_8 (
    .in0(result), .in1(mips_ram_1_p8), .in2(PC_4), .in3(PC_imm), .out(RDin), .sel(priority_encoder_2_out));
  D_Flip_Flop #(.trigger("high"), .Pre_Clr_Positions("LEGACY"), .NegatePresetClear("false"), .enable("true"), .NewFFLayout("false")) d_ff_1 (.Q(d_ff_1_q));  // open: clk, D, Qn, preset, en, reset
  // Probe on 13'hc
  or or_2 (or_2_out, jal, jalr);
  Comparator #(.width(13), .mode("twosComplement")) comparator_2 (
    .a(CNT_num), .b(13'hc), .eq(comparator_2_eq), .lt(comparator_2_lt));  // open: gt
  Clock #(.highDuration(1), .lowDuration(1)) clock_1 (.out(clock_1_out));
  Counter #(.width(13), .max('h1fff), .ongoal("stay"), .trigger("rising"), .behavior("old")) counter_2 (
    .count(comparator_2_lt), .Q(CNT_num), .clk(clock_1_out));  // open: load, D, carry, clr, preset
  nand nand_1 (nand_1_out, d_ff_1_q, comparator_2_eq);
  assign CLK = nand_1_out ? clock_1_out : 1'bz;  // Controlled_Buffer controlled_buffer_1
  Pull_Resistor #(.pull(1)) pull_resistor_1 (.node(CLK));

  // Notes on the sheet:
  //   中断源
  //   中断等待指示
  //   数码管输出应该用寄存器锁存，否则显示数据只能一闪而过
  //   数码管输出
  //   指令探针
  //   指令存储器
  //   指令字
  //   contents of rom_1 (hex, n*v repeats v):
  //   100493 100006f 100493 200913 300993 100006f 100493 200913 300993 100006f 100493 200913 300993
  //   100006f 100493 200913 300993 29c000ef 100413 100493 1f49493 900533 2200893 73 24d493 48463 fedff06f
  //   900533 2200893 73 100493 249493 900533 2200893 73 48463 fedff06f 100493 1f49493 900533 2200893 73
  //   4034d493 900533 2200893 73 4044d493 900533 2200893 73 4044d493 900533 2200893 73 4044d493 900533
  //   2200893 73 4044d493 900533 2200893 73 4044d493 900533 2200893 73 4044d493 900533 2200893 73 4044d493
  //   900533 2200893 73 100413 1f41993 41f9d993 433 c00913 300b13 140413 f47413 800293 100313 499993
  //   89e9b3 1300533 2200893 73 406282b3 fe0294e3 140413 f00f93 1f47433 1c41413 800293 100313 49d993
  //   89e9b3 1300533 2200893 73 406282b3 fe0294e3 1c45413 406b0b33 b0463 f95ff06f 2b3 fff2c293 829293
  //   ff2e293 500533 2200893 73 fff00413 493 84a023 140413 448493 84a023 140413 448493 84a023 140413
  //   448493 84a023 140413 448493 84a023 140413 448493 84a023 140413 448493 84a023 140413 448493 84a023
  //   140413 448493 84a023 140413 448493 84a023 140413 448493 84a023 140413 448493 84a023 140413 448493
  //   84a023 140413 448493 84a023 140413 448493 84a023 140413 448493 84a023 140413 448493 140413 433
  //   3c00493 42983 4aa03 149a2b3 28663 134a023 1442023 ffc48493 fe9412e3 800533 2200893 73 440413 3c00493
  //   fc9416e3 a00893 73 413 140413 800533 2200893 73 240413 800533 2200893 73 340413 800533 2200893 73
  //   440413 800533 2200893 73 540413 800533 2200893 73 640413 800533 2200893 73 740413 800533 2200893 73
  //   840413 800533 2200893 2200893 73 8067
  //   JAL
  //   JALR
  //   Beq
  //   Bne
  //   MemToReg
  //   MemWrite
  //   AluOP
  //   AluSrcB
  //   RegWrite
  //   为方便自动评测，需要输出PC，IR，寄存器堆写如数据RDin
  //   数据存储器
  //   RAM写使能MemWrite、RAM写入数据MDin等信号
  //   控制位
  //   暂停节拍，不能为0
  //   戳工具置1进入计数暂停模式，ctrl+k时钟自动运行到对应节拍暂停
  //   ctrl+k关闭时钟连续运行，将控制位置零，进入单步调试模式调试
  //   用这个时钟源需要去掉电路中的其他时钟源
  //   可计数暂停的时钟源
endmodule

// 单周期硬布线控制器
module \单周期硬布线控制器  (
  input  [4:0] OP,
  input  [4:0] Funct,
  input  in_3,
  output [3:0] ALU_OP,
  output uret,
  output MemToReg,
  output ecall,
  output MemWrite,
  output ALU_SRC,
  output RegWrite,
  output S_type,
  output Beq,
  output Bne,
  output Jalr,
  output JAL,
  output AUIPC,
  output BGEU,
  output SB,
  output Rs1used,
  output Rs2used,
  output CSRRSI,
  output CSRRCI
);

  wire \控制信号自动生成_1_ecall ;

  \运算控制器自动生成  \u_运算控制器自动生成_1  (
    .OP2(OP[0]), .OP3(OP[1]), .OP4(OP[2]), .OP5(OP[3]), .OP6(OP[4]), .F12(Funct[0]), .F13(Funct[1]),
    .F14(Funct[2]), .F25(Funct[3]), .F30(Funct[4]), .S0(ALU_OP[0]), .S1(ALU_OP[1]), .S2(ALU_OP[2]),
    .S3(ALU_OP[3]));
  \控制信号自动生成  \u_控制信号自动生成_1  (
    .OP2(OP[0]), .OP3(OP[1]), .MemToReg(MemToReg), .OP4(OP[2]), .OP5(OP[3]), .OP6(OP[4]), .F12(Funct[0]),
    .MemWrite(MemWrite), .F13(Funct[1]), .F14(Funct[2]), .F25(Funct[3]), .CSRRSI(CSRRSI), .F30(Funct[4]),
    .CSRRCI(CSRRCI), .Rs1used(Rs1used), .Rs2used(Rs2used), .AUIPC(AUIPC), .BGEU(BGEU), .SB(SB),
    .ALU_SRC(ALU_SRC), .RegWrite(RegWrite), .ecall(\控制信号自动生成_1_ecall ), .S_Type(S_type), .BEQ(Beq),
    .BNE(Bne), .JALR(Jalr), .JAL(JAL));
  and and_1 (uret, in_3, \控制信号自动生成_1_ecall );
  and and_2 (ecall, ~in_3, \控制信号自动生成_1_ecall );  // AND_Gate

  // Other names for the same wires on the sheet: IR21 = in_3; OP_CODE[4:0] = OP

  // Notes on the sheet:
  //   运算器控制器，根据指令生成运算器功能选择信号
  //   控制信号生成，产生数据通路需要的其他控制信号
endmodule

// 运算器控制器
module \运算控制器自动生成  (
  input  OP2,
  input  OP3,
  input  OP4,
  input  OP5,
  input  OP6,
  input  F12,
  input  F13,
  input  F14,
  input  F25,
  input  F30,
  output S0,
  output S1,
  output S2,
  output S3
);

  wire and_1_out, and_2_out, and_3_out, and_4_out, and_5_out, and_6_out, and_7_out, and_8_out, and_9_out,
       and_10_out, and_11_out, and_12_out, and_13_out, and_14_out, and_15_out, and_16_out, and_17_out,
       and_18_out, and_19_out, and_20_out, and_21_out, and_22_out, and_23_out, and_24_out, and_25_out,
       and_26_out, and_27_out, and_28_out, and_29_out, and_30_out, and_31_out, and_32_out, and_33_out,
       and_34_out, and_35_out, and_36_out, not_1_out, not_2_out, not_3_out, not_4_out, not_5_out, not_6_out,
       not_7_out, not_8_out, not_9_out, not_10_out, not_11_out, not_12_out, not_13_out, not_14_out,
       not_15_out, not_16_out, not_17_out, not_18_out, not_19_out, not_20_out, not_21_out, not_22_out,
       not_23_out, not_24_out, not_25_out, not_26_out, not_27_out, not_28_out, not_29_out, not_30_out,
       not_31_out, not_32_out, not_33_out, not_34_out, not_35_out, not_36_out, not_37_out, not_38_out,
       not_39_out, not_40_out, not_41_out, not_42_out, not_43_out, not_44_out, not_45_out, not_46_out,
       not_47_out, not_48_out, not_49_out, not_50_out, not_51_out, not_52_out, not_53_out, not_54_out,
       not_55_out, not_56_out, not_57_out, not_58_out, not_59_out, not_60_out, not_61_out, not_62_out,
       not_63_out, not_64_out, not_65_out, not_66_out, not_67_out, not_68_out, not_69_out, not_70_out,
       not_71_out, not_72_out, not_73_out, not_74_out, not_75_out, not_76_out, not_77_out, not_78_out,
       not_79_out, not_80_out, not_81_out, not_82_out, not_83_out, not_84_out, not_85_out, not_86_out,
       not_87_out, not_88_out, not_89_out, not_90_out, not_91_out, not_92_out, not_93_out, not_94_out,
       not_95_out, not_96_out, not_97_out, not_98_out, not_99_out, not_100_out, not_101_out, not_102_out,
       not_103_out, not_104_out, not_105_out, not_106_out, not_107_out, not_108_out, not_109_out,
       not_110_out, not_111_out, not_112_out, not_113_out, not_114_out, not_115_out, not_116_out,
       not_117_out, not_118_out, not_119_out, not_120_out, not_121_out, not_122_out, not_123_out,
       not_124_out, not_125_out, not_126_out, not_127_out, not_128_out, not_129_out, not_130_out,
       not_131_out, not_132_out, not_133_out, not_134_out, not_135_out, not_136_out, not_137_out,
       not_138_out, not_139_out, not_140_out, not_141_out, not_142_out, not_143_out, not_144_out,
       not_145_out, not_146_out, not_147_out, not_148_out, not_149_out, not_150_out, not_151_out,
       not_152_out, not_153_out, not_154_out, not_155_out, not_156_out, not_157_out, not_158_out,
       not_159_out, not_160_out, not_161_out, not_162_out, not_163_out, not_164_out, not_165_out,
       not_166_out, not_167_out, not_168_out, not_169_out, not_170_out, not_171_out, not_172_out,
       not_173_out, not_174_out, not_175_out, not_176_out, not_177_out, not_178_out, not_179_out,
       not_180_out, not_181_out, not_182_out, not_183_out, not_184_out, not_185_out, not_186_out,
       not_187_out, not_188_out, not_189_out, not_190_out, not_191_out, not_192_out, not_193_out,
       not_194_out, not_195_out, not_196_out, not_197_out, not_198_out, not_199_out, not_200_out,
       not_201_out, not_202_out, not_203_out, not_204_out, not_205_out, not_206_out;

  not not_1 (not_1_out, F30);
  not not_2 (not_2_out, F25);
  not not_3 (not_3_out, F14);
  not not_4 (not_4_out, F13);
  not not_5 (not_5_out, F12);
  not not_6 (not_6_out, OP6);
  not not_7 (not_7_out, OP3);
  not not_8 (not_8_out, OP2);
  not not_9 (not_9_out, F30);
  not not_10 (not_10_out, F25);
  not not_11 (not_11_out, OP6);
  not not_12 (not_12_out, OP3);
  not not_13 (not_13_out, OP2);
  not not_14 (not_14_out, F30);
  not not_15 (not_15_out, F25);
  not not_16 (not_16_out, F14);
  not not_17 (not_17_out, F12);
  not not_18 (not_18_out, OP6);
  not not_19 (not_19_out, OP3);
  not not_20 (not_20_out, OP2);
  not not_21 (not_21_out, F14);
  not not_22 (not_22_out, F13);
  not not_23 (not_23_out, F12);
  not not_24 (not_24_out, OP6);
  not not_25 (not_25_out, OP5);
  not not_26 (not_26_out, OP3);
  not not_27 (not_27_out, OP2);
  not not_28 (not_28_out, OP6);
  not not_29 (not_29_out, OP5);
  not not_30 (not_30_out, OP3);
  not not_31 (not_31_out, OP2);
  not not_32 (not_32_out, F13);
  not not_33 (not_33_out, F12);
  not not_34 (not_34_out, OP6);
  not not_35 (not_35_out, OP5);
  not not_36 (not_36_out, OP3);
  not not_37 (not_37_out, OP2);
  not not_38 (not_38_out, F14);
  not not_39 (not_39_out, F12);
  not not_40 (not_40_out, OP6);
  not not_41 (not_41_out, OP5);
  not not_42 (not_42_out, OP3);
  not not_43 (not_43_out, OP2);
  not not_44 (not_44_out, F25);
  not not_45 (not_45_out, F13);
  not not_46 (not_46_out, OP6);
  not not_47 (not_47_out, OP5);
  not not_48 (not_48_out, OP3);
  not not_49 (not_49_out, OP2);
  not not_50 (not_50_out, F25);
  not not_51 (not_51_out, F14);
  not not_52 (not_52_out, F13);
  not not_53 (not_53_out, F12);
  not not_54 (not_54_out, OP6);
  not not_55 (not_55_out, OP3);
  not not_56 (not_56_out, OP2);
  not not_57 (not_57_out, F30);
  not not_58 (not_58_out, F25);
  not not_59 (not_59_out, OP6);
  not not_60 (not_60_out, OP3);
  not not_61 (not_61_out, OP2);
  not not_62 (not_62_out, F30);
  not not_63 (not_63_out, F25);
  not not_64 (not_64_out, F14);
  not not_65 (not_65_out, F12);
  not not_66 (not_66_out, OP6);
  not not_67 (not_67_out, OP3);
  not not_68 (not_68_out, OP2);
  not not_69 (not_69_out, OP6);
  not not_70 (not_70_out, OP5);
  not not_71 (not_71_out, OP3);
  not not_72 (not_72_out, OP2);
  not not_73 (not_73_out, F14);
  not not_74 (not_74_out, F12);
  not not_75 (not_75_out, OP6);
  not not_76 (not_76_out, OP5);
  not not_77 (not_77_out, OP3);
  not not_78 (not_78_out, OP2);
  not not_79 (not_79_out, F30);
  not not_80 (not_80_out, F25);
  not not_81 (not_81_out, F13);
  not not_82 (not_82_out, OP6);
  not not_83 (not_83_out, OP5);
  not not_84 (not_84_out, OP3);
  not not_85 (not_85_out, OP2);
  not not_86 (not_86_out, F14);
  not not_87 (not_87_out, F13);
  not not_88 (not_88_out, F12);
  not not_89 (not_89_out, OP4);
  not not_90 (not_90_out, OP3);
  not not_91 (not_91_out, OP2);
  not not_92 (not_92_out, F14);
  not not_93 (not_93_out, F13);
  not not_94 (not_94_out, OP4);
  not not_95 (not_95_out, OP3);
  not not_96 (not_96_out, OP2);
  not not_97 (not_97_out, F14);
  not not_98 (not_98_out, F13);
  not not_99 (not_99_out, F12);
  not not_100 (not_100_out, OP4);
  not not_101 (not_101_out, OP3);
  not not_102 (not_102_out, F30);
  not not_103 (not_103_out, F25);
  not not_104 (not_104_out, F14);
  not not_105 (not_105_out, F13);
  not not_106 (not_106_out, F12);
  not not_107 (not_107_out, OP6);
  not not_108 (not_108_out, OP3);
  not not_109 (not_109_out, OP2);
  not not_110 (not_110_out, F25);
  not not_111 (not_111_out, F14);
  not not_112 (not_112_out, F13);
  not not_113 (not_113_out, F12);
  not not_114 (not_114_out, OP6);
  not not_115 (not_115_out, OP3);
  not not_116 (not_116_out, OP2);
  not not_117 (not_117_out, F30);
  not not_118 (not_118_out, F25);
  not not_119 (not_119_out, OP6);
  not not_120 (not_120_out, OP3);
  not not_121 (not_121_out, OP2);
  not not_122 (not_122_out, F30);
  not not_123 (not_123_out, F25);
  not not_124 (not_124_out, F14);
  not not_125 (not_125_out, OP6);
  not not_126 (not_126_out, OP3);
  not not_127 (not_127_out, OP2);
  not not_128 (not_128_out, F14);
  not not_129 (not_129_out, F13);
  not not_130 (not_130_out, F12);
  not not_131 (not_131_out, OP6);
  not not_132 (not_132_out, OP5);
  not not_133 (not_133_out, OP3);
  not not_134 (not_134_out, OP2);
  not not_135 (not_135_out, OP6);
  not not_136 (not_136_out, OP5);
  not not_137 (not_137_out, OP3);
  not not_138 (not_138_out, OP2);
  not not_139 (not_139_out, F14);
  not not_140 (not_140_out, F13);
  not not_141 (not_141_out, F12);
  not not_142 (not_142_out, OP4);
  not not_143 (not_143_out, OP3);
  not not_144 (not_144_out, OP2);
  not not_145 (not_145_out, F14);
  not not_146 (not_146_out, F13);
  not not_147 (not_147_out, OP4);
  not not_148 (not_148_out, OP3);
  not not_149 (not_149_out, OP2);
  not not_150 (not_150_out, F14);
  not not_151 (not_151_out, F13);
  not not_152 (not_152_out, F12);
  not not_153 (not_153_out, OP4);
  not not_154 (not_154_out, OP3);
  not not_155 (not_155_out, F14);
  not not_156 (not_156_out, OP6);
  not not_157 (not_157_out, OP5);
  not not_158 (not_158_out, OP3);
  not not_159 (not_159_out, OP2);
  not not_160 (not_160_out, OP4);
  not not_161 (not_161_out, OP3);
  not not_162 (not_162_out, OP2);
  not not_163 (not_163_out, F30);
  not not_164 (not_164_out, F25);
  not not_165 (not_165_out, F12);
  not not_166 (not_166_out, OP6);
  not not_167 (not_167_out, OP3);
  not not_168 (not_168_out, OP2);
  not not_169 (not_169_out, F30);
  not not_170 (not_170_out, F25);
  not not_171 (not_171_out, F14);
  not not_172 (not_172_out, F12);
  not not_173 (not_173_out, OP6);
  not not_174 (not_174_out, OP3);
  not not_175 (not_175_out, OP2);
  not not_176 (not_176_out, F30);
  not not_177 (not_177_out, F25);
  not not_178 (not_178_out, F14);
  not not_179 (not_179_out, OP6);
  not not_180 (not_180_out, OP3);
  not not_181 (not_181_out, OP2);
  not not_182 (not_182_out, F12);
  not not_183 (not_183_out, OP6);
  not not_184 (not_184_out, OP5);
  not not_185 (not_185_out, OP3);
  not not_186 (not_186_out, OP2);
  not not_187 (not_187_out, F13);
  not not_188 (not_188_out, F12);
  not not_189 (not_189_out, OP6);
  not not_190 (not_190_out, OP5);
  not not_191 (not_191_out, OP3);
  not not_192 (not_192_out, OP2);
  not not_193 (not_193_out, F14);
  not not_194 (not_194_out, F12);
  not not_195 (not_195_out, OP6);
  not not_196 (not_196_out, OP5);
  not not_197 (not_197_out, OP3);
  not not_198 (not_198_out, OP2);
  not not_199 (not_199_out, F14);
  not not_200 (not_200_out, OP6);
  not not_201 (not_201_out, OP5);
  not not_202 (not_202_out, OP3);
  not not_203 (not_203_out, OP2);
  not not_204 (not_204_out, OP4);
  not not_205 (not_205_out, OP3);
  not not_206 (not_206_out, OP2);
  and and_1 (and_1_out, not_1_out, not_2_out, not_3_out, not_4_out, not_5_out, not_6_out, OP5, OP4, not_7_out, not_8_out);
  and and_2 (and_2_out, not_9_out, not_10_out, F14, F13, F12, not_11_out, OP5, OP4, not_12_out, not_13_out);
  and and_3 (and_3_out, not_14_out, not_15_out, not_16_out, F13, not_17_out, not_18_out, OP5, OP4, not_19_out, not_20_out);
  and and_4 (and_4_out, not_21_out, not_22_out, not_23_out, not_24_out, not_25_out, OP4, not_26_out, not_27_out);
  and and_5 (and_5_out, F14, F13, F12, not_28_out, not_29_out, OP4, not_30_out, not_31_out);
  and and_6 (and_6_out, F14, not_32_out, not_33_out, not_34_out, not_35_out, OP4, not_36_out, not_37_out);
  and and_7 (and_7_out, not_38_out, F13, not_39_out, not_40_out, not_41_out, OP4, not_42_out, not_43_out);
  and and_8 (and_8_out, F30, not_44_out, F14, not_45_out, F12, not_46_out, not_47_out, OP4, not_48_out, not_49_out);
  and and_9 (and_9_out, F30, not_50_out, not_51_out, not_52_out, not_53_out, not_54_out, OP5, OP4, not_55_out, not_56_out);
  and and_10 (and_10_out, not_57_out, not_58_out, F14, F13, F12, not_59_out, OP5, OP4, not_60_out, not_61_out);
  and and_11 (and_11_out, not_62_out, not_63_out, not_64_out, F13, not_65_out, not_66_out, OP5, OP4, not_67_out, not_68_out);
  and and_12 (and_12_out, F14, F13, F12, not_69_out, not_70_out, OP4, not_71_out, not_72_out);
  and and_13 (and_13_out, not_73_out, F13, not_74_out, not_75_out, not_76_out, OP4, not_77_out, not_78_out);
  and and_14 (and_14_out, not_79_out, not_80_out, F14, not_81_out, F12, not_82_out, not_83_out, OP4, not_84_out, not_85_out);
  and and_15 (and_15_out, not_86_out, not_87_out, not_88_out, OP6, OP5, not_89_out, not_90_out, not_91_out);
  and and_16 (and_16_out, not_92_out, not_93_out, F12, OP6, OP5, not_94_out, not_95_out, not_96_out);
  and and_17 (and_17_out, not_97_out, not_98_out, not_99_out, OP6, OP5, not_100_out, not_101_out, OP2);
  and and_18 (and_18_out, not_102_out, not_103_out, not_104_out, not_105_out, not_106_out, not_107_out, OP5, OP4, not_108_out, not_109_out);
  and and_19 (and_19_out, F30, not_110_out, not_111_out, not_112_out, not_113_out, not_114_out, OP5, OP4, not_115_out, not_116_out);
  and and_20 (and_20_out, not_117_out, not_118_out, F14, F13, F12, not_119_out, OP5, OP4, not_120_out, not_121_out);
  and and_21 (and_21_out, not_122_out, not_123_out, not_124_out, F13, F12, not_125_out, OP5, OP4, not_126_out, not_127_out);
  and and_22 (and_22_out, not_128_out, not_129_out, not_130_out, not_131_out, not_132_out, OP4, not_133_out, not_134_out);
  and and_23 (and_23_out, F14, F13, F12, not_135_out, not_136_out, OP4, not_137_out, not_138_out);
  and and_24 (and_24_out, not_139_out, not_140_out, not_141_out, OP6, OP5, not_142_out, not_143_out, not_144_out);
  and and_25 (and_25_out, not_145_out, not_146_out, F12, OP6, OP5, not_147_out, not_148_out, not_149_out);
  and and_26 (and_26_out, not_150_out, not_151_out, not_152_out, OP6, OP5, not_153_out, not_154_out, OP2);
  and and_27 (and_27_out, not_155_out, F13, F12, not_156_out, not_157_out, OP4, not_158_out, not_159_out);
  and and_28 (and_28_out, F14, F13, F12, OP6, OP5, not_160_out, not_161_out, not_162_out);
  and and_29 (and_29_out, not_163_out, not_164_out, F14, F13, not_165_out, not_166_out, OP5, OP4, not_167_out, not_168_out);
  and and_30 (and_30_out, not_169_out, not_170_out, not_171_out, F13, not_172_out, not_173_out, OP5, OP4, not_174_out, not_175_out);
  and and_31 (and_31_out, not_176_out, not_177_out, not_178_out, F13, F12, not_179_out, OP5, OP4, not_180_out, not_181_out);
  and and_32 (and_32_out, F14, F13, not_182_out, not_183_out, not_184_out, OP4, not_185_out, not_186_out);
  and and_33 (and_33_out, F14, not_187_out, not_188_out, not_189_out, not_190_out, OP4, not_191_out, not_192_out);
  and and_34 (and_34_out, not_193_out, F13, not_194_out, not_195_out, not_196_out, OP4, not_197_out, not_198_out);
  and and_35 (and_35_out, not_199_out, F13, F12, not_200_out, not_201_out, OP4, not_202_out, not_203_out);
  and and_36 (and_36_out, F14, F13, F12, OP6, OP5, not_204_out, not_205_out, not_206_out);
  or or_1 (S0, and_1_out, and_2_out, and_3_out, and_4_out, and_5_out, and_6_out, and_7_out, and_8_out);
  or or_2 (S1, and_9_out, and_10_out, and_11_out, and_12_out, and_13_out, and_14_out, and_15_out, and_16_out, and_17_out);
  or or_3 (S2, and_18_out, and_19_out, and_20_out, and_21_out, and_22_out, and_23_out, and_24_out, and_25_out, and_26_out, and_27_out, and_28_out);
  or or_4 (S3, and_29_out, and_30_out, and_31_out, and_32_out, and_33_out, and_34_out, and_35_out, and_36_out);
endmodule

// 控制信号生成
module \控制信号自动生成  (
  input  OP2,
  input  OP3,
  input  OP4,
  input  OP5,
  input  OP6,
  input  F12,
  input  F13,
  input  F14,
  input  F25,
  input  F30,
  output MemToReg,
  output MemWrite,
  output CSRRSI,
  output CSRRCI,
  output Rs1used,
  output Rs2used,
  output AUIPC,
  output BGEU,
  output SB,
  output ALU_SRC,
  output RegWrite,
  output ecall,
  output S_Type,
  output BEQ,
  output BNE,
  output JALR,
  output JAL
);

  wire and_5_out, and_6_out, and_7_out, and_8_out, and_9_out, and_10_out, and_11_out, and_12_out, and_13_out,
       and_14_out, and_15_out, and_16_out, and_17_out, and_18_out, and_19_out, and_20_out, and_24_out,
       and_25_out, and_26_out, and_27_out, and_28_out, and_29_out, and_30_out, and_31_out, and_32_out,
       and_33_out, and_34_out, and_35_out, and_36_out, and_37_out, and_38_out, and_39_out, and_40_out,
       not_1_out, not_2_out, not_3_out, not_4_out, not_5_out, not_6_out, not_7_out, not_8_out, not_9_out,
       not_10_out, not_11_out, not_12_out, not_13_out, not_14_out, not_15_out, not_16_out, not_17_out,
       not_18_out, not_19_out, not_20_out, not_21_out, not_22_out, not_23_out, not_24_out, not_25_out,
       not_26_out, not_27_out, not_28_out, not_29_out, not_30_out, not_31_out, not_32_out, not_33_out,
       not_34_out, not_35_out, not_36_out, not_37_out, not_38_out, not_39_out, not_40_out, not_41_out,
       not_42_out, not_43_out, not_44_out, not_45_out, not_46_out, not_47_out, not_48_out, not_49_out,
       not_50_out, not_51_out, not_52_out, not_53_out, not_54_out, not_55_out, not_56_out, not_57_out,
       not_58_out, not_59_out, not_60_out, not_61_out, not_62_out, not_63_out, not_64_out, not_65_out,
       not_66_out, not_67_out, not_68_out, not_69_out, not_70_out, not_71_out, not_72_out, not_73_out,
       not_74_out, not_75_out, not_76_out, not_77_out, not_78_out, not_79_out, not_80_out, not_81_out,
       not_82_out, not_83_out, not_84_out, not_85_out, not_86_out, not_87_out, not_88_out, not_89_out,
       not_90_out, not_91_out, not_92_out, not_93_out, not_94_out, not_95_out, not_96_out, not_97_out,
       not_98_out, not_99_out, not_100_out, not_101_out, not_102_out, not_103_out, not_104_out, not_105_out,
       not_106_out, not_107_out, not_108_out, not_109_out, not_110_out, not_111_out, not_112_out,
       not_113_out, not_114_out, not_115_out, not_116_out, not_117_out, not_118_out, not_119_out,
       not_120_out, not_121_out, not_122_out, not_123_out, not_124_out, not_125_out, not_126_out,
       not_127_out, not_128_out, not_129_out, not_130_out, not_131_out, not_132_out, not_133_out,
       not_134_out, not_135_out, not_136_out, not_137_out, not_138_out, not_139_out, not_140_out,
       not_141_out, not_142_out, not_143_out, not_144_out, not_145_out, not_146_out, not_147_out,
       not_148_out, not_149_out, not_150_out, not_151_out, not_152_out, not_153_out, not_154_out,
       not_155_out, not_156_out, not_157_out, not_158_out, not_159_out, not_160_out, not_161_out,
       not_162_out, not_163_out, not_164_out, not_165_out, not_166_out, not_167_out, not_168_out,
       not_169_out, not_170_out, not_171_out, not_172_out, not_173_out, not_174_out, not_175_out,
       not_176_out, not_177_out, not_178_out, not_179_out, not_180_out, not_181_out, not_182_out,
       not_183_out, not_184_out, not_185_out, not_186_out, not_187_out, not_188_out, not_189_out,
       not_190_out, not_191_out, not_192_out, not_193_out, not_194_out, not_195_out, not_196_out,
       not_197_out, not_198_out, not_199_out, not_200_out, not_201_out, not_202_out, not_203_out,
       not_204_out, not_205_out, not_206_out, not_207_out, not_208_out, not_209_out, not_210_out,
       not_211_out, not_212_out, not_213_out, not_214_out, not_215_out, not_216_out, not_217_out,
       not_218_out, not_219_out, not_220_out, not_221_out, not_222_out, not_223_out;

  not not_1 (not_1_out, OP2);
  not not_2 (not_2_out, OP3);
  not not_3 (not_3_out, OP4);
  not not_4 (not_4_out, OP5);
  not not_5 (not_5_out, OP6);
  not not_6 (not_6_out, F12);
  not not_7 (not_7_out, F14);
  not not_8 (not_8_out, OP2);
  not not_9 (not_9_out, OP3);
  not not_10 (not_10_out, OP4);
  not not_11 (not_11_out, OP6);
  not not_12 (not_12_out, F12);
  not not_13 (not_13_out, F14);
  not not_14 (not_14_out, F12);
  not not_15 (not_15_out, OP3);
  not not_16 (not_16_out, OP2);
  not not_17 (not_17_out, OP3);
  not not_18 (not_18_out, OP2);
  not not_19 (not_19_out, OP2);
  not not_20 (not_20_out, OP3);
  not not_21 (not_21_out, OP5);
  not not_22 (not_22_out, OP6);
  not not_23 (not_23_out, F12);
  not not_24 (not_24_out, F14);
  not not_25 (not_25_out, OP2);
  not not_26 (not_26_out, OP3);
  not not_27 (not_27_out, OP4);
  not not_28 (not_28_out, OP6);
  not not_29 (not_29_out, F12);
  not not_30 (not_30_out, F14);
  not not_31 (not_31_out, OP2);
  not not_32 (not_32_out, OP3);
  not not_33 (not_33_out, OP4);
  not not_34 (not_34_out, F13);
  not not_35 (not_35_out, F14);
  not not_36 (not_36_out, OP3);
  not not_37 (not_37_out, OP4);
  not not_38 (not_38_out, F12);
  not not_39 (not_39_out, F13);
  not not_40 (not_40_out, F14);
  not not_41 (not_41_out, OP2);
  not not_42 (not_42_out, OP3);
  not not_43 (not_43_out, OP4);
  not not_44 (not_44_out, OP2);
  not not_45 (not_45_out, OP3);
  not not_46 (not_46_out, OP5);
  not not_47 (not_47_out, OP6);
  not not_48 (not_48_out, F12);
  not not_49 (not_49_out, OP2);
  not not_50 (not_50_out, OP3);
  not not_51 (not_51_out, OP5);
  not not_52 (not_52_out, OP6);
  not not_53 (not_53_out, F25);
  not not_54 (not_54_out, F30);
  not not_55 (not_55_out, OP2);
  not not_56 (not_56_out, OP3);
  not not_57 (not_57_out, OP6);
  not not_58 (not_58_out, F12);
  not not_59 (not_59_out, F13);
  not not_60 (not_60_out, F14);
  not not_61 (not_61_out, F25);
  not not_62 (not_62_out, OP2);
  not not_63 (not_63_out, OP3);
  not not_64 (not_64_out, OP5);
  not not_65 (not_65_out, OP6);
  not not_66 (not_66_out, F25);
  not not_67 (not_67_out, OP2);
  not not_68 (not_68_out, OP3);
  not not_69 (not_69_out, OP5);
  not not_70 (not_70_out, OP6);
  not not_71 (not_71_out, OP2);
  not not_72 (not_72_out, OP3);
  not not_73 (not_73_out, OP6);
  not not_74 (not_74_out, F25);
  not not_75 (not_75_out, F30);
  not not_76 (not_76_out, OP2);
  not not_77 (not_77_out, OP3);
  not not_78 (not_78_out, OP4);
  not not_79 (not_79_out, OP6);
  not not_80 (not_80_out, F12);
  not not_81 (not_81_out, F14);
  not not_82 (not_82_out, OP2);
  not not_83 (not_83_out, OP3);
  not not_84 (not_84_out, OP6);
  not not_85 (not_85_out, F12);
  not not_86 (not_86_out, F13);
  not not_87 (not_87_out, F14);
  not not_88 (not_88_out, F25);
  not not_89 (not_89_out, OP2);
  not not_90 (not_90_out, OP3);
  not not_91 (not_91_out, OP4);
  not not_92 (not_92_out, F13);
  not not_93 (not_93_out, F14);
  not not_94 (not_94_out, OP2);
  not not_95 (not_95_out, OP3);
  not not_96 (not_96_out, OP4);
  not not_97 (not_97_out, OP2);
  not not_98 (not_98_out, OP3);
  not not_99 (not_99_out, OP6);
  not not_100 (not_100_out, F25);
  not not_101 (not_101_out, F30);
  not not_102 (not_102_out, OP3);
  not not_103 (not_103_out, OP5);
  not not_104 (not_104_out, OP6);
  not not_105 (not_105_out, OP2);
  not not_106 (not_106_out, OP3);
  not not_107 (not_107_out, OP4);
  not not_108 (not_108_out, OP2);
  not not_109 (not_109_out, OP3);
  not not_110 (not_110_out, OP4);
  not not_111 (not_111_out, OP6);
  not not_112 (not_112_out, F12);
  not not_113 (not_113_out, F13);
  not not_114 (not_114_out, F14);
  not not_115 (not_115_out, OP2);
  not not_116 (not_116_out, OP3);
  not not_117 (not_117_out, OP5);
  not not_118 (not_118_out, OP6);
  not not_119 (not_119_out, F12);
  not not_120 (not_120_out, F14);
  not not_121 (not_121_out, OP2);
  not not_122 (not_122_out, OP3);
  not not_123 (not_123_out, OP4);
  not not_124 (not_124_out, OP6);
  not not_125 (not_125_out, F12);
  not not_126 (not_126_out, F14);
  not not_127 (not_127_out, OP2);
  not not_128 (not_128_out, OP3);
  not not_129 (not_129_out, OP5);
  not not_130 (not_130_out, OP6);
  not not_131 (not_131_out, F12);
  not not_132 (not_132_out, OP2);
  not not_133 (not_133_out, OP3);
  not not_134 (not_134_out, OP5);
  not not_135 (not_135_out, OP6);
  not not_136 (not_136_out, F25);
  not not_137 (not_137_out, F30);
  not not_138 (not_138_out, OP2);
  not not_139 (not_139_out, OP3);
  not not_140 (not_140_out, OP5);
  not not_141 (not_141_out, OP6);
  not not_142 (not_142_out, F25);
  not not_143 (not_143_out, OP2);
  not not_144 (not_144_out, OP3);
  not not_145 (not_145_out, OP5);
  not not_146 (not_146_out, OP6);
  not not_147 (not_147_out, OP3);
  not not_148 (not_148_out, OP4);
  not not_149 (not_149_out, F12);
  not not_150 (not_150_out, F13);
  not not_151 (not_151_out, F14);
  not not_152 (not_152_out, OP2);
  not not_153 (not_153_out, OP3);
  not not_154 (not_154_out, OP5);
  not not_155 (not_155_out, OP6);
  not not_156 (not_156_out, F12);
  not not_157 (not_157_out, F14);
  not not_158 (not_158_out, OP2);
  not not_159 (not_159_out, OP3);
  not not_160 (not_160_out, OP6);
  not not_161 (not_161_out, F12);
  not not_162 (not_162_out, F13);
  not not_163 (not_163_out, F14);
  not not_164 (not_164_out, F25);
  not not_165 (not_165_out, OP3);
  not not_166 (not_166_out, OP5);
  not not_167 (not_167_out, OP6);
  not not_168 (not_168_out, F12);
  not not_169 (not_169_out, OP3);
  not not_170 (not_170_out, OP5);
  not not_171 (not_171_out, OP6);
  not not_172 (not_172_out, F25);
  not not_173 (not_173_out, F30);
  not not_174 (not_174_out, OP3);
  not not_175 (not_175_out, OP5);
  not not_176 (not_176_out, OP6);
  not not_177 (not_177_out, F25);
  not not_178 (not_178_out, OP2);
  not not_179 (not_179_out, OP3);
  not not_180 (not_180_out, OP6);
  not not_181 (not_181_out, F25);
  not not_182 (not_182_out, F30);
  not not_183 (not_183_out, OP3);
  not not_184 (not_184_out, OP5);
  not not_185 (not_185_out, OP6);
  not not_186 (not_186_out, OP4);
  not not_187 (not_187_out, F12);
  not not_188 (not_188_out, F13);
  not not_189 (not_189_out, F14);
  not not_190 (not_190_out, OP3);
  not not_191 (not_191_out, OP5);
  not not_192 (not_192_out, OP6);
  not not_193 (not_193_out, OP4);
  not not_194 (not_194_out, OP2);
  not not_195 (not_195_out, OP3);
  not not_196 (not_196_out, F12);
  not not_197 (not_197_out, F13);
  not not_198 (not_198_out, F14);
  not not_199 (not_199_out, F25);
  not not_200 (not_200_out, F30);
  not not_201 (not_201_out, OP2);
  not not_202 (not_202_out, OP3);
  not not_203 (not_203_out, OP4);
  not not_204 (not_204_out, OP6);
  not not_205 (not_205_out, F12);
  not not_206 (not_206_out, F14);
  not not_207 (not_207_out, OP2);
  not not_208 (not_208_out, OP3);
  not not_209 (not_209_out, OP4);
  not not_210 (not_210_out, F12);
  not not_211 (not_211_out, F13);
  not not_212 (not_212_out, F14);
  not not_213 (not_213_out, OP2);
  not not_214 (not_214_out, OP3);
  not not_215 (not_215_out, OP4);
  not not_216 (not_216_out, F13);
  not not_217 (not_217_out, F14);
  not not_218 (not_218_out, OP3);
  not not_219 (not_219_out, OP4);
  not not_220 (not_220_out, F12);
  not not_221 (not_221_out, F13);
  not not_222 (not_222_out, F14);
  not not_223 (not_223_out, OP4);
  and and_1 (MemToReg, not_1_out, not_2_out, not_3_out, not_4_out, not_5_out, not_6_out, F13, not_7_out);
  and and_2 (MemWrite, not_8_out, not_9_out, not_10_out, OP5, not_11_out, not_12_out, not_13_out);
  and and_3 (CSRRSI, F14, F13, not_14_out, OP6, OP5, OP4, not_15_out, not_16_out);
  and and_4 (CSRRCI, F14, F13, F12, OP6, OP5, OP4, not_17_out, not_18_out);
  and and_5 (and_5_out, not_19_out, not_20_out, not_21_out, not_22_out, not_23_out, F13, not_24_out);
  and and_6 (and_6_out, not_25_out, not_26_out, not_27_out, OP5, not_28_out, not_29_out, not_30_out);
  and and_7 (and_7_out, not_31_out, not_32_out, not_33_out, OP5, OP6, not_34_out, not_35_out);
  and and_8 (and_8_out, not_36_out, not_37_out, OP5, OP6, not_38_out, not_39_out, not_40_out);
  and and_9 (and_9_out, not_41_out, not_42_out, not_43_out, OP5, OP6, F12, F13, F14);
  and and_10 (and_10_out, not_44_out, not_45_out, OP4, not_46_out, not_47_out, not_48_out);
  and and_11 (and_11_out, not_49_out, not_50_out, OP4, not_51_out, not_52_out, not_53_out, not_54_out);
  and and_12 (and_12_out, not_55_out, not_56_out, OP4, not_57_out, not_58_out, not_59_out, not_60_out, not_61_out);
  and and_13 (and_13_out, not_62_out, not_63_out, OP4, not_64_out, not_65_out, F14, not_66_out);
  and and_14 (and_14_out, not_67_out, not_68_out, OP4, not_69_out, not_70_out, F13);
  and and_15 (and_15_out, not_71_out, not_72_out, OP4, not_73_out, F13, not_74_out, not_75_out);
  and and_16 (and_16_out, not_76_out, not_77_out, not_78_out, OP5, not_79_out, not_80_out, not_81_out);
  and and_17 (and_17_out, not_82_out, not_83_out, OP5, not_84_out, not_85_out, not_86_out, not_87_out, not_88_out);
  and and_18 (and_18_out, not_89_out, not_90_out, not_91_out, OP5, OP6, not_92_out, not_93_out);
  and and_19 (and_19_out, not_94_out, not_95_out, not_96_out, OP5, OP6, F12, F13, F14);
  and and_20 (and_20_out, not_97_out, not_98_out, OP4, OP5, not_99_out, F13, not_100_out, not_101_out);
  and and_21 (AUIPC, OP2, not_102_out, OP4, not_103_out, not_104_out);
  and and_22 (BGEU, not_105_out, not_106_out, not_107_out, OP5, OP6, F12, F13, F14);
  and and_23 (SB, not_108_out, not_109_out, not_110_out, OP5, not_111_out, not_112_out, not_113_out, not_114_out);
  and and_24 (and_24_out, not_115_out, not_116_out, not_117_out, not_118_out, not_119_out, F13, not_120_out);
  and and_25 (and_25_out, not_121_out, not_122_out, not_123_out, OP5, not_124_out, not_125_out, not_126_out);
  and and_26 (and_26_out, not_127_out, not_128_out, OP4, not_129_out, not_130_out, not_131_out);
  and and_27 (and_27_out, not_132_out, not_133_out, OP4, not_134_out, not_135_out, not_136_out, not_137_out);
  and and_28 (and_28_out, not_138_out, not_139_out, OP4, not_140_out, not_141_out, F14, not_142_out);
  and and_29 (and_29_out, not_143_out, not_144_out, OP4, not_145_out, not_146_out, F13);
  and and_30 (and_30_out, OP2, not_147_out, not_148_out, OP5, OP6, not_149_out, not_150_out, not_151_out);
  and and_31 (and_31_out, not_152_out, not_153_out, not_154_out, not_155_out, not_156_out, F13, not_157_out);
  and and_32 (and_32_out, not_158_out, not_159_out, OP4, not_160_out, not_161_out, not_162_out, not_163_out, not_164_out);
  and and_33 (and_33_out, not_165_out, OP4, not_166_out, not_167_out, not_168_out);
  and and_34 (and_34_out, not_169_out, OP4, not_170_out, not_171_out, not_172_out, not_173_out);
  and and_35 (and_35_out, not_174_out, OP4, not_175_out, not_176_out, F14, not_177_out);
  and and_36 (and_36_out, not_178_out, not_179_out, OP4, not_180_out, F13, not_181_out, not_182_out);
  and and_37 (and_37_out, not_183_out, OP4, not_184_out, not_185_out, F13);
  and and_38 (and_38_out, OP2, not_186_out, OP5, OP6, not_187_out, not_188_out, not_189_out);
  and and_39 (and_39_out, OP2, not_190_out, OP4, not_191_out, not_192_out);
  and and_40 (and_40_out, OP2, OP3, not_193_out, OP5, OP6);
  and and_41 (ecall, not_194_out, not_195_out, OP4, OP5, OP6, not_196_out, not_197_out, not_198_out, not_199_out, not_200_out);
  and and_42 (S_Type, not_201_out, not_202_out, not_203_out, OP5, not_204_out, not_205_out, not_206_out);
  and and_43 (BEQ, not_207_out, not_208_out, not_209_out, OP5, OP6, not_210_out, not_211_out, not_212_out);
  and and_44 (BNE, not_213_out, not_214_out, not_215_out, OP5, OP6, F12, not_216_out, not_217_out);
  and and_45 (JALR, OP2, not_218_out, not_219_out, OP5, OP6, not_220_out, not_221_out, not_222_out);
  and and_46 (JAL, OP2, OP3, not_223_out, OP5, OP6);
  or or_1 (Rs2used, and_16_out, and_17_out, and_18_out, and_19_out, and_20_out);
  or or_2 (ALU_SRC, and_24_out, and_25_out, and_26_out, and_27_out, and_28_out, and_29_out, and_30_out);
  or or_3 (Rs1used, and_5_out, and_6_out, and_7_out, and_8_out, and_9_out, and_10_out, and_11_out, and_12_out, and_13_out, and_14_out, and_15_out);
  or or_4 (RegWrite, and_31_out, and_32_out, and_33_out, and_34_out, and_35_out, and_36_out, and_37_out, and_38_out, and_39_out, and_40_out);
endmodule

// ALU
module ALU (
  input  [31:0] X,
  input  [31:0] Y,
  input  [3:0] AluOP,
  output out_4,
  output Equal,
  output out_6,
  output [31:0] Result,
  output [31:0] Result_2
);

  wire [0:0] comparator_1_lt, comparator_2_lt;
  wire [31:0] adder_1_out, AND_out, divider_1_out, divider_1_rem, multiplier_1_cout, multiplier_1_out,
       NOR_out, OR_out, shifter_1_out, shifter_2_out, shifter_3_out, subtractor_1_out, XOR_out;

  assign AND_out = X & Y;  // AND_Gate AND, 32 bits wide
  assign OR_out = X | Y;  // OR_Gate OR, 32 bits wide
  Shifter #(.width(32), .shift("ll")) shifter_1 (.in(X), .\dist (Y[4:0]), .out(shifter_1_out));
  Shifter #(.width(32), .shift("ar")) shifter_2 (.in(X), .\dist (Y[4:0]), .out(shifter_2_out));
  Shifter #(.width(32), .shift("lr")) shifter_3 (.in(X), .\dist (Y[4:0]), .out(shifter_3_out));
  Multiplier #(.width(32)) multiplier_1 (.a(X), .b(Y), .out(multiplier_1_out), .cout(multiplier_1_cout));  // open: cin
  Divider #(.width(32)) divider_1 (.a(X), .b(Y), .out(divider_1_out), .rem(divider_1_rem));  // open: upper
  Adder #(.width(32)) adder_1 (.a(X), .b(Y), .out(adder_1_out));  // open: cin, cout
  Subtractor #(.width(32)) subtractor_1 (.a(X), .b(Y), .out(subtractor_1_out));  // open: bin, bout
  assign XOR_out = X ^ Y;  // XOR_Gate XOR, 32 bits wide
  assign NOR_out = ~(X | Y);  // NOR_Gate NOR, 32 bits wide
  Comparator #(.width(32), .mode("twosComplement")) comparator_1 (
    .a(X), .b(Y), .eq(Equal), .lt(comparator_1_lt[0]));  // open: gt
  Comparator #(.width(32), .mode("unsigned")) comparator_2 (.a(X), .b(Y), .lt(comparator_2_lt[0]));  // open: gt, eq
  Multiplexer #(.select(4), .width(32), .disabled("Z"), .enable("false")) multiplexer_1 (
    .in0(shifter_1_out), .in1(shifter_2_out), .in2(shifter_3_out), .in3(multiplier_1_out),
    .in4(divider_1_out), .in5(adder_1_out), .in6(subtractor_1_out), .in7(AND_out), .in8(OR_out),
    .in9(XOR_out), .in10(NOR_out), .in11({{31{1'b0}}, comparator_1_lt[0]}),
    .in12({{31{1'b0}}, comparator_2_lt[0]}), .in13({32{1'b0}}), .in14({32{1'b0}}), .in15({32{1'b0}}),
    .out(Result), .sel(AluOP));
  Multiplexer #(.select(4), .width(32), .disabled("Z"), .enable("false")) multiplexer_2 (
    .in0({32{1'b0}}), .in1({32{1'b0}}), .in2({32{1'b0}}), .in3(multiplier_1_cout), .in4(divider_1_rem),
    .in5({32{1'b0}}), .in6({32{1'b0}}), .in7({32{1'b0}}), .in8({32{1'b0}}), .in9({32{1'b0}}),
    .in10({32{1'b0}}), .in11({32{1'b0}}), .in12({32{1'b0}}), .in13({32{1'b0}}), .in14({32{1'b0}}),
    .in15({32{1'b0}}), .out(Result_2), .sel(AluOP));
  Multiplexer #(.select(4), .width(1), .disabled("Z"), .enable("false")) multiplexer_3 (
    .in0(1'b0), .in1(1'b0), .in2(1'b0), .in3(1'b0), .in4(1'b0), .in5(1'b0), .in6(1'b0), .in7(1'b0),
    .in8(1'b0), .in9(1'b0), .in10(1'b0), .in11(comparator_1_lt[0]), .in12(comparator_2_lt[0]), .in13(1'b0),
    .in14(1'b0), .in15(1'b0), .out(out_6), .sel(AluOP));
  not not_1 (out_4, out_6);

  // Other names for the same wires on the sheet: Result2[31:0] = Result_2; S[3:0] = AluOP; tunnel = out_6;
  //   tunnel_t = out_4

  // Notes on the sheet:
  //   不要改变此引脚区域内容，也不要改变ALU封装形式
  //   输入引脚
  //   输出引脚
endmodule

module Regifile (
  input  [31:0] Din,
  input  Clk,
  input  WE,
  input  [4:0] R2_num,
  input  [4:0] W_num,
  input  [4:0] R1_num,
  output [31:0] R1,
  output [31:0] R2
);

  // RegisterFile registerfile_1: pin names not known; wires that end beside it: Din, Clk, WE, W_num, R1_num, R2_num, R1, R2
endmodule

module \理想流水线  (
  output RegWrite,
  output MemWrite,
  output [31:0] IF_PC,
  output [31:0] ID_PC,
  output [31:0] EX_PC,
  output [31:0] M_PC,
  output [31:0] WB_PC,
  output [31:0] RDin,
  output [31:0] MDin,
  output [31:0] LedData
);

  wire alu_1_equal, alu_1_out_4, and_1_out, and_2_out, and_3_out, and_4_out, CLK, clock_1_out, clock_2_out,
       comparator_1_eq, comparator_1_lt, comparator_2_eq, d_ff_1_q, ecall, EX_halt, ex_mem_1_out_21,
       ex_mem_1_out_23, ex_mem_1_out_24, ex_mem_1_out_25, ex_mem_1_out_26, ex_mem_1_out_27, ex_mem_1_out_28,
       Go, halt, id_ex_1_out_33, id_ex_1_out_34, id_ex_1_out_35, id_ex_1_out_36, id_ex_1_out_37,
       id_ex_1_out_38, id_ex_1_out_40, id_ex_1_out_41, id_ex_1_out_42, id_ex_1_out_43, id_ex_1_out_44,
       id_ex_1_out_45, IR1, IR2, IR3, mem_wb_1_out_19, mem_wb_1_out_22, mem_wb_1_out_23, mem_wb_1_out_24,
       mem_wb_1_out_25, mem_wb_1_out_26, nand_1_out, not_1_out, not_2_out, not_3_out, not_4_out, not_5_out,
       not_6_out, or_1_out, or_2_out, RST, SB, W1, W2, W3, \单周期硬布线控制器_1_alu_src , \单周期硬布线控制器_1_auipc ,
       \单周期硬布线控制器_1_beq , \单周期硬布线控制器_1_bgeu , \单周期硬布线控制器_1_bne , \单周期硬布线控制器_1_jal , \单周期硬布线控制器_1_jalr ,
       \单周期硬布线控制器_1_memtoreg , \单周期硬布线控制器_1_memwrite , \单周期硬布线控制器_1_regwrite , \单周期硬布线控制器_1_s_type ,
       \单周期硬布线控制器_1_sb ;
  wire [1:0] priority_encoder_1_out, priority_encoder_2_out;
  wire [3:0] decoder_1_out0, id_ex_1_out_46, mips_ram_1_p4, \单周期硬布线控制器_1_alu_op ;
  wire [4:0] ex_mem_1_out_31, id_ex_1_out_47, multiplexer_2_out, multiplexer_3_out, WriteReg_num;
  wire [12:0] CNT_num;
  wire [15:0] \LoadUse次数 , \总周期数 , \插入气泡数 , \无条件分支数 , \条件分支成功数 ;
  wire [19:0] ex_mem_1_out_33_2;
  wire [31:0] adder_4_out, ALU_result, b_branch, bit_extender_1_out, bit_extender_2_out, bit_extender_3_out,
       bit_extender_4_out, bit_extender_5_out, EX_IR, ex_mem_1_out_32, ex_mem_1_out_33, ex_mem_1_out_34,
       ex_mem_1_out_37, id_ex_1_out_48, id_ex_1_out_49, id_ex_1_out_50, id_ex_1_out_51, id_ex_1_out_52,
       id_ex_1_out_53, id_ex_1_out_56, ID_IR, if_id_1_pc_4_2, IF_IR, jal_branch, MEM_IR, mem_wb_1_out_28,
       mem_wb_1_out_29, mem_wb_1_out_30, mem_wb_1_out_33, mips_ram_1_p8, multiplexer_1_out,
       multiplexer_4_out, multiplexer_5_out, PC_4, regifile_1_r1, regifile_1_r2, shifter_1_out,
       shifter_2_out, shifter_3_out, WB_IR;

  Button \u_总复位  (.out(RST));
  Button _1 (.out(IR1));
  Button _2 (.out(IR2));
  Button _3 (.out(IR3));
  // Probe on \总周期数 
  // Probe on \总周期数 
  Button \u_继续运行  (.out(Go));
  LED #(.active("true")) led_1 (.in(W1));
  LED #(.active("true")) led_2 (.in(W2));
  LED #(.active("true")) led_3 (.in(W3));
  Hex_Digit_Display hex_digit_display_1 (.value(LedData[31:28]));  // open: dp
  // Probe on IF_PC[19:0]
  // RiscV_Probe riscv_probe_1: pin names not known; wires that end beside it: IF_IR
  Hex_Digit_Display hex_digit_display_2 (.value(LedData[23:20]));  // open: dp
  Hex_Digit_Display hex_digit_display_3 (.value(LedData[27:24]));  // open: dp
  // Probe on ID_PC[19:0]
  // RiscV_Probe riscv_probe_2: pin names not known; wires that end beside it: ID_IR
  Hex_Digit_Display hex_digit_display_4 (.value(LedData[19:16]));  // open: dp
  Hex_Digit_Display hex_digit_display_5 (.value(LedData[15:12]));  // open: dp
  Hex_Digit_Display hex_digit_display_6 (.value(LedData[7:4]));  // open: dp
  Hex_Digit_Display hex_digit_display_7 (.value(LedData[11:8]));  // open: dp
  Clock #(.highDuration(1), .lowDuration(1)) clock_1 (.out(clock_1_out));
  // Probe on EX_PC[19:0]
  // RiscV_Probe riscv_probe_3: pin names not known; wires that end beside it: clock_1_out, EX_IR, CLK
  Multiplexer #(.select(2), .width(32), .disabled("Z"), .enable("false")) multiplexer_1 (
    .in0(PC_4), .in1(ALU_result), .in2(jal_branch), .in3(b_branch), .out(multiplexer_1_out),
    .sel(priority_encoder_1_out));
  Hex_Digit_Display hex_digit_display_8 (.value(LedData[3:0]));  // open: dp
  Register #(.width(32), .trigger("rising"), .Select("low")) PC (
    .D(multiplexer_1_out), .en(not_1_out), .Q(IF_PC), .clk(CLK), .clr(RST));
  not not_1 (not_1_out, halt);
  // Probe on \总周期数 
  // Probe on M_PC[19:0]
  // RiscV_Probe riscv_probe_4: pin names not known; wires that end beside it: MEM_IR
  // Probe on \总周期数 
  // Probe on \无条件分支数 
  // Probe on \条件分支成功数 
  // Probe on \插入气泡数 
  // Probe on \LoadUse次数 
  not not_2 (not_2_out, halt);
  Adder #(.width(32)) adder_1 (.a(IF_PC), .b(32'h4), .out(PC_4));  // open: cin, cout
  // Probe on IF_PC[11:0]
  // Probe on WB_PC[19:0]
  // RiscV_Probe riscv_probe_5: pin names not known; wires that end beside it: WB_IR
  Counter #(.width(16), .max('hffff), .ongoal("wrap"), .trigger("rising"), .behavior("new")) counter_1 (
    .count(not_2_out), .Q(\总周期数 ), .clk(CLK), .clr(RST));  // open: load, D, carry, preset, down
  // RiscV_Probe riscv_probe_6: pin names not known; wires that end beside it: IF_IR, CLK
  ROM #(.addrWidth(10), .dataWidth(32), .Select("high")) rom_1 (.addr(IF_PC[11:2]), .data(IF_IR));
  // Probe on ID_PC[11:0]
  // Probe on EX_PC[11:0]
  IF_ID if_id_1 (
    .IR(IF_IR), .PC(IF_PC), .PC_4(PC_4), .IR_2(ID_IR), .PC_2(ID_PC), .PC_4_2(if_id_1_pc_4_2),
    .BranchTaken(1'b0), .en(not_3_out), .clk(CLK), .reset(1'b0));  // open: PredictJump, out_9
  not not_3 (not_3_out, halt);
  // Probe on M_PC[11:0]
  D_Flip_Flop #(.trigger("high"), .Pre_Clr_Positions("LEGACY"), .NegatePresetClear("false"), .enable("true"), .NewFFLayout("false")) d_ff_1 (.Q(d_ff_1_q));  // open: clk, D, Qn, preset, en, reset
  // Probe on 13'hc
  // Probe on WB_PC[11:0]
  Comparator #(.width(13), .mode("twosComplement")) comparator_1 (
    .a(CNT_num), .b(13'hc), .eq(comparator_1_eq), .lt(comparator_1_lt));  // open: gt
  Clock #(.highDuration(1), .lowDuration(1)) clock_2 (.out(clock_2_out));
  nand nand_1 (nand_1_out, d_ff_1_q, comparator_1_eq);
  Counter #(.width(13), .max('h1fff), .ongoal("stay"), .trigger("rising"), .behavior("old")) counter_2 (
    .count(comparator_1_lt), .Q(CNT_num), .clk(clock_2_out));  // open: load, D, carry, clr, preset
  \单周期硬布线控制器  \u_单周期硬布线控制器_1  (
    .Funct({ID_IR[30], ID_IR[25], ID_IR[14:12]}), .OP(ID_IR[6:2]), .ALU_OP(\单周期硬布线控制器_1_alu_op ),
    .MemToReg(\单周期硬布线控制器_1_memtoreg ), .MemWrite(\单周期硬布线控制器_1_memwrite ), .ALU_SRC(\单周期硬布线控制器_1_alu_src ),
    .RegWrite(\单周期硬布线控制器_1_regwrite ), .ecall(ecall), .S_type(\单周期硬布线控制器_1_s_type ),
    .Jalr(\单周期硬布线控制器_1_jalr ), .Beq(\单周期硬布线控制器_1_beq ), .JAL(\单周期硬布线控制器_1_jal ), .Bne(\单周期硬布线控制器_1_bne ),
    .in_3(ID_IR[21]), .AUIPC(\单周期硬布线控制器_1_auipc ), .BGEU(\单周期硬布线控制器_1_bgeu ), .SB(\单周期硬布线控制器_1_sb ));  // open: uret, Rs1used, Rs2used, CSRRSI, CSRRCI
  Multiplexer #(.select(1), .width(5), .disabled("Z"), .enable("false")) multiplexer_2 (
    .in0(ID_IR[19:15]), .in1(5'b10001), .out(multiplexer_2_out), .sel(ecall));
  Multiplexer #(.select(1), .width(5), .disabled("Z"), .enable("false")) multiplexer_3 (
    .in0(ID_IR[24:20]), .in1(5'b01010), .out(multiplexer_3_out), .sel(ecall));
  assign bit_extender_1_out = {{20{ID_IR[31]}}, ID_IR[31:20]};  // Bit_Extender bit_extender_1
  assign bit_extender_2_out = {{20{ID_IR[31]}}, {ID_IR[31:25], ID_IR[11:7]}};  // Bit_Extender bit_extender_2
  assign bit_extender_3_out = {{20{ID_IR[31]}}, {ID_IR[31], ID_IR[7], ID_IR[30:25], ID_IR[11:8]}};  // Bit_Extender bit_extender_3
  assign bit_extender_4_out = {{12{ID_IR[31]}}, {ID_IR[31], ID_IR[19:12], ID_IR[20], ID_IR[30:21]}};  // Bit_Extender bit_extender_4
  assign bit_extender_5_out = {{12{ID_IR[31]}}, ID_IR[31:12]};  // Bit_Extender bit_extender_5
  assign CLK = nand_1_out ? clock_2_out : 1'bz;  // Controlled_Buffer controlled_buffer_1
  Multiplexer #(.select(1), .width(32), .disabled("Z"), .enable("false")) multiplexer_4 (
    .in0(bit_extender_1_out), .in1(bit_extender_2_out), .out(multiplexer_4_out), .sel(\单周期硬布线控制器_1_s_type ));
  Pull_Resistor #(.pull(1)) pull_resistor_1 (.node(CLK));
  Regifile regifile_1 (
    .Din(RDin), .Clk(CLK), .R1(regifile_1_r1), .R2(regifile_1_r2), .WE(RegWrite), .W_num(WriteReg_num),
    .R1_num(multiplexer_2_out), .R2_num(multiplexer_3_out));
  not not_4 (not_4_out, halt);
  ID_EX id_ex_1 (
    .BEQ(\单周期硬布线控制器_1_beq ), .BNE(\单周期硬布线控制器_1_bne ), .MEMTOREG(\单周期硬布线控制器_1_memtoreg ),
    .MEMWRITE(\单周期硬布线控制器_1_memwrite ), .ALUSRCB(\单周期硬布线控制器_1_alu_src ), .REGWRITE(\单周期硬布线控制器_1_regwrite ),
    .ECALL(ecall), .JAL(\单周期硬布线控制器_1_jal ), .JALR(\单周期硬布线控制器_1_jalr ), .AUIPC(\单周期硬布线控制器_1_auipc ),
    .BGEU(\单周期硬布线控制器_1_bgeu ), .SB(\单周期硬布线控制器_1_sb ), .ALUop(\单周期硬布线控制器_1_alu_op ), .rd(ID_IR[11:7]),
    .R1(regifile_1_r1), .R2(regifile_1_r2), .imm1(multiplexer_4_out), .imm2(bit_extender_3_out),
    .imm3(bit_extender_5_out), .IR(ID_IR), .PC(ID_PC), .PC_4(if_id_1_pc_4_2), .out_33(id_ex_1_out_33),
    .out_34(id_ex_1_out_34), .out_35(id_ex_1_out_35), .out_36(id_ex_1_out_36), .out_37(id_ex_1_out_37),
    .out_38(id_ex_1_out_38), .out_40(id_ex_1_out_40), .out_41(id_ex_1_out_41), .out_42(id_ex_1_out_42),
    .out_43(id_ex_1_out_43), .out_44(id_ex_1_out_44), .out_45(id_ex_1_out_45), .out_46(id_ex_1_out_46),
    .out_47(id_ex_1_out_47), .out_49(id_ex_1_out_49), .out_50(id_ex_1_out_50), .out_51(id_ex_1_out_51),
    .out_52(id_ex_1_out_52), .out_53(id_ex_1_out_53), .out_54(EX_IR), .out_55(EX_PC),
    .out_56(id_ex_1_out_56), .flush(1'b0), .en(not_4_out), .clk(CLK), .imm4(bit_extender_4_out),
    .out_48(id_ex_1_out_48), .reset(1'b0));  // open: Rs1Forward, out_57, Rs2Forward, out_58, URET, out_39, PredictJump, out_32
  Priority_Encoder #(.select(2), .disabled("Z")) priority_encoder_1 (
    .in0(1'b1), .in1(id_ex_1_out_42), .in2(id_ex_1_out_41), .in3(or_1_out), .out(priority_encoder_1_out));  // open: gs, en_out, en_in
  Multiplexer #(.select(1), .width(32), .disabled("Z"), .enable("false")) multiplexer_5 (
    .in0(id_ex_1_out_50), .in1(id_ex_1_out_51), .out(multiplexer_5_out), .sel(id_ex_1_out_37));
  Shifter #(.width(32), .shift("ll")) shifter_1 (.in(id_ex_1_out_52), .\dist (5'b00001), .out(shifter_1_out));
  Shifter #(.width(32), .shift("ll")) shifter_2 (.in(id_ex_1_out_48), .\dist (5'b00001), .out(shifter_2_out));
  Shifter #(.width(32), .shift("ll")) shifter_3 (.in(id_ex_1_out_53), .\dist (5'b01100), .out(shifter_3_out));
  Comparator #(.width(32), .mode("twosComplement")) comparator_2 (
    .a(32'h22), .b(id_ex_1_out_49), .eq(comparator_2_eq));  // open: gt, lt
  or or_1 (or_1_out, and_1_out, and_2_out, and_4_out);
  and and_1 (and_1_out, id_ex_1_out_33, alu_1_equal);
  and and_2 (and_2_out, id_ex_1_out_34, ~alu_1_equal);  // AND_Gate
  ALU alu_1 (
    .X(id_ex_1_out_49), .Y(multiplexer_5_out), .AluOP(id_ex_1_out_46), .Equal(alu_1_equal),
    .Result(ALU_result), .out_4(alu_1_out_4));  // open: Result_2, out_6
  Adder #(.width(32)) adder_2 (.a(shifter_1_out), .b(EX_PC), .out(b_branch));  // open: cin, cout
  Adder #(.width(32)) adder_3 (.a(shifter_2_out), .b(EX_PC), .out(jal_branch));  // open: cin, cout
  Adder #(.width(32)) adder_4 (.a(shifter_3_out), .b(EX_PC), .out(adder_4_out));  // open: cin, cout
  and and_3 (and_3_out, comparator_2_eq, id_ex_1_out_40);
  and and_4 (and_4_out, id_ex_1_out_44, alu_1_out_4);
  Register #(.width(32), .trigger("rising"), .Select("low")) register_1 (
    .D(id_ex_1_out_50), .en(and_3_out), .Q(LedData), .clk(CLK), .clr(RST));
  and and_5 (EX_halt, ~comparator_2_eq, id_ex_1_out_40);  // AND_Gate
  EX_MEM ex_mem_1 (
    .MEMTOREG(id_ex_1_out_35), .MEMWRITE(id_ex_1_out_36), .REGWRITE(id_ex_1_out_38), .HALT(EX_halt),
    .ECALL(id_ex_1_out_40), .JAL(id_ex_1_out_41), .JALR(id_ex_1_out_42), .AUIPC(id_ex_1_out_43),
    .SB(id_ex_1_out_45), .rd(id_ex_1_out_47), .R2(id_ex_1_out_50), .Result(ALU_result), .imm3(adder_4_out),
    .IR(EX_IR), .PC(EX_PC), .PC_4(id_ex_1_out_56), .out_21(ex_mem_1_out_21), .out_22(MemWrite),
    .out_23(ex_mem_1_out_23), .out_24(ex_mem_1_out_24), .out_25(ex_mem_1_out_25), .out_26(ex_mem_1_out_26),
    .out_27(ex_mem_1_out_27), .out_28(ex_mem_1_out_28), .out_30(SB), .out_31(ex_mem_1_out_31),
    .out_32(ex_mem_1_out_32), .out_33({ex_mem_1_out_33[31:22], ex_mem_1_out_33_2, ex_mem_1_out_33[1:0]}),
    .out_34(ex_mem_1_out_34), .out_35(MEM_IR), .out_36(M_PC), .out_37(ex_mem_1_out_37), .reset(1'b0),
    .en(not_5_out), .clk(CLK));  // open: out_29, URET
  not not_5 (not_5_out, halt);
  Multiplexer #(.select(1), .width(32), .disabled("Z"), .enable("false")) multiplexer_6 (
    .in0(ex_mem_1_out_32),
    .in1({ex_mem_1_out_32[7:0], ex_mem_1_out_32[7:0], ex_mem_1_out_32[7:0], ex_mem_1_out_32[7:0]}),
    .out(MDin), .sel(SB));
  Decoder #(.select(2), .tristate("false"), .disabled("Z"), .enable("false")) decoder_1 (
    .out0(decoder_1_out0[0]), .out1(decoder_1_out0[1]), .out2(decoder_1_out0[2]), .out3(decoder_1_out0[3]),
    .sel(ex_mem_1_out_33[1:0]));
  // MIPS_RAM mips_ram_1: pin names not known; wires that end beside it: ex_mem_1_out_33_2, MDin, MemWrite, mips_ram_1_p4, CLK, 1'b1, RST, mips_ram_1_p8
  Multiplexer #(.select(1), .width(4), .disabled("Z"), .enable("false")) multiplexer_7 (
    .in0(4'b1111), .in1(decoder_1_out0), .out(mips_ram_1_p4), .sel(SB));
  MEM_WB mem_wb_1 (
    .MEMTOREG(ex_mem_1_out_21), .REGWRITE(ex_mem_1_out_23), .HALT(ex_mem_1_out_24), .ECALL(ex_mem_1_out_25),
    .JAL(ex_mem_1_out_26), .JALR(ex_mem_1_out_27), .AUIPC(ex_mem_1_out_28), .rd(ex_mem_1_out_31),
    .Result({ex_mem_1_out_33[31:22], ex_mem_1_out_33_2, ex_mem_1_out_33[1:0]}), .data(mips_ram_1_p8),
    .imm3(ex_mem_1_out_34), .IR(MEM_IR), .PC(M_PC), .PC_4(ex_mem_1_out_37), .out_19(mem_wb_1_out_19),
    .out_21(RegWrite), .out_22(mem_wb_1_out_22), .out_23(mem_wb_1_out_23), .out_24(mem_wb_1_out_24),
    .out_25(mem_wb_1_out_25), .out_26(mem_wb_1_out_26), .out_27(WriteReg_num), .out_28(mem_wb_1_out_28),
    .out_29(mem_wb_1_out_29), .out_30(mem_wb_1_out_30), .out_31(WB_IR), .out_32(WB_PC),
    .out_33(mem_wb_1_out_33), .reset(1'b0), .en(not_6_out), .clk(CLK));  // open: URET, out_20
  not not_6 (not_6_out, halt);
  or or_2 (or_2_out, mem_wb_1_out_24, mem_wb_1_out_25);
  D_Flip_Flop #(.trigger("high"), .Pre_Clr_Positions("LEGACY"), .NegatePresetClear("false"), .enable("true"), .NewFFLayout("false")) d_ff_2 (
    .clk(mem_wb_1_out_22), .D(1'b1), .Q(halt), .en(mem_wb_1_out_23), .reset(Go));  // open: Qn, preset
  Multiplexer #(.select(2), .width(32), .disabled("Z"), .enable("false")) multiplexer_8 (
    .in0(mem_wb_1_out_28), .in1(mem_wb_1_out_29), .in2(mem_wb_1_out_33), .in3(mem_wb_1_out_30), .out(RDin),
    .sel(priority_encoder_2_out));
  Priority_Encoder #(.select(2), .disabled("Z")) priority_encoder_2 (
    .in0(1'b1), .in1(mem_wb_1_out_19), .in2(or_2_out), .in3(mem_wb_1_out_26), .out(priority_encoder_2_out));  // open: gs, en_out, en_in

  // Other names for the same wires on the sheet: MEM_PC[31:0] = M_PC

  // Notes on the sheet:
  //   中断源
  //   时空图监测，可删除
  //   中断等待指示
  //   数码管输出
  //   指令存储器
  //   指令探针
  //   contents of rom_1 (hex, n*v repeats v):
  //   413 493 913 993 46413 14e493 296913 39e993 842023 942223 1242423 1342623 a00893 493 913 993 73
  //   控制位
  //   流水调试日志用
  //   暂停节拍，不能为0
  //   戳工具置1进入计数暂停模式，ctrl+k时钟自动运行到对应节拍暂停
  //   ctrl+k关闭时钟连续运行，将控制位置零，进入单步调试模式调试
  //   用这个时钟源需要去掉电路中的其他时钟源
  //   Beq
  //   Bne
  //   MemToReg
  //   MemWrite
  //   AluOP
  //   AluSrcB
  //   RegWrite
  //   可计数暂停的时钟源
  //   为方便自动评测，需要输出流水线各段保存的PC值，注意是PC不是PC+4，另外ID段寄存器写入信息，Mem段内存写入信息也要输出
endmodule

module \气泡流水线  (
  output RegWrite,
  output MemWrite,
  output [31:0] IF_PC,
  output [31:0] ID_PC,
  output [31:0] EX_PC,
  output [31:0] M_PC,
  output [31:0] WB_PC,
  output [31:0] RDin,
  output [31:0] MDin,
  output [31:0] LedData
);

  wire alu_1_equal, alu_1_out_4, and_1_out, and_2_out, and_3_out, and_4_out, and_5_out, and_7_out, and_8_out,
       CLK, clock_1_out, clock_2_out, comparator_1_eq, comparator_1_lt, comparator_2_eq, d_ff_1_q, ecall,
       EX_halt, ex_mem_1_out_21, ex_mem_1_out_23, ex_mem_1_out_24, ex_mem_1_out_25, ex_mem_1_out_26,
       ex_mem_1_out_27, ex_mem_1_out_28, Go, halt, id_ex_1_out_33, id_ex_1_out_34, id_ex_1_out_35,
       id_ex_1_out_36, id_ex_1_out_37, id_ex_1_out_38, id_ex_1_out_40, id_ex_1_out_41, id_ex_1_out_42,
       id_ex_1_out_43, id_ex_1_out_44, id_ex_1_out_45, IR1, IR2, IR3, mem_wb_1_out_19, mem_wb_1_out_22,
       mem_wb_1_out_23, mem_wb_1_out_24, mem_wb_1_out_25, mem_wb_1_out_26, multiplexer_2_out,
       multiplexer_7_out, multiplexer_9_out, nand_1_out, nor_1_out, nor_2_out, not_1_out, not_2_out,
       not_3_out, not_4_out, not_5_out, not_6_out, not_7_out, not_8_out, or_1_out, or_2_out, or_3_out,
       or_4_out, RST, SB, stall, W1, W2, W3, \单周期硬布线控制器_1_alu_src , \单周期硬布线控制器_1_auipc , \单周期硬布线控制器_1_beq ,
       \单周期硬布线控制器_1_bgeu , \单周期硬布线控制器_1_bne , \单周期硬布线控制器_1_jal , \单周期硬布线控制器_1_jalr , \单周期硬布线控制器_1_memtoreg ,
       \单周期硬布线控制器_1_memwrite , \单周期硬布线控制器_1_regwrite , \单周期硬布线控制器_1_rs1used , \单周期硬布线控制器_1_rs2used ,
       \单周期硬布线控制器_1_s_type , \单周期硬布线控制器_1_sb , \气泡数据相关检测逻辑_1_flush ;
  wire [1:0] priority_encoder_1_out, priority_encoder_2_out;
  wire [3:0] decoder_1_out0, id_ex_1_out_46, mips_ram_1_p4, \单周期硬布线控制器_1_alu_op ;
  wire [4:0] ex_mem_1_out_31, id_ex_1_out_47, multiplexer_3_out, multiplexer_4_out, WriteReg_num;
  wire [12:0] CNT_num;
  wire [15:0] \LoadUse次数 , \总周期数 , \插入气泡数 , \无条件分支数 , \条件分支成功数 ;
  wire [19:0] ex_mem_1_out_33_2;
  wire [31:0] adder_4_out, ALU_result, b_branch, bit_extender_1_out, bit_extender_2_out, bit_extender_3_out,
       bit_extender_4_out, bit_extender_5_out, EX_IR, ex_mem_1_out_32, ex_mem_1_out_33, ex_mem_1_out_34,
       ex_mem_1_out_37, id_ex_1_out_48, id_ex_1_out_49, id_ex_1_out_50, id_ex_1_out_51, id_ex_1_out_52,
       id_ex_1_out_53, id_ex_1_out_56, ID_IR, if_id_1_pc_4_2, IF_IR, jal_branch, MEM_IR, mem_wb_1_out_28,
       mem_wb_1_out_29, mem_wb_1_out_30, mem_wb_1_out_33, mips_ram_1_p8, multiplexer_1_out,
       multiplexer_5_out, multiplexer_6_out, PC_4, regifile_1_r1, regifile_1_r2, shifter_1_out,
       shifter_2_out, shifter_3_out, WB_IR;

  Button \u_总复位  (.out(RST));
  Button _1 (.out(IR1));
  Button _2 (.out(IR2));
  Button _3 (.out(IR3));
  // Probe on \总周期数 
  // Probe on \总周期数 
  Button \u_继续运行  (.out(Go));
  LED #(.active("true")) led_1 (.in(W1));
  LED #(.active("true")) led_2 (.in(W2));
  LED #(.active("true")) led_3 (.in(W3));
  Hex_Digit_Display hex_digit_display_1 (.value(LedData[31:28]));  // open: dp
  // Probe on IF_PC[19:0]
  // RiscV_Probe riscv_probe_1: pin names not known; wires that end beside it: IF_IR
  Hex_Digit_Display hex_digit_display_2 (.value(LedData[23:20]));  // open: dp
  Hex_Digit_Display hex_digit_display_3 (.value(LedData[27:24]));  // open: dp
  // Probe on ID_PC[19:0]
  // RiscV_Probe riscv_probe_2: pin names not known; wires that end beside it: ID_IR
  Hex_Digit_Display hex_digit_display_4 (.value(LedData[19:16]));  // open: dp
  Hex_Digit_Display hex_digit_display_5 (.value(LedData[15:12]));  // open: dp
  Hex_Digit_Display hex_digit_display_6 (.value(LedData[11:8]));  // open: dp
  Hex_Digit_Display hex_digit_display_7 (.value(LedData[7:4]));  // open: dp
  Clock #(.highDuration(1), .lowDuration(1)) clock_1 (.out(clock_1_out));
  // Probe on EX_PC[19:0]
  // RiscV_Probe riscv_probe_3: pin names not known; wires that end beside it: clock_1_out, EX_IR, CLK
  Multiplexer #(.select(2), .width(32), .disabled("Z"), .enable("false")) multiplexer_1 (
    .in0(PC_4), .in1(ALU_result), .in2(jal_branch), .in3(b_branch), .out(multiplexer_1_out),
    .sel(priority_encoder_1_out));
  Hex_Digit_Display hex_digit_display_8 (.value(LedData[3:0]));  // open: dp
  \气泡数据相关检测逻辑  \u_气泡数据相关检测逻辑_1  (
    .in_1(ID_IR), .BranchTaken(or_1_out), .ecall(ecall), .rs1used(\单周期硬布线控制器_1_rs1used ),
    .rs2used(\单周期硬布线控制器_1_rs2used ), .EX_RegWrite(id_ex_1_out_38), .MEM_RegWrite(ex_mem_1_out_23),
    .EX_WriteReg_num(id_ex_1_out_47), .MEM_WriteReg_num(ex_mem_1_out_31), .stall(stall),
    .flush(\气泡数据相关检测逻辑_1_flush ));
  nor nor_1 (nor_1_out, halt, stall);
  Register #(.width(32), .trigger("rising"), .Select("low")) PC (
    .D(multiplexer_1_out), .en(nor_1_out), .Q(IF_PC), .clk(CLK), .clr(RST));
  // Probe on \总周期数 
  // Probe on M_PC[19:0]
  // RiscV_Probe riscv_probe_4: pin names not known; wires that end beside it: MEM_IR
  not not_1 (not_1_out, halt);
  and and_1 (and_1_out, stall, CLK);
  // Probe on \总周期数 
  // Probe on \无条件分支数 
  // Probe on \条件分支成功数 
  // Probe on \插入气泡数 
  // Probe on \LoadUse次数 
  Counter #(.width(16), .max('hffff), .ongoal("wrap"), .trigger("rising"), .behavior("new")) counter_1 (
    .count(not_1_out), .Q(\插入气泡数 ), .clk(multiplexer_2_out), .clr(RST));  // open: load, D, carry, preset, down
  Multiplexer #(.select(1), .width(1), .disabled("Z"), .enable("false")) multiplexer_2 (
    .in0(and_1_out), .in1(1'b0), .out(multiplexer_2_out), .sel(CLK));
  not not_2 (not_2_out, halt);
  Adder #(.width(32)) adder_1 (.a(IF_PC), .b(32'h4), .out(PC_4));  // open: cin, cout
  // Probe on IF_PC[11:0]
  // Probe on WB_PC[19:0]
  // RiscV_Probe riscv_probe_5: pin names not known; wires that end beside it: WB_IR
  Counter #(.width(16), .max('hffff), .ongoal("wrap"), .trigger("rising"), .behavior("new")) counter_2 (
    .count(not_2_out), .Q(\总周期数 ), .clk(CLK), .clr(RST));  // open: load, D, carry, preset, down
  // RiscV_Probe riscv_probe_6: pin names not known; wires that end beside it: IF_IR, CLK
  ROM #(.addrWidth(10), .dataWidth(32), .Select("high")) rom_1 (.addr(IF_PC[11:2]), .data(IF_IR));
  // Probe on ID_PC[11:0]
  // Probe on EX_PC[11:0]
  IF_ID if_id_1 (
    .IR(IF_IR), .PC(IF_PC), .PC_4(PC_4), .IR_2(ID_IR), .PC_2(ID_PC), .PC_4_2(if_id_1_pc_4_2),
    .BranchTaken(or_1_out), .en(nor_2_out), .clk(CLK), .reset(1'b0));  // open: PredictJump, out_9
  nor nor_2 (nor_2_out, stall, halt);
  // Probe on M_PC[11:0]
  D_Flip_Flop #(.trigger("high"), .Pre_Clr_Positions("LEGACY"), .NegatePresetClear("false"), .enable("true"), .NewFFLayout("false")) d_ff_1 (.Q(d_ff_1_q));  // open: clk, D, Qn, preset, en, reset
  // Probe on 13'h58
  // Probe on WB_PC[11:0]
  Comparator #(.width(13), .mode("twosComplement")) comparator_1 (
    .a(CNT_num), .b(13'h58), .eq(comparator_1_eq), .lt(comparator_1_lt));  // open: gt
  Clock #(.highDuration(1), .lowDuration(1)) clock_2 (.out(clock_2_out));
  nand nand_1 (nand_1_out, d_ff_1_q, comparator_1_eq);
  Counter #(.width(13), .max('h1fff), .ongoal("stay"), .trigger("rising"), .behavior("old")) counter_3 (
    .count(comparator_1_lt), .Q(CNT_num), .clk(clock_2_out));  // open: load, D, carry, clr, preset
  \单周期硬布线控制器  \u_单周期硬布线控制器_1  (
    .Funct({ID_IR[30], ID_IR[25], ID_IR[14:12]}), .OP(ID_IR[6:2]), .ALU_OP(\单周期硬布线控制器_1_alu_op ),
    .MemToReg(\单周期硬布线控制器_1_memtoreg ), .MemWrite(\单周期硬布线控制器_1_memwrite ), .ALU_SRC(\单周期硬布线控制器_1_alu_src ),
    .RegWrite(\单周期硬布线控制器_1_regwrite ), .ecall(ecall), .S_type(\单周期硬布线控制器_1_s_type ),
    .Jalr(\单周期硬布线控制器_1_jalr ), .Beq(\单周期硬布线控制器_1_beq ), .JAL(\单周期硬布线控制器_1_jal ), .Bne(\单周期硬布线控制器_1_bne ),
    .in_3(ID_IR[21]), .AUIPC(\单周期硬布线控制器_1_auipc ), .BGEU(\单周期硬布线控制器_1_bgeu ), .SB(\单周期硬布线控制器_1_sb ),
    .Rs1used(\单周期硬布线控制器_1_rs1used ), .Rs2used(\单周期硬布线控制器_1_rs2used ));  // open: uret, CSRRSI, CSRRCI
  Multiplexer #(.select(1), .width(5), .disabled("Z"), .enable("false")) multiplexer_3 (
    .in0(ID_IR[19:15]), .in1(5'b10001), .out(multiplexer_3_out), .sel(ecall));
  Multiplexer #(.select(1), .width(5), .disabled("Z"), .enable("false")) multiplexer_4 (
    .in0(ID_IR[24:20]), .in1(5'b01010), .out(multiplexer_4_out), .sel(ecall));
  assign bit_extender_1_out = {{20{ID_IR[31]}}, ID_IR[31:20]};  // Bit_Extender bit_extender_1
  assign bit_extender_2_out = {{20{ID_IR[31]}}, {ID_IR[31:25], ID_IR[11:7]}};  // Bit_Extender bit_extender_2
  assign bit_extender_3_out = {{20{ID_IR[31]}}, {ID_IR[31], ID_IR[7], ID_IR[30:25], ID_IR[11:8]}};  // Bit_Extender bit_extender_3
  assign bit_extender_4_out = {{12{ID_IR[31]}}, {ID_IR[31], ID_IR[19:12], ID_IR[20], ID_IR[30:21]}};  // Bit_Extender bit_extender_4
  assign bit_extender_5_out = {{12{ID_IR[31]}}, ID_IR[31:12]};  // Bit_Extender bit_extender_5
  assign CLK = nand_1_out ? clock_2_out : 1'bz;  // Controlled_Buffer controlled_buffer_1
  Multiplexer #(.select(1), .width(32), .disabled("Z"), .enable("false")) multiplexer_5 (
    .in0(bit_extender_1_out), .in1(bit_extender_2_out), .out(multiplexer_5_out), .sel(\单周期硬布线控制器_1_s_type ));
  Pull_Resistor #(.pull(1)) pull_resistor_1 (.node(CLK));
  not not_3 (not_3_out, CLK);
  Regifile regifile_1 (
    .Din(RDin), .Clk(not_3_out), .R1(regifile_1_r1), .R2(regifile_1_r2), .WE(RegWrite), .W_num(WriteReg_num),
    .R1_num(multiplexer_3_out), .R2_num(multiplexer_4_out));
  not not_4 (not_4_out, halt);
  ID_EX id_ex_1 (
    .BEQ(\单周期硬布线控制器_1_beq ), .BNE(\单周期硬布线控制器_1_bne ), .MEMTOREG(\单周期硬布线控制器_1_memtoreg ),
    .MEMWRITE(\单周期硬布线控制器_1_memwrite ), .ALUSRCB(\单周期硬布线控制器_1_alu_src ), .REGWRITE(\单周期硬布线控制器_1_regwrite ),
    .ECALL(ecall), .JAL(\单周期硬布线控制器_1_jal ), .JALR(\单周期硬布线控制器_1_jalr ), .AUIPC(\单周期硬布线控制器_1_auipc ),
    .BGEU(\单周期硬布线控制器_1_bgeu ), .SB(\单周期硬布线控制器_1_sb ), .ALUop(\单周期硬布线控制器_1_alu_op ), .rd(ID_IR[11:7]),
    .R1(regifile_1_r1), .R2(regifile_1_r2), .imm1(multiplexer_5_out), .imm2(bit_extender_3_out),
    .imm3(bit_extender_5_out), .IR(ID_IR), .PC(ID_PC), .PC_4(if_id_1_pc_4_2), .out_33(id_ex_1_out_33),
    .out_34(id_ex_1_out_34), .out_35(id_ex_1_out_35), .out_36(id_ex_1_out_36), .out_37(id_ex_1_out_37),
    .out_38(id_ex_1_out_38), .out_40(id_ex_1_out_40), .out_41(id_ex_1_out_41), .out_42(id_ex_1_out_42),
    .out_43(id_ex_1_out_43), .out_44(id_ex_1_out_44), .out_45(id_ex_1_out_45), .out_46(id_ex_1_out_46),
    .out_47(id_ex_1_out_47), .out_49(id_ex_1_out_49), .out_50(id_ex_1_out_50), .out_51(id_ex_1_out_51),
    .out_52(id_ex_1_out_52), .out_53(id_ex_1_out_53), .out_54(EX_IR), .out_55(EX_PC),
    .out_56(id_ex_1_out_56), .flush(\气泡数据相关检测逻辑_1_flush ), .en(not_4_out), .clk(CLK),
    .imm4(bit_extender_4_out), .out_48(id_ex_1_out_48), .reset(1'b0));  // open: Rs1Forward, out_57, Rs2Forward, out_58, URET, out_39, PredictJump, out_32
  or or_1 (or_1_out, or_2_out, id_ex_1_out_41, id_ex_1_out_42);
  Multiplexer #(.select(1), .width(32), .disabled("Z"), .enable("false")) multiplexer_6 (
    .in0(id_ex_1_out_50), .in1(id_ex_1_out_51), .out(multiplexer_6_out), .sel(id_ex_1_out_37));
  Shifter #(.width(32), .shift("ll")) shifter_1 (.in(id_ex_1_out_52), .\dist (5'b00001), .out(shifter_1_out));
  Shifter #(.width(32), .shift("ll")) shifter_2 (.in(id_ex_1_out_48), .\dist (5'b00001), .out(shifter_2_out));
  Shifter #(.width(32), .shift("ll")) shifter_3 (.in(id_ex_1_out_53), .\dist (5'b01100), .out(shifter_3_out));
  Comparator #(.width(32), .mode("twosComplement")) comparator_2 (
    .a(32'h22), .b(id_ex_1_out_49), .eq(comparator_2_eq));  // open: gt, lt
  or or_2 (or_2_out, and_2_out, and_3_out, and_5_out);
  and and_2 (and_2_out, id_ex_1_out_33, alu_1_equal);
  and and_3 (and_3_out, id_ex_1_out_34, ~alu_1_equal);  // AND_Gate
  ALU alu_1 (
    .X(id_ex_1_out_49), .Y(multiplexer_6_out), .AluOP(id_ex_1_out_46), .Equal(alu_1_equal),
    .Result(ALU_result), .out_4(alu_1_out_4));  // open: Result_2, out_6
  Adder #(.width(32)) adder_2 (.a(shifter_1_out), .b(EX_PC), .out(b_branch));  // open: cin, cout
  Adder #(.width(32)) adder_3 (.a(shifter_2_out), .b(EX_PC), .out(jal_branch));  // open: cin, cout
  Adder #(.width(32)) adder_4 (.a(shifter_3_out), .b(EX_PC), .out(adder_4_out));  // open: cin, cout
  and and_4 (and_4_out, comparator_2_eq, id_ex_1_out_40);
  and and_5 (and_5_out, id_ex_1_out_44, alu_1_out_4);
  Register #(.width(32), .trigger("rising"), .Select("low")) register_1 (
    .D(id_ex_1_out_50), .en(and_4_out), .Q(LedData), .clk(CLK), .clr(RST));
  and and_6 (EX_halt, ~comparator_2_eq, id_ex_1_out_40);  // AND_Gate
  Priority_Encoder #(.select(2), .disabled("Z")) priority_encoder_1 (
    .in0(1'b1), .in1(id_ex_1_out_42), .in2(id_ex_1_out_41), .in3(or_2_out), .out(priority_encoder_1_out));  // open: gs, en_out, en_in
  and and_7 (and_7_out, or_2_out, CLK);
  EX_MEM ex_mem_1 (
    .MEMTOREG(id_ex_1_out_35), .MEMWRITE(id_ex_1_out_36), .REGWRITE(id_ex_1_out_38), .HALT(EX_halt),
    .ECALL(id_ex_1_out_40), .JAL(id_ex_1_out_41), .JALR(id_ex_1_out_42), .AUIPC(id_ex_1_out_43),
    .SB(id_ex_1_out_45), .rd(id_ex_1_out_47), .R2(id_ex_1_out_50), .Result(ALU_result), .imm3(adder_4_out),
    .IR(EX_IR), .PC(EX_PC), .PC_4(id_ex_1_out_56), .out_21(ex_mem_1_out_21), .out_22(MemWrite),
    .out_23(ex_mem_1_out_23), .out_24(ex_mem_1_out_24), .out_25(ex_mem_1_out_25), .out_26(ex_mem_1_out_26),
    .out_27(ex_mem_1_out_27), .out_28(ex_mem_1_out_28), .out_30(SB), .out_31(ex_mem_1_out_31),
    .out_32(ex_mem_1_out_32), .out_33({ex_mem_1_out_33[31:22], ex_mem_1_out_33_2, ex_mem_1_out_33[1:0]}),
    .out_34(ex_mem_1_out_34), .out_35(MEM_IR), .out_36(M_PC), .out_37(ex_mem_1_out_37), .reset(1'b0),
    .en(not_5_out), .clk(CLK));  // open: out_29, URET
  not not_5 (not_5_out, halt);
  not not_6 (not_6_out, halt);
  Multiplexer #(.select(1), .width(1), .disabled("Z"), .enable("false")) multiplexer_7 (
    .in0(and_7_out), .in1(1'b0), .out(multiplexer_7_out), .sel(CLK));
  Counter #(.width(16), .max('hffff), .ongoal("wrap"), .trigger("rising"), .behavior("new")) counter_4 (
    .count(not_6_out), .Q(\条件分支成功数 ), .clk(multiplexer_7_out), .clr(RST));  // open: load, D, carry, preset, down
  not not_7 (not_7_out, halt);
  and and_8 (and_8_out, or_3_out, CLK);
  or or_3 (or_3_out, id_ex_1_out_41, id_ex_1_out_42);
  Multiplexer #(.select(1), .width(32), .disabled("Z"), .enable("false")) multiplexer_8 (
    .in0(ex_mem_1_out_32),
    .in1({ex_mem_1_out_32[7:0], ex_mem_1_out_32[7:0], ex_mem_1_out_32[7:0], ex_mem_1_out_32[7:0]}),
    .out(MDin), .sel(SB));
  Decoder #(.select(2), .tristate("false"), .disabled("Z"), .enable("false")) decoder_1 (
    .out0(decoder_1_out0[0]), .out1(decoder_1_out0[1]), .out2(decoder_1_out0[2]), .out3(decoder_1_out0[3]),
    .sel(ex_mem_1_out_33[1:0]));
  Counter #(.width(16), .max('hffff), .ongoal("wrap"), .trigger("rising"), .behavior("new")) counter_5 (
    .count(not_7_out), .Q(\无条件分支数 ), .clk(multiplexer_9_out), .clr(RST));  // open: load, D, carry, preset, down
  Multiplexer #(.select(1), .width(1), .disabled("Z"), .enable("false")) multiplexer_9 (
    .in0(and_8_out), .in1(1'b0), .out(multiplexer_9_out), .sel(CLK));
  // MIPS_RAM mips_ram_1: pin names not known; wires that end beside it: ex_mem_1_out_33_2, MDin, MemWrite, mips_ram_1_p4, CLK, 1'b1, RST, mips_ram_1_p8
  Multiplexer #(.select(1), .width(4), .disabled("Z"), .enable("false")) multiplexer_10 (
    .in0(4'b1111), .in1(decoder_1_out0), .out(mips_ram_1_p4), .sel(SB));
  MEM_WB mem_wb_1 (
    .MEMTOREG(ex_mem_1_out_21), .REGWRITE(ex_mem_1_out_23), .HALT(ex_mem_1_out_24), .ECALL(ex_mem_1_out_25),
    .JAL(ex_mem_1_out_26), .JALR(ex_mem_1_out_27), .AUIPC(ex_mem_1_out_28), .rd(ex_mem_1_out_31),
    .Result({ex_mem_1_out_33[31:22], ex_mem_1_out_33_2, ex_mem_1_out_33[1:0]}), .data(mips_ram_1_p8),
    .imm3(ex_mem_1_out_34), .IR(MEM_IR), .PC(M_PC), .PC_4(ex_mem_1_out_37), .out_19(mem_wb_1_out_19),
    .out_21(RegWrite), .out_22(mem_wb_1_out_22), .out_23(mem_wb_1_out_23), .out_24(mem_wb_1_out_24),
    .out_25(mem_wb_1_out_25), .out_26(mem_wb_1_out_26), .out_27(WriteReg_num), .out_28(mem_wb_1_out_28),
    .out_29(mem_wb_1_out_29), .out_30(mem_wb_1_out_30), .out_31(WB_IR), .out_32(WB_PC),
    .out_33(mem_wb_1_out_33), .reset(1'b0), .en(not_8_out), .clk(CLK));  // open: URET, out_20
  not not_8 (not_8_out, halt);
  or or_4 (or_4_out, mem_wb_1_out_24, mem_wb_1_out_25);
  D_Flip_Flop #(.trigger("rising"), .Pre_Clr_Positions("LEGACY"), .NegatePresetClear("false"), .enable("true"), .NewFFLayout("false")) d_ff_2 (
    .clk(mem_wb_1_out_22), .D(1'b1), .Q(halt), .en(mem_wb_1_out_23), .reset(Go));  // open: Qn, preset
  Multiplexer #(.select(2), .width(32), .disabled("Z"), .enable("false")) multiplexer_11 (
    .in0(mem_wb_1_out_28), .in1(mem_wb_1_out_29), .in2(mem_wb_1_out_33), .in3(mem_wb_1_out_30), .out(RDin),
    .sel(priority_encoder_2_out));
  Priority_Encoder #(.select(2), .disabled("Z")) priority_encoder_2 (
    .in0(1'b1), .in1(mem_wb_1_out_19), .in2(or_4_out), .in3(mem_wb_1_out_26), .out(priority_encoder_2_out));  // open: gs, en_out, en_in

  // Other names for the same wires on the sheet: MEM_PC[31:0] = M_PC

  // Notes on the sheet:
  //   中断源
  //   时空图监测，可删除
  //   中断等待指示
  //   数码管输出
  //   指令存储器
  //   指令探针
  //   contents of rom_1 (hex, n*v repeats v):
  //   100493 100006f 100493 200913 300993 100006f 100493 200913 300993 100006f 100493 200913 300993
  //   100006f 100493 200913 300993 29c000ef 100413 100493 1f49493 900533 2200893 73 24d493 48463 fedff06f
  //   900533 2200893 73 100493 249493 900533 2200893 73 48463 fedff06f 100493 1f49493 900533 2200893 73
  //   4034d493 900533 2200893 73 4044d493 900533 2200893 73 4044d493 900533 2200893 73 4044d493 900533
  //   2200893 73 4044d493 900533 2200893 73 4044d493 900533 2200893 73 4044d493 900533 2200893 73 4044d493
  //   900533 2200893 73 100413 1f41993 41f9d993 433 c00913 300b13 140413 f47413 800293 100313 499993
  //   89e9b3 1300533 2200893 73 406282b3 fe0294e3 140413 f00f93 1f47433 1c41413 800293 100313 49d993
  //   89e9b3 1300533 2200893 73 406282b3 fe0294e3 1c45413 406b0b33 b0463 f95ff06f 2b3 fff2c293 829293
  //   ff2e293 500533 2200893 73 fff00413 493 84a023 140413 448493 84a023 140413 448493 84a023 140413
  //   448493 84a023 140413 448493 84a023 140413 448493 84a023 140413 448493 84a023 140413 448493 84a023
  //   140413 448493 84a023 140413 448493 84a023 140413 448493 84a023 140413 448493 84a023 140413 448493
  //   84a023 140413 448493 84a023 140413 448493 84a023 140413 448493 84a023 140413 448493 140413 433
  //   3c00493 42983 4aa03 149a2b3 28663 134a023 1442023 ffc48493 fe9412e3 800533 2200893 73 440413 3c00493
  //   fc9416e3 a00893 73 413 140413 800533 2200893 73 240413 800533 2200893 73 340413 800533 2200893 73
  //   440413 800533 2200893 73 540413 800533 2200893 73 640413 800533 2200893 73 740413 800533 2200893 73
  //   840413 800533 2200893 2200893 73 8067
  //   控制位
  //   流水调试日志用
  //   暂停节拍，不能为0
  //   用这个时钟源需要去掉电路中的其他时钟源
  //   戳工具置1进入计数暂停模式，ctrl+k时钟自动运行到对应节拍暂停
  //   ctrl+k关闭时钟连续运行，将控制位置零，进入单步调试模式调试
  //   Beq
  //   Bne
  //   MemToReg
  //   MemWrite
  //   AluOP
  //   AluSrcB
  //   RegWrite
  //   可计数暂停的时钟源
  //   为方便自动评测，需要输出流水线各段保存的PC值，注意是PC不是PC+4，另外ID段寄存器写入信息，Mem段内存写入信息也要输出
endmodule
module \重定向流水线  (
  output RegWrite,
  output MemWrite,
  output [31:0] IF_PC,
  output [31:0] ID_PC,
  output [31:0] EX_PC,
  output [31:0] M_PC,
  output [31:0] WB_PC,
  output [31:0] RDin,
  output [31:0] MDin,
  output [31:0] LedData
);

  wire alu_1_equal, alu_1_out_4, and_1_out, and_2_out, and_3_out, and_4_out, and_5_out, and_7_out, and_8_out,
       CLK, clock_1_out, clock_2_out, comparator_1_eq, comparator_1_lt, comparator_2_eq, d_ff_1_q, ecall,
       EX_halt, ex_mem_1_out_21, ex_mem_1_out_23, ex_mem_1_out_24, ex_mem_1_out_25, ex_mem_1_out_26,
       ex_mem_1_out_27, ex_mem_1_out_28, Go, halt, id_ex_1_out_33, id_ex_1_out_34, id_ex_1_out_35,
       id_ex_1_out_36, id_ex_1_out_37, id_ex_1_out_38, id_ex_1_out_40, id_ex_1_out_41, id_ex_1_out_42,
       id_ex_1_out_43, id_ex_1_out_44, id_ex_1_out_45, IR1, IR2, IR3, mem_wb_1_out_19, mem_wb_1_out_22,
       mem_wb_1_out_23, mem_wb_1_out_24, mem_wb_1_out_25, mem_wb_1_out_26, multiplexer_2_out,
       multiplexer_9_out, multiplexer_11_out, nand_1_out, nor_1_out, nor_2_out, not_1_out, not_2_out,
       not_3_out, not_4_out, not_5_out, not_6_out, not_7_out, not_8_out, or_1_out, or_2_out, or_3_out,
       or_4_out, RST, SB, stall, W1, W2, W3, \单周期硬布线控制器_1_alu_src , \单周期硬布线控制器_1_auipc , \单周期硬布线控制器_1_beq ,
       \单周期硬布线控制器_1_bgeu , \单周期硬布线控制器_1_bne , \单周期硬布线控制器_1_jal , \单周期硬布线控制器_1_jalr , \单周期硬布线控制器_1_memtoreg ,
       \单周期硬布线控制器_1_memwrite , \单周期硬布线控制器_1_regwrite , \单周期硬布线控制器_1_rs1used , \单周期硬布线控制器_1_rs2used ,
       \单周期硬布线控制器_1_s_type , \单周期硬布线控制器_1_sb , \重定向数据相关检测逻辑_1_flush ;
  wire [1:0] id_ex_1_out_57, id_ex_1_out_58, priority_encoder_1_out, priority_encoder_2_out,
       \重定向数据相关检测逻辑_1_out_13 , \重定向数据相关检测逻辑_1_out_14 ;
  wire [3:0] decoder_1_out0, id_ex_1_out_46, mips_ram_1_p4, \单周期硬布线控制器_1_alu_op ;
  wire [4:0] ex_mem_1_out_31, id_ex_1_out_47, multiplexer_3_out, multiplexer_4_out, WriteReg_num;
  wire [12:0] CNT_num;
  wire [15:0] \LoadUse次数 , \总周期数 , \无条件分支数 , \条件分支成功数 ;
  wire [31:0] adder_4_out, ALU_result, b_branch, bit_extender_1_out, bit_extender_2_out, bit_extender_3_out,
       bit_extender_4_out, bit_extender_5_out, EX_IR, ex_mem_1_out_32, ex_mem_1_out_34, ex_mem_1_out_37,
       id_ex_1_out_48, id_ex_1_out_49, id_ex_1_out_50, id_ex_1_out_51, id_ex_1_out_52, id_ex_1_out_53,
       id_ex_1_out_56, ID_IR, if_id_1_pc_4_2, IF_IR, jal_branch, MEM_ALU_result, MEM_IR, mem_wb_1_out_28,
       mem_wb_1_out_29, mem_wb_1_out_30, mem_wb_1_out_33, mips_ram_1_p8, multiplexer_1_out,
       multiplexer_5_out, multiplexer_6_out, multiplexer_7_out, multiplexer_8_out, PC_4, regifile_1_r1,
       regifile_1_r2, shifter_1_out, shifter_2_out, shifter_3_out, WB_IR;

  Button \u_总复位  (.out(RST));
  Button _1 (.out(IR1));
  Button _2 (.out(IR2));
  Button _3 (.out(IR3));
  // Probe on \总周期数 
  // Probe on \总周期数 
  Button \u_继续运行  (.out(Go));
  LED #(.active("true")) led_1 (.in(W1));
  LED #(.active("true")) led_2 (.in(W2));
  LED #(.active("true")) led_3 (.in(W3));
  Hex_Digit_Display hex_digit_display_1 (.value(LedData[31:28]));  // open: dp
  // Probe on IF_PC[19:0]
  // RiscV_Probe riscv_probe_1: pin names not known; wires that end beside it: IF_IR
  Hex_Digit_Display hex_digit_display_2 (.value(LedData[23:20]));  // open: dp
  Hex_Digit_Display hex_digit_display_3 (.value(LedData[27:24]));  // open: dp
  // Probe on ID_PC[19:0]
  // RiscV_Probe riscv_probe_2: pin names not known; wires that end beside it: ID_IR
  Hex_Digit_Display hex_digit_display_4 (.value(LedData[19:16]));  // open: dp
  Hex_Digit_Display hex_digit_display_5 (.value(LedData[15:12]));  // open: dp
  Hex_Digit_Display hex_digit_display_6 (.value(LedData[7:4]));  // open: dp
  Hex_Digit_Display hex_digit_display_7 (.value(LedData[11:8]));  // open: dp
  Clock #(.highDuration(1), .lowDuration(1)) clock_1 (.out(clock_1_out));
  // Probe on EX_PC[19:0]
  // RiscV_Probe riscv_probe_3: pin names not known; wires that end beside it: clock_1_out, EX_IR, CLK
  Multiplexer #(.select(2), .width(32), .disabled("Z"), .enable("false")) multiplexer_1 (
    .in0(PC_4), .in1(ALU_result), .in2(jal_branch), .in3(b_branch), .out(multiplexer_1_out),
    .sel(priority_encoder_1_out));
  Hex_Digit_Display hex_digit_display_8 (.value(LedData[3:0]));  // open: dp
  nor nor_1 (nor_1_out, halt, stall);
  Register #(.width(32), .trigger("rising"), .Select("low")) PC (
    .D(multiplexer_1_out), .en(nor_1_out), .Q(IF_PC), .clk(CLK), .clr(RST));
  // Probe on \总周期数 
  // Probe on M_PC[19:0]
  // RiscV_Probe riscv_probe_4: pin names not known; wires that end beside it: MEM_IR
  \重定向数据相关检测逻辑  \u_重定向数据相关检测逻辑_1  (
    .in_1(ID_IR), .BranchTaken(or_1_out), .EX_MemToReg(id_ex_1_out_35), .rs1used(\单周期硬布线控制器_1_rs1used ),
    .rs2used(\单周期硬布线控制器_1_rs2used ), .EX_RegWrite(id_ex_1_out_38), .MEM_RegWrite(ex_mem_1_out_23),
    .ecall(ecall), .EX_WriteReg_num(id_ex_1_out_47), .MEM_WriteReg_num(ex_mem_1_out_31), .stall(stall),
    .flush(\重定向数据相关检测逻辑_1_flush ), .out_13(\重定向数据相关检测逻辑_1_out_13 ), .out_14(\重定向数据相关检测逻辑_1_out_14 ));
  not not_1 (not_1_out, halt);
  and and_1 (and_1_out, stall, CLK);
  // Probe on \总周期数 
  // Probe on \无条件分支数 
  // Probe on \条件分支成功数 
  // Probe on \LoadUse次数 
  // Probe on \LoadUse次数 
  Counter #(.width(16), .max('hffff), .ongoal("wrap"), .trigger("rising"), .behavior("new")) counter_1 (
    .count(not_1_out), .Q(\LoadUse次数 ), .clk(multiplexer_2_out), .clr(RST));  // open: load, D, carry, preset, down
  Multiplexer #(.select(1), .width(1), .disabled("Z"), .enable("false")) multiplexer_2 (
    .in0(and_1_out), .in1(1'b0), .out(multiplexer_2_out), .sel(CLK));
  not not_2 (not_2_out, halt);
  Adder #(.width(32)) adder_1 (.a(IF_PC), .b(32'h4), .out(PC_4));  // open: cin, cout
  // Probe on IF_PC[11:0]
  // Probe on WB_PC[19:0]
  // RiscV_Probe riscv_probe_5: pin names not known; wires that end beside it: WB_IR
  Counter #(.width(16), .max('hffff), .ongoal("wrap"), .trigger("rising"), .behavior("new")) counter_2 (
    .count(not_2_out), .Q(\总周期数 ), .clk(CLK), .clr(RST));  // open: load, D, carry, preset, down
  // RiscV_Probe riscv_probe_6: pin names not known; wires that end beside it: IF_IR, CLK
  ROM #(.addrWidth(10), .dataWidth(32), .Select("high")) rom_1 (.addr(IF_PC[11:2]), .data(IF_IR));
  // Probe on EX_PC[11:0]
  // Probe on ID_PC[11:0]
  IF_ID if_id_1 (
    .IR(IF_IR), .PC(IF_PC), .PC_4(PC_4), .IR_2(ID_IR), .PC_2(ID_PC), .PC_4_2(if_id_1_pc_4_2),
    .BranchTaken(or_1_out), .en(nor_2_out), .clk(CLK), .reset(1'b0));  // open: PredictJump, out_9
  nor nor_2 (nor_2_out, stall, halt);
  // Probe on M_PC[11:0]
  D_Flip_Flop #(.trigger("high"), .Pre_Clr_Positions("LEGACY"), .NegatePresetClear("false"), .enable("true"), .NewFFLayout("false")) d_ff_1 (.Q(d_ff_1_q));  // open: clk, D, Qn, preset, en, reset
  // Probe on 13'hc
  // Probe on WB_PC[11:0]
  Comparator #(.width(13), .mode("twosComplement")) comparator_1 (
    .a(CNT_num), .b(13'hc), .eq(comparator_1_eq), .lt(comparator_1_lt));  // open: gt
  Clock #(.highDuration(1), .lowDuration(1)) clock_2 (.out(clock_2_out));
  nand nand_1 (nand_1_out, d_ff_1_q, comparator_1_eq);
  Counter #(.width(13), .max('h1fff), .ongoal("stay"), .trigger("rising"), .behavior("old")) counter_3 (
    .count(comparator_1_lt), .Q(CNT_num), .clk(clock_2_out));  // open: load, D, carry, clr, preset
  \单周期硬布线控制器  \u_单周期硬布线控制器_1  (
    .Funct({ID_IR[30], ID_IR[25], ID_IR[14:12]}), .OP(ID_IR[6:2]), .ALU_OP(\单周期硬布线控制器_1_alu_op ),
    .MemToReg(\单周期硬布线控制器_1_memtoreg ), .MemWrite(\单周期硬布线控制器_1_memwrite ), .ALU_SRC(\单周期硬布线控制器_1_alu_src ),
    .RegWrite(\单周期硬布线控制器_1_regwrite ), .ecall(ecall), .S_type(\单周期硬布线控制器_1_s_type ),
    .Jalr(\单周期硬布线控制器_1_jalr ), .Beq(\单周期硬布线控制器_1_beq ), .JAL(\单周期硬布线控制器_1_jal ), .Bne(\单周期硬布线控制器_1_bne ),
    .in_3(ID_IR[21]), .AUIPC(\单周期硬布线控制器_1_auipc ), .BGEU(\单周期硬布线控制器_1_bgeu ), .SB(\单周期硬布线控制器_1_sb ),
    .Rs1used(\单周期硬布线控制器_1_rs1used ), .Rs2used(\单周期硬布线控制器_1_rs2used ));  // open: uret, CSRRSI, CSRRCI
  Multiplexer #(.select(1), .width(5), .disabled("Z"), .enable("false")) multiplexer_3 (
    .in0(ID_IR[19:15]), .in1(5'b10001), .out(multiplexer_3_out), .sel(ecall));
  Multiplexer #(.select(1), .width(5), .disabled("Z"), .enable("false")) multiplexer_4 (
    .in0(ID_IR[24:20]), .in1(5'b01010), .out(multiplexer_4_out), .sel(ecall));
  assign bit_extender_1_out = {{20{ID_IR[31]}}, ID_IR[31:20]};  // Bit_Extender bit_extender_1
  assign bit_extender_2_out = {{20{ID_IR[31]}}, {ID_IR[31:25], ID_IR[11:7]}};  // Bit_Extender bit_extender_2
  assign bit_extender_3_out = {{20{ID_IR[31]}}, {ID_IR[31], ID_IR[7], ID_IR[30:25], ID_IR[11:8]}};  // Bit_Extender bit_extender_3
  assign bit_extender_4_out = {{12{ID_IR[31]}}, {ID_IR[31], ID_IR[19:12], ID_IR[20], ID_IR[30:21]}};  // Bit_Extender bit_extender_4
  assign bit_extender_5_out = {{12{ID_IR[31]}}, ID_IR[31:12]};  // Bit_Extender bit_extender_5
  assign CLK = nand_1_out ? clock_2_out : 1'bz;  // Controlled_Buffer controlled_buffer_1
  Multiplexer #(.select(1), .width(32), .disabled("Z"), .enable("false")) multiplexer_5 (
    .in0(bit_extender_1_out), .in1(bit_extender_2_out), .out(multiplexer_5_out), .sel(\单周期硬布线控制器_1_s_type ));
  Pull_Resistor #(.pull(1)) pull_resistor_1 (.node(CLK));
  not not_3 (not_3_out, CLK);
  Regifile regifile_1 (
    .Din(RDin), .Clk(not_3_out), .R1(regifile_1_r1), .R2(regifile_1_r2), .WE(RegWrite), .W_num(WriteReg_num),
    .R1_num(multiplexer_3_out), .R2_num(multiplexer_4_out));
  not not_4 (not_4_out, halt);
  ID_EX id_ex_1 (
    .BEQ(\单周期硬布线控制器_1_beq ), .BNE(\单周期硬布线控制器_1_bne ), .MEMTOREG(\单周期硬布线控制器_1_memtoreg ),
    .MEMWRITE(\单周期硬布线控制器_1_memwrite ), .ALUSRCB(\单周期硬布线控制器_1_alu_src ), .REGWRITE(\单周期硬布线控制器_1_regwrite ),
    .ECALL(ecall), .JAL(\单周期硬布线控制器_1_jal ), .JALR(\单周期硬布线控制器_1_jalr ), .AUIPC(\单周期硬布线控制器_1_auipc ),
    .BGEU(\单周期硬布线控制器_1_bgeu ), .SB(\单周期硬布线控制器_1_sb ), .ALUop(\单周期硬布线控制器_1_alu_op ), .rd(ID_IR[11:7]),
    .R1(regifile_1_r1), .R2(regifile_1_r2), .imm1(multiplexer_5_out), .imm2(bit_extender_3_out),
    .imm3(bit_extender_5_out), .IR(ID_IR), .PC(ID_PC), .PC_4(if_id_1_pc_4_2), .out_33(id_ex_1_out_33),
    .out_34(id_ex_1_out_34), .out_35(id_ex_1_out_35), .out_36(id_ex_1_out_36), .out_37(id_ex_1_out_37),
    .out_38(id_ex_1_out_38), .out_40(id_ex_1_out_40), .out_41(id_ex_1_out_41), .out_42(id_ex_1_out_42),
    .out_43(id_ex_1_out_43), .out_44(id_ex_1_out_44), .out_45(id_ex_1_out_45), .out_46(id_ex_1_out_46),
    .out_47(id_ex_1_out_47), .out_49(id_ex_1_out_49), .out_50(id_ex_1_out_50), .out_51(id_ex_1_out_51),
    .out_52(id_ex_1_out_52), .out_53(id_ex_1_out_53), .out_54(EX_IR), .out_55(EX_PC),
    .out_56(id_ex_1_out_56), .flush(\重定向数据相关检测逻辑_1_flush ), .en(not_4_out), .clk(CLK),
    .Rs1Forward(\重定向数据相关检测逻辑_1_out_13 ), .out_57(id_ex_1_out_57), .Rs2Forward(\重定向数据相关检测逻辑_1_out_14 ),
    .out_58(id_ex_1_out_58), .imm4(bit_extender_4_out), .out_48(id_ex_1_out_48), .reset(1'b0));  // open: URET, out_39, PredictJump, out_32
  Multiplexer #(.select(2), .width(32), .disabled("Z"), .enable("false")) multiplexer_6 (
    .in0(id_ex_1_out_49), .in1(RDin), .in2(MEM_ALU_result), .out(multiplexer_6_out), .sel(id_ex_1_out_57));  // open: in3
  Multiplexer #(.select(2), .width(32), .disabled("Z"), .enable("false")) multiplexer_7 (
    .in0(id_ex_1_out_50), .in1(RDin), .in2(MEM_ALU_result), .out(multiplexer_7_out), .sel(id_ex_1_out_58));  // open: in3
  or or_1 (or_1_out, or_2_out, id_ex_1_out_41, id_ex_1_out_42);
  Multiplexer #(.select(1), .width(32), .disabled("Z"), .enable("false")) multiplexer_8 (
    .in0(multiplexer_7_out), .in1(id_ex_1_out_51), .out(multiplexer_8_out), .sel(id_ex_1_out_37));
  Shifter #(.width(32), .shift("ll")) shifter_1 (.in(id_ex_1_out_52), .\dist (5'b00001), .out(shifter_1_out));
  Shifter #(.width(32), .shift("ll")) shifter_2 (.in(id_ex_1_out_48), .\dist (5'b00001), .out(shifter_2_out));
  Shifter #(.width(32), .shift("ll")) shifter_3 (.in(id_ex_1_out_53), .\dist (5'b01100), .out(shifter_3_out));
  and and_2 (and_2_out, id_ex_1_out_33, alu_1_equal);
  Comparator #(.width(32), .mode("twosComplement")) comparator_2 (
    .a(32'h22), .b(multiplexer_6_out), .eq(comparator_2_eq));  // open: gt, lt
  or or_2 (or_2_out, and_2_out, and_3_out, and_4_out);
  and and_3 (and_3_out, id_ex_1_out_34, ~alu_1_equal);  // AND_Gate
  and and_4 (and_4_out, id_ex_1_out_44, alu_1_out_4);
  ALU alu_1 (
    .X(multiplexer_6_out), .Y(multiplexer_8_out), .AluOP(id_ex_1_out_46), .Equal(alu_1_equal),
    .Result(ALU_result), .out_4(alu_1_out_4));  // open: Result_2, out_6
  Adder #(.width(32)) adder_2 (.a(shifter_1_out), .b(EX_PC), .out(b_branch));  // open: cin, cout
  Adder #(.width(32)) adder_3 (.a(shifter_2_out), .b(EX_PC), .out(jal_branch));  // open: cin, cout
  Adder #(.width(32)) adder_4 (.a(shifter_3_out), .b(EX_PC), .out(adder_4_out));  // open: cin, cout
  and and_5 (and_5_out, comparator_2_eq, id_ex_1_out_40);
  and and_6 (EX_halt, ~comparator_2_eq, id_ex_1_out_40);  // AND_Gate
  Priority_Encoder #(.select(2), .disabled("Z")) priority_encoder_1 (
    .in0(1'b1), .in1(id_ex_1_out_42), .in2(id_ex_1_out_41), .in3(or_2_out), .out(priority_encoder_1_out));  // open: gs, en_out, en_in
  Register #(.width(32), .trigger("rising"), .Select("low")) register_1 (
    .D(multiplexer_7_out), .en(and_5_out), .Q(LedData), .clk(CLK), .clr(RST));
  not not_5 (not_5_out, halt);
  and and_7 (and_7_out, or_2_out, CLK);
  EX_MEM ex_mem_1 (
    .MEMTOREG(id_ex_1_out_35), .MEMWRITE(id_ex_1_out_36), .REGWRITE(id_ex_1_out_38), .HALT(EX_halt),
    .ECALL(id_ex_1_out_40), .JAL(id_ex_1_out_41), .JALR(id_ex_1_out_42), .AUIPC(id_ex_1_out_43),
    .SB(id_ex_1_out_45), .rd(id_ex_1_out_47), .R2(multiplexer_7_out), .Result(ALU_result),
    .imm3(adder_4_out), .IR(EX_IR), .PC(EX_PC), .PC_4(id_ex_1_out_56), .out_21(ex_mem_1_out_21),
    .out_22(MemWrite), .out_23(ex_mem_1_out_23), .out_24(ex_mem_1_out_24), .out_25(ex_mem_1_out_25),
    .out_26(ex_mem_1_out_26), .out_27(ex_mem_1_out_27), .out_28(ex_mem_1_out_28), .out_30(SB),
    .out_31(ex_mem_1_out_31), .out_32(ex_mem_1_out_32), .out_33(MEM_ALU_result), .out_34(ex_mem_1_out_34),
    .out_35(MEM_IR), .out_36(M_PC), .out_37(ex_mem_1_out_37), .reset(1'b0), .en(not_5_out), .clk(CLK));  // open: out_29, URET
  not not_6 (not_6_out, halt);
  Counter #(.width(16), .max('hffff), .ongoal("wrap"), .trigger("rising"), .behavior("new")) counter_4 (
    .count(not_6_out), .Q(\条件分支成功数 ), .clk(multiplexer_9_out), .clr(RST));  // open: load, D, carry, preset, down
  Multiplexer #(.select(1), .width(1), .disabled("Z"), .enable("false")) multiplexer_9 (
    .in0(and_7_out), .in1(1'b0), .out(multiplexer_9_out), .sel(CLK));
  Multiplexer #(.select(1), .width(32), .disabled("Z"), .enable("false")) multiplexer_10 (
    .in0(ex_mem_1_out_32),
    .in1({ex_mem_1_out_32[7:0], ex_mem_1_out_32[7:0], ex_mem_1_out_32[7:0], ex_mem_1_out_32[7:0]}),
    .out(MDin), .sel(SB));
  not not_7 (not_7_out, halt);
  and and_8 (and_8_out, or_3_out, CLK);
  or or_3 (or_3_out, id_ex_1_out_41, id_ex_1_out_42);
  Decoder #(.select(2), .tristate("false"), .disabled("Z"), .enable("false")) decoder_1 (
    .out0(decoder_1_out0[0]), .out1(decoder_1_out0[1]), .out2(decoder_1_out0[2]), .out3(decoder_1_out0[3]),
    .sel(MEM_ALU_result[1:0]));
  Counter #(.width(16), .max('hffff), .ongoal("wrap"), .trigger("rising"), .behavior("new")) counter_5 (
    .count(not_7_out), .Q(\无条件分支数 ), .clk(multiplexer_11_out), .clr(RST));  // open: load, D, carry, preset, down
  Multiplexer #(.select(1), .width(1), .disabled("Z"), .enable("false")) multiplexer_11 (
    .in0(and_8_out), .in1(1'b0), .out(multiplexer_11_out), .sel(CLK));
  // MIPS_RAM mips_ram_1: pin names not known; wires that end beside it: MEM_ALU_result[21:2], MDin, MemWrite, mips_ram_1_p4, CLK, 1'b1, RST, mips_ram_1_p8
  Multiplexer #(.select(1), .width(4), .disabled("Z"), .enable("false")) multiplexer_12 (
    .in0(4'b1111), .in1(decoder_1_out0), .out(mips_ram_1_p4), .sel(SB));
  MEM_WB mem_wb_1 (
    .MEMTOREG(ex_mem_1_out_21), .REGWRITE(ex_mem_1_out_23), .HALT(ex_mem_1_out_24), .ECALL(ex_mem_1_out_25),
    .JAL(ex_mem_1_out_26), .JALR(ex_mem_1_out_27), .AUIPC(ex_mem_1_out_28), .rd(ex_mem_1_out_31),
    .Result(MEM_ALU_result), .data(mips_ram_1_p8), .imm3(ex_mem_1_out_34), .IR(MEM_IR), .PC(M_PC),
    .PC_4(ex_mem_1_out_37), .out_19(mem_wb_1_out_19), .out_21(RegWrite), .out_22(mem_wb_1_out_22),
    .out_23(mem_wb_1_out_23), .out_24(mem_wb_1_out_24), .out_25(mem_wb_1_out_25), .out_26(mem_wb_1_out_26),
    .out_27(WriteReg_num), .out_28(mem_wb_1_out_28), .out_29(mem_wb_1_out_29), .out_30(mem_wb_1_out_30),
    .out_31(WB_IR), .out_32(WB_PC), .out_33(mem_wb_1_out_33), .reset(1'b0), .en(not_8_out), .clk(CLK));  // open: URET, out_20
  not not_8 (not_8_out, halt);
  or or_4 (or_4_out, mem_wb_1_out_24, mem_wb_1_out_25);
  D_Flip_Flop #(.trigger("high"), .Pre_Clr_Positions("LEGACY"), .NegatePresetClear("false"), .enable("true"), .NewFFLayout("false")) d_ff_2 (
    .clk(mem_wb_1_out_22), .D(1'b1), .Q(halt), .en(mem_wb_1_out_23), .reset(Go));  // open: Qn, preset
  Priority_Encoder #(.select(2), .disabled("Z")) priority_encoder_2 (
    .in0(1'b1), .in1(mem_wb_1_out_19), .in2(or_4_out), .in3(mem_wb_1_out_26), .out(priority_encoder_2_out));  // open: gs, en_out, en_in
  Multiplexer #(.select(2), .width(32), .disabled("Z"), .enable("false")) multiplexer_13 (
    .in0(mem_wb_1_out_28), .in1(mem_wb_1_out_29), .in2(mem_wb_1_out_33), .in3(mem_wb_1_out_30), .out(RDin),
    .sel(priority_encoder_2_out));

  // Other names for the same wires on the sheet: MEM_PC[31:0] = M_PC; 插入气泡数[15:0] = \LoadUse次数 

  // Notes on the sheet:
  //   中断源
  //   时空图监测，可删除
  //   中断等待指示
  //   数码管输出
  //   指令存储器
  //   指令探针
  //   contents of rom_1 (hex, n*v repeats v):
  //   100493 100006f 100493 200913 300993 100006f 100493 200913 300993 100006f 100493 200913 300993
  //   100006f 100493 200913 300993 29c000ef 100413 100493 1f49493 900533 2200893 73 24d493 48463 fedff06f
  //   900533 2200893 73 100493 249493 900533 2200893 73 48463 fedff06f 100493 1f49493 900533 2200893 73
  //   4034d493 900533 2200893 73 4044d493 900533 2200893 73 4044d493 900533 2200893 73 4044d493 900533
  //   2200893 73 4044d493 900533 2200893 73 4044d493 900533 2200893 73 4044d493 900533 2200893 73 4044d493
  //   900533 2200893 73 100413 1f41993 41f9d993 433 c00913 300b13 140413 f47413 800293 100313 499993
  //   89e9b3 1300533 2200893 73 406282b3 fe0294e3 140413 f00f93 1f47433 1c41413 800293 100313 49d993
  //   89e9b3 1300533 2200893 73 406282b3 fe0294e3 1c45413 406b0b33 b0463 f95ff06f 2b3 fff2c293 829293
  //   ff2e293 500533 2200893 73 fff00413 493 84a023 140413 448493 84a023 140413 448493 84a023 140413
  //   448493 84a023 140413 448493 84a023 140413 448493 84a023 140413 448493 84a023 140413 448493 84a023
  //   140413 448493 84a023 140413 448493 84a023 140413 448493 84a023 140413 448493 84a023 140413 448493
  //   84a023 140413 448493 84a023 140413 448493 84a023 140413 448493 84a023 140413 448493 140413 433
  //   3c00493 42983 4aa03 149a2b3 28663 134a023 1442023 ffc48493 fe9412e3 800533 2200893 73 440413 3c00493
  //   fc9416e3 a00893 73 413 140413 800533 2200893 73 240413 800533 2200893 73 340413 800533 2200893 73
  //   440413 800533 2200893 73 540413 800533 2200893 73 640413 800533 2200893 73 740413 800533 2200893 73
  //   840413 800533 2200893 2200893 73 8067
  //   控制位
  //   流水调试日志用
  //   暂停节拍，不能为0
  //   戳工具置1进入计数暂停模式，ctrl+k时钟自动运行到对应节拍暂停
  //   ctrl+k关闭时钟连续运行，将控制位置零，进入单步调试模式调试
  //   Beq
  //   Bne
  //   MemToReg
  //   MemWrite
  //   AluOP
  //   AluSrcB
  //   RegWrite
  //   可计数暂停的时钟源
  //   为方便自动评测，需要输出流水线各段保存的PC值，注意是PC不是PC+4，另外ID段寄存器写入信息，Mem段内存写入信息也要输出
endmodule

module \中断按键参考电路  (
  input  \同步清零信号 ,
  output \与中断屏蔽位与 
);

  wire \_1号中断_out , and_1_out, clock_1_out, d_ff_1_q, or_1_out, or_2_out;

  Clock #(.highDuration(1), .lowDuration(1)) clock_1 (.out(clock_1_out));
  Button \_1号中断  (.out(\_1号中断_out ));
  LED #(.active("true")) \_1号中断等待指示灯  (.in(or_1_out));
  or or_1 (or_1_out, \与中断屏蔽位与 , d_ff_1_q);
  D_Flip_Flop #(.trigger("rising"), .Pre_Clr_Positions("LEGACY"), .NegatePresetClear("false"), .enable("true"), .NewFFLayout("false")) d_ff_1 (
    .clk(\_1号中断_out ), .D(1'b1), .Q(d_ff_1_q), .reset(\与中断屏蔽位与 ));  // open: Qn, preset, en
  or or_2 (or_2_out, d_ff_1_q, \与中断屏蔽位与 );
  and and_1 (and_1_out, or_2_out, ~\同步清零信号 );  // AND_Gate
  D_Flip_Flop #(.trigger("rising"), .Pre_Clr_Positions("LEGACY"), .NegatePresetClear("false"), .enable("true"), .NewFFLayout("false")) IR1 (
    .clk(clock_1_out), .D(and_1_out), .Q(\与中断屏蔽位与 ));  // open: Qn, preset, en, reset

  // Notes on the sheet:
  //   中断信号采样参考电路
  //   Reset 
endmodule

module \单周期_单级中断  (
  input  IR1,
  input  IR2,
  input  IR3,
  output RegWrite,
  output MemWrite,
  output [31:0] PC,
  output [31:0] IR,
  output [31:0] RDin,
  output [31:0] MDin,
  output [31:0] LedData
);

  wire and_1_out, and_2_out, and_3_out, and_4_out, and_5_out, and_6_out, and_7_out, and_9_out, AUIPC, Beq,
       BGEU, Bne, CLK, clr1, clr2, clr3, comparator_1_eq, comparator_2_eq, comparator_3_eq, comparator_4_eq,
       comparator_5_eq, d_ff_1_q, d_ff_2_q, d_ff_3_q, decoder_2_out0, decoder_2_out1, decoder_2_out2, ecall,
       equal, GE, Go, halt, IE, IR1_2_q, IR1_3_q, IR1_q, IR1_t, IR2_t, IR3_t, IRA, IRB, IRC, jal, jalr,
       MemToReg, not_1_out, not_2_out, or_1_out, or_3_out, or_8_out, or_9_out, or_10_out, or_12_out,
       priority_encoder_2_gs, RST, SB, uret, W1, W2, W3, \中断信号 , \单周期硬布线控制器_1_alu_src , \单周期硬布线控制器_1_s_type ;
  wire [1:0] priority_encoder_1_out, priority_encoder_3_out, register_2_q, \中断号 ;
  wire [3:0] decoder_1_out0, mips_ram_1_p4, \单周期硬布线控制器_1_alu_op ;
  wire [4:0] multiplexer_4_out, multiplexer_5_out;
  wire [15:0] \总周期数 ;
  wire [31:0] adder_2_out, adder_3_out, bit_extender_1_out, bit_extender_2_out, bit_extender_3_out,
       bit_extender_4_out, bit_extender_5_out, mips_ram_1_p9, multiplexer_2_out, multiplexer_3_out,
       multiplexer_6_out, multiplexer_8_out, NowPC, PC_4, PC_imm, regifile_1_r1, regifile_1_r2, result,
       RetPC, shifter_1_out, shifter_2_out, shifter_3_out, \中断服务地址 ;

  Clock #(.highDuration(1), .lowDuration(1)) clock_1 (.out(CLK));
  Button _1 ();  // open: out
  Button _2 ();  // open: out
  Button _3 ();  // open: out
  Button \u_继续运行  (.out(Go));
  LED #(.active("true")) led_1 (.in(W1));
  LED #(.active("true")) led_2 (.in(W2));
  LED #(.active("true")) led_3 (.in(W3));
  Hex_Digit_Display hex_digit_display_1 (.value(LedData[31:28]));  // open: dp
  Comparator #(.width(16), .mode("twosComplement")) comparator_1 (
    .a(16'h23b), .b(\总周期数 ), .eq(comparator_1_eq));  // open: gt, lt
  Comparator #(.width(16), .mode("twosComplement")) comparator_2 (
    .a(\总周期数 ), .b(16'h1), .eq(comparator_2_eq));  // open: gt, lt
  Comparator #(.width(16), .mode("twosComplement")) comparator_3 (
    .a(\总周期数 ), .b(16'h4), .eq(comparator_3_eq));  // open: gt, lt
  Comparator #(.width(16), .mode("twosComplement")) comparator_4 (
    .a(\总周期数 ), .b(16'h7), .eq(comparator_4_eq));  // open: gt, lt
  Hex_Digit_Display hex_digit_display_2 (.value(LedData[23:20]));  // open: dp
  Hex_Digit_Display hex_digit_display_3 (.value(LedData[27:24]));  // open: dp
  or or_1 (or_1_out, comparator_1_eq, comparator_2_eq);
  assign IRA = or_1_out ? ~CLK : 1'bz;  // Controlled_Inverter controlled_inverter_1
  assign IRB = comparator_3_eq ? ~CLK : 1'bz;  // Controlled_Inverter controlled_inverter_2
  assign IRC = comparator_4_eq ? ~CLK : 1'bz;  // Controlled_Inverter controlled_inverter_3
  Hex_Digit_Display hex_digit_display_4 (.value(LedData[15:12]));  // open: dp
  Hex_Digit_Display hex_digit_display_5 (.value(LedData[19:16]));  // open: dp
  Pull_Resistor #(.pull(0)) pull_resistor_1 (.node(IRA));
  Pull_Resistor #(.pull(0)) pull_resistor_2 (.node(IRB));
  Pull_Resistor #(.pull(0)) pull_resistor_3 (.node(IRC));
  Hex_Digit_Display hex_digit_display_6 (.value(LedData[11:8]));  // open: dp
  Hex_Digit_Display hex_digit_display_7 (.value(LedData[7:4]));  // open: dp
  // Probe on \总周期数 
  Hex_Digit_Display hex_digit_display_8 (.value(LedData[3:0]));  // open: dp
  Multiplexer #(.select(2), .width(32), .disabled("Z"), .enable("false")) multiplexer_1 (
    .in0(PC_4), .in1(result), .in2(adder_3_out), .in3(adder_2_out), .out(NowPC), .sel(priority_encoder_1_out));
  Multiplexer #(.select(1), .width(32), .disabled("Z"), .enable("false")) multiplexer_2 (
    .in0(NowPC), .in1(RetPC), .out(multiplexer_2_out), .sel(uret));
  or or_2 (IR1_t, IR1, IRA);
  Priority_Encoder #(.select(2), .disabled("Z")) priority_encoder_1 (
    .in0(1'b1), .in1(jalr), .in2(jal), .in3(or_3_out), .out(priority_encoder_1_out));  // open: gs, en_out, en_in
  or or_3 (or_3_out, and_1_out, and_3_out, and_2_out);
  and and_1 (and_1_out, Beq, equal);
  Multiplexer #(.select(1), .width(32), .disabled("Z"), .enable("false")) multiplexer_3 (
    .in0(multiplexer_2_out), .in1(\中断服务地址 ), .out(multiplexer_3_out), .sel(\中断信号 ));
  not not_1 (not_1_out, halt);
  or or_4 (W1, IR1_q, d_ff_1_q);
  or or_5 (W2, IR1_2_q, d_ff_2_q);
  or or_6 (W3, IR1_3_q, d_ff_3_q);
  or or_7 (IR2_t, IR2, IRB);
  and and_2 (and_2_out, ~equal, Bne);  // AND_Gate
  and and_3 (and_3_out, GE, BGEU);
  Register #(.width(32), .trigger("rising"), .Select("low")) u_PC (
    .D(multiplexer_3_out), .en(not_1_out), .Q(PC), .clk(CLK), .clr(RST));
  D_Flip_Flop #(.trigger("rising"), .Pre_Clr_Positions("LEGACY"), .NegatePresetClear("false"), .enable("true"), .NewFFLayout("false")) d_ff_1 (
    .clk(IR1_t), .D(1'b1), .Q(d_ff_1_q), .reset(IR1_q));  // open: Qn, preset, en
  D_Flip_Flop #(.trigger("rising"), .Pre_Clr_Positions("LEGACY"), .NegatePresetClear("false"), .enable("true"), .NewFFLayout("false")) d_ff_2 (
    .clk(IR2_t), .D(1'b1), .Q(d_ff_2_q), .reset(IR1_2_q));  // open: Qn, preset, en
  D_Flip_Flop #(.trigger("rising"), .Pre_Clr_Positions("LEGACY"), .NegatePresetClear("false"), .enable("true"), .NewFFLayout("false")) d_ff_3 (
    .clk(IR3_t), .D(1'b1), .Q(d_ff_3_q), .reset(IR1_3_q));  // open: Qn, preset, en
  Adder #(.width(32)) adder_1 (.a(PC), .b(32'h4), .out(PC_4));  // open: cin, cout
  or or_8 (or_8_out, d_ff_1_q, IR1_q);
  or or_9 (or_9_out, d_ff_2_q, IR1_2_q);
  or or_10 (or_10_out, d_ff_3_q, IR1_3_q);
  or or_11 (IR3_t, IR3, IRC);
  // RiscV_Probe riscv_probe_1: pin names not known; wires that end beside it: IR, IR
  and and_4 (and_4_out, or_8_out, ~clr1);  // AND_Gate
  and and_5 (and_5_out, or_9_out, ~clr2);  // AND_Gate
  and and_6 (and_6_out, or_10_out, ~clr3);  // AND_Gate
  ROM #(.addrWidth(10), .dataWidth(32), .Select("high")) rom_1 (.addr(PC[11:2]), .data(IR));
  D_Flip_Flop #(.trigger("rising"), .Pre_Clr_Positions("LEGACY"), .NegatePresetClear("false"), .enable("true"), .NewFFLayout("false")) u_IR1 (
    .clk(CLK), .D(and_4_out), .Q(IR1_q), .reset(RST));  // open: Qn, preset, en
  D_Flip_Flop #(.trigger("rising"), .Pre_Clr_Positions("LEGACY"), .NegatePresetClear("false"), .enable("true"), .NewFFLayout("false")) IR1_2 (
    .clk(CLK), .D(and_5_out), .Q(IR1_2_q), .reset(RST));  // open: Qn, preset, en
  D_Flip_Flop #(.trigger("rising"), .Pre_Clr_Positions("LEGACY"), .NegatePresetClear("false"), .enable("true"), .NewFFLayout("false")) IR1_3 (
    .clk(CLK), .D(and_6_out), .Q(IR1_3_q), .reset(RST));  // open: Qn, preset, en
  \单周期硬布线控制器  \u_单周期硬布线控制器_1  (
    .Funct({IR[30], IR[25], IR[14:12]}), .OP(IR[6:2]), .ALU_OP(\单周期硬布线控制器_1_alu_op ), .MemToReg(MemToReg),
    .MemWrite(MemWrite), .ALU_SRC(\单周期硬布线控制器_1_alu_src ), .RegWrite(RegWrite), .ecall(ecall),
    .S_type(\单周期硬布线控制器_1_s_type ), .Jalr(jalr), .Beq(Beq), .JAL(jal), .Bne(Bne), .in_3(IR[21]), .uret(uret),
    .AUIPC(AUIPC), .BGEU(BGEU), .SB(SB));  // open: Rs1used, Rs2used, CSRRSI, CSRRCI
  Multiplexer #(.select(1), .width(5), .disabled("Z"), .enable("false")) multiplexer_4 (
    .in0(IR[19:15]), .in1(5'b10001), .out(multiplexer_4_out), .sel(ecall));
  Multiplexer #(.select(1), .width(5), .disabled("Z"), .enable("false")) multiplexer_5 (
    .in0(IR[24:20]), .in1(5'b01010), .out(multiplexer_5_out), .sel(ecall));
  assign bit_extender_1_out = {{20{IR[31]}}, IR[31:20]};  // Bit_Extender bit_extender_1
  Multiplexer #(.select(1), .width(32), .disabled("Z"), .enable("false")) multiplexer_6 (
    .in0(bit_extender_1_out), .in1(bit_extender_2_out), .out(multiplexer_6_out), .sel(\单周期硬布线控制器_1_s_type ));
  assign bit_extender_2_out = {{20{IR[31]}}, {IR[31:25], IR[11:7]}};  // Bit_Extender bit_extender_2
  assign bit_extender_3_out = {{20{IR[31]}}, {IR[31], IR[7], IR[30:25], IR[11:8]}};  // Bit_Extender bit_extender_3
  assign bit_extender_4_out = {{12{IR[31]}}, {IR[31], IR[19:12], IR[20], IR[30:21]}};  // Bit_Extender bit_extender_4
  assign bit_extender_5_out = {{12{IR[31]}}, IR[31:12]};  // Bit_Extender bit_extender_5
  Priority_Encoder #(.select(2), .disabled("Z")) priority_encoder_2 (
    .in0(IR1_q), .in1(IR1_2_q), .in2(IR1_3_q), .out(\中断号 ), .gs(priority_encoder_2_gs));  // open: in3, en_out, en_in
  and and_7 (and_7_out, priority_encoder_2_gs, ~uret);  // AND_Gate
  Shifter #(.width(32), .shift("ll")) shifter_1 (.in(bit_extender_3_out), .\dist (5'b00001), .out(shifter_1_out));
  Shifter #(.width(32), .shift("ll")) shifter_2 (.in(bit_extender_4_out), .\dist (5'b00001), .out(shifter_2_out));
  Shifter #(.width(32), .shift("ll")) shifter_3 (.in(bit_extender_5_out), .\dist (5'b01100), .out(shifter_3_out));
  D_Flip_Flop #(.trigger("rising"), .Pre_Clr_Positions("LEGACY"), .NegatePresetClear("false"), .enable("true"), .NewFFLayout("false")) d_ff_4 (
    .clk(CLK), .D(and_7_out), .Qn(IE), .reset(RST));  // open: Q, preset, en
  and and_8 (\中断信号 , priority_encoder_2_gs, IE);
  Regifile regifile_1 (
    .Din(RDin), .Clk(CLK), .R1(regifile_1_r1), .R2(regifile_1_r2), .WE(RegWrite), .W_num(IR[11:7]),
    .R1_num(multiplexer_4_out), .R2_num(multiplexer_5_out));
  Adder #(.width(32)) adder_2 (.a(shifter_1_out), .b(PC), .out(adder_2_out));  // open: cin, cout
  Adder #(.width(32)) adder_3 (.a(shifter_2_out), .b(PC), .out(adder_3_out));  // open: cin, cout
  Adder #(.width(32)) adder_4 (.a(shifter_3_out), .b(PC), .out(PC_imm));  // open: cin, cout
  Multiplexer #(.select(2), .width(32), .disabled("Z"), .enable("false")) multiplexer_7 (
    .in0(32'h30ac), .in1(32'h3150), .in2(32'h31f4), .out(\中断服务地址 ), .sel(\中断号 ));  // open: in3
  Multiplexer #(.select(1), .width(32), .disabled("Z"), .enable("false")) multiplexer_8 (
    .in0(regifile_1_r2), .in1(multiplexer_6_out), .out(multiplexer_8_out), .sel(\单周期硬布线控制器_1_alu_src ));
  ALU alu_1 (
    .X(regifile_1_r1), .Y(multiplexer_8_out), .AluOP(\单周期硬布线控制器_1_alu_op ), .Equal(equal), .Result(result),
    .out_4(GE));  // open: Result_2, out_6
  Multiplexer #(.select(1), .width(32), .disabled("Z"), .enable("false")) multiplexer_9 (
    .in0(regifile_1_r2),
    .in1({regifile_1_r2[7:0], regifile_1_r2[7:0], regifile_1_r2[7:0], regifile_1_r2[7:0]}), .out(MDin),
    .sel(SB));
  Register #(.width(32), .trigger("rising"), .Select("low")) register_1 (
    .D(NowPC), .en(\中断信号 ), .Q(RetPC), .clk(CLK), .clr(RST));
  Button button_1 (.out(RST));
  Decoder #(.select(2), .tristate("false"), .disabled("Z"), .enable("false")) decoder_1 (
    .out0(decoder_1_out0[0]), .out1(decoder_1_out0[1]), .out2(decoder_1_out0[2]), .out3(decoder_1_out0[3]),
    .sel(result[1:0]));
  Comparator #(.width(32), .mode("twosComplement")) comparator_5 (
    .a(32'h22), .b(regifile_1_r1), .eq(comparator_5_eq));  // open: gt, lt
  Register #(.width(2), .trigger("rising"), .Select("low")) register_2 (
    .D(\中断号 ), .en(\中断信号 ), .Q(register_2_q), .clk(CLK), .clr(RST));
  Decoder #(.select(2), .tristate("false"), .disabled("Z"), .enable("false")) decoder_2 (
    .out0(decoder_2_out0), .out1(decoder_2_out1), .out2(decoder_2_out2), .sel(register_2_q));  // open: out3
  not not_2 (not_2_out, halt);
  and and_9 (and_9_out, comparator_5_eq, ecall);
  and and_10 (clr1, decoder_2_out0, uret);
  and and_11 (clr2, decoder_2_out1, uret);
  and and_12 (clr3, decoder_2_out2, uret);
  Counter #(.width(16), .max('hffff), .ongoal("wrap"), .trigger("rising"), .behavior("new")) counter_1 (
    .count(not_2_out), .Q(\总周期数 ), .clk(CLK), .clr(RST));  // open: load, D, carry, preset, down
  // MIPS_RAM mips_ram_1: pin names not known; wires that end beside it: result[21:2], MDin, MemWrite, mips_ram_1_p4, CLK, LedData, 1'b1, RST, mips_ram_1_p9
  Multiplexer #(.select(1), .width(4), .disabled("Z"), .enable("false")) multiplexer_10 (
    .in0(4'b1111), .in1(decoder_1_out0), .out(mips_ram_1_p4), .sel(SB));
  Register #(.width(32), .trigger("rising"), .Select("low")) register_3 (
    .D(regifile_1_r2), .en(and_9_out), .Q(LedData), .clk(CLK), .clr(RST));
  and and_13 (halt, ~comparator_5_eq, ~Go, ecall);  // AND_Gate
  Priority_Encoder #(.select(2), .disabled("Z")) priority_encoder_3 (
    .in0(1'b1), .in1(MemToReg), .in2(or_12_out), .in3(AUIPC), .out(priority_encoder_3_out));  // open: gs, en_out, en_in
  Multiplexer #(.select(2), .width(32), .disabled("Z"), .enable("false")) multiplexer_11 (
    .in0(result), .in1(mips_ram_1_p9), .in2(PC_4), .in3(PC_imm), .out(RDin), .sel(priority_encoder_3_out));
  or or_12 (or_12_out, jal, jalr);

  // Notes on the sheet:
  //   中断源
  //   中断等待指示
  //   总复位信号应将除ROM以外所有存储组件全部清零
  //   单级中断测试信号模拟器
  //   数码管输出
  //   数码管输出应该用寄存器锁存，否则显示数据只能一闪而过
  //   指令探针
  //   指令存储器
  //   Reset 
  //   Reset 
  //   Reset 
  //   指令字
  //   contents of rom_1 (hex, n*v repeats v):
  //   7d000113 100413 1f41993 41f9d993 433 c00913 800b13 140413 f47413 800293 100313 499993 89e9b3 1300533
  //   2200893 73 406282b3 fe0294e3 140413 f00f93 1f47433 1c41413 800293 100313 49d993 89e9b3 1300533
  //   2200893 73 406282b3 fe0294e3 1c45413 406b0b33 b0463 f95ff06f 2b3 fff2c293 1029293 fff2e293 500533
  //   2200893 73 f5dff06f 1112023 410113 a12023 410113 812023 410113 1312023 410113 1412023 410113 1512023
  //   410113 1612023 410113 100b13 300a13 100a93 1600433 441413 14469b3 1300533 2200893 73 fe0416e3
  //   415a0a33 fe0a10e3 ffc10113 12b03 ffc10113 12a83 ffc10113 12a03 ffc10113 12983 ffc10113 12403
  //   ffc10113 12503 ffc10113 12883 200073 1112023 410113 a12023 410113 812023 410113 1312023 410113
  //   1412023 410113 1512023 410113 1612023 410113 200b13 300a13 100a93 1600433 441413 14469b3 1300533
  //   2200893 73 fe0416e3 415a0a33 fe0a10e3 ffc10113 12b03 ffc10113 12a83 ffc10113 12a03 ffc10113 12983
  //   ffc10113 12403 ffc10113 12503 ffc10113 12883 200073 1112023 410113 a12023 410113 812023 410113
  //   1312023 410113 1412023 410113 1512023 410113 1612023 410113 300b13 300a13 100a93 1600433 441413
  //   14469b3 1300533 2200893 73 fe0416e3 415a0a33 fe0a10e3 ffc10113 12b03 ffc10113 12a83 ffc10113 12a03
  //   ffc10113 12983 ffc10113 12403 ffc10113 12503 ffc10113 12883 200073
  //   JALR
  //   为方便自动评测，需要输出PC，IR，寄存器堆写如数据RDin
  //   Beq
  //   Bne
  //   MemToReg
  //   MemWrite
  //   AluOP
  //   AluSrcB
  //   RegWrite
  //   RAM写使能MemWrite、RAM写入数据MDin等信号
  //   数据存储器
endmodule

module \封装正确性测试  (
);

  wire IR1, IR2, IR3, MemW, RegW;
  wire [31:0] EX_PC, ID_PC, IF_PC, IR, LED, MDin, MDinr, MEM_PC, PC, RDin, RDinr, WB_PC;

  \单周期RISC_V  \u_单周期risc_v_1  (
    .RegWrite(RegW), .MemWrite(MemW), .PC(PC), .IR(IR), .RDin(RDin), .MDin(MDin), .LedData(LED));
  \气泡流水线  \u_气泡流水线_1  (
    .RegWrite(RegW), .MemWrite(MemW), .IF_PC(IF_PC), .ID_PC(ID_PC), .EX_PC(EX_PC), .M_PC(MEM_PC),
    .WB_PC(WB_PC), .RDin(RDinr), .MDin(MDinr), .LedData(LED));
  \单周期_单级中断  \u_单周期_单级中断_1  (
    .IR1(IR1), .IR2(IR2), .IR3(IR3), .RegWrite(RegW), .MemWrite(MemW), .PC(PC), .IR(IR), .RDin(RDin),
    .MDin(MDin), .LedData(LED));
  \理想流水线  \u_理想流水线_1  (
    .RegWrite(RegW), .MemWrite(MemW), .IF_PC(IF_PC), .ID_PC(ID_PC), .EX_PC(EX_PC), .M_PC(MEM_PC),
    .WB_PC(WB_PC), .RDin(RDinr), .MDin(MDinr), .LedData(LED));
  \重定向流水线  \u_重定向流水线_1  (
    .RegWrite(RegW), .MemWrite(MemW), .IF_PC(IF_PC), .ID_PC(ID_PC), .EX_PC(EX_PC), .M_PC(MEM_PC),
    .WB_PC(WB_PC), .RDin(RDinr), .MDin(MDinr), .LedData(LED));
  \单周期_多级中断  \u_单周期_多级中断_1  (
    .IR1(IR1), .IR2(IR2), .IR3(IR3), .RegWrite(RegW), .MemWrite(MemW), .PC(PC), .IR(IR), .RDin(RDin),
    .MDin(MDin), .LedData(LED));

  // Notes on the sheet:
  //   单周期封装测试
  //   气泡流水封装测试
  //   单周期+单级中断封装测试
  //   请检查上面封装有无位宽不匹配，引脚标签是否和连接的标签相对应，否则无法在educoder平台上正确测试
  //   理想流水封装测试
  //   重定向流水封装测试
  //   单周期+多级中断封装测试
endmodule

module \单周期_多级中断  (
  input  IR1,
  input  IR2,
  input  IR3,
  output RegWrite,
  output MemWrite,
  output [31:0] PC,
  output [31:0] IR,
  output [31:0] RDin,
  output [31:0] MDin,
  output [31:0] LedData
);

  wire and_1_out, and_2_out, and_3_out, and_4_out, and_5_out, and_6_out, and_11_out, and_12_out, and_13_out,
       and_16_out, and_17_out, and_18_out, and_19_out, and_20_out, and_21_out, and_22_out, and_23_out, AUIPC,
       Beq, BGEU, Bne, CLK, close, clr1, clr2, clr3, comparator_1_eq, comparator_2_eq, comparator_3_eq,
       comparator_4_eq, comparator_5_eq, comparator_6_eq, comparator_7_eq, comparator_8_eq, comparator_9_eq,
       comparator_10_eq, comparator_11_gt, comparator_12_lt, comparator_13_gt, comparator_14_lt,
       comparator_15_gt, comparator_16_lt, d_ff_1_q, d_ff_2_q, d_ff_3_q, d_ff_4_q, d_ff_6_q, d_ff_7_q,
       d_ff_8_q, d_ff_9_q, d_ff_10_q, d_ff_11_q, d_ff_12_q, d_ff_13_q, d_ff_14_q, decoder_1_out1,
       decoder_1_out2, decoder_1_out3, decoder_3_out1, decoder_3_out2, decoder_3_out3, decoder_4_out1,
       decoder_4_out2, decoder_4_out3, ecall, equal, GE, Go, halt, hasrun1, hasrun2, IE, IR1_2_q, IR1_3_q,
       IR1_q, IR1_t, IR2_t, IR3_t, IRA, IRB, IRC, jal, jalr, MemToReg, not_1_out, not_2_out, not_3_out,
       not_4_out, not_5_out, open, or_1_out, or_2_out, or_4_out, or_9_out, or_10_out, or_11_out, or_13_out,
       or_14_out, or_15_out, or_16_out, or_17_out, or_18_out, or_19_out, or_20_out, or_21_out, or_22_out,
       or_23_out, register_3_q, register_4_q, register_5_q, RST, SB, uret, W1, W2, W3, \中断信号 ,
       \单周期硬布线控制器_1_alu_src , \单周期硬布线控制器_1_s_type , \发生中断 ;
  wire [1:0] priority_encoder_1_out, priority_encoder_3_out, register_1_q, \中断号 , \当前中断号 ;
  wire [3:0] decoder_2_out0, mips_ram_1_p4, \单周期硬布线控制器_1_alu_op ;
  wire [4:0] multiplexer_4_out, multiplexer_5_out;
  wire [15:0] \总周期数 ;
  wire [31:0] adder_2_out, adder_3_out, bit_extender_1_out, bit_extender_2_out, bit_extender_3_out,
       bit_extender_4_out, bit_extender_5_out, mips_ram_1_p9, multiplexer_2_out, multiplexer_3_out,
       multiplexer_6_out, multiplexer_7_out, NowPC, PC_4, PC_imm, regifile_1_r1, regifile_1_r2, register_6_q,
       register_7_q, register_8_q, result, RetPC, shifter_1_out, shifter_2_out, shifter_3_out, \中断服务地址 ;

  Clock #(.highDuration(1), .lowDuration(1)) clock_1 (.out(CLK));
  Button _1 ();  // open: out
  Button _2 ();  // open: out
  Button _3 ();  // open: out
  Button \u_继续运行  (.out(Go));
  LED #(.active("true")) led_1 (.in(W1));
  LED #(.active("true")) led_2 (.in(W2));
  LED #(.active("true")) led_3 (.in(W3));
  Hex_Digit_Display hex_digit_display_1 (.value(LedData[31:28]));  // open: dp
  Comparator #(.width(16), .mode("twosComplement")) comparator_1 (
    .a(\总周期数 ), .b(16'h7), .eq(comparator_1_eq));  // open: gt, lt
  Comparator #(.width(16), .mode("twosComplement")) comparator_2 (
    .a(\总周期数 ), .b(16'h241), .eq(comparator_2_eq));  // open: gt, lt
  Hex_Digit_Display hex_digit_display_2 (.value(LedData[23:20]));  // open: dp
  Hex_Digit_Display hex_digit_display_3 (.value(LedData[27:24]));  // open: dp
  Comparator #(.width(16), .mode("twosComplement")) comparator_3 (
    .a(16'h258), .b(\总周期数 ), .eq(comparator_3_eq));  // open: gt, lt
  or or_1 (or_1_out, comparator_3_eq, comparator_4_eq);
  Comparator #(.width(16), .mode("twosComplement")) comparator_4 (
    .a(\总周期数 ), .b(16'h1), .eq(comparator_4_eq));  // open: gt, lt
  Comparator #(.width(16), .mode("twosComplement")) comparator_5 (
    .a(\总周期数 ), .b(16'h4), .eq(comparator_5_eq));  // open: gt, lt
  or or_2 (or_2_out, comparator_1_eq, comparator_2_eq);
  Hex_Digit_Display hex_digit_display_4 (.value(LedData[15:12]));  // open: dp
  Hex_Digit_Display hex_digit_display_5 (.value(LedData[19:16]));  // open: dp
  Pull_Resistor #(.pull(0)) pull_resistor_1 (.node(IRA));
  assign IRA = or_1_out ? ~CLK : 1'bz;  // Controlled_Inverter controlled_inverter_1
  Pull_Resistor #(.pull(0)) pull_resistor_2 (.node(IRB));
  assign IRB = comparator_5_eq ? ~CLK : 1'bz;  // Controlled_Inverter controlled_inverter_2
  Pull_Resistor #(.pull(0)) pull_resistor_3 (.node(IRC));
  assign IRC = or_2_out ? ~CLK : 1'bz;  // Controlled_Inverter controlled_inverter_3
  Hex_Digit_Display hex_digit_display_6 (.value(LedData[11:8]));  // open: dp
  Hex_Digit_Display hex_digit_display_7 (.value(LedData[7:4]));  // open: dp
  // Probe on \总周期数 
  Hex_Digit_Display hex_digit_display_8 (.value(LedData[3:0]));  // open: dp
  Multiplexer #(.select(2), .width(32), .disabled("Z"), .enable("false")) multiplexer_1 (
    .in0(PC_4), .in1(result), .in2(adder_3_out), .in3(adder_2_out), .out(NowPC), .sel(priority_encoder_1_out));
  Multiplexer #(.select(1), .width(32), .disabled("Z"), .enable("false")) multiplexer_2 (
    .in0(NowPC), .in1(RetPC), .out(multiplexer_2_out), .sel(uret));
  or or_3 (IR1_t, IR1, IRA);
  Priority_Encoder #(.select(2), .disabled("Z")) priority_encoder_1 (
    .in0(1'b1), .in1(jalr), .in2(jal), .in3(or_4_out), .out(priority_encoder_1_out));  // open: gs, en_out, en_in
  or or_4 (or_4_out, and_1_out, and_2_out, and_3_out);
  and and_1 (and_1_out, Beq, equal);
  Multiplexer #(.select(1), .width(32), .disabled("Z"), .enable("false")) multiplexer_3 (
    .in0(multiplexer_2_out), .in1(\中断服务地址 ), .out(multiplexer_3_out), .sel(\发生中断 ));
  not not_1 (not_1_out, halt);
  or or_5 (W1, IR1_q, d_ff_1_q);
  or or_6 (W2, IR1_2_q, d_ff_2_q);
  or or_7 (W3, IR1_3_q, d_ff_3_q);
  or or_8 (IR2_t, IR2, IRB);
  and and_2 (and_2_out, GE, BGEU);
  and and_3 (and_3_out, ~equal, Bne);  // AND_Gate
  Register #(.width(32), .trigger("rising"), .Select("low")) u_PC (
    .D(multiplexer_3_out), .en(not_1_out), .Q(PC), .clk(CLK), .clr(RST));
  D_Flip_Flop #(.trigger("rising"), .Pre_Clr_Positions("LEGACY"), .NegatePresetClear("false"), .enable("true"), .NewFFLayout("false")) d_ff_1 (
    .clk(IR1_t), .D(1'b1), .Q(d_ff_1_q), .reset(IR1_q));  // open: Qn, preset, en
  D_Flip_Flop #(.trigger("rising"), .Pre_Clr_Positions("LEGACY"), .NegatePresetClear("false"), .enable("true"), .NewFFLayout("false")) d_ff_2 (
    .clk(IR2_t), .D(1'b1), .Q(d_ff_2_q), .reset(IR1_2_q));  // open: Qn, preset, en
  D_Flip_Flop #(.trigger("rising"), .Pre_Clr_Positions("LEGACY"), .NegatePresetClear("false"), .enable("true"), .NewFFLayout("false")) d_ff_3 (
    .clk(IR3_t), .D(1'b1), .Q(d_ff_3_q), .reset(IR1_3_q));  // open: Qn, preset, en
  Adder #(.width(32)) adder_1 (.a(PC), .b(32'h4), .out(PC_4));  // open: cin, cout
  or or_9 (or_9_out, d_ff_1_q, IR1_q);
  or or_10 (or_10_out, d_ff_2_q, IR1_2_q);
  or or_11 (or_11_out, d_ff_3_q, IR1_3_q);
  or or_12 (IR3_t, IR3, IRC);
  // RiscV_Probe riscv_probe_1: pin names not known; wires that end beside it: IR, IR
  and and_4 (and_4_out, or_9_out, ~clr1);  // AND_Gate
  and and_5 (and_5_out, or_10_out, ~clr2);  // AND_Gate
  and and_6 (and_6_out, or_11_out, ~clr3);  // AND_Gate
  ROM #(.addrWidth(10), .dataWidth(32), .Select("high")) rom_1 (.addr(PC[11:2]), .data(IR));
  D_Flip_Flop #(.trigger("rising"), .Pre_Clr_Positions("LEGACY"), .NegatePresetClear("false"), .enable("true"), .NewFFLayout("false")) u_IR1 (
    .clk(CLK), .D(and_4_out), .Q(IR1_q), .reset(RST));  // open: Qn, preset, en
  D_Flip_Flop #(.trigger("rising"), .Pre_Clr_Positions("LEGACY"), .NegatePresetClear("false"), .enable("true"), .NewFFLayout("false")) IR1_2 (
    .clk(CLK), .D(and_5_out), .Q(IR1_2_q), .reset(RST));  // open: Qn, preset, en
  D_Flip_Flop #(.trigger("rising"), .Pre_Clr_Positions("LEGACY"), .NegatePresetClear("false"), .enable("true"), .NewFFLayout("false")) IR1_3 (
    .clk(CLK), .D(and_6_out), .Q(IR1_3_q), .reset(RST));  // open: Qn, preset, en
  \单周期硬布线控制器  \u_单周期硬布线控制器_1  (
    .Funct({IR[30], IR[25], IR[14:12]}), .OP(IR[6:2]), .ALU_OP(\单周期硬布线控制器_1_alu_op ), .MemToReg(MemToReg),
    .MemWrite(MemWrite), .ALU_SRC(\单周期硬布线控制器_1_alu_src ), .RegWrite(RegWrite), .ecall(ecall),
    .S_type(\单周期硬布线控制器_1_s_type ), .Jalr(jalr), .Beq(Beq), .JAL(jal), .Bne(Bne), .in_3(IR[21]), .uret(uret),
    .AUIPC(AUIPC), .BGEU(BGEU), .SB(SB), .CSRRSI(open), .CSRRCI(close));  // open: Rs1used, Rs2used
  Multiplexer #(.select(1), .width(5), .disabled("Z"), .enable("false")) multiplexer_4 (
    .in0(IR[19:15]), .in1(5'b10001), .out(multiplexer_4_out), .sel(ecall));
  Multiplexer #(.select(1), .width(5), .disabled("Z"), .enable("false")) multiplexer_5 (
    .in0(IR[24:20]), .in1(5'b01010), .out(multiplexer_5_out), .sel(ecall));
  assign bit_extender_1_out = {{20{IR[31]}}, IR[31:20]};  // Bit_Extender bit_extender_1
  Multiplexer #(.select(1), .width(32), .disabled("Z"), .enable("false")) multiplexer_6 (
    .in0(bit_extender_1_out), .in1(bit_extender_2_out), .out(multiplexer_6_out), .sel(\单周期硬布线控制器_1_s_type ));
  assign bit_extender_2_out = {{20{IR[31]}}, {IR[31:25], IR[11:7]}};  // Bit_Extender bit_extender_2
  assign bit_extender_3_out = {{20{IR[31]}}, {IR[31], IR[7], IR[30:25], IR[11:8]}};  // Bit_Extender bit_extender_3
  assign bit_extender_4_out = {{12{IR[31]}}, {IR[31], IR[19:12], IR[20], IR[30:21]}};  // Bit_Extender bit_extender_4
  assign bit_extender_5_out = {{12{IR[31]}}, IR[31:12]};  // Bit_Extender bit_extender_5
  Priority_Encoder #(.select(2), .disabled("Z")) priority_encoder_2 (
    .in0(1'b1), .in1(IR1_q), .in2(IR1_2_q), .in3(IR1_3_q), .out(\中断号 ));  // open: gs, en_out, en_in
  or or_13 (or_13_out, IR1_q, IR1_2_q, IR1_3_q);
  Shifter #(.width(32), .shift("ll")) shifter_1 (.in(bit_extender_3_out), .\dist (5'b00001), .out(shifter_1_out));
  Shifter #(.width(32), .shift("ll")) shifter_2 (.in(bit_extender_4_out), .\dist (5'b00001), .out(shifter_2_out));
  Shifter #(.width(32), .shift("ll")) shifter_3 (.in(bit_extender_5_out), .\dist (5'b01100), .out(shifter_3_out));
  and and_7 (\中断信号 , or_13_out, IE);
  Regifile regifile_1 (
    .Din(RDin), .Clk(CLK), .R1(regifile_1_r1), .R2(regifile_1_r2), .WE(RegWrite), .W_num(IR[11:7]),
    .R1_num(multiplexer_4_out), .R2_num(multiplexer_5_out));
  Adder #(.width(32)) adder_2 (.a(shifter_1_out), .b(PC), .out(adder_2_out));  // open: cin, cout
  Adder #(.width(32)) adder_3 (.a(shifter_2_out), .b(PC), .out(adder_3_out));  // open: cin, cout
  Adder #(.width(32)) adder_4 (.a(shifter_3_out), .b(PC), .out(PC_imm));  // open: cin, cout
  Register #(.width(2), .trigger("rising"), .Select("low")) register_1 (
    .D(\当前中断号 ), .Q(register_1_q), .clk(CLK), .clr(RST));  // open: en
  Multiplexer #(.select(1), .width(32), .disabled("Z"), .enable("false")) multiplexer_7 (
    .in0(regifile_1_r2), .in1(multiplexer_6_out), .out(multiplexer_7_out), .sel(\单周期硬布线控制器_1_alu_src ));
  or or_14 (or_14_out, close, \发生中断 );
  Decoder #(.select(2), .tristate("false"), .disabled("Z"), .enable("false")) decoder_1 (
    .out1(decoder_1_out1), .out2(decoder_1_out2), .out3(decoder_1_out3), .sel(register_1_q));  // open: out0
  Comparator #(.width(2), .mode("unsigned")) comparator_6 (
    .a(\当前中断号 ), .b(2'b01), .eq(comparator_6_eq));  // open: gt, lt
  not not_2 (not_2_out, hasrun1);
  Comparator #(.width(2), .mode("unsigned")) comparator_7 (
    .a(\当前中断号 ), .b(2'b10), .eq(comparator_7_eq));  // open: gt, lt
  not not_3 (not_3_out, hasrun2);
  Comparator #(.width(2), .mode("unsigned")) comparator_8 (
    .a(\当前中断号 ), .b(2'b11), .eq(comparator_8_eq));  // open: gt, lt
  ALU alu_1 (
    .X(regifile_1_r1), .Y(multiplexer_7_out), .AluOP(\单周期硬布线控制器_1_alu_op ), .Equal(equal), .Result(result),
    .out_4(GE));  // open: Result_2, out_6
  Multiplexer #(.select(1), .width(32), .disabled("Z"), .enable("false")) multiplexer_8 (
    .in0(regifile_1_r2),
    .in1({regifile_1_r2[7:0], regifile_1_r2[7:0], regifile_1_r2[7:0], regifile_1_r2[7:0]}), .out(MDin),
    .sel(SB));
  Multiplexer #(.select(2), .width(32), .disabled("Z"), .enable("false")) multiplexer_9 (
    .in1(32'h30ac), .in2(32'h3158), .in3(32'h3204), .out(\中断服务地址 ), .sel(\当前中断号 ));  // open: in0
  D_Flip_Flop #(.trigger("rising"), .Pre_Clr_Positions("LEGACY"), .NegatePresetClear("false"), .enable("true"), .NewFFLayout("false")) d_ff_4 (
    .Q(d_ff_4_q), .preset(or_14_out), .reset(or_15_out));  // open: clk, D, Qn, en
  or or_15 (or_15_out, uret, RST, open);
  Comparator #(.width(2), .mode("unsigned")) comparator_9 (
    .a(register_1_q), .b(\当前中断号 ), .eq(comparator_9_eq));  // open: gt, lt
  and and_8 (clr1, decoder_1_out1, uret);
  and and_9 (clr2, decoder_1_out2, uret);
  and and_10 (clr3, decoder_1_out3, uret);
  and and_11 (and_11_out, comparator_6_eq, not_2_out);
  and and_12 (and_12_out, comparator_7_eq, not_3_out);
  Button button_1 (.out(RST));
  Decoder #(.select(2), .tristate("false"), .disabled("Z"), .enable("false")) decoder_2 (
    .out0(decoder_2_out0[0]), .out1(decoder_2_out0[1]), .out2(decoder_2_out0[2]), .out3(decoder_2_out0[3]),
    .sel(result[1:0]));
  Comparator #(.width(32), .mode("twosComplement")) comparator_10 (
    .a(32'h22), .b(regifile_1_r1), .eq(comparator_10_eq));  // open: gt, lt
  D_Flip_Flop #(.trigger("rising"), .Pre_Clr_Positions("LEGACY"), .NegatePresetClear("false"), .enable("true"), .NewFFLayout("false")) d_ff_5 (
    .clk(CLK), .D(d_ff_4_q), .Qn(IE), .reset(RST));  // open: Q, preset, en
  not not_4 (not_4_out, halt);
  and and_13 (and_13_out, comparator_10_eq, ecall);
  not not_5 (not_5_out, comparator_9_eq);
  or or_16 (or_16_out, and_11_out, and_12_out, comparator_8_eq);
  Counter #(.width(16), .max('hffff), .ongoal("wrap"), .trigger("rising"), .behavior("new")) counter_1 (
    .count(not_4_out), .Q(\总周期数 ), .clk(CLK), .clr(RST));  // open: load, D, carry, preset, down
  // MIPS_RAM mips_ram_1: pin names not known; wires that end beside it: result[21:2], MDin, MemWrite, mips_ram_1_p4, CLK, LedData, 1'b1, RST, mips_ram_1_p9
  Multiplexer #(.select(1), .width(4), .disabled("Z"), .enable("false")) multiplexer_10 (
    .in0(4'b1111), .in1(decoder_2_out0), .out(mips_ram_1_p4), .sel(SB));
  Register #(.width(32), .trigger("rising"), .Select("low")) register_2 (
    .D(regifile_1_r2), .en(and_13_out), .Q(LedData), .clk(CLK), .clr(RST));
  and and_14 (halt, ~comparator_10_eq, ~Go, ecall);  // AND_Gate
  and and_15 (\发生中断 , not_5_out, or_16_out);
  Decoder #(.select(2), .tristate("false"), .disabled("Z"), .enable("false")) decoder_3 (
    .out1(decoder_3_out1), .out2(decoder_3_out2), .out3(decoder_3_out3), .sel(\中断号 ));  // open: out0
  Priority_Encoder #(.select(2), .disabled("Z")) priority_encoder_3 (
    .in0(1'b1), .in1(MemToReg), .in2(or_17_out), .in3(AUIPC), .out(priority_encoder_3_out));  // open: gs, en_out, en_in
  Multiplexer #(.select(2), .width(32), .disabled("Z"), .enable("false")) multiplexer_11 (
    .in0(result), .in1(mips_ram_1_p9), .in2(PC_4), .in3(PC_imm), .out(RDin), .sel(priority_encoder_3_out));
  Decoder #(.select(2), .tristate("false"), .disabled("Z"), .enable("false")) decoder_4 (
    .out1(decoder_4_out1), .out2(decoder_4_out2), .out3(decoder_4_out3), .sel(\中断号 ));  // open: out0
  and and_16 (and_16_out, decoder_3_out1, \中断信号 );
  and and_17 (and_17_out, decoder_3_out2, \中断信号 );
  and and_18 (and_18_out, decoder_3_out3, \中断信号 );
  and and_19 (and_19_out, decoder_4_out1, \发生中断 );
  and and_20 (and_20_out, decoder_4_out2, \发生中断 );
  and and_21 (and_21_out, decoder_4_out3, \发生中断 );
  or or_17 (or_17_out, jal, jalr);
  Register #(.width(1), .trigger("rising"), .Select("low")) register_3 (
    .Q(register_3_q), .clk(CLK), .clr(or_18_out), .preset(and_16_out));  // open: D, en, cs
  or or_18 (or_18_out, d_ff_9_q, RST);
  Register #(.width(1), .trigger("rising"), .Select("low")) register_4 (
    .Q(register_4_q), .clk(CLK), .clr(or_19_out), .preset(and_17_out));  // open: D, en, cs
  or or_19 (or_19_out, d_ff_10_q, RST);
  Register #(.width(1), .trigger("rising"), .Select("low")) register_5 (
    .Q(register_5_q), .clk(CLK), .clr(or_20_out), .preset(and_18_out));  // open: D, en, cs
  or or_20 (or_20_out, d_ff_11_q, RST);
  Register #(.width(32), .trigger("rising"), .Select("low")) register_6 (
    .D(NowPC), .en(and_19_out), .Q(register_6_q), .clk(CLK), .clr(or_21_out));
  or or_21 (or_21_out, d_ff_6_q, RST);
  Register #(.width(32), .trigger("rising"), .Select("low")) register_7 (
    .D(NowPC), .en(and_20_out), .Q(register_7_q), .clk(CLK), .clr(or_22_out));
  or or_22 (or_22_out, d_ff_7_q, RST);
  Register #(.width(32), .trigger("rising"), .Select("low")) register_8 (
    .D(NowPC), .en(and_21_out), .Q(register_8_q), .clk(CLK), .clr(or_23_out));
  or or_23 (or_23_out, d_ff_8_q, RST);
  Priority_Encoder #(.select(2), .disabled("Z")) priority_encoder_4 (
    .in0(1'b1), .in1(register_3_q), .in2(register_4_q), .in3(register_5_q), .out(\当前中断号 ));  // open: gs, en_out, en_in
  D_Flip_Flop #(.trigger("rising"), .Pre_Clr_Positions("LEGACY"), .NegatePresetClear("false"), .enable("true"), .NewFFLayout("false")) d_ff_6 (
    .clk(CLK), .D(d_ff_12_q), .Q(d_ff_6_q));  // open: Qn, preset, en, reset
  D_Flip_Flop #(.trigger("rising"), .Pre_Clr_Positions("LEGACY"), .NegatePresetClear("false"), .enable("true"), .NewFFLayout("false")) d_ff_7 (
    .clk(CLK), .D(d_ff_13_q), .Q(d_ff_7_q));  // open: Qn, preset, en, reset
  D_Flip_Flop #(.trigger("rising"), .Pre_Clr_Positions("LEGACY"), .NegatePresetClear("false"), .enable("true"), .NewFFLayout("false")) d_ff_8 (
    .clk(CLK), .D(d_ff_14_q), .Q(d_ff_8_q));  // open: Qn, preset, en, reset
  Comparator #(.width(32), .mode("unsigned")) comparator_11 (
    .a(register_7_q), .b(32'h30ac), .gt(comparator_11_gt));  // open: eq, lt
  Comparator #(.width(32), .mode("unsigned")) comparator_12 (
    .a(register_7_q), .b(32'h3158), .lt(comparator_12_lt));  // open: gt, eq
  Comparator #(.width(32), .mode("unsigned")) comparator_13 (
    .a(register_8_q), .b(32'h30ac), .gt(comparator_13_gt));  // open: eq, lt
  Comparator #(.width(32), .mode("unsigned")) comparator_14 (
    .a(register_8_q), .b(32'h3158), .lt(comparator_14_lt));  // open: gt, eq
  Comparator #(.width(32), .mode("unsigned")) comparator_15 (
    .a(register_8_q), .b(32'h3158), .gt(comparator_15_gt));  // open: eq, lt
  Comparator #(.width(32), .mode("unsigned")) comparator_16 (
    .a(register_8_q), .b(32'h3204), .lt(comparator_16_lt));  // open: gt, eq
  D_Flip_Flop #(.trigger("rising"), .Pre_Clr_Positions("LEGACY"), .NegatePresetClear("false"), .enable("true"), .NewFFLayout("false")) d_ff_9 (
    .clk(CLK), .D(clr1), .Q(d_ff_9_q));  // open: Qn, preset, en, reset
  D_Flip_Flop #(.trigger("rising"), .Pre_Clr_Positions("LEGACY"), .NegatePresetClear("false"), .enable("true"), .NewFFLayout("false")) d_ff_10 (
    .clk(CLK), .D(clr2), .Q(d_ff_10_q));  // open: Qn, preset, en, reset
  D_Flip_Flop #(.trigger("rising"), .Pre_Clr_Positions("LEGACY"), .NegatePresetClear("false"), .enable("true"), .NewFFLayout("false")) d_ff_11 (
    .clk(CLK), .D(clr3), .Q(d_ff_11_q));  // open: Qn, preset, en, reset
  D_Flip_Flop #(.trigger("rising"), .Pre_Clr_Positions("LEGACY"), .NegatePresetClear("false"), .enable("true"), .NewFFLayout("false")) d_ff_12 (
    .clk(CLK), .D(clr1), .Q(d_ff_12_q));  // open: Qn, preset, en, reset
  D_Flip_Flop #(.trigger("rising"), .Pre_Clr_Positions("LEGACY"), .NegatePresetClear("false"), .enable("true"), .NewFFLayout("false")) d_ff_13 (
    .clk(CLK), .D(clr2), .Q(d_ff_13_q));  // open: Qn, preset, en, reset
  D_Flip_Flop #(.trigger("rising"), .Pre_Clr_Positions("LEGACY"), .NegatePresetClear("false"), .enable("true"), .NewFFLayout("false")) d_ff_14 (
    .clk(CLK), .D(clr3), .Q(d_ff_14_q));  // open: Qn, preset, en, reset
  and and_22 (and_22_out, comparator_11_gt, comparator_12_lt);
  and and_23 (and_23_out, comparator_13_gt, comparator_14_lt);
  and and_24 (hasrun2, comparator_15_gt, comparator_16_lt);
  Multiplexer #(.select(2), .width(32), .disabled("Z"), .enable("false")) multiplexer_12 (
    .in0(register_6_q), .in1(register_7_q), .in2(register_8_q), .out(RetPC), .sel(\当前中断号 ));  // open: in3
  or or_24 (hasrun1, and_22_out, and_23_out);

  // Notes on the sheet:
  //   中断源
  //   中断等待指示
  //   总复位信号应将除ROM以外所有存储组件全部清零
  //   多级中断测试信号模拟器
  //   数码管输出
  //   数码管输出应该用寄存器锁存，否则显示数据只能一闪而过
  //   指令探针
  //   指令存储器
  //   Reset 
  //   Reset 
  //   Reset 
  //   指令字
  //   contents of rom_1 (hex, n*v repeats v):
  //   7d000113 100413 1f41993 41f9d993 433 c00913 800b13 140413 f47413 800293 100313 499993 89e9b3 1300533
  //   2200893 73 406282b3 fe0294e3 140413 f00f93 1f47433 1c41413 800293 100313 49d993 89e9b3 1300533
  //   2200893 73 406282b3 fe0294e3 1c45413 406b0b33 b0463 f95ff06f 2b3 fff2c293 1029293 fff2e293 500533
  //   2200893 73 f5dff06f 1112023 410113 a12023 410113 812023 410113 1312023 410113 1412023 410113 1512023
  //   410113 1612023 410113 40e073 100b13 300a13 100a93 1600433 441413 14469b3 1300533 2200893 73 fe0416e3
  //   415a0a33 fe0a10e3 40f073 ffc10113 12b03 ffc10113 12a83 ffc10113 12a03 ffc10113 12983 ffc10113 12403
  //   ffc10113 12503 ffc10113 12883 200073 1112023 410113 a12023 410113 812023 410113 1312023 410113
  //   1412023 410113 1512023 410113 1612023 410113 40e073 200b13 300a13 100a93 1600433 441413 14469b3
  //   1300533 2200893 73 fe0416e3 415a0a33 fe0a10e3 40f073 ffc10113 12b03 ffc10113 12a83 ffc10113 12a03
  //   ffc10113 12983 ffc10113 12403 ffc10113 12503 ffc10113 12883 200073 1112023 410113 a12023 410113
  //   812023 410113 1312023 410113 1412023 410113 1512023 410113 1612023 410113 40e073 300b13 300a13
  //   100a93 1600433 441413 14469b3 1300533 2200893 73 fe0416e3 415a0a33 fe0a10e3 40f073 ffc10113 12b03
  //   ffc10113 12a83 ffc10113 12a03 ffc10113 12983 ffc10113 12403 ffc10113 12503 ffc10113 12883 200073
  //   JALR
  //   为方便自动评测，需要输出PC，IR，寄存器堆写如数据RDin
  //   Beq
  //   Bne
  //   MemToReg
  //   MemWrite
  //   AluOP
  //   AluSrcB
  //   RegWrite
  //   RAM写使能MemWrite、RAM写入数据MDin等信号
  //   数据存储器
endmodule

module IF_ID (
  input  PredictJump,
  input  [31:0] IR,
  input  [31:0] PC,
  input  [31:0] PC_4,
  input  en,
  input  clk,
  input  reset,
  input  BranchTaken,
  output out_9,
  output [31:0] IR_2,
  output [31:0] PC_2,
  output [31:0] PC_4_2
);

  wire multiplexer_1_out, or_1_out;
  wire [31:0] multiplexer_2_out, multiplexer_3_out, multiplexer_4_out;

  Multiplexer #(.select(1), .width(1), .disabled("Z"), .enable("false")) multiplexer_1 (
    .in0(PredictJump), .in1(1'b0), .out(multiplexer_1_out), .sel(or_1_out));
  Multiplexer #(.select(1), .width(32), .disabled("Z"), .enable("false")) multiplexer_2 (
    .in0(IR), .in1({32{1'b0}}), .out(multiplexer_2_out), .sel(or_1_out));
  Multiplexer #(.select(1), .width(32), .disabled("Z"), .enable("false")) multiplexer_3 (
    .in0(PC), .in1({32{1'b0}}), .out(multiplexer_3_out), .sel(or_1_out));
  Multiplexer #(.select(1), .width(32), .disabled("Z"), .enable("false")) multiplexer_4 (
    .in0(PC_4), .in1({32{1'b0}}), .out(multiplexer_4_out), .sel(or_1_out));
  or or_1 (or_1_out, reset, BranchTaken);
  Register #(.width(1), .trigger("rising"), .Select("low")) register_1 (
    .D(multiplexer_1_out), .en(en), .Q(out_9), .clk(clk));  // open: clr
  Register #(.width(32), .trigger("rising"), .Select("low")) register_2 (
    .D(multiplexer_2_out), .en(en), .Q(IR_2), .clk(clk));  // open: clr
  Register #(.width(32), .trigger("rising"), .Select("low")) register_3 (
    .D(multiplexer_3_out), .en(en), .Q(PC_2), .clk(clk));  // open: clr
  Register #(.width(32), .trigger("rising"), .Select("low")) register_4 (
    .D(multiplexer_4_out), .en(en), .Q(PC_4_2), .clk(clk));  // open: clr
endmodule

module ID_EX (
  input  PredictJump,
  input  BEQ,
  input  BNE,
  input  MEMTOREG,
  input  MEMWRITE,
  input  ALUSRCB,
  input  REGWRITE,
  input  URET,
  input  ECALL,
  input  JAL,
  input  JALR,
  input  AUIPC,
  input  BGEU,
  input  SB,
  input  [3:0] ALUop,
  input  [4:0] rd,
  input  [31:0] imm4,
  input  [31:0] R1,
  input  [31:0] R2,
  input  [31:0] imm1,
  input  [31:0] imm2,
  input  [31:0] imm3,
  input  [31:0] IR,
  input  [31:0] PC,
  input  [31:0] PC_4,
  input  [1:0] Rs1Forward,
  input  [1:0] Rs2Forward,
  input  reset,
  input  flush,
  input  en,
  input  clk,
  output out_32,
  output out_33,
  output out_34,
  output out_35,
  output out_36,
  output out_37,
  output out_38,
  output out_39,
  output out_40,
  output out_41,
  output out_42,
  output out_43,
  output out_44,
  output out_45,
  output [3:0] out_46,
  output [4:0] out_47,
  output [31:0] out_48,
  output [31:0] out_49,
  output [31:0] out_50,
  output [31:0] out_51,
  output [31:0] out_52,
  output [31:0] out_53,
  output [31:0] out_54,
  output [31:0] out_55,
  output [31:0] out_56,
  output [1:0] out_57,
  output [1:0] out_58
);

  wire multiplexer_1_out, multiplexer_2_out, multiplexer_3_out, multiplexer_4_out, multiplexer_5_out,
       multiplexer_6_out, multiplexer_7_out, multiplexer_8_out, multiplexer_9_out, multiplexer_10_out,
       multiplexer_11_out, multiplexer_12_out, multiplexer_13_out, multiplexer_14_out, or_1_out;
  wire [1:0] multiplexer_26_out, multiplexer_27_out;
  wire [3:0] multiplexer_15_out;
  wire [4:0] multiplexer_16_out;
  wire [31:0] multiplexer_17_out, multiplexer_18_out, multiplexer_19_out, multiplexer_20_out,
       multiplexer_21_out, multiplexer_22_out, multiplexer_23_out, multiplexer_24_out, multiplexer_25_out;

  Multiplexer #(.select(1), .width(1), .disabled("Z"), .enable("false")) multiplexer_1 (
    .in0(PredictJump), .in1(1'b0), .out(multiplexer_1_out), .sel(or_1_out));
  Multiplexer #(.select(1), .width(1), .disabled("Z"), .enable("false")) multiplexer_2 (
    .in0(BEQ), .in1(1'b0), .out(multiplexer_2_out), .sel(or_1_out));
  Multiplexer #(.select(1), .width(1), .disabled("Z"), .enable("false")) multiplexer_3 (
    .in0(BNE), .in1(1'b0), .out(multiplexer_3_out), .sel(or_1_out));
  Multiplexer #(.select(1), .width(1), .disabled("Z"), .enable("false")) multiplexer_4 (
    .in0(MEMTOREG), .in1(1'b0), .out(multiplexer_4_out), .sel(or_1_out));
  Multiplexer #(.select(1), .width(1), .disabled("Z"), .enable("false")) multiplexer_5 (
    .in0(MEMWRITE), .in1(1'b0), .out(multiplexer_5_out), .sel(or_1_out));
  Multiplexer #(.select(1), .width(1), .disabled("Z"), .enable("false")) multiplexer_6 (
    .in0(ALUSRCB), .in1(1'b0), .out(multiplexer_6_out), .sel(or_1_out));
  Multiplexer #(.select(1), .width(1), .disabled("Z"), .enable("false")) multiplexer_7 (
    .in0(REGWRITE), .in1(1'b0), .out(multiplexer_7_out), .sel(or_1_out));
  Multiplexer #(.select(1), .width(1), .disabled("Z"), .enable("false")) multiplexer_8 (
    .in0(URET), .in1(1'b0), .out(multiplexer_8_out), .sel(or_1_out));
  Multiplexer #(.select(1), .width(1), .disabled("Z"), .enable("false")) multiplexer_9 (
    .in0(ECALL), .in1(1'b0), .out(multiplexer_9_out), .sel(or_1_out));
  Multiplexer #(.select(1), .width(1), .disabled("Z"), .enable("false")) multiplexer_10 (
    .in0(JAL), .in1(1'b0), .out(multiplexer_10_out), .sel(or_1_out));
  Multiplexer #(.select(1), .width(1), .disabled("Z"), .enable("false")) multiplexer_11 (
    .in0(JALR), .in1(1'b0), .out(multiplexer_11_out), .sel(or_1_out));
  Multiplexer #(.select(1), .width(1), .disabled("Z"), .enable("false")) multiplexer_12 (
    .in0(AUIPC), .in1(1'b0), .out(multiplexer_12_out), .sel(or_1_out));
  Multiplexer #(.select(1), .width(1), .disabled("Z"), .enable("false")) multiplexer_13 (
    .in0(BGEU), .in1(1'b0), .out(multiplexer_13_out), .sel(or_1_out));
  Multiplexer #(.select(1), .width(1), .disabled("Z"), .enable("false")) multiplexer_14 (
    .in0(SB), .in1(1'b0), .out(multiplexer_14_out), .sel(or_1_out));
  Multiplexer #(.select(1), .width(4), .disabled("Z"), .enable("false")) multiplexer_15 (
    .in0(ALUop), .in1(4'b0000), .out(multiplexer_15_out), .sel(or_1_out));
  Multiplexer #(.select(1), .width(5), .disabled("Z"), .enable("false")) multiplexer_16 (
    .in0(rd), .in1({5{1'b0}}), .out(multiplexer_16_out), .sel(or_1_out));
  Multiplexer #(.select(1), .width(32), .disabled("Z"), .enable("false")) multiplexer_17 (
    .in0(imm4), .in1({32{1'b0}}), .out(multiplexer_17_out), .sel(or_1_out));
  Multiplexer #(.select(1), .width(32), .disabled("Z"), .enable("false")) multiplexer_18 (
    .in0(R1), .in1({32{1'b0}}), .out(multiplexer_18_out), .sel(or_1_out));
  Multiplexer #(.select(1), .width(32), .disabled("Z"), .enable("false")) multiplexer_19 (
    .in0(R2), .in1({32{1'b0}}), .out(multiplexer_19_out), .sel(or_1_out));
  Multiplexer #(.select(1), .width(32), .disabled("Z"), .enable("false")) multiplexer_20 (
    .in0(imm1), .in1({32{1'b0}}), .out(multiplexer_20_out), .sel(or_1_out));
  Multiplexer #(.select(1), .width(32), .disabled("Z"), .enable("false")) multiplexer_21 (
    .in0(imm2), .in1({32{1'b0}}), .out(multiplexer_21_out), .sel(or_1_out));
  Multiplexer #(.select(1), .width(32), .disabled("Z"), .enable("false")) multiplexer_22 (
    .in0(imm3), .in1({32{1'b0}}), .out(multiplexer_22_out), .sel(or_1_out));
  Multiplexer #(.select(1), .width(32), .disabled("Z"), .enable("false")) multiplexer_23 (
    .in0(IR), .in1({32{1'b0}}), .out(multiplexer_23_out), .sel(or_1_out));
  Multiplexer #(.select(1), .width(32), .disabled("Z"), .enable("false")) multiplexer_24 (
    .in0(PC), .in1({32{1'b0}}), .out(multiplexer_24_out), .sel(or_1_out));
  Multiplexer #(.select(1), .width(32), .disabled("Z"), .enable("false")) multiplexer_25 (
    .in0(PC_4), .in1({32{1'b0}}), .out(multiplexer_25_out), .sel(or_1_out));
  Multiplexer #(.select(1), .width(2), .disabled("Z"), .enable("false")) multiplexer_26 (
    .in0(Rs1Forward), .in1(2'b00), .out(multiplexer_26_out), .sel(or_1_out));
  Multiplexer #(.select(1), .width(2), .disabled("Z"), .enable("false")) multiplexer_27 (
    .in0(Rs2Forward), .in1(2'b00), .out(multiplexer_27_out), .sel(or_1_out));
  or or_1 (or_1_out, reset, flush);
  Register #(.width(1), .trigger("rising"), .Select("low")) register_1 (
    .D(multiplexer_1_out), .en(en), .Q(out_32), .clk(clk));  // open: clr
  Register #(.width(1), .trigger("rising"), .Select("low")) register_2 (
    .D(multiplexer_2_out), .en(en), .Q(out_33), .clk(clk));  // open: clr
  Register #(.width(1), .trigger("rising"), .Select("low")) register_3 (
    .D(multiplexer_3_out), .en(en), .Q(out_34), .clk(clk));  // open: clr
  Register #(.width(1), .trigger("rising"), .Select("low")) register_4 (
    .D(multiplexer_4_out), .en(en), .Q(out_35), .clk(clk));  // open: clr
  Register #(.width(1), .trigger("rising"), .Select("low")) register_5 (
    .D(multiplexer_5_out), .en(en), .Q(out_36), .clk(clk));  // open: clr
  Register #(.width(1), .trigger("rising"), .Select("low")) register_6 (
    .D(multiplexer_6_out), .en(en), .Q(out_37), .clk(clk));  // open: clr
  Register #(.width(1), .trigger("rising"), .Select("low")) register_7 (
    .D(multiplexer_7_out), .en(en), .Q(out_38), .clk(clk));  // open: clr
  Register #(.width(1), .trigger("rising"), .Select("low")) register_8 (
    .D(multiplexer_8_out), .en(en), .Q(out_39), .clk(clk));  // open: clr
  Register #(.width(1), .trigger("rising"), .Select("low")) register_9 (
    .D(multiplexer_9_out), .en(en), .Q(out_40), .clk(clk));  // open: clr
  Register #(.width(1), .trigger("rising"), .Select("low")) register_10 (
    .D(multiplexer_10_out), .en(en), .Q(out_41), .clk(clk));  // open: clr
  Register #(.width(1), .trigger("rising"), .Select("low")) register_11 (
    .D(multiplexer_11_out), .en(en), .Q(out_42), .clk(clk));  // open: clr
  Register #(.width(1), .trigger("rising"), .Select("low")) register_12 (
    .D(multiplexer_12_out), .en(en), .Q(out_43), .clk(clk));  // open: clr
  Register #(.width(1), .trigger("rising"), .Select("low")) register_13 (
    .D(multiplexer_13_out), .en(en), .Q(out_44), .clk(clk));  // open: clr
  Register #(.width(1), .trigger("rising"), .Select("low")) register_14 (
    .D(multiplexer_14_out), .en(en), .Q(out_45), .clk(clk));  // open: clr
  Register #(.width(4), .trigger("rising"), .Select("low")) register_15 (
    .D(multiplexer_15_out), .en(en), .Q(out_46), .clk(clk));  // open: clr
  Register #(.width(5), .trigger("rising"), .Select("low")) register_16 (
    .D(multiplexer_16_out), .en(en), .Q(out_47), .clk(clk));  // open: clr
  Register #(.width(32), .trigger("rising"), .Select("low")) register_17 (
    .D(multiplexer_17_out), .en(en), .Q(out_48), .clk(clk));  // open: clr
  Register #(.width(32), .trigger("rising"), .Select("low")) register_18 (
    .D(multiplexer_18_out), .en(en), .Q(out_49), .clk(clk));  // open: clr
  Register #(.width(32), .trigger("rising"), .Select("low")) register_19 (
    .D(multiplexer_19_out), .en(en), .Q(out_50), .clk(clk));  // open: clr
  Register #(.width(32), .trigger("rising"), .Select("low")) register_20 (
    .D(multiplexer_20_out), .en(en), .Q(out_51), .clk(clk));  // open: clr
  Register #(.width(32), .trigger("rising"), .Select("low")) register_21 (
    .D(multiplexer_21_out), .en(en), .Q(out_52), .clk(clk));  // open: clr
  Register #(.width(32), .trigger("rising"), .Select("low")) register_22 (
    .D(multiplexer_22_out), .en(en), .Q(out_53), .clk(clk));  // open: clr
  Register #(.width(32), .trigger("rising"), .Select("low")) register_23 (
    .D(multiplexer_23_out), .en(en), .Q(out_54), .clk(clk));  // open: clr
  Register #(.width(32), .trigger("rising"), .Select("low")) register_24 (
    .D(multiplexer_24_out), .en(en), .Q(out_55), .clk(clk));  // open: clr
  Register #(.width(32), .trigger("rising"), .Select("low")) register_25 (
    .D(multiplexer_25_out), .en(en), .Q(out_56), .clk(clk));  // open: clr
  Register #(.width(2), .trigger("rising"), .Select("low")) register_26 (
    .D(multiplexer_26_out), .en(en), .Q(out_57), .clk(clk));  // open: clr
  Register #(.width(2), .trigger("rising"), .Select("low")) register_27 (
    .D(multiplexer_27_out), .en(en), .Q(out_58), .clk(clk));  // open: clr
endmodule

module EX_MEM (
  input  MEMTOREG,
  input  MEMWRITE,
  input  REGWRITE,
  input  HALT,
  input  ECALL,
  input  JAL,
  input  JALR,
  input  AUIPC,
  input  URET,
  input  SB,
  input  [4:0] rd,
  input  [31:0] R2,
  input  [31:0] Result,
  input  [31:0] imm3,
  input  [31:0] IR,
  input  [31:0] PC,
  input  [31:0] PC_4,
  input  reset,
  input  en,
  input  clk,
  output out_21,
  output out_22,
  output out_23,
  output out_24,
  output out_25,
  output out_26,
  output out_27,
  output out_28,
  output out_29,
  output out_30,
  output [4:0] out_31,
  output [31:0] out_32,
  output [31:0] out_33,
  output [31:0] out_34,
  output [31:0] out_35,
  output [31:0] out_36,
  output [31:0] out_37
);

  wire multiplexer_1_out, multiplexer_2_out, multiplexer_3_out, multiplexer_4_out, multiplexer_5_out,
       multiplexer_6_out, multiplexer_7_out, multiplexer_8_out, multiplexer_9_out, multiplexer_10_out;
  wire [4:0] multiplexer_11_out;
  wire [31:0] multiplexer_12_out, multiplexer_13_out, multiplexer_14_out, multiplexer_15_out,
       multiplexer_16_out, multiplexer_17_out;

  Multiplexer #(.select(1), .width(1), .disabled("Z"), .enable("false")) multiplexer_1 (
    .in0(MEMTOREG), .in1(1'b0), .out(multiplexer_1_out), .sel(reset));
  Multiplexer #(.select(1), .width(1), .disabled("Z"), .enable("false")) multiplexer_2 (
    .in0(MEMWRITE), .in1(1'b0), .out(multiplexer_2_out), .sel(reset));
  Multiplexer #(.select(1), .width(1), .disabled("Z"), .enable("false")) multiplexer_3 (
    .in0(REGWRITE), .in1(1'b0), .out(multiplexer_3_out), .sel(reset));
  Multiplexer #(.select(1), .width(1), .disabled("Z"), .enable("false")) multiplexer_4 (
    .in0(HALT), .in1(1'b0), .out(multiplexer_4_out), .sel(reset));
  Multiplexer #(.select(1), .width(1), .disabled("Z"), .enable("false")) multiplexer_5 (
    .in0(ECALL), .in1(1'b0), .out(multiplexer_5_out), .sel(reset));
  Multiplexer #(.select(1), .width(1), .disabled("Z"), .enable("false")) multiplexer_6 (
    .in0(JAL), .in1(1'b0), .out(multiplexer_6_out), .sel(reset));
  Multiplexer #(.select(1), .width(1), .disabled("Z"), .enable("false")) multiplexer_7 (
    .in0(JALR), .in1(1'b0), .out(multiplexer_7_out), .sel(reset));
  Multiplexer #(.select(1), .width(1), .disabled("Z"), .enable("false")) multiplexer_8 (
    .in0(AUIPC), .in1(1'b0), .out(multiplexer_8_out), .sel(reset));
  Multiplexer #(.select(1), .width(1), .disabled("Z"), .enable("false")) multiplexer_9 (
    .in0(URET), .in1(1'b0), .out(multiplexer_9_out), .sel(reset));
  Multiplexer #(.select(1), .width(1), .disabled("Z"), .enable("false")) multiplexer_10 (
    .in0(SB), .in1(1'b0), .out(multiplexer_10_out), .sel(reset));
  Multiplexer #(.select(1), .width(5), .disabled("Z"), .enable("false")) multiplexer_11 (
    .in0(rd), .in1({5{1'b0}}), .out(multiplexer_11_out), .sel(reset));
  Multiplexer #(.select(1), .width(32), .disabled("Z"), .enable("false")) multiplexer_12 (
    .in0(R2), .in1({32{1'b0}}), .out(multiplexer_12_out), .sel(reset));
  Multiplexer #(.select(1), .width(32), .disabled("Z"), .enable("false")) multiplexer_13 (
    .in0(Result), .in1({32{1'b0}}), .out(multiplexer_13_out), .sel(reset));
  Multiplexer #(.select(1), .width(32), .disabled("Z"), .enable("false")) multiplexer_14 (
    .in0(imm3), .in1({32{1'b0}}), .out(multiplexer_14_out), .sel(reset));
  Multiplexer #(.select(1), .width(32), .disabled("Z"), .enable("false")) multiplexer_15 (
    .in0(IR), .in1({32{1'b0}}), .out(multiplexer_15_out), .sel(reset));
  Multiplexer #(.select(1), .width(32), .disabled("Z"), .enable("false")) multiplexer_16 (
    .in0(PC), .in1({32{1'b0}}), .out(multiplexer_16_out), .sel(reset));
  Multiplexer #(.select(1), .width(32), .disabled("Z"), .enable("false")) multiplexer_17 (
    .in0(PC_4), .in1({32{1'b0}}), .out(multiplexer_17_out), .sel(reset));
  Register #(.width(1), .trigger("rising"), .Select("low")) register_1 (
    .D(multiplexer_1_out), .en(en), .Q(out_21), .clk(clk));  // open: clr
  Register #(.width(1), .trigger("rising"), .Select("low")) register_2 (
    .D(multiplexer_2_out), .en(en), .Q(out_22), .clk(clk));  // open: clr
  Register #(.width(1), .trigger("rising"), .Select("low")) register_3 (
    .D(multiplexer_3_out), .en(en), .Q(out_23), .clk(clk));  // open: clr
  Register #(.width(1), .trigger("rising"), .Select("low")) register_4 (
    .D(multiplexer_4_out), .en(en), .Q(out_24), .clk(clk));  // open: clr
  Register #(.width(1), .trigger("rising"), .Select("low")) register_5 (
    .D(multiplexer_5_out), .en(en), .Q(out_25), .clk(clk));  // open: clr
  Register #(.width(1), .trigger("rising"), .Select("low")) register_6 (
    .D(multiplexer_6_out), .en(en), .Q(out_26), .clk(clk));  // open: clr
  Register #(.width(1), .trigger("rising"), .Select("low")) register_7 (
    .D(multiplexer_7_out), .en(en), .Q(out_27), .clk(clk));  // open: clr
  Register #(.width(1), .trigger("rising"), .Select("low")) register_8 (
    .D(multiplexer_8_out), .en(en), .Q(out_28), .clk(clk));  // open: clr
  Register #(.width(1), .trigger("rising"), .Select("low")) register_9 (
    .D(multiplexer_9_out), .en(en), .Q(out_29), .clk(clk));  // open: clr
  Register #(.width(1), .trigger("rising"), .Select("low")) register_10 (
    .D(multiplexer_10_out), .en(en), .Q(out_30), .clk(clk));  // open: clr
  Register #(.width(5), .trigger("rising"), .Select("low")) register_11 (
    .D(multiplexer_11_out), .en(en), .Q(out_31), .clk(clk));  // open: clr
  Register #(.width(32), .trigger("rising"), .Select("low")) register_12 (
    .D(multiplexer_12_out), .en(en), .Q(out_32), .clk(clk));  // open: clr
  Register #(.width(32), .trigger("rising"), .Select("low")) register_13 (
    .D(multiplexer_13_out), .en(en), .Q(out_33), .clk(clk));  // open: clr
  Register #(.width(32), .trigger("rising"), .Select("low")) register_14 (
    .D(multiplexer_14_out), .en(en), .Q(out_34), .clk(clk));  // open: clr
  Register #(.width(32), .trigger("rising"), .Select("low")) register_15 (
    .D(multiplexer_15_out), .en(en), .Q(out_35), .clk(clk));  // open: clr
  Register #(.width(32), .trigger("rising"), .Select("low")) register_16 (
    .D(multiplexer_16_out), .en(en), .Q(out_36), .clk(clk));  // open: clr
  Register #(.width(32), .trigger("rising"), .Select("low")) register_17 (
    .D(multiplexer_17_out), .en(en), .Q(out_37), .clk(clk));  // open: clr
endmodule

module MEM_WB (
  input  MEMTOREG,
  input  URET,
  input  REGWRITE,
  input  HALT,
  input  ECALL,
  input  JAL,
  input  JALR,
  input  AUIPC,
  input  [4:0] rd,
  input  [31:0] Result,
  input  [31:0] data,
  input  [31:0] imm3,
  input  [31:0] IR,
  input  [31:0] PC,
  input  [31:0] PC_4,
  input  reset,
  input  en,
  input  clk,
  output out_19,
  output out_20,
  output out_21,
  output out_22,
  output out_23,
  output out_24,
  output out_25,
  output out_26,
  output [4:0] out_27,
  output [31:0] out_28,
  output [31:0] out_29,
  output [31:0] out_30,
  output [31:0] out_31,
  output [31:0] out_32,
  output [31:0] out_33
);

  wire multiplexer_1_out, multiplexer_2_out, multiplexer_3_out, multiplexer_4_out, multiplexer_5_out,
       multiplexer_6_out, multiplexer_7_out, multiplexer_8_out;
  wire [4:0] multiplexer_9_out;
  wire [31:0] multiplexer_10_out, multiplexer_11_out, multiplexer_12_out, multiplexer_13_out,
       multiplexer_14_out, multiplexer_15_out;

  Multiplexer #(.select(1), .width(1), .disabled("Z"), .enable("false")) multiplexer_1 (
    .in0(MEMTOREG), .in1(1'b0), .out(multiplexer_1_out), .sel(reset));
  Multiplexer #(.select(1), .width(1), .disabled("Z"), .enable("false")) multiplexer_2 (
    .in0(URET), .in1(1'b0), .out(multiplexer_2_out), .sel(reset));
  Multiplexer #(.select(1), .width(1), .disabled("Z"), .enable("false")) multiplexer_3 (
    .in0(REGWRITE), .in1(1'b0), .out(multiplexer_3_out), .sel(reset));
  Multiplexer #(.select(1), .width(1), .disabled("Z"), .enable("false")) multiplexer_4 (
    .in0(HALT), .in1(1'b0), .out(multiplexer_4_out), .sel(reset));
  Multiplexer #(.select(1), .width(1), .disabled("Z"), .enable("false")) multiplexer_5 (
    .in0(ECALL), .in1(1'b0), .out(multiplexer_5_out), .sel(reset));
  Multiplexer #(.select(1), .width(1), .disabled("Z"), .enable("false")) multiplexer_6 (
    .in0(JAL), .in1(1'b0), .out(multiplexer_6_out), .sel(reset));
  Multiplexer #(.select(1), .width(1), .disabled("Z"), .enable("false")) multiplexer_7 (
    .in0(JALR), .in1(1'b0), .out(multiplexer_7_out), .sel(reset));
  Multiplexer #(.select(1), .width(1), .disabled("Z"), .enable("false")) multiplexer_8 (
    .in0(AUIPC), .in1(1'b0), .out(multiplexer_8_out), .sel(reset));
  Multiplexer #(.select(1), .width(5), .disabled("Z"), .enable("false")) multiplexer_9 (
    .in0(rd), .in1({5{1'b0}}), .out(multiplexer_9_out), .sel(reset));
  Multiplexer #(.select(1), .width(32), .disabled("Z"), .enable("false")) multiplexer_10 (
    .in0(Result), .in1({32{1'b0}}), .out(multiplexer_10_out), .sel(reset));
  Multiplexer #(.select(1), .width(32), .disabled("Z"), .enable("false")) multiplexer_11 (
    .in0(data), .in1({32{1'b0}}), .out(multiplexer_11_out), .sel(reset));
  Multiplexer #(.select(1), .width(32), .disabled("Z"), .enable("false")) multiplexer_12 (
    .in0(imm3), .in1({32{1'b0}}), .out(multiplexer_12_out), .sel(reset));
  Multiplexer #(.select(1), .width(32), .disabled("Z"), .enable("false")) multiplexer_13 (
    .in0(IR), .in1({32{1'b0}}), .out(multiplexer_13_out), .sel(reset));
  Multiplexer #(.select(1), .width(32), .disabled("Z"), .enable("false")) multiplexer_14 (
    .in0(PC), .in1({32{1'b0}}), .out(multiplexer_14_out), .sel(reset));
  Multiplexer #(.select(1), .width(32), .disabled("Z"), .enable("false")) multiplexer_15 (
    .in0(PC_4), .in1({32{1'b0}}), .out(multiplexer_15_out), .sel(reset));
  Register #(.width(1), .trigger("rising"), .Select("low")) register_1 (
    .D(multiplexer_1_out), .en(en), .Q(out_19), .clk(clk));  // open: clr
  Register #(.width(1), .trigger("rising"), .Select("low")) register_2 (
    .D(multiplexer_2_out), .en(en), .Q(out_20), .clk(clk));  // open: clr
  Register #(.width(1), .trigger("rising"), .Select("low")) register_3 (
    .D(multiplexer_3_out), .en(en), .Q(out_21), .clk(clk));  // open: clr
  Register #(.width(1), .trigger("rising"), .Select("low")) register_4 (
    .D(multiplexer_4_out), .en(en), .Q(out_22), .clk(clk));  // open: clr
  Register #(.width(1), .trigger("rising"), .Select("low")) register_5 (
    .D(multiplexer_5_out), .en(en), .Q(out_23), .clk(clk));  // open: clr
  Register #(.width(1), .trigger("rising"), .Select("low")) register_6 (
    .D(multiplexer_6_out), .en(en), .Q(out_24), .clk(clk));  // open: clr
  Register #(.width(1), .trigger("rising"), .Select("low")) register_7 (
    .D(multiplexer_7_out), .en(en), .Q(out_25), .clk(clk));  // open: clr
  Register #(.width(1), .trigger("rising"), .Select("low")) register_8 (
    .D(multiplexer_8_out), .en(en), .Q(out_26), .clk(clk));  // open: clr
  Register #(.width(5), .trigger("rising"), .Select("low")) register_9 (
    .D(multiplexer_9_out), .en(en), .Q(out_27), .clk(clk));  // open: clr
  Register #(.width(32), .trigger("rising"), .Select("low")) register_10 (
    .D(multiplexer_10_out), .en(en), .Q(out_28), .clk(clk));  // open: clr
  Register #(.width(32), .trigger("rising"), .Select("low")) register_11 (
    .D(multiplexer_11_out), .en(en), .Q(out_29), .clk(clk));  // open: clr
  Register #(.width(32), .trigger("rising"), .Select("low")) register_12 (
    .D(multiplexer_12_out), .en(en), .Q(out_30), .clk(clk));  // open: clr
  Register #(.width(32), .trigger("rising"), .Select("low")) register_13 (
    .D(multiplexer_13_out), .en(en), .Q(out_31), .clk(clk));  // open: clr
  Register #(.width(32), .trigger("rising"), .Select("low")) register_14 (
    .D(multiplexer_14_out), .en(en), .Q(out_32), .clk(clk));  // open: clr
  Register #(.width(32), .trigger("rising"), .Select("low")) register_15 (
    .D(multiplexer_15_out), .en(en), .Q(out_33), .clk(clk));  // open: clr
endmodule

module \气泡数据相关检测逻辑  (
  input  [31:0] in_1,
  input  BranchTaken,
  input  ecall,
  input  rs1used,
  input  rs2used,
  input  EX_RegWrite,
  input  MEM_RegWrite,
  input  [4:0] EX_WriteReg_num,
  input  [4:0] MEM_WriteReg_num,
  output stall,
  output flush
);

  wire and_1_out, and_2_out, and_3_out, and_4_out, and_5_out, and_6_out, comparator_1_eq, comparator_2_eq,
       comparator_3_eq, comparator_4_eq, comparator_5_eq, comparator_6_eq, comparator_7_eq, comparator_8_eq,
       comparator_9_eq, comparator_10_eq, comparator_11_eq, comparator_12_eq, not_1_out, not_2_out,
       not_3_out, not_4_out, or_2_out, or_3_out;

  or or_1 (flush, stall, BranchTaken);
  Comparator #(.width(5), .mode("twosComplement")) comparator_1 (
    .a(5'b10001), .b(EX_WriteReg_num), .eq(comparator_1_eq));  // open: gt, lt
  Comparator #(.width(5), .mode("twosComplement")) comparator_2 (
    .a(EX_WriteReg_num), .b(5'b01010), .eq(comparator_2_eq));  // open: gt, lt
  Comparator #(.width(5), .mode("twosComplement")) comparator_3 (
    .a(5'b10001), .b(MEM_WriteReg_num), .eq(comparator_3_eq));  // open: gt, lt
  Comparator #(.width(5), .mode("twosComplement")) comparator_4 (
    .a(MEM_WriteReg_num), .b(5'b01010), .eq(comparator_4_eq));  // open: gt, lt
  Comparator #(.width(5), .mode("twosComplement")) comparator_5 (
    .a({5{1'b0}}), .b(in_1[19:15]), .eq(comparator_5_eq));  // open: gt, lt
  not not_1 (not_1_out, comparator_5_eq);
  Comparator #(.width(5), .mode("twosComplement")) comparator_6 (
    .a(in_1[19:15]), .b(EX_WriteReg_num), .eq(comparator_6_eq));  // open: gt, lt
  Comparator #(.width(5), .mode("twosComplement")) comparator_7 (
    .a({5{1'b0}}), .b(in_1[24:20]), .eq(comparator_7_eq));  // open: gt, lt
  not not_2 (not_2_out, comparator_7_eq);
  Comparator #(.width(5), .mode("twosComplement")) comparator_8 (
    .a(in_1[24:20]), .b(EX_WriteReg_num), .eq(comparator_8_eq));  // open: gt, lt
  not not_3 (not_3_out, comparator_9_eq);
  Comparator #(.width(5), .mode("twosComplement")) comparator_9 (
    .a({5{1'b0}}), .b(in_1[19:15]), .eq(comparator_9_eq));  // open: gt, lt
  Comparator #(.width(5), .mode("twosComplement")) comparator_10 (
    .a(in_1[19:15]), .b(MEM_WriteReg_num), .eq(comparator_10_eq));  // open: gt, lt
  Comparator #(.width(5), .mode("twosComplement")) comparator_11 (
    .a({5{1'b0}}), .b(in_1[24:20]), .eq(comparator_11_eq));  // open: gt, lt
  not not_4 (not_4_out, comparator_11_eq);
  Comparator #(.width(5), .mode("twosComplement")) comparator_12 (
    .a(in_1[24:20]), .b(MEM_WriteReg_num), .eq(comparator_12_eq));  // open: gt, lt
  or or_2 (or_2_out, comparator_1_eq, comparator_2_eq);
  or or_3 (or_3_out, comparator_3_eq, comparator_4_eq);
  and and_1 (and_1_out, not_1_out, comparator_6_eq, EX_RegWrite, rs1used);
  and and_2 (and_2_out, not_2_out, comparator_8_eq, EX_RegWrite, rs2used);
  and and_3 (and_3_out, not_3_out, comparator_10_eq, MEM_RegWrite, rs1used);
  and and_4 (and_4_out, not_4_out, comparator_12_eq, MEM_RegWrite, rs2used);
  and and_5 (and_5_out, ecall, EX_RegWrite, or_2_out);
  and and_6 (and_6_out, ecall, MEM_RegWrite, or_3_out);
  or or_4 (stall, and_1_out, and_2_out, and_3_out, and_4_out, and_5_out, and_6_out);

  // Other names for the same wires on the sheet: DataHazzard = stall; rs1[4:0] = in_1[19:15]; rs2[4:0] = in_1[24:20]
endmodule

module \重定向数据相关检测逻辑  (
  input  [31:0] in_1,
  input  BranchTaken,
  input  EX_MemToReg,
  input  rs1used,
  input  rs2used,
  input  EX_RegWrite,
  input  MEM_RegWrite,
  input  ecall,
  input  [4:0] EX_WriteReg_num,
  input  [4:0] MEM_WriteReg_num,
  output stall,
  output flush,
  output [1:0] out_13,
  output [1:0] out_14
);

  wire and_1_out, and_2_out, and_3_out, and_4_out, and_5_out, and_6_out, and_8_out, and_9_out, and_10_out,
       and_11_out, comparator_1_eq, comparator_2_eq, comparator_3_eq, comparator_4_eq, comparator_5_eq,
       comparator_6_eq, comparator_7_eq, comparator_8_eq, comparator_9_eq, comparator_10_eq,
       comparator_11_eq, comparator_12_eq, comparator_13_eq, comparator_14_eq, comparator_15_eq,
       comparator_16_eq, not_1_out, not_2_out, not_3_out, not_4_out, not_5_out, not_6_out, or_4_out, or_6_out;

  or or_1 (flush, stall, BranchTaken);
  Comparator #(.width(5), .mode("twosComplement")) comparator_1 (
    .a({5{1'b0}}), .b(in_1[19:15]), .eq(comparator_1_eq));  // open: gt, lt
  Comparator #(.width(5), .mode("twosComplement")) comparator_2 (
    .a(in_1[19:15]), .b(EX_WriteReg_num), .eq(comparator_2_eq));  // open: gt, lt
  Comparator #(.width(5), .mode("twosComplement")) comparator_3 (
    .a({5{1'b0}}), .b(in_1[24:20]), .eq(comparator_3_eq));  // open: gt, lt
  Comparator #(.width(5), .mode("twosComplement")) comparator_4 (
    .a(in_1[24:20]), .b(EX_WriteReg_num), .eq(comparator_4_eq));  // open: gt, lt
  not not_1 (not_1_out, comparator_1_eq);
  not not_2 (not_2_out, comparator_3_eq);
  not not_3 (not_3_out, comparator_5_eq);
  Comparator #(.width(5), .mode("twosComplement")) comparator_5 (
    .a({5{1'b0}}), .b(in_1[19:15]), .eq(comparator_5_eq));  // open: gt, lt
  Comparator #(.width(5), .mode("twosComplement")) comparator_6 (
    .a(in_1[19:15]), .b(EX_WriteReg_num), .eq(comparator_6_eq));  // open: gt, lt
  Comparator #(.width(5), .mode("twosComplement")) comparator_7 (
    .a(EX_WriteReg_num), .b(5'b10001), .eq(comparator_7_eq));  // open: gt, lt
  not not_4 (not_4_out, comparator_8_eq);
  Comparator #(.width(5), .mode("twosComplement")) comparator_8 (
    .a({5{1'b0}}), .b(in_1[19:15]), .eq(comparator_8_eq));  // open: gt, lt
  Comparator #(.width(5), .mode("twosComplement")) comparator_9 (
    .a(in_1[19:15]), .b(MEM_WriteReg_num), .eq(comparator_9_eq));  // open: gt, lt
  Comparator #(.width(5), .mode("twosComplement")) comparator_10 (
    .a(MEM_WriteReg_num), .b(5'b10001), .eq(comparator_10_eq));  // open: gt, lt
  and and_1 (and_1_out, rs1used, EX_MemToReg, not_1_out, comparator_2_eq);
  and and_2 (and_2_out, rs1used, EX_MemToReg, not_2_out, comparator_4_eq);
  and and_3 (and_3_out, rs1used, EX_RegWrite, not_3_out, comparator_6_eq);
  and and_4 (and_4_out, ecall, EX_RegWrite, comparator_7_eq);
  and and_5 (and_5_out, rs1used, MEM_RegWrite, not_4_out, comparator_9_eq);
  and and_6 (and_6_out, ecall, MEM_RegWrite, comparator_10_eq);
  or or_2 (stall, and_1_out, and_2_out);
  or or_3 (out_13[1], and_3_out, and_4_out);
  or or_4 (or_4_out, and_5_out, and_6_out);
  and and_7 (out_13[0], ~out_13[1], or_4_out);  // AND_Gate
  Comparator #(.width(5), .mode("twosComplement")) comparator_11 (
    .a({5{1'b0}}), .b(in_1[24:20]), .eq(comparator_11_eq));  // open: gt, lt
  Comparator #(.width(5), .mode("twosComplement")) comparator_12 (
    .a(in_1[24:20]), .b(EX_WriteReg_num), .eq(comparator_12_eq));  // open: gt, lt
  Comparator #(.width(5), .mode("twosComplement")) comparator_13 (
    .a({5{1'b0}}), .b(in_1[24:20]), .eq(comparator_13_eq));  // open: gt, lt
  Comparator #(.width(5), .mode("twosComplement")) comparator_14 (
    .a(in_1[24:20]), .b(MEM_WriteReg_num), .eq(comparator_14_eq));  // open: gt, lt
  not not_5 (not_5_out, comparator_11_eq);
  Comparator #(.width(5), .mode("twosComplement")) comparator_15 (
    .a(EX_WriteReg_num), .b(5'b01010), .eq(comparator_15_eq));  // open: gt, lt
  not not_6 (not_6_out, comparator_13_eq);
  Comparator #(.width(5), .mode("twosComplement")) comparator_16 (
    .a(MEM_WriteReg_num), .b(5'b01010), .eq(comparator_16_eq));  // open: gt, lt
  and and_8 (and_8_out, rs2used, EX_RegWrite, not_5_out, comparator_12_eq);
  and and_9 (and_9_out, ecall, EX_RegWrite, comparator_15_eq);
  and and_10 (and_10_out, rs2used, MEM_RegWrite, not_6_out, comparator_14_eq);
  and and_11 (and_11_out, ecall, MEM_RegWrite, comparator_16_eq);
  or or_5 (out_14[1], and_8_out, and_9_out);
  or or_6 (or_6_out, and_10_out, and_11_out);
  and and_12 (out_14[0], ~out_14[1], or_6_out);  // AND_Gate

  // Other names for the same wires on the sheet: rs1[4:0] = in_1[19:15]; rs2[4:0] = in_1[24:20]; LoadUse = stall;
  //   Rs1Forward[1:0] = out_13; Rs2Forward[1:0] = out_14
endmodule
module \重定向_动态分支预测  (
  output RegWrite,
  output MemWrite,
  output [31:0] IF_PC,
  output [31:0] ID_PC,
  output [31:0] EX_PC,
  output [31:0] M_PC,
  output [31:0] WB_PC,
  output [31:0] RDin,
  output [31:0] MDin,
  output [31:0] LedData
);

  wire alu_1_equal, alu_1_out_4, and_1_out, and_2_out, and_3_out, and_4_out, and_5_out, and_6_out, and_7_out,
       and_9_out, and_10_out, CLK, clock_1_out, clock_2_out, comparator_1_eq, comparator_1_lt,
       comparator_2_eq, comparator_3_eq, d_ff_1_q, ecall, EX_Branch, EX_BranchTaken, EX_halt,
       ex_mem_1_out_21, ex_mem_1_out_23, ex_mem_1_out_24, ex_mem_1_out_25, ex_mem_1_out_26, ex_mem_1_out_27,
       ex_mem_1_out_28, EX_PredictJump, Go, halt, id_ex_1_out_33, id_ex_1_out_34, id_ex_1_out_35,
       id_ex_1_out_36, id_ex_1_out_37, id_ex_1_out_38, id_ex_1_out_40, id_ex_1_out_43, id_ex_1_out_44,
       id_ex_1_out_45, if_id_1_out_9, IF_PredictJump, IR1, IR2, IR3, LoadUse, mem_wb_1_out_19,
       mem_wb_1_out_22, mem_wb_1_out_23, mem_wb_1_out_24, mem_wb_1_out_25, mem_wb_1_out_26,
       multiplexer_1_out, multiplexer_2_out, multiplexer_6_out, multiplexer_14_out, multiplexer_16_out,
       nand_1_out, nor_1_out, nor_2_out, not_1_out, not_2_out, not_3_out, not_4_out, not_5_out, not_6_out,
       not_8_out, not_9_out, not_10_out, not_11_out, or_1_out, or_5_out, or_6_out, or_7_out, PredictError,
       RST, SB, W1, W2, W3, \单周期硬布线控制器_1_alu_src , \单周期硬布线控制器_1_auipc , \单周期硬布线控制器_1_beq ,
       \单周期硬布线控制器_1_bgeu , \单周期硬布线控制器_1_bne , \单周期硬布线控制器_1_jal , \单周期硬布线控制器_1_jalr , \单周期硬布线控制器_1_memtoreg ,
       \单周期硬布线控制器_1_memwrite , \单周期硬布线控制器_1_regwrite , \单周期硬布线控制器_1_rs1used , \单周期硬布线控制器_1_rs2used ,
       \单周期硬布线控制器_1_s_type , \单周期硬布线控制器_1_sb ;
  wire [1:0] id_ex_1_out_57, id_ex_1_out_58, priority_encoder_1_out, \重定向数据相关检测逻辑_1_out_13 ,
       \重定向数据相关检测逻辑_1_out_14 ;
  wire [2:0] id_ex_1_out_42;
  wire [3:0] decoder_1_out0, id_ex_1_out_46, mips_ram_1_p4, \单周期硬布线控制器_1_alu_op ;
  wire [4:0] ex_mem_1_out_31, id_ex_1_out_47, multiplexer_7_out, multiplexer_8_out, WriteReg_num;
  wire [12:0] CNT_num;
  wire [15:0] \LoadUse次数 , \分支预测失败次数 , \分支预测成功次数 , \总周期数 , \无条件分支数 , \条件分支成功数 ;
  wire [31:0] adder_4_out, ALU_result, b_branch, bit_extender_1_out, bit_extender_2_out, bit_extender_3_out,
       bit_extender_4_out, bit_extender_5_out, EX_BranchAddr, EX_IR, ex_mem_1_out_32, ex_mem_1_out_34,
       ex_mem_1_out_37, EX_PC_4, id_ex_1_out_48, id_ex_1_out_49, id_ex_1_out_50, id_ex_1_out_51,
       id_ex_1_out_52, id_ex_1_out_53, ID_IR, if_id_1_pc_4_2, IF_IR, jal_branch, JumpAddr, MEM_ALU_result,
       MEM_IR, mem_wb_1_out_28, mem_wb_1_out_29, mem_wb_1_out_30, mem_wb_1_out_33, mips_ram_1_p8,
       multiplexer_3_out, multiplexer_4_out, multiplexer_5_out, multiplexer_9_out, multiplexer_10_out,
       multiplexer_11_out, multiplexer_12_out, PC_4, regifile_1_r1, regifile_1_r2, shifter_1_out,
       shifter_2_out, shifter_3_out, WB_IR;

  Button \u_总复位  (.out(RST));
  Button _1 (.out(IR1));
  Button _2 (.out(IR2));
  Button _3 (.out(IR3));
  // Probe on \总周期数 
  // Probe on \总周期数 
  Button \u_继续运行  (.out(Go));
  LED #(.active("true")) led_1 (.in(W1));
  LED #(.active("true")) led_2 (.in(W2));
  LED #(.active("true")) led_3 (.in(W3));
  Hex_Digit_Display hex_digit_display_1 (.value(LedData[31:28]));  // open: dp
  // Probe on IF_PC[19:0]
  // RiscV_Probe riscv_probe_1: pin names not known; wires that end beside it: IF_IR
  Hex_Digit_Display hex_digit_display_2 (.value(LedData[27:24]));  // open: dp
  Hex_Digit_Display hex_digit_display_3 (.value(LedData[23:20]));  // open: dp
  // Probe on ID_PC[19:0]
  // RiscV_Probe riscv_probe_2: pin names not known; wires that end beside it: ID_IR
  Hex_Digit_Display hex_digit_display_4 (.value(LedData[15:12]));  // open: dp
  Hex_Digit_Display hex_digit_display_5 (.value(LedData[19:16]));  // open: dp
  not not_1 (not_1_out, halt);
  Multiplexer #(.select(1), .width(1), .disabled("Z"), .enable("false")) multiplexer_1 (
    .in0(and_1_out), .in1(1'b0), .out(multiplexer_1_out), .sel(CLK));
  and and_1 (and_1_out, PredictError, CLK);
  not not_2 (not_2_out, halt);
  Multiplexer #(.select(1), .width(1), .disabled("Z"), .enable("false")) multiplexer_2 (
    .in0(and_2_out), .in1(1'b0), .out(multiplexer_2_out), .sel(CLK));
  and and_2 (and_2_out, ~PredictError, EX_Branch, CLK);  // AND_Gate
  Multiplexer #(.select(1), .width(32), .disabled("Z"), .enable("false")) multiplexer_3 (
    .in0(multiplexer_4_out), .in1(multiplexer_5_out), .out(multiplexer_3_out), .sel(PredictError));
  Hex_Digit_Display hex_digit_display_6 (.value(LedData[7:4]));  // open: dp
  Hex_Digit_Display hex_digit_display_7 (.value(LedData[11:8]));  // open: dp
  Clock #(.highDuration(1), .lowDuration(1)) clock_1 (.out(clock_1_out));
  // Probe on EX_PC[19:0]
  // RiscV_Probe riscv_probe_3: pin names not known; wires that end beside it: clock_1_out, EX_IR, CLK
  Counter #(.width(16), .max('hffff), .ongoal("wrap"), .trigger("rising"), .behavior("new")) counter_1 (
    .count(not_1_out), .Q(\分支预测失败次数 ), .clk(multiplexer_1_out), .clr(RST));  // open: load, D, carry, preset, down
  Counter #(.width(16), .max('hffff), .ongoal("wrap"), .trigger("rising"), .behavior("new")) counter_2 (
    .count(not_2_out), .Q(\分支预测成功次数 ), .clk(multiplexer_2_out), .clr(RST));  // open: load, D, carry, preset, down
  Multiplexer #(.select(1), .width(32), .disabled("Z"), .enable("false")) multiplexer_4 (
    .in0(PC_4), .in1(JumpAddr), .out(multiplexer_4_out), .sel(IF_PredictJump));
  Multiplexer #(.select(1), .width(32), .disabled("Z"), .enable("false")) multiplexer_5 (
    .in0(EX_PC_4), .in1(EX_BranchAddr), .out(multiplexer_5_out), .sel(EX_BranchTaken));
  Hex_Digit_Display hex_digit_display_8 (.value(LedData[3:0]));  // open: dp
  nor nor_1 (nor_1_out, halt, LoadUse);
  Register #(.width(32), .trigger("rising"), .Select("low")) PC (
    .D(multiplexer_3_out), .en(nor_1_out), .Q(IF_PC), .clk(CLK), .clr(RST));
  // Probe on \总周期数 
  // Probe on M_PC[19:0]
  // RiscV_Probe riscv_probe_4: pin names not known; wires that end beside it: MEM_IR
  \重定向数据相关检测逻辑  \u_重定向数据相关检测逻辑_1  (
    .in_1(ID_IR), .BranchTaken(EX_BranchTaken), .EX_MemToReg(id_ex_1_out_35),
    .rs1used(\单周期硬布线控制器_1_rs1used ), .rs2used(\单周期硬布线控制器_1_rs2used ), .EX_RegWrite(id_ex_1_out_38),
    .MEM_RegWrite(ex_mem_1_out_23), .ecall(ecall), .EX_WriteReg_num(id_ex_1_out_47),
    .MEM_WriteReg_num(ex_mem_1_out_31), .stall(LoadUse), .out_13(\重定向数据相关检测逻辑_1_out_13 ),
    .out_14(\重定向数据相关检测逻辑_1_out_14 ));  // open: flush
  not not_3 (not_3_out, halt);
  and and_3 (and_3_out, LoadUse, CLK);
  // Probe on \总周期数 
  // Probe on \无条件分支数 
  // Probe on \条件分支成功数 
  // Probe on \LoadUse次数 
  // Probe on \LoadUse次数 
  // Probe on \分支预测失败次数 
  // Probe on \分支预测成功次数 
  Counter #(.width(16), .max('hffff), .ongoal("wrap"), .trigger("rising"), .behavior("new")) counter_3 (
    .count(not_3_out), .Q(\LoadUse次数 ), .clk(multiplexer_6_out), .clr(RST));  // open: load, D, carry, preset, down
  Multiplexer #(.select(1), .width(1), .disabled("Z"), .enable("false")) multiplexer_6 (
    .in0(and_3_out), .in1(1'b0), .out(multiplexer_6_out), .sel(CLK));
  not not_4 (not_4_out, halt);
  Adder #(.width(32)) adder_1 (.a(IF_PC), .b(32'h4), .out(PC_4));  // open: cin, cout
  // Probe on IF_PC[11:0]
  // Probe on WB_PC[19:0]
  // RiscV_Probe riscv_probe_5: pin names not known; wires that end beside it: WB_IR
  Counter #(.width(16), .max('hffff), .ongoal("wrap"), .trigger("rising"), .behavior("new")) counter_4 (
    .count(not_4_out), .Q(\总周期数 ), .clk(CLK), .clr(RST));  // open: load, D, carry, preset, down
  // RiscV_Probe riscv_probe_6: pin names not known; wires that end beside it: IF_IR
  ROM #(.addrWidth(10), .dataWidth(32), .Select("high")) rom_1 (.addr(IF_PC[11:2]), .data(IF_IR));
  BTB btb_1 (
    .PC(IF_PC), .EX_PC(EX_PC), .EX_BranchAddr(EX_BranchAddr), .CLK(CLK), .EX_Branch(EX_Branch),
    .EX_BranchTaken(EX_BranchTaken), .ID_PredictJump(IF_PredictJump), .JumpAddr(JumpAddr));
  // Probe on EX_PC[11:0]
  // Probe on ID_PC[11:0]
  IF_ID if_id_1 (
    .IR(IF_IR), .PC(IF_PC), .PC_4(PC_4), .IR_2(ID_IR), .PC_2(ID_PC), .PC_4_2(if_id_1_pc_4_2),
    .BranchTaken(PredictError), .en(nor_2_out), .clk(CLK), .reset(1'b0), .PredictJump(IF_PredictJump),
    .out_9(if_id_1_out_9));
  nor nor_2 (nor_2_out, LoadUse, halt);
  // Probe on M_PC[11:0]
  D_Flip_Flop #(.trigger("high"), .Pre_Clr_Positions("LEGACY"), .NegatePresetClear("false"), .enable("true"), .NewFFLayout("false")) d_ff_1 (.Q(d_ff_1_q));  // open: clk, D, Qn, preset, en, reset
  // Probe on 13'hc
  // Probe on WB_PC[11:0]
  Comparator #(.width(13), .mode("twosComplement")) comparator_1 (
    .a(CNT_num), .b(13'hc), .eq(comparator_1_eq), .lt(comparator_1_lt));  // open: gt
  Clock #(.highDuration(1), .lowDuration(1)) clock_2 (.out(clock_2_out));
  nand nand_1 (nand_1_out, d_ff_1_q, comparator_1_eq);
  Counter #(.width(13), .max('h1fff), .ongoal("stay"), .trigger("rising"), .behavior("old")) counter_5 (
    .count(comparator_1_lt), .Q(CNT_num), .clk(clock_2_out));  // open: load, D, carry, clr, preset
  \单周期硬布线控制器  \u_单周期硬布线控制器_1  (
    .Funct({ID_IR[30], ID_IR[25], ID_IR[14:12]}), .OP(ID_IR[6:2]), .ALU_OP(\单周期硬布线控制器_1_alu_op ),
    .MemToReg(\单周期硬布线控制器_1_memtoreg ), .MemWrite(\单周期硬布线控制器_1_memwrite ), .ALU_SRC(\单周期硬布线控制器_1_alu_src ),
    .RegWrite(\单周期硬布线控制器_1_regwrite ), .ecall(ecall), .S_type(\单周期硬布线控制器_1_s_type ),
    .Jalr(\单周期硬布线控制器_1_jalr ), .Beq(\单周期硬布线控制器_1_beq ), .JAL(\单周期硬布线控制器_1_jal ), .Bne(\单周期硬布线控制器_1_bne ),
    .in_3(ID_IR[21]), .AUIPC(\单周期硬布线控制器_1_auipc ), .BGEU(\单周期硬布线控制器_1_bgeu ), .SB(\单周期硬布线控制器_1_sb ),
    .Rs1used(\单周期硬布线控制器_1_rs1used ), .Rs2used(\单周期硬布线控制器_1_rs2used ));  // open: uret, CSRRSI, CSRRCI
  Multiplexer #(.select(1), .width(5), .disabled("Z"), .enable("false")) multiplexer_7 (
    .in0(ID_IR[19:15]), .in1(5'b10001), .out(multiplexer_7_out), .sel(ecall));
  Multiplexer #(.select(1), .width(5), .disabled("Z"), .enable("false")) multiplexer_8 (
    .in0(ID_IR[24:20]), .in1(5'b01010), .out(multiplexer_8_out), .sel(ecall));
  assign bit_extender_1_out = {{20{ID_IR[31]}}, ID_IR[31:20]};  // Bit_Extender bit_extender_1
  assign bit_extender_2_out = {{20{ID_IR[31]}}, {ID_IR[31:25], ID_IR[11:7]}};  // Bit_Extender bit_extender_2
  assign bit_extender_3_out = {{20{ID_IR[31]}}, {ID_IR[31], ID_IR[7], ID_IR[30:25], ID_IR[11:8]}};  // Bit_Extender bit_extender_3
  assign bit_extender_4_out = {{12{ID_IR[31]}}, {ID_IR[31], ID_IR[19:12], ID_IR[20], ID_IR[30:21]}};  // Bit_Extender bit_extender_4
  assign bit_extender_5_out = {{12{ID_IR[31]}}, ID_IR[31:12]};  // Bit_Extender bit_extender_5
  assign CLK = nand_1_out ? clock_2_out : 1'bz;  // Controlled_Buffer controlled_buffer_1
  Multiplexer #(.select(1), .width(32), .disabled("Z"), .enable("false")) multiplexer_9 (
    .in0(bit_extender_1_out), .in1(bit_extender_2_out), .out(multiplexer_9_out), .sel(\单周期硬布线控制器_1_s_type ));
  Pull_Resistor #(.pull(1)) pull_resistor_1 (.node(CLK));
  not not_5 (not_5_out, CLK);
  Regifile regifile_1 (
    .Din(RDin), .Clk(not_5_out), .R1(regifile_1_r1), .R2(regifile_1_r2), .WE(RegWrite), .W_num(WriteReg_num),
    .R1_num(multiplexer_7_out), .R2_num(multiplexer_8_out));
  not not_6 (not_6_out, halt);
  or or_1 (or_1_out, PredictError, LoadUse);
  ID_EX id_ex_1 (
    .BEQ(\单周期硬布线控制器_1_beq ), .BNE(\单周期硬布线控制器_1_bne ), .MEMTOREG(\单周期硬布线控制器_1_memtoreg ),
    .MEMWRITE(\单周期硬布线控制器_1_memwrite ), .ALUSRCB(\单周期硬布线控制器_1_alu_src ), .REGWRITE(\单周期硬布线控制器_1_regwrite ),
    .ECALL(ecall), .JAL(\单周期硬布线控制器_1_jal ), .JALR(\单周期硬布线控制器_1_jalr ), .AUIPC(\单周期硬布线控制器_1_auipc ),
    .BGEU(\单周期硬布线控制器_1_bgeu ), .SB(\单周期硬布线控制器_1_sb ), .ALUop(\单周期硬布线控制器_1_alu_op ), .rd(ID_IR[11:7]),
    .R1(regifile_1_r1), .R2(regifile_1_r2), .imm1(multiplexer_9_out), .imm2(bit_extender_3_out),
    .imm3(bit_extender_5_out), .IR(ID_IR), .PC(ID_PC), .PC_4(if_id_1_pc_4_2), .out_33(id_ex_1_out_33),
    .out_34(id_ex_1_out_34), .out_35(id_ex_1_out_35), .out_36(id_ex_1_out_36), .out_37(id_ex_1_out_37),
    .out_38(id_ex_1_out_38), .out_40(id_ex_1_out_40), .out_41(id_ex_1_out_42[1]), .out_42(id_ex_1_out_42[0]),
    .out_43(id_ex_1_out_43), .out_44(id_ex_1_out_44), .out_45(id_ex_1_out_45), .out_46(id_ex_1_out_46),
    .out_47(id_ex_1_out_47), .out_49(id_ex_1_out_49), .out_50(id_ex_1_out_50), .out_51(id_ex_1_out_51),
    .out_52(id_ex_1_out_52), .out_53(id_ex_1_out_53), .out_54(EX_IR), .out_55(EX_PC), .out_56(EX_PC_4),
    .flush(or_1_out), .en(not_6_out), .clk(CLK), .Rs1Forward(\重定向数据相关检测逻辑_1_out_13 ),
    .out_57(id_ex_1_out_57), .Rs2Forward(\重定向数据相关检测逻辑_1_out_14 ), .out_58(id_ex_1_out_58),
    .imm4(bit_extender_4_out), .out_48(id_ex_1_out_48), .reset(1'b0), .PredictJump(if_id_1_out_9),
    .out_32(EX_PredictJump));  // open: URET, out_39
  Comparator #(.width(1), .mode("unsigned")) comparator_2 (
    .a(EX_BranchTaken), .b(EX_PredictJump), .eq(comparator_2_eq));  // open: gt, lt
  not not_7 (PredictError, comparator_2_eq);
  Multiplexer #(.select(2), .width(32), .disabled("Z"), .enable("false")) multiplexer_10 (
    .in0(id_ex_1_out_49), .in1(RDin), .in2(MEM_ALU_result), .out(multiplexer_10_out), .sel(id_ex_1_out_57));  // open: in3
  Multiplexer #(.select(2), .width(32), .disabled("Z"), .enable("false")) multiplexer_11 (
    .in0(id_ex_1_out_50), .in1(RDin), .in2(MEM_ALU_result), .out(multiplexer_11_out), .sel(id_ex_1_out_58));  // open: in3
  or or_2 (EX_Branch, id_ex_1_out_44, id_ex_1_out_34, id_ex_1_out_33, id_ex_1_out_42[0], id_ex_1_out_42[1]);
  or or_3 (id_ex_1_out_42[2], id_ex_1_out_33, id_ex_1_out_34, id_ex_1_out_44);
  or or_4 (EX_BranchTaken, or_5_out, id_ex_1_out_42[1], id_ex_1_out_42[0]);
  Multiplexer #(.select(1), .width(32), .disabled("Z"), .enable("false")) multiplexer_12 (
    .in0(multiplexer_11_out), .in1(id_ex_1_out_51), .out(multiplexer_12_out), .sel(id_ex_1_out_37));
  Shifter #(.width(32), .shift("ll")) shifter_1 (.in(id_ex_1_out_52), .\dist (5'b00001), .out(shifter_1_out));
  Shifter #(.width(32), .shift("ll")) shifter_2 (.in(id_ex_1_out_48), .\dist (5'b00001), .out(shifter_2_out));
  Shifter #(.width(32), .shift("ll")) shifter_3 (.in(id_ex_1_out_53), .\dist (5'b01100), .out(shifter_3_out));
  Multiplexer #(.select(3), .width(32), .disabled("Z"), .enable("false")) multiplexer_13 (
    .in0(PC_4), .in1(ALU_result), .in2(jal_branch), .in4(b_branch), .out(EX_BranchAddr), .sel(id_ex_1_out_42));  // open: in3, in5, in6, in7
  and and_4 (and_4_out, id_ex_1_out_33, alu_1_equal);
  Comparator #(.width(32), .mode("twosComplement")) comparator_3 (
    .a(32'h22), .b(multiplexer_10_out), .eq(comparator_3_eq));  // open: gt, lt
  or or_5 (or_5_out, and_4_out, and_6_out, and_5_out);
  and and_5 (and_5_out, id_ex_1_out_44, alu_1_out_4);
  and and_6 (and_6_out, id_ex_1_out_34, ~alu_1_equal);  // AND_Gate
  ALU alu_1 (
    .X(multiplexer_10_out), .Y(multiplexer_12_out), .AluOP(id_ex_1_out_46), .Equal(alu_1_equal),
    .Result(ALU_result), .out_4(alu_1_out_4));  // open: Result_2, out_6
  Adder #(.width(32)) adder_2 (.a(shifter_1_out), .b(EX_PC), .out(b_branch));  // open: cin, cout
  Adder #(.width(32)) adder_3 (.a(shifter_2_out), .b(EX_PC), .out(jal_branch));  // open: cin, cout
  Adder #(.width(32)) adder_4 (.a(shifter_3_out), .b(EX_PC), .out(adder_4_out));  // open: cin, cout
  and and_7 (and_7_out, comparator_3_eq, id_ex_1_out_40);
  and and_8 (EX_halt, ~comparator_3_eq, id_ex_1_out_40);  // AND_Gate
  Register #(.width(32), .trigger("rising"), .Select("low")) register_1 (
    .D(multiplexer_11_out), .en(and_7_out), .Q(LedData), .clk(CLK), .clr(RST));
  not not_8 (not_8_out, halt);
  and and_9 (and_9_out, or_5_out, CLK);
  EX_MEM ex_mem_1 (
    .MEMTOREG(id_ex_1_out_35), .MEMWRITE(id_ex_1_out_36), .REGWRITE(id_ex_1_out_38), .HALT(EX_halt),
    .ECALL(id_ex_1_out_40), .JAL(id_ex_1_out_42[1]), .JALR(id_ex_1_out_42[0]), .AUIPC(id_ex_1_out_43),
    .SB(id_ex_1_out_45), .rd(id_ex_1_out_47), .R2(multiplexer_11_out), .Result(ALU_result),
    .imm3(adder_4_out), .IR(EX_IR), .PC(EX_PC), .PC_4(EX_PC_4), .out_21(ex_mem_1_out_21), .out_22(MemWrite),
    .out_23(ex_mem_1_out_23), .out_24(ex_mem_1_out_24), .out_25(ex_mem_1_out_25), .out_26(ex_mem_1_out_26),
    .out_27(ex_mem_1_out_27), .out_28(ex_mem_1_out_28), .out_30(SB), .out_31(ex_mem_1_out_31),
    .out_32(ex_mem_1_out_32), .out_33(MEM_ALU_result), .out_34(ex_mem_1_out_34), .out_35(MEM_IR),
    .out_36(M_PC), .out_37(ex_mem_1_out_37), .reset(1'b0), .en(not_8_out), .clk(CLK));  // open: out_29, URET
  not not_9 (not_9_out, halt);
  Counter #(.width(16), .max('hffff), .ongoal("wrap"), .trigger("rising"), .behavior("new")) counter_6 (
    .count(not_9_out), .Q(\条件分支成功数 ), .clk(multiplexer_14_out), .clr(RST));  // open: load, D, carry, preset, down
  Multiplexer #(.select(1), .width(1), .disabled("Z"), .enable("false")) multiplexer_14 (
    .in0(and_9_out), .in1(1'b0), .out(multiplexer_14_out), .sel(CLK));
  Multiplexer #(.select(1), .width(32), .disabled("Z"), .enable("false")) multiplexer_15 (
    .in0(ex_mem_1_out_32),
    .in1({ex_mem_1_out_32[7:0], ex_mem_1_out_32[7:0], ex_mem_1_out_32[7:0], ex_mem_1_out_32[7:0]}),
    .out(MDin), .sel(SB));
  not not_10 (not_10_out, halt);
  and and_10 (and_10_out, or_6_out, CLK);
  or or_6 (or_6_out, id_ex_1_out_42[1], id_ex_1_out_42[0]);
  Decoder #(.select(2), .tristate("false"), .disabled("Z"), .enable("false")) decoder_1 (
    .out0(decoder_1_out0[0]), .out1(decoder_1_out0[1]), .out2(decoder_1_out0[2]), .out3(decoder_1_out0[3]),
    .sel(MEM_ALU_result[1:0]));
  Counter #(.width(16), .max('hffff), .ongoal("wrap"), .trigger("rising"), .behavior("new")) counter_7 (
    .count(not_10_out), .Q(\无条件分支数 ), .clk(multiplexer_16_out), .clr(RST));  // open: load, D, carry, preset, down
  Multiplexer #(.select(1), .width(1), .disabled("Z"), .enable("false")) multiplexer_16 (
    .in0(and_10_out), .in1(1'b0), .out(multiplexer_16_out), .sel(CLK));
  // MIPS_RAM mips_ram_1: pin names not known; wires that end beside it: MEM_ALU_result[21:2], MDin, MemWrite, mips_ram_1_p4, CLK, 1'b1, RST, mips_ram_1_p8
  Multiplexer #(.select(1), .width(4), .disabled("Z"), .enable("false")) multiplexer_17 (
    .in0(4'b1111), .in1(decoder_1_out0), .out(mips_ram_1_p4), .sel(SB));
  MEM_WB mem_wb_1 (
    .MEMTOREG(ex_mem_1_out_21), .REGWRITE(ex_mem_1_out_23), .HALT(ex_mem_1_out_24), .ECALL(ex_mem_1_out_25),
    .JAL(ex_mem_1_out_26), .JALR(ex_mem_1_out_27), .AUIPC(ex_mem_1_out_28), .rd(ex_mem_1_out_31),
    .Result(MEM_ALU_result), .data(mips_ram_1_p8), .imm3(ex_mem_1_out_34), .IR(MEM_IR), .PC(M_PC),
    .PC_4(ex_mem_1_out_37), .out_19(mem_wb_1_out_19), .out_21(RegWrite), .out_22(mem_wb_1_out_22),
    .out_23(mem_wb_1_out_23), .out_24(mem_wb_1_out_24), .out_25(mem_wb_1_out_25), .out_26(mem_wb_1_out_26),
    .out_27(WriteReg_num), .out_28(mem_wb_1_out_28), .out_29(mem_wb_1_out_29), .out_30(mem_wb_1_out_30),
    .out_31(WB_IR), .out_32(WB_PC), .out_33(mem_wb_1_out_33), .reset(1'b0), .en(not_11_out), .clk(CLK));  // open: URET, out_20
  not not_11 (not_11_out, halt);
  or or_7 (or_7_out, mem_wb_1_out_24, mem_wb_1_out_25);
  D_Flip_Flop #(.trigger("high"), .Pre_Clr_Positions("LEGACY"), .NegatePresetClear("false"), .enable("true"), .NewFFLayout("false")) d_ff_2 (
    .clk(mem_wb_1_out_22), .D(1'b1), .Q(halt), .en(mem_wb_1_out_23), .reset(Go));  // open: Qn, preset
  Priority_Encoder #(.select(2), .disabled("Z")) priority_encoder_1 (
    .in0(1'b1), .in1(mem_wb_1_out_19), .in2(or_7_out), .in3(mem_wb_1_out_26), .out(priority_encoder_1_out));  // open: gs, en_out, en_in
  Multiplexer #(.select(2), .width(32), .disabled("Z"), .enable("false")) multiplexer_18 (
    .in0(mem_wb_1_out_28), .in1(mem_wb_1_out_29), .in2(mem_wb_1_out_33), .in3(mem_wb_1_out_30), .out(RDin),
    .sel(priority_encoder_1_out));

  // Other names for the same wires on the sheet: MEM_PC[31:0] = M_PC; stall = LoadUse; 插入气泡数[15:0] = \LoadUse次数 

  // Notes on the sheet:
  //   中断源
  //   中断等待指示
  //   数码管输出
  //   指令存储器
  //   指令探针
  //   contents of rom_1 (hex, n*v repeats v):
  //   100493 100006f 100493 200913 300993 100006f 100493 200913 300993 100006f 100493 200913 300993
  //   100006f 100493 200913 300993 29c000ef 100413 100493 1f49493 900533 2200893 73 24d493 48463 fedff06f
  //   900533 2200893 73 100493 249493 900533 2200893 73 48463 fedff06f 100493 1f49493 900533 2200893 73
  //   4034d493 900533 2200893 73 4044d493 900533 2200893 73 4044d493 900533 2200893 73 4044d493 900533
  //   2200893 73 4044d493 900533 2200893 73 4044d493 900533 2200893 73 4044d493 900533 2200893 73 4044d493
  //   900533 2200893 73 100413 1f41993 41f9d993 433 c00913 300b13 140413 f47413 800293 100313 499993
  //   89e9b3 1300533 2200893 73 406282b3 fe0294e3 140413 f00f93 1f47433 1c41413 800293 100313 49d993
  //   89e9b3 1300533 2200893 73 406282b3 fe0294e3 1c45413 406b0b33 b0463 f95ff06f 2b3 fff2c293 829293
  //   ff2e293 500533 2200893 73 fff00413 493 84a023 140413 448493 84a023 140413 448493 84a023 140413
  //   448493 84a023 140413 448493 84a023 140413 448493 84a023 140413 448493 84a023 140413 448493 84a023
  //   140413 448493 84a023 140413 448493 84a023 140413 448493 84a023 140413 448493 84a023 140413 448493
  //   84a023 140413 448493 84a023 140413 448493 84a023 140413 448493 84a023 140413 448493 140413 433
  //   3c00493 42983 4aa03 149a2b3 28663 134a023 1442023 ffc48493 fe9412e3 800533 2200893 73 440413 3c00493
  //   fc9416e3 a00893 73 413 140413 800533 2200893 73 240413 800533 2200893 73 340413 800533 2200893 73
  //   440413 800533 2200893 73 540413 800533 2200893 73 640413 800533 2200893 73 740413 800533 2200893 73
  //   840413 800533 2200893 2200893 73 8067
  //   控制位
  //   流水调试日志用
  //   暂停节拍，不能为0
  //   戳工具置1进入计数暂停模式，ctrl+k时钟自动运行到对应节拍暂停
  //   ctrl+k关闭时钟连续运行，将控制位置零，进入单步调试模式调试
  //   Beq
  //   Bne
  //   MemToReg
  //   MemWrite
  //   AluOP
  //   AluSrcB
  //   RegWrite
  //   可计数暂停的时钟源
  //   为方便自动评测，需要输出流水线各段保存的PC值，注意是PC不是PC+4，另外ID段寄存器写入信息，Mem段内存写入信息也要输出
endmodule

module \重定向_单级中断  (
  input  IR1,
  input  IR2,
  input  IR3,
  output RegWrite,
  output MemWrite,
  output [31:0] IF_PC,
  output [31:0] ID_PC,
  output [31:0] EX_PC,
  output [31:0] M_PC,
  output [31:0] WB_PC,
  output [31:0] RDin,
  output [31:0] MDin,
  output [31:0] LedData
);

  wire alu_1_equal, alu_1_out_4, and_1_out, and_2_out, and_3_out, and_4_out, and_5_out, and_10_out,
       and_11_out, and_12_out, and_13_out, and_15_out, and_16_out, BranchTaken, CLK, clock_1_out,
       clock_2_out, clr1, clr2, clr3, comparator_1_eq, comparator_1_lt, comparator_2_eq, comparator_3_eq,
       comparator_4_eq, comparator_5_eq, comparator_6_eq, d_ff_1_q, d_ff_2_q, d_ff_3_q, d_ff_4_q,
       decoder_1_out0, decoder_1_out1, decoder_1_out2, ecall, EX_halt, ex_mem_1_out_21, ex_mem_1_out_23,
       ex_mem_1_out_24, ex_mem_1_out_25, ex_mem_1_out_26, ex_mem_1_out_27, ex_mem_1_out_28, Go, halt,
       id_ex_1_out_33, id_ex_1_out_34, id_ex_1_out_35, id_ex_1_out_36, id_ex_1_out_37, id_ex_1_out_38,
       id_ex_1_out_40, id_ex_1_out_41, id_ex_1_out_42, id_ex_1_out_43, id_ex_1_out_44, id_ex_1_out_45, IE,
       IR1_2_q, IR1_3_q, IR1_q, IR1_t, IR2_t, IR3_t, IRA, IRB, IRC, LoadUse, mem_wb_1_out_19,
       mem_wb_1_out_22, mem_wb_1_out_23, mem_wb_1_out_24, mem_wb_1_out_25, mem_wb_1_out_26,
       multiplexer_4_out, multiplexer_13_out, multiplexer_15_out, nand_1_out, nor_1_out, nor_2_out,
       not_1_out, not_2_out, not_3_out, not_4_out, not_5_out, not_6_out, not_7_out, not_8_out, or_4_out,
       or_5_out, or_6_out, or_7_out, or_12_out, or_13_out, or_14_out, or_15_out, priority_encoder_1_gs, RST,
       SB, uret, W1, W2, W3, \中断信号 , \单周期硬布线控制器_1_alu_src , \单周期硬布线控制器_1_auipc , \单周期硬布线控制器_1_beq ,
       \单周期硬布线控制器_1_bgeu , \单周期硬布线控制器_1_bne , \单周期硬布线控制器_1_jal , \单周期硬布线控制器_1_jalr , \单周期硬布线控制器_1_memtoreg ,
       \单周期硬布线控制器_1_memwrite , \单周期硬布线控制器_1_regwrite , \单周期硬布线控制器_1_rs1used , \单周期硬布线控制器_1_rs2used ,
       \单周期硬布线控制器_1_s_type , \单周期硬布线控制器_1_sb , \单周期硬布线控制器_1_uret , \重定向数据相关检测逻辑_1_flush ;
  wire [1:0] id_ex_1_out_57, id_ex_1_out_58, priority_encoder_2_out, priority_encoder_3_out, register_1_q,
       \中断号 , \重定向数据相关检测逻辑_1_out_13 , \重定向数据相关检测逻辑_1_out_14 ;
  wire [2:0] register_2_q;
  wire [3:0] decoder_2_out0, id_ex_1_out_46, mips_ram_1_p4, \单周期硬布线控制器_1_alu_op ;
  wire [4:0] ex_mem_1_out_31, id_ex_1_out_47, multiplexer_5_out, multiplexer_6_out, WriteReg_num;
  wire [12:0] CNT_num;
  wire [15:0] \LoadUse次数 , \总周期数 , \无条件分支数 , \条件分支成功数 ;
  wire [31:0] adder_4_out, ALU_result, b_branch, bit_extender_1_out, bit_extender_2_out, bit_extender_3_out,
       bit_extender_4_out, bit_extender_5_out, EX_IR, ex_mem_1_out_32, ex_mem_1_out_34, ex_mem_1_out_37,
       id_ex_1_out_48, id_ex_1_out_49, id_ex_1_out_50, id_ex_1_out_51, id_ex_1_out_52, id_ex_1_out_53,
       id_ex_1_out_56, ID_IR, if_id_1_pc_4_2, IF_IR, jal_branch, MEM_ALU_result, MEM_IR, mem_wb_1_out_28,
       mem_wb_1_out_29, mem_wb_1_out_30, mem_wb_1_out_33, mips_ram_1_p8, multiplexer_1_out,
       multiplexer_2_out, multiplexer_3_out, multiplexer_7_out, multiplexer_9_out, multiplexer_10_out,
       multiplexer_11_out, multiplexer_12_out, PC_4, regifile_1_r1, regifile_1_r2, RetPC, shifter_1_out,
       shifter_2_out, shifter_3_out, WB_IR, \中断服务地址 ;

  Button \u_总复位  (.out(RST));
  Button _1 ();  // open: out
  Button _2 ();  // open: out
  Button _3 ();  // open: out
  // Probe on \总周期数 
  // Probe on \总周期数 
  Button \u_继续运行  (.out(Go));
  LED #(.active("true")) led_1 (.in(W1));
  LED #(.active("true")) led_2 (.in(W2));
  LED #(.active("true")) led_3 (.in(W3));
  Hex_Digit_Display hex_digit_display_1 (.value(LedData[31:28]));  // open: dp
  // Probe on IF_PC[19:0]
  // RiscV_Probe riscv_probe_1: pin names not known; wires that end beside it: IR1_t, IR2_t, IR3_t, IF_IR
  Hex_Digit_Display hex_digit_display_2 (.value(LedData[27:24]));  // open: dp
  Hex_Digit_Display hex_digit_display_3 (.value(LedData[23:20]));  // open: dp
  // Probe on ID_PC[19:0]
  // RiscV_Probe riscv_probe_2: pin names not known; wires that end beside it: ID_IR
  Hex_Digit_Display hex_digit_display_4 (.value(LedData[19:16]));  // open: dp
  Hex_Digit_Display hex_digit_display_5 (.value(LedData[15:12]));  // open: dp
  Multiplexer #(.select(2), .width(32), .disabled("Z"), .enable("false")) multiplexer_1 (
    .in0(PC_4), .in1(ALU_result), .in2(jal_branch), .in3(b_branch), .out(multiplexer_1_out),
    .sel(priority_encoder_2_out));
  Multiplexer #(.select(1), .width(32), .disabled("Z"), .enable("false")) multiplexer_2 (
    .in0(multiplexer_1_out), .in1(RetPC), .out(multiplexer_2_out), .sel(uret));
  Hex_Digit_Display hex_digit_display_6 (.value(LedData[11:8]));  // open: dp
  Hex_Digit_Display hex_digit_display_7 (.value(LedData[7:4]));  // open: dp
  Clock #(.highDuration(1), .lowDuration(1)) clock_1 (.out(clock_1_out));
  // Probe on EX_PC[19:0]
  // RiscV_Probe riscv_probe_3: pin names not known; wires that end beside it: clock_1_out, EX_IR, CLK
  Multiplexer #(.select(1), .width(32), .disabled("Z"), .enable("false")) multiplexer_3 (
    .in0(multiplexer_2_out), .in1(\中断服务地址 ), .out(multiplexer_3_out), .sel(\中断信号 ));
  Hex_Digit_Display hex_digit_display_8 (.value(LedData[3:0]));  // open: dp
  nor nor_1 (nor_1_out, halt, LoadUse);
  Register #(.width(32), .trigger("rising"), .Select("low")) PC (
    .D(multiplexer_3_out), .en(nor_1_out), .Q(IF_PC), .clk(CLK), .clr(RST));
  // Probe on \总周期数 
  // Probe on M_PC[19:0]
  // RiscV_Probe riscv_probe_4: pin names not known; wires that end beside it: MEM_IR
  \重定向数据相关检测逻辑  \u_重定向数据相关检测逻辑_1  (
    .in_1(ID_IR), .BranchTaken(BranchTaken), .EX_MemToReg(id_ex_1_out_35), .rs1used(\单周期硬布线控制器_1_rs1used ),
    .rs2used(\单周期硬布线控制器_1_rs2used ), .EX_RegWrite(id_ex_1_out_38), .MEM_RegWrite(ex_mem_1_out_23),
    .ecall(ecall), .EX_WriteReg_num(id_ex_1_out_47), .MEM_WriteReg_num(ex_mem_1_out_31), .stall(LoadUse),
    .flush(\重定向数据相关检测逻辑_1_flush ), .out_13(\重定向数据相关检测逻辑_1_out_13 ), .out_14(\重定向数据相关检测逻辑_1_out_14 ));
  not not_1 (not_1_out, halt);
  and and_1 (and_1_out, LoadUse, CLK);
  D_Flip_Flop #(.trigger("rising"), .Pre_Clr_Positions("LEGACY"), .NegatePresetClear("false"), .enable("true"), .NewFFLayout("false")) d_ff_1 (
    .clk(IR1_t), .D(1'b1), .Q(d_ff_1_q), .reset(IR1_q));  // open: Qn, preset, en
  or or_1 (W1, IR1_q, d_ff_1_q);
  D_Flip_Flop #(.trigger("rising"), .Pre_Clr_Positions("LEGACY"), .NegatePresetClear("false"), .enable("true"), .NewFFLayout("false")) d_ff_2 (
    .clk(IR2_t), .D(1'b1), .Q(d_ff_2_q), .reset(IR1_2_q));  // open: Qn, preset, en
  or or_2 (W2, IR1_2_q, d_ff_2_q);
  D_Flip_Flop #(.trigger("rising"), .Pre_Clr_Positions("LEGACY"), .NegatePresetClear("false"), .enable("true"), .NewFFLayout("false")) d_ff_3 (
    .clk(IR3_t), .D(1'b1), .Q(d_ff_3_q), .reset(IR1_3_q));  // open: Qn, preset, en
  or or_3 (W3, IR1_3_q, d_ff_3_q);
  // Probe on \总周期数 
  // Probe on \无条件分支数 
  // Probe on \条件分支成功数 
  // Probe on \LoadUse次数 
  // Probe on \LoadUse次数 
  Counter #(.width(16), .max('hffff), .ongoal("wrap"), .trigger("rising"), .behavior("new")) counter_1 (
    .count(not_1_out), .Q(\LoadUse次数 ), .clk(multiplexer_4_out), .clr(RST));  // open: load, D, carry, preset, down
  Multiplexer #(.select(1), .width(1), .disabled("Z"), .enable("false")) multiplexer_4 (
    .in0(and_1_out), .in1(1'b0), .out(multiplexer_4_out), .sel(CLK));
  not not_2 (not_2_out, halt);
  Adder #(.width(32)) adder_1 (.a(IF_PC), .b(32'h4), .out(PC_4));  // open: cin, cout
  or or_4 (or_4_out, d_ff_1_q, IR1_q);
  or or_5 (or_5_out, d_ff_2_q, IR1_2_q);
  or or_6 (or_6_out, d_ff_3_q, IR1_3_q);
  // Probe on IF_PC[11:0]
  // Probe on WB_PC[19:0]
  // RiscV_Probe riscv_probe_5: pin names not known; wires that end beside it: WB_IR
  Counter #(.width(16), .max('hffff), .ongoal("wrap"), .trigger("rising"), .behavior("new")) counter_2 (
    .count(not_2_out), .Q(\总周期数 ), .clk(CLK), .clr(RST));  // open: load, D, carry, preset, down
  // RiscV_Probe riscv_probe_6: pin names not known; wires that end beside it: IF_IR, CLK
  ROM #(.addrWidth(10), .dataWidth(32), .Select("high")) rom_1 (.addr(IF_PC[11:2]), .data(IF_IR));
  and and_2 (and_2_out, or_4_out, ~clr1);  // AND_Gate
  and and_3 (and_3_out, or_5_out, ~clr2);  // AND_Gate
  and and_4 (and_4_out, or_6_out, ~clr3);  // AND_Gate
  // Probe on EX_PC[11:0]
  // Probe on ID_PC[11:0]
  IF_ID if_id_1 (
    .IR(IF_IR), .PC(IF_PC), .PC_4(PC_4), .IR_2(ID_IR), .PC_2(ID_PC), .PC_4_2(if_id_1_pc_4_2),
    .BranchTaken(BranchTaken), .en(nor_2_out), .clk(CLK), .reset(or_7_out));  // open: PredictJump, out_9
  nor nor_2 (nor_2_out, LoadUse, halt);
  D_Flip_Flop #(.trigger("rising"), .Pre_Clr_Positions("LEGACY"), .NegatePresetClear("false"), .enable("true"), .NewFFLayout("false")) u_IR1 (
    .clk(CLK), .D(and_2_out), .Q(IR1_q), .reset(RST));  // open: Qn, preset, en
  D_Flip_Flop #(.trigger("rising"), .Pre_Clr_Positions("LEGACY"), .NegatePresetClear("false"), .enable("true"), .NewFFLayout("false")) IR1_2 (
    .clk(CLK), .D(and_3_out), .Q(IR1_2_q), .reset(RST));  // open: Qn, preset, en
  D_Flip_Flop #(.trigger("rising"), .Pre_Clr_Positions("LEGACY"), .NegatePresetClear("false"), .enable("true"), .NewFFLayout("false")) IR1_3 (
    .clk(CLK), .D(and_4_out), .Q(IR1_3_q), .reset(RST));  // open: Qn, preset, en
  // Probe on M_PC[11:0]
  D_Flip_Flop #(.trigger("high"), .Pre_Clr_Positions("LEGACY"), .NegatePresetClear("false"), .enable("true"), .NewFFLayout("false")) d_ff_4 (.Q(d_ff_4_q));  // open: clk, D, Qn, preset, en, reset
  // Probe on 13'hc
  or or_7 (or_7_out, uret, \中断信号 );
  // Probe on WB_PC[11:0]
  Comparator #(.width(13), .mode("twosComplement")) comparator_1 (
    .a(CNT_num), .b(13'hc), .eq(comparator_1_eq), .lt(comparator_1_lt));  // open: gt
  Clock #(.highDuration(1), .lowDuration(1)) clock_2 (.out(clock_2_out));
  Priority_Encoder #(.select(2), .disabled("Z")) priority_encoder_1 (
    .in0(IR1_q), .in1(IR1_2_q), .in2(IR1_3_q), .out(\中断号 ), .gs(priority_encoder_1_gs));  // open: in3, en_out, en_in
  nand nand_1 (nand_1_out, d_ff_4_q, comparator_1_eq);
  Counter #(.width(13), .max('h1fff), .ongoal("stay"), .trigger("rising"), .behavior("old")) counter_3 (
    .count(comparator_1_lt), .Q(CNT_num), .clk(clock_2_out));  // open: load, D, carry, clr, preset
  \单周期硬布线控制器  \u_单周期硬布线控制器_1  (
    .Funct({ID_IR[30], ID_IR[25], ID_IR[14:12]}), .OP(ID_IR[6:2]), .ALU_OP(\单周期硬布线控制器_1_alu_op ),
    .MemToReg(\单周期硬布线控制器_1_memtoreg ), .MemWrite(\单周期硬布线控制器_1_memwrite ), .ALU_SRC(\单周期硬布线控制器_1_alu_src ),
    .RegWrite(\单周期硬布线控制器_1_regwrite ), .ecall(ecall), .S_type(\单周期硬布线控制器_1_s_type ),
    .Jalr(\单周期硬布线控制器_1_jalr ), .Beq(\单周期硬布线控制器_1_beq ), .JAL(\单周期硬布线控制器_1_jal ), .Bne(\单周期硬布线控制器_1_bne ),
    .in_3(ID_IR[21]), .uret(\单周期硬布线控制器_1_uret ), .AUIPC(\单周期硬布线控制器_1_auipc ), .BGEU(\单周期硬布线控制器_1_bgeu ),
    .SB(\单周期硬布线控制器_1_sb ), .Rs1used(\单周期硬布线控制器_1_rs1used ), .Rs2used(\单周期硬布线控制器_1_rs2used ));  // open: CSRRSI, CSRRCI
  Multiplexer #(.select(1), .width(5), .disabled("Z"), .enable("false")) multiplexer_5 (
    .in0(ID_IR[19:15]), .in1(5'b10001), .out(multiplexer_5_out), .sel(ecall));
  Multiplexer #(.select(1), .width(5), .disabled("Z"), .enable("false")) multiplexer_6 (
    .in0(ID_IR[24:20]), .in1(5'b01010), .out(multiplexer_6_out), .sel(ecall));
  assign bit_extender_1_out = {{20{ID_IR[31]}}, ID_IR[31:20]};  // Bit_Extender bit_extender_1
  assign bit_extender_2_out = {{20{ID_IR[31]}}, {ID_IR[31:25], ID_IR[11:7]}};  // Bit_Extender bit_extender_2
  assign bit_extender_3_out = {{20{ID_IR[31]}}, {ID_IR[31], ID_IR[7], ID_IR[30:25], ID_IR[11:8]}};  // Bit_Extender bit_extender_3
  assign bit_extender_4_out = {{12{ID_IR[31]}}, {ID_IR[31], ID_IR[19:12], ID_IR[20], ID_IR[30:21]}};  // Bit_Extender bit_extender_4
  assign bit_extender_5_out = {{12{ID_IR[31]}}, ID_IR[31:12]};  // Bit_Extender bit_extender_5
  and and_5 (and_5_out, priority_encoder_1_gs, ~uret);  // AND_Gate
  and and_6 (\中断信号 , priority_encoder_1_gs, IE);
  assign CLK = nand_1_out ? clock_2_out : 1'bz;  // Controlled_Buffer controlled_buffer_1
  Multiplexer #(.select(1), .width(32), .disabled("Z"), .enable("false")) multiplexer_7 (
    .in0(bit_extender_1_out), .in1(bit_extender_2_out), .out(multiplexer_7_out), .sel(\单周期硬布线控制器_1_s_type ));
  Multiplexer #(.select(2), .width(32), .disabled("Z"), .enable("false")) multiplexer_8 (
    .in0(32'h30ac), .in1(32'h3150), .in2(32'h31f4), .out(\中断服务地址 ), .sel(\中断号 ));  // open: in3
  D_Flip_Flop #(.trigger("rising"), .Pre_Clr_Positions("LEGACY"), .NegatePresetClear("false"), .enable("true"), .NewFFLayout("false")) d_ff_5 (
    .clk(CLK), .D(and_5_out), .Qn(IE), .reset(RST));  // open: Q, preset, en
  Pull_Resistor #(.pull(1)) pull_resistor_1 (.node(CLK));
  not not_3 (not_3_out, CLK);
  Regifile regifile_1 (
    .Din(RDin), .Clk(not_3_out), .R1(regifile_1_r1), .R2(regifile_1_r2), .WE(RegWrite), .W_num(WriteReg_num),
    .R1_num(multiplexer_5_out), .R2_num(multiplexer_6_out));
  not not_4 (not_4_out, halt);
  ID_EX id_ex_1 (
    .BEQ(\单周期硬布线控制器_1_beq ), .BNE(\单周期硬布线控制器_1_bne ), .MEMTOREG(\单周期硬布线控制器_1_memtoreg ),
    .MEMWRITE(\单周期硬布线控制器_1_memwrite ), .ALUSRCB(\单周期硬布线控制器_1_alu_src ), .REGWRITE(\单周期硬布线控制器_1_regwrite ),
    .ECALL(ecall), .JAL(\单周期硬布线控制器_1_jal ), .JALR(\单周期硬布线控制器_1_jalr ), .AUIPC(\单周期硬布线控制器_1_auipc ),
    .BGEU(\单周期硬布线控制器_1_bgeu ), .SB(\单周期硬布线控制器_1_sb ), .ALUop(\单周期硬布线控制器_1_alu_op ), .rd(ID_IR[11:7]),
    .R1(regifile_1_r1), .R2(regifile_1_r2), .imm1(multiplexer_7_out), .imm2(bit_extender_3_out),
    .imm3(bit_extender_5_out), .IR(ID_IR), .PC(ID_PC), .PC_4(if_id_1_pc_4_2), .out_33(id_ex_1_out_33),
    .out_34(id_ex_1_out_34), .out_35(id_ex_1_out_35), .out_36(id_ex_1_out_36), .out_37(id_ex_1_out_37),
    .out_38(id_ex_1_out_38), .out_40(id_ex_1_out_40), .out_41(id_ex_1_out_41), .out_42(id_ex_1_out_42),
    .out_43(id_ex_1_out_43), .out_44(id_ex_1_out_44), .out_45(id_ex_1_out_45), .out_46(id_ex_1_out_46),
    .out_47(id_ex_1_out_47), .out_49(id_ex_1_out_49), .out_50(id_ex_1_out_50), .out_51(id_ex_1_out_51),
    .out_52(id_ex_1_out_52), .out_53(id_ex_1_out_53), .out_54(EX_IR), .out_55(EX_PC),
    .out_56(id_ex_1_out_56), .flush(\重定向数据相关检测逻辑_1_flush ), .en(not_4_out), .clk(CLK),
    .Rs1Forward(\重定向数据相关检测逻辑_1_out_13 ), .out_57(id_ex_1_out_57), .Rs2Forward(\重定向数据相关检测逻辑_1_out_14 ),
    .out_58(id_ex_1_out_58), .imm4(bit_extender_4_out), .out_48(id_ex_1_out_48), .reset(or_7_out),
    .URET(\单周期硬布线控制器_1_uret ), .out_39(uret));  // open: PredictJump, out_32
  Register #(.width(2), .trigger("rising"), .Select("low")) register_1 (
    .D(\中断号 ), .en(\中断信号 ), .Q(register_1_q), .clk(CLK), .clr(RST));
  Register #(.width(1), .trigger("rising"), .Select("low")) register_2 (
    .D(BranchTaken), .Q(register_2_q[0]), .clk(CLK), .clr(RST));  // open: en
  Register #(.width(1), .trigger("rising"), .Select("low")) register_3 (
    .D(LoadUse), .Q(register_2_q[2]), .clk(CLK), .clr(RST));  // open: en
  or or_8 (IR1_t, IR1, IRA);
  Multiplexer #(.select(2), .width(32), .disabled("Z"), .enable("false")) multiplexer_9 (
    .in0(id_ex_1_out_49), .in1(RDin), .in2(MEM_ALU_result), .out(multiplexer_9_out), .sel(id_ex_1_out_57));  // open: in3
  Multiplexer #(.select(2), .width(32), .disabled("Z"), .enable("false")) multiplexer_10 (
    .in0(id_ex_1_out_50), .in1(RDin), .in2(MEM_ALU_result), .out(multiplexer_10_out), .sel(id_ex_1_out_58));  // open: in3
  Decoder #(.select(2), .tristate("false"), .disabled("Z"), .enable("false")) decoder_1 (
    .out0(decoder_1_out0), .out1(decoder_1_out1), .out2(decoder_1_out2), .sel(register_1_q));  // open: out3
  Register #(.width(1), .trigger("rising"), .Select("low")) register_4 (
    .D(register_2_q[0]), .Q(register_2_q[1]), .clk(CLK), .clr(RST));  // open: en
  and and_7 (clr1, decoder_1_out0, uret);
  and and_8 (clr2, decoder_1_out1, uret);
  and and_9 (clr3, decoder_1_out2, uret);
  Multiplexer #(.select(3), .width(32), .disabled("Z"), .enable("false")) multiplexer_11 (
    .in0(EX_PC), .in1(IF_PC), .in2(ID_PC), .in4(ID_PC), .out(multiplexer_11_out), .sel(register_2_q));  // open: in3, in5, in6, in7
  or or_9 (IR2_t, IR2, IRB);
  or or_10 (BranchTaken, or_12_out, id_ex_1_out_41, id_ex_1_out_42);
  Multiplexer #(.select(1), .width(32), .disabled("Z"), .enable("false")) multiplexer_12 (
    .in0(multiplexer_10_out), .in1(id_ex_1_out_51), .out(multiplexer_12_out), .sel(id_ex_1_out_37));
  Shifter #(.width(32), .shift("ll")) shifter_1 (.in(id_ex_1_out_52), .\dist (5'b00001), .out(shifter_1_out));
  Shifter #(.width(32), .shift("ll")) shifter_2 (.in(id_ex_1_out_48), .\dist (5'b00001), .out(shifter_2_out));
  Shifter #(.width(32), .shift("ll")) shifter_3 (.in(id_ex_1_out_53), .\dist (5'b01100), .out(shifter_3_out));
  or or_11 (IR3_t, IR3, IRC);
  and and_10 (and_10_out, id_ex_1_out_33, alu_1_equal);
  Comparator #(.width(32), .mode("twosComplement")) comparator_2 (
    .a(32'h22), .b(multiplexer_9_out), .eq(comparator_2_eq));  // open: gt, lt
  Register #(.width(32), .trigger("rising"), .Select("low")) register_5 (
    .D(multiplexer_11_out), .en(\中断信号 ), .Q(RetPC), .clk(CLK), .clr(RST));
  or or_12 (or_12_out, and_10_out, and_11_out, and_12_out);
  and and_11 (and_11_out, id_ex_1_out_34, ~alu_1_equal);  // AND_Gate
  and and_12 (and_12_out, id_ex_1_out_44, alu_1_out_4);
  ALU alu_1 (
    .X(multiplexer_9_out), .Y(multiplexer_12_out), .AluOP(id_ex_1_out_46), .Equal(alu_1_equal),
    .Result(ALU_result), .out_4(alu_1_out_4));  // open: Result_2, out_6
  Adder #(.width(32)) adder_2 (.a(shifter_1_out), .b(EX_PC), .out(b_branch));  // open: cin, cout
  Adder #(.width(32)) adder_3 (.a(shifter_2_out), .b(EX_PC), .out(jal_branch));  // open: cin, cout
  Adder #(.width(32)) adder_4 (.a(shifter_3_out), .b(EX_PC), .out(adder_4_out));  // open: cin, cout
  and and_13 (and_13_out, comparator_2_eq, id_ex_1_out_40);
  and and_14 (EX_halt, ~comparator_2_eq, id_ex_1_out_40);  // AND_Gate
  Priority_Encoder #(.select(2), .disabled("Z")) priority_encoder_2 (
    .in0(1'b1), .in1(id_ex_1_out_42), .in2(id_ex_1_out_41), .in3(or_12_out), .out(priority_encoder_2_out));  // open: gs, en_out, en_in
  Register #(.width(32), .trigger("rising"), .Select("low")) register_6 (
    .D(multiplexer_10_out), .en(and_13_out), .Q(LedData), .clk(CLK), .clr(RST));
  not not_5 (not_5_out, halt);
  and and_15 (and_15_out, or_12_out, CLK);
  EX_MEM ex_mem_1 (
    .MEMTOREG(id_ex_1_out_35), .MEMWRITE(id_ex_1_out_36), .REGWRITE(id_ex_1_out_38), .HALT(EX_halt),
    .ECALL(id_ex_1_out_40), .JAL(id_ex_1_out_41), .JALR(id_ex_1_out_42), .AUIPC(id_ex_1_out_43),
    .SB(id_ex_1_out_45), .rd(id_ex_1_out_47), .R2(multiplexer_10_out), .Result(ALU_result),
    .imm3(adder_4_out), .IR(EX_IR), .PC(EX_PC), .PC_4(id_ex_1_out_56), .out_21(ex_mem_1_out_21),
    .out_22(MemWrite), .out_23(ex_mem_1_out_23), .out_24(ex_mem_1_out_24), .out_25(ex_mem_1_out_25),
    .out_26(ex_mem_1_out_26), .out_27(ex_mem_1_out_27), .out_28(ex_mem_1_out_28), .out_30(SB),
    .out_31(ex_mem_1_out_31), .out_32(ex_mem_1_out_32), .out_33(MEM_ALU_result), .out_34(ex_mem_1_out_34),
    .out_35(MEM_IR), .out_36(M_PC), .out_37(ex_mem_1_out_37), .reset(1'b0), .en(not_5_out), .clk(CLK));  // open: out_29, URET
  Counter #(.width(16), .max('hffff), .ongoal("wrap"), .trigger("rising"), .behavior("new")) counter_4 (
    .count(not_6_out), .Q(\条件分支成功数 ), .clk(multiplexer_13_out), .clr(RST));  // open: load, D, carry, preset, down
  not not_6 (not_6_out, halt);
  Multiplexer #(.select(1), .width(1), .disabled("Z"), .enable("false")) multiplexer_13 (
    .in0(and_15_out), .in1(1'b0), .out(multiplexer_13_out), .sel(CLK));
  Multiplexer #(.select(1), .width(32), .disabled("Z"), .enable("false")) multiplexer_14 (
    .in0(ex_mem_1_out_32),
    .in1({ex_mem_1_out_32[7:0], ex_mem_1_out_32[7:0], ex_mem_1_out_32[7:0], ex_mem_1_out_32[7:0]}),
    .out(MDin), .sel(SB));
  not not_7 (not_7_out, halt);
  and and_16 (and_16_out, or_13_out, CLK);
  or or_13 (or_13_out, id_ex_1_out_41, id_ex_1_out_42);
  Decoder #(.select(2), .tristate("false"), .disabled("Z"), .enable("false")) decoder_2 (
    .out0(decoder_2_out0[0]), .out1(decoder_2_out0[1]), .out2(decoder_2_out0[2]), .out3(decoder_2_out0[3]),
    .sel(MEM_ALU_result[1:0]));
  Comparator #(.width(16), .mode("twosComplement")) comparator_3 (
    .a(16'h23b), .b(\总周期数 ), .eq(comparator_3_eq));  // open: gt, lt
  or or_14 (or_14_out, comparator_3_eq, comparator_4_eq);
  Comparator #(.width(16), .mode("twosComplement")) comparator_4 (
    .a(\总周期数 ), .b(16'h1), .eq(comparator_4_eq));  // open: gt, lt
  Comparator #(.width(16), .mode("twosComplement")) comparator_5 (
    .a(\总周期数 ), .b(16'h4), .eq(comparator_5_eq));  // open: gt, lt
  Comparator #(.width(16), .mode("twosComplement")) comparator_6 (
    .a(\总周期数 ), .b(16'h7), .eq(comparator_6_eq));  // open: gt, lt
  Counter #(.width(16), .max('hffff), .ongoal("wrap"), .trigger("rising"), .behavior("new")) counter_5 (
    .count(not_7_out), .Q(\无条件分支数 ), .clk(multiplexer_15_out), .clr(RST));  // open: load, D, carry, preset, down
  Multiplexer #(.select(1), .width(1), .disabled("Z"), .enable("false")) multiplexer_15 (
    .in0(and_16_out), .in1(1'b0), .out(multiplexer_15_out), .sel(CLK));
  // MIPS_RAM mips_ram_1: pin names not known; wires that end beside it: MEM_ALU_result[21:2], MDin, MemWrite, mips_ram_1_p4, CLK, 1'b1, RST, mips_ram_1_p8
  Multiplexer #(.select(1), .width(4), .disabled("Z"), .enable("false")) multiplexer_16 (
    .in0(4'b1111), .in1(decoder_2_out0), .out(mips_ram_1_p4), .sel(SB));
  Pull_Resistor #(.pull(0)) pull_resistor_2 (.node(IRA));
  assign IRA = or_14_out ? ~CLK : 1'bz;  // Controlled_Inverter controlled_inverter_1
  Pull_Resistor #(.pull(0)) pull_resistor_3 (.node(IRB));
  assign IRB = comparator_5_eq ? ~CLK : 1'bz;  // Controlled_Inverter controlled_inverter_2
  Pull_Resistor #(.pull(0)) pull_resistor_4 (.node(IRC));
  assign IRC = comparator_6_eq ? ~CLK : 1'bz;  // Controlled_Inverter controlled_inverter_3
  MEM_WB mem_wb_1 (
    .MEMTOREG(ex_mem_1_out_21), .REGWRITE(ex_mem_1_out_23), .HALT(ex_mem_1_out_24), .ECALL(ex_mem_1_out_25),
    .JAL(ex_mem_1_out_26), .JALR(ex_mem_1_out_27), .AUIPC(ex_mem_1_out_28), .rd(ex_mem_1_out_31),
    .Result(MEM_ALU_result), .data(mips_ram_1_p8), .imm3(ex_mem_1_out_34), .IR(MEM_IR), .PC(M_PC),
    .PC_4(ex_mem_1_out_37), .out_19(mem_wb_1_out_19), .out_21(RegWrite), .out_22(mem_wb_1_out_22),
    .out_23(mem_wb_1_out_23), .out_24(mem_wb_1_out_24), .out_25(mem_wb_1_out_25), .out_26(mem_wb_1_out_26),
    .out_27(WriteReg_num), .out_28(mem_wb_1_out_28), .out_29(mem_wb_1_out_29), .out_30(mem_wb_1_out_30),
    .out_31(WB_IR), .out_32(WB_PC), .out_33(mem_wb_1_out_33), .reset(1'b0), .en(not_8_out), .clk(CLK));  // open: URET, out_20
  not not_8 (not_8_out, halt);
  or or_15 (or_15_out, mem_wb_1_out_24, mem_wb_1_out_25);
  D_Flip_Flop #(.trigger("high"), .Pre_Clr_Positions("LEGACY"), .NegatePresetClear("false"), .enable("true"), .NewFFLayout("false")) d_ff_6 (
    .clk(mem_wb_1_out_22), .D(1'b1), .Q(halt), .en(mem_wb_1_out_23), .reset(Go));  // open: Qn, preset
  Priority_Encoder #(.select(2), .disabled("Z")) priority_encoder_3 (
    .in0(1'b1), .in1(mem_wb_1_out_19), .in2(or_15_out), .in3(mem_wb_1_out_26), .out(priority_encoder_3_out));  // open: gs, en_out, en_in
  Multiplexer #(.select(2), .width(32), .disabled("Z"), .enable("false")) multiplexer_17 (
    .in0(mem_wb_1_out_28), .in1(mem_wb_1_out_29), .in2(mem_wb_1_out_33), .in3(mem_wb_1_out_30), .out(RDin),
    .sel(priority_encoder_3_out));

  // Other names for the same wires on the sheet: MEM_PC[31:0] = M_PC; stall = LoadUse; 插入气泡数[15:0] = \LoadUse次数 

  // Notes on the sheet:
  //   中断源
  //   中断等待指示
  //   数码管输出
  //   指令存储器
  //   指令探针
  //   contents of rom_1 (hex, n*v repeats v):
  //   7d000113 100413 1f41993 41f9d993 433 c00913 800b13 140413 f47413 800293 100313 499993 89e9b3 1300533
  //   2200893 73 406282b3 fe0294e3 140413 f00f93 1f47433 1c41413 800293 100313 49d993 89e9b3 1300533
  //   2200893 73 406282b3 fe0294e3 1c45413 406b0b33 b0463 f95ff06f 2b3 fff2c293 1029293 fff2e293 500533
  //   2200893 73 f5dff06f 1112023 410113 a12023 410113 812023 410113 1312023 410113 1412023 410113 1512023
  //   410113 1612023 410113 100b13 300a13 100a93 1600433 441413 14469b3 1300533 2200893 73 fe0416e3
  //   415a0a33 fe0a10e3 ffc10113 12b03 ffc10113 12a83 ffc10113 12a03 ffc10113 12983 ffc10113 12403
  //   ffc10113 12503 ffc10113 12883 200073 1112023 410113 a12023 410113 812023 410113 1312023 410113
  //   1412023 410113 1512023 410113 1612023 410113 200b13 300a13 100a93 1600433 441413 14469b3 1300533
  //   2200893 73 fe0416e3 415a0a33 fe0a10e3 ffc10113 12b03 ffc10113 12a83 ffc10113 12a03 ffc10113 12983
  //   ffc10113 12403 ffc10113 12503 ffc10113 12883 200073 1112023 410113 a12023 410113 812023 410113
  //   1312023 410113 1412023 410113 1512023 410113 1612023 410113 300b13 300a13 100a93 1600433 441413
  //   14469b3 1300533 2200893 73 fe0416e3 415a0a33 fe0a10e3 ffc10113 12b03 ffc10113 12a83 ffc10113 12a03
  //   ffc10113 12983 ffc10113 12403 ffc10113 12503 ffc10113 12883 200073
  //   控制位
  //   Reset 
  //   Reset 
  //   Reset 
  //   流水调试日志用
  //   暂停节拍，不能为0
  //   戳工具置1进入计数暂停模式，ctrl+k时钟自动运行到对应节拍暂停
  //   ctrl+k关闭时钟连续运行，将控制位置零，进入单步调试模式调试
  //   Beq
  //   Bne
  //   MemToReg
  //   MemWrite
  //   AluOP
  //   AluSrcB
  //   RegWrite
  //   可计数暂停的时钟源
  //   为方便自动评测，需要输出流水线各段保存的PC值，注意是PC不是PC+4，另外ID段寄存器写入信息，Mem段内存写入信息也要输出
  //   单级中断测试信号模拟器
endmodule

module MAX (
  input  [15:0] X,
  input  [15:0] Y,
  input  [2:0] X_num,
  input  [2:0] Y_num,
  output [15:0] MAX,
  output [2:0] MAX_num
);

  wire comparator_1_lt;

  Comparator #(.width(16), .mode("unsigned")) comparator_1 (.a(X), .b(Y), .lt(comparator_1_lt));  // open: gt, eq
  Multiplexer #(.select(1), .width(16), .disabled("Z"), .enable("false")) multiplexer_1 (
    .in0(X), .in1(Y), .out(MAX), .sel(comparator_1_lt));
  Multiplexer #(.select(1), .width(3), .disabled("Z"), .enable("false")) multiplexer_2 (
    .in0(X_num), .in1(Y_num), .out(MAX_num), .sel(comparator_1_lt));
endmodule

module BTB (
  input  [31:0] PC,
  input  [31:0] EX_PC,
  input  [31:0] EX_BranchAddr,
  input  CLK,
  input  EX_Branch,
  input  EX_BranchTaken,
  output ID_PredictJump,
  output [31:0] JumpAddr
);

  wire and_1_out, and_2_out, and_3_out, and_4_out, and_5_out, and_6_out, and_7_out, and_8_out, and_25_out,
       comparator_1_eq, comparator_2_eq, comparator_3_eq, comparator_4_eq, comparator_5_eq, comparator_6_eq,
       comparator_7_eq, comparator_8_eq, comparator_9_eq, comparator_10_eq, comparator_11_eq,
       comparator_12_eq, comparator_13_eq, comparator_14_eq, comparator_15_eq, comparator_16_eq, d_ff_1_q,
       d_ff_2_q, d_ff_3_q, d_ff_4_q, d_ff_5_q, d_ff_6_q, d_ff_7_q, d_ff_8_q, decoder_1_out0, decoder_1_out1,
       decoder_1_out2, decoder_1_out3, decoder_1_out4, decoder_1_out5, decoder_1_out6, decoder_1_out7,
       decoder_2_out0, decoder_2_out1, decoder_2_out2, decoder_2_out3, decoder_2_out4, decoder_2_out5,
       decoder_2_out6, decoder_2_out7, L0, L1, L2, L3, L4, L5, L6, L7, M0, M1, M2, M3, M4, M5, M6, M7, miss,
       not_2_out, not_3_out, not_4_out, not_5_out, not_6_out, not_7_out, not_8_out, not_9_out, or_1_out,
       or_2_out, or_3_out, or_4_out, or_5_out, or_6_out, or_7_out, or_8_out, or_9_out, or_10_out, or_11_out,
       or_12_out, or_13_out, or_14_out, or_15_out, or_16_out, or_17_out, priority_encoder_1_gs, v0, v1, v2,
       v3, v4, v5, v6, v7, w0, w1, w2, w3, w4, w5, w6, w7;
  wire [0:0] controlled_buffer_9_out, controlled_buffer_10_out, controlled_buffer_11_out,
       controlled_buffer_12_out, controlled_buffer_13_out, controlled_buffer_14_out,
       controlled_buffer_15_out, controlled_buffer_16_out;
  wire [1:0] register_25_q, register_26_q, register_27_q, register_28_q, register_29_q, register_30_q,
       register_31_q, register_32_q, \状态机_1_次态 , \状态机_2_次态 , \状态机_3_次态 , \状态机_4_次态 , \状态机_5_次态 , \状态机_6_次态 ,
       \状态机_7_次态 , \状态机_8_次态 ;
  wire [2:0] max_1_max_num, max_2_max_num, max_3_max_num, max_4_max_num, max_5_max_num, max_6_max_num,
       max_7_max_num, priority_encoder_1_out;
  wire [15:0] c0, c1, c2, c3, c4, c5, c6, c7, max_1_max, max_2_max, max_3_max, max_4_max, max_5_max,
       max_6_max;
  wire [31:0] register_17_q, register_18_q, register_19_q, register_20_q, register_21_q, register_22_q,
       register_23_q, register_24_q, tag0, tag1, tag2, tag3, tag4, tag5, tag6, tag7;

  Register #(.width(1), .trigger("rising"), .Select("low")) register_1 (
    .D(1'b1), .en(w0), .Q(v0), .clk(CLK));  // open: clr
  Register #(.width(1), .trigger("rising"), .Select("low")) register_2 (
    .D(1'b1), .en(w1), .Q(v1), .clk(CLK));  // open: clr
  Register #(.width(1), .trigger("rising"), .Select("low")) register_3 (
    .D(1'b1), .en(w2), .Q(v2), .clk(CLK));  // open: clr
  Register #(.width(1), .trigger("rising"), .Select("low")) register_4 (
    .D(1'b1), .en(w3), .Q(v3), .clk(CLK));  // open: clr
  Register #(.width(1), .trigger("rising"), .Select("low")) register_5 (
    .D(1'b1), .en(w4), .Q(v4), .clk(CLK));  // open: clr
  Register #(.width(1), .trigger("rising"), .Select("low")) register_6 (
    .D(1'b1), .en(w5), .Q(v5), .clk(CLK));  // open: clr
  Register #(.width(1), .trigger("rising"), .Select("low")) register_7 (
    .D(1'b1), .en(w6), .Q(v6), .clk(CLK));  // open: clr
  Register #(.width(1), .trigger("rising"), .Select("low")) register_8 (
    .D(1'b1), .en(w7), .Q(v7), .clk(CLK));  // open: clr
  Register #(.width(32), .trigger("rising"), .Select("low")) register_9 (
    .D(EX_PC), .en(w0), .Q(tag0), .clk(CLK));  // open: clr
  Register #(.width(32), .trigger("rising"), .Select("low")) register_10 (
    .D(EX_PC), .en(w1), .Q(tag1), .clk(CLK));  // open: clr
  Register #(.width(32), .trigger("rising"), .Select("low")) register_11 (
    .D(EX_PC), .en(w2), .Q(tag2), .clk(CLK));  // open: clr
  Register #(.width(32), .trigger("rising"), .Select("low")) register_12 (
    .D(EX_PC), .en(w3), .Q(tag3), .clk(CLK));  // open: clr
  Register #(.width(32), .trigger("rising"), .Select("low")) register_13 (
    .D(EX_PC), .en(w4), .Q(tag4), .clk(CLK));  // open: clr
  Register #(.width(32), .trigger("rising"), .Select("low")) register_14 (
    .D(EX_PC), .en(w5), .Q(tag5), .clk(CLK));  // open: clr
  Register #(.width(32), .trigger("rising"), .Select("low")) register_15 (
    .D(EX_PC), .en(w6), .Q(tag6), .clk(CLK));  // open: clr
  Register #(.width(32), .trigger("rising"), .Select("low")) register_16 (
    .D(EX_PC), .en(w7), .Q(tag7), .clk(CLK));  // open: clr
  Counter #(.width(16), .max('hffff), .ongoal("wrap"), .trigger("rising"), .behavior("new")) counter_1 (
    .Q(c0), .clk(CLK), .clr(d_ff_1_q));  // open: load, D, count, carry, preset, down
  Counter #(.width(16), .max('hffff), .ongoal("wrap"), .trigger("rising"), .behavior("new")) counter_2 (
    .Q(c1), .clk(CLK), .clr(d_ff_2_q));  // open: load, D, count, carry, preset, down
  Counter #(.width(16), .max('hffff), .ongoal("wrap"), .trigger("rising"), .behavior("new")) counter_3 (
    .Q(c2), .clk(CLK), .clr(d_ff_3_q));  // open: load, D, count, carry, preset, down
  Counter #(.width(16), .max('hffff), .ongoal("wrap"), .trigger("rising"), .behavior("new")) counter_4 (
    .Q(c3), .clk(CLK), .clr(d_ff_4_q));  // open: load, D, count, carry, preset, down
  Counter #(.width(16), .max('hffff), .ongoal("wrap"), .trigger("rising"), .behavior("new")) counter_5 (
    .Q(c4), .clk(CLK), .clr(d_ff_5_q));  // open: load, D, count, carry, preset, down
  Counter #(.width(16), .max('hffff), .ongoal("wrap"), .trigger("rising"), .behavior("new")) counter_6 (
    .Q(c5), .clk(CLK), .clr(d_ff_6_q));  // open: load, D, count, carry, preset, down
  Counter #(.width(16), .max('hffff), .ongoal("wrap"), .trigger("rising"), .behavior("new")) counter_7 (
    .Q(c6), .clk(CLK), .clr(d_ff_7_q));  // open: load, D, count, carry, preset, down
  Counter #(.width(16), .max('hffff), .ongoal("wrap"), .trigger("rising"), .behavior("new")) counter_8 (
    .Q(c7), .clk(CLK), .clr(d_ff_8_q));  // open: load, D, count, carry, preset, down
  D_Flip_Flop #(.trigger("rising"), .Pre_Clr_Positions("LEGACY"), .NegatePresetClear("false"), .enable("true"), .NewFFLayout("false")) d_ff_1 (
    .clk(CLK), .D(or_1_out), .Q(d_ff_1_q));  // open: Qn, preset, en, reset
  or or_1 (or_1_out, w0, L0);
  D_Flip_Flop #(.trigger("rising"), .Pre_Clr_Positions("LEGACY"), .NegatePresetClear("false"), .enable("true"), .NewFFLayout("false")) d_ff_2 (
    .clk(CLK), .D(or_2_out), .Q(d_ff_2_q));  // open: Qn, preset, en, reset
  or or_2 (or_2_out, w1, L1);
  D_Flip_Flop #(.trigger("rising"), .Pre_Clr_Positions("LEGACY"), .NegatePresetClear("false"), .enable("true"), .NewFFLayout("false")) d_ff_3 (
    .clk(CLK), .D(or_3_out), .Q(d_ff_3_q));  // open: Qn, preset, en, reset
  or or_3 (or_3_out, w2, L2);
  D_Flip_Flop #(.trigger("rising"), .Pre_Clr_Positions("LEGACY"), .NegatePresetClear("false"), .enable("true"), .NewFFLayout("false")) d_ff_4 (
    .clk(CLK), .D(or_4_out), .Q(d_ff_4_q));  // open: Qn, preset, en, reset
  or or_4 (or_4_out, w3, L3);
  D_Flip_Flop #(.trigger("rising"), .Pre_Clr_Positions("LEGACY"), .NegatePresetClear("false"), .enable("true"), .NewFFLayout("false")) d_ff_5 (
    .clk(CLK), .D(or_5_out), .Q(d_ff_5_q));  // open: Qn, preset, en, reset
  or or_5 (or_5_out, w4, L4);
  D_Flip_Flop #(.trigger("rising"), .Pre_Clr_Positions("LEGACY"), .NegatePresetClear("false"), .enable("true"), .NewFFLayout("false")) d_ff_6 (
    .clk(CLK), .D(or_6_out), .Q(d_ff_6_q));  // open: Qn, preset, en, reset
  or or_6 (or_6_out, w5, L5);
  D_Flip_Flop #(.trigger("rising"), .Pre_Clr_Positions("LEGACY"), .NegatePresetClear("false"), .enable("true"), .NewFFLayout("false")) d_ff_7 (
    .clk(CLK), .D(or_7_out), .Q(d_ff_7_q));  // open: Qn, preset, en, reset
  or or_7 (or_7_out, w6, L6);
  D_Flip_Flop #(.trigger("rising"), .Pre_Clr_Positions("LEGACY"), .NegatePresetClear("false"), .enable("true"), .NewFFLayout("false")) d_ff_8 (
    .clk(CLK), .D(or_8_out), .Q(d_ff_8_q));  // open: Qn, preset, en, reset
  or or_8 (or_8_out, w7, L7);
  Register #(.width(32), .trigger("rising"), .Select("low")) register_17 (
    .D(EX_BranchAddr), .en(w0), .Q(register_17_q), .clk(CLK));  // open: clr
  Register #(.width(32), .trigger("rising"), .Select("low")) register_18 (
    .D(EX_BranchAddr), .en(w1), .Q(register_18_q), .clk(CLK));  // open: clr
  Register #(.width(32), .trigger("rising"), .Select("low")) register_19 (
    .D(EX_BranchAddr), .en(w2), .Q(register_19_q), .clk(CLK));  // open: clr
  Register #(.width(32), .trigger("rising"), .Select("low")) register_20 (
    .D(EX_BranchAddr), .en(w3), .Q(register_20_q), .clk(CLK));  // open: clr
  Register #(.width(32), .trigger("rising"), .Select("low")) register_21 (
    .D(EX_BranchAddr), .en(w4), .Q(register_21_q), .clk(CLK));  // open: clr
  Register #(.width(32), .trigger("rising"), .Select("low")) register_22 (
    .D(EX_BranchAddr), .en(w5), .Q(register_22_q), .clk(CLK));  // open: clr
  Register #(.width(32), .trigger("rising"), .Select("low")) register_23 (
    .D(EX_BranchAddr), .en(w6), .Q(register_23_q), .clk(CLK));  // open: clr
  Register #(.width(32), .trigger("rising"), .Select("low")) register_24 (
    .D(EX_BranchAddr), .en(w7), .Q(register_24_q), .clk(CLK));  // open: clr
  assign JumpAddr = L0 ? register_17_q : 32'bz;  // Controlled_Buffer controlled_buffer_1
  assign JumpAddr = L1 ? register_18_q : 32'bz;  // Controlled_Buffer controlled_buffer_2
  assign JumpAddr = L2 ? register_19_q : 32'bz;  // Controlled_Buffer controlled_buffer_3
  assign JumpAddr = L3 ? register_20_q : 32'bz;  // Controlled_Buffer controlled_buffer_4
  assign JumpAddr = L4 ? register_21_q : 32'bz;  // Controlled_Buffer controlled_buffer_5
  assign JumpAddr = L5 ? register_22_q : 32'bz;  // Controlled_Buffer controlled_buffer_6
  assign JumpAddr = L6 ? register_23_q : 32'bz;  // Controlled_Buffer controlled_buffer_7
  assign JumpAddr = L7 ? register_24_q : 32'bz;  // Controlled_Buffer controlled_buffer_8
  \状态机  \u_状态机_1  (.\现态 (register_25_q), .BranchTaken(EX_BranchTaken), .\次态 (\状态机_1_次态 ));
  \状态机  \u_状态机_2  (.\现态 (register_26_q), .BranchTaken(EX_BranchTaken), .\次态 (\状态机_2_次态 ));
  \状态机  \u_状态机_3  (.\现态 (register_27_q), .BranchTaken(EX_BranchTaken), .\次态 (\状态机_3_次态 ));
  \状态机  \u_状态机_4  (.\现态 (register_28_q), .BranchTaken(EX_BranchTaken), .\次态 (\状态机_4_次态 ));
  \状态机  \u_状态机_5  (.\现态 (register_29_q), .BranchTaken(EX_BranchTaken), .\次态 (\状态机_5_次态 ));
  \状态机  \u_状态机_6  (.\现态 (register_30_q), .BranchTaken(EX_BranchTaken), .\次态 (\状态机_6_次态 ));
  \状态机  \u_状态机_7  (.\现态 (register_31_q), .BranchTaken(EX_BranchTaken), .\次态 (\状态机_7_次态 ));
  \状态机  \u_状态机_8  (.\现态 (register_32_q), .BranchTaken(EX_BranchTaken), .\次态 (\状态机_8_次态 ));
  Register #(.width(2), .trigger("rising"), .Select("low")) register_25 (
    .D(\状态机_1_次态 ), .en(and_1_out), .Q(register_25_q), .clk(CLK));  // open: clr
  and and_1 (and_1_out, EX_Branch, M0);
  Register #(.width(2), .trigger("rising"), .Select("low")) register_26 (
    .D(\状态机_2_次态 ), .en(and_2_out), .Q(register_26_q), .clk(CLK));  // open: clr
  and and_2 (and_2_out, EX_Branch, M1);
  Register #(.width(2), .trigger("rising"), .Select("low")) register_27 (
    .D(\状态机_3_次态 ), .en(and_3_out), .Q(register_27_q), .clk(CLK));  // open: clr
  and and_3 (and_3_out, EX_Branch, M2);
  Register #(.width(2), .trigger("rising"), .Select("low")) register_28 (
    .D(\状态机_4_次态 ), .en(and_4_out), .Q(register_28_q), .clk(CLK));  // open: clr
  and and_4 (and_4_out, EX_Branch, M3);
  Register #(.width(2), .trigger("rising"), .Select("low")) register_29 (
    .D(\状态机_5_次态 ), .en(and_5_out), .Q(register_29_q), .clk(CLK));  // open: clr
  and and_5 (and_5_out, EX_Branch, M4);
  Register #(.width(2), .trigger("rising"), .Select("low")) register_30 (
    .D(\状态机_6_次态 ), .en(and_6_out), .Q(register_30_q), .clk(CLK));  // open: clr
  and and_6 (and_6_out, EX_Branch, M5);
  Register #(.width(2), .trigger("rising"), .Select("low")) register_31 (
    .D(\状态机_7_次态 ), .en(and_7_out), .Q(register_31_q), .clk(CLK));  // open: clr
  and and_7 (and_7_out, EX_Branch, M6);
  Register #(.width(2), .trigger("rising"), .Select("low")) register_32 (
    .D(\状态机_8_次态 ), .en(and_8_out), .Q(register_32_q), .clk(CLK));  // open: clr
  and and_8 (and_8_out, EX_Branch, M7);
  assign {ID_PredictJump, controlled_buffer_9_out[0]} = L0 ? register_25_q : 2'bz;  // Controlled_Buffer controlled_buffer_9
  assign {ID_PredictJump, controlled_buffer_10_out[0]} = L1 ? register_26_q : 2'bz;  // Controlled_Buffer controlled_buffer_10
  assign {ID_PredictJump, controlled_buffer_11_out[0]} = L2 ? register_27_q : 2'bz;  // Controlled_Buffer controlled_buffer_11
  assign {ID_PredictJump, controlled_buffer_12_out[0]} = L3 ? register_28_q : 2'bz;  // Controlled_Buffer controlled_buffer_12
  assign {ID_PredictJump, controlled_buffer_13_out[0]} = L4 ? register_29_q : 2'bz;  // Controlled_Buffer controlled_buffer_13
  assign {ID_PredictJump, controlled_buffer_14_out[0]} = L5 ? register_30_q : 2'bz;  // Controlled_Buffer controlled_buffer_14
  assign {ID_PredictJump, controlled_buffer_15_out[0]} = L6 ? register_31_q : 2'bz;  // Controlled_Buffer controlled_buffer_15
  Pull_Resistor #(.pull(0)) pull_resistor_1 (.node(ID_PredictJump));
  assign {ID_PredictJump, controlled_buffer_16_out[0]} = L7 ? register_32_q : 2'bz;  // Controlled_Buffer controlled_buffer_16
  Comparator #(.width(32), .mode("unsigned")) comparator_1 (.a(tag0), .b(PC), .eq(comparator_1_eq));  // open: gt, lt
  Comparator #(.width(32), .mode("unsigned")) comparator_2 (.a(tag1), .b(PC), .eq(comparator_2_eq));  // open: gt, lt
  Comparator #(.width(32), .mode("unsigned")) comparator_3 (.a(tag2), .b(PC), .eq(comparator_3_eq));  // open: gt, lt
  Comparator #(.width(32), .mode("unsigned")) comparator_4 (.a(tag3), .b(PC), .eq(comparator_4_eq));  // open: gt, lt
  Comparator #(.width(32), .mode("unsigned")) comparator_5 (.a(tag4), .b(PC), .eq(comparator_5_eq));  // open: gt, lt
  Comparator #(.width(32), .mode("unsigned")) comparator_6 (.a(tag5), .b(PC), .eq(comparator_6_eq));  // open: gt, lt
  Comparator #(.width(32), .mode("unsigned")) comparator_7 (.a(tag6), .b(PC), .eq(comparator_7_eq));  // open: gt, lt
  Comparator #(.width(32), .mode("unsigned")) comparator_8 (.a(tag7), .b(PC), .eq(comparator_8_eq));  // open: gt, lt
  Comparator #(.width(32), .mode("unsigned")) comparator_9 (.a(tag0), .b(EX_PC), .eq(comparator_9_eq));  // open: gt, lt
  Comparator #(.width(32), .mode("unsigned")) comparator_10 (
    .a(tag1), .b(EX_PC), .eq(comparator_10_eq));  // open: gt, lt
  Comparator #(.width(32), .mode("unsigned")) comparator_11 (
    .a(tag2), .b(EX_PC), .eq(comparator_11_eq));  // open: gt, lt
  Comparator #(.width(32), .mode("unsigned")) comparator_12 (
    .a(tag3), .b(EX_PC), .eq(comparator_12_eq));  // open: gt, lt
  Comparator #(.width(32), .mode("unsigned")) comparator_13 (
    .a(tag4), .b(EX_PC), .eq(comparator_13_eq));  // open: gt, lt
  Comparator #(.width(32), .mode("unsigned")) comparator_14 (
    .a(tag5), .b(EX_PC), .eq(comparator_14_eq));  // open: gt, lt
  Comparator #(.width(32), .mode("unsigned")) comparator_15 (
    .a(tag6), .b(EX_PC), .eq(comparator_15_eq));  // open: gt, lt
  Comparator #(.width(32), .mode("unsigned")) comparator_16 (
    .a(tag7), .b(EX_PC), .eq(comparator_16_eq));  // open: gt, lt
  and and_9 (L0, v0, comparator_1_eq);
  and and_10 (L1, v1, comparator_2_eq);
  and and_11 (L2, v2, comparator_3_eq);
  and and_12 (L3, v3, comparator_4_eq);
  and and_13 (L4, v4, comparator_5_eq);
  and and_14 (L5, v5, comparator_6_eq);
  and and_15 (L6, v6, comparator_7_eq);
  and and_16 (L7, v7, comparator_8_eq);
  and and_17 (M0, v0, comparator_9_eq);
  and and_18 (M1, v1, comparator_10_eq);
  and and_19 (M2, v2, comparator_11_eq);
  and and_20 (M3, v3, comparator_12_eq);
  and and_21 (M4, v4, comparator_13_eq);
  and and_22 (M5, v5, comparator_14_eq);
  and and_23 (M6, v6, comparator_15_eq);
  and and_24 (M7, v7, comparator_16_eq);
  not not_1 (miss, or_9_out);
  or or_9 (or_9_out, M0, M1, M2, M3, M4, M5, M6, M7);
  not not_2 (not_2_out, v0);
  not not_3 (not_3_out, v1);
  not not_4 (not_4_out, v2);
  not not_5 (not_5_out, v3);
  not not_6 (not_6_out, v4);
  not not_7 (not_7_out, v5);
  not not_8 (not_8_out, v6);
  not not_9 (not_9_out, v7);
  Priority_Encoder #(.select(3), .disabled("Z")) priority_encoder_1 (
    .in0(not_2_out), .in1(not_3_out), .in2(not_4_out), .in3(not_5_out), .in4(not_6_out), .in5(not_7_out),
    .in6(not_8_out), .in7(not_9_out), .out(priority_encoder_1_out), .gs(priority_encoder_1_gs));  // open: en_out, en_in
  MAX max_1 (.X(c0), .Y(c1), .X_num(3'b000), .Y_num(3'b001), .MAX(max_1_max), .MAX_num(max_1_max_num));
  MAX max_2 (.X(c2), .Y(c3), .X_num(3'b010), .Y_num(3'b011), .MAX(max_2_max), .MAX_num(max_2_max_num));
  MAX max_3 (.X(c4), .Y(c5), .X_num(3'b100), .Y_num(3'b101), .MAX(max_3_max), .MAX_num(max_3_max_num));
  MAX max_4 (.X(c6), .Y(c7), .X_num(3'b110), .Y_num(3'b111), .MAX(max_4_max), .MAX_num(max_4_max_num));
  and and_25 (and_25_out, v0, v1, v2, v3, v4, v5, v6, v7);
  MAX max_5 (
    .X(max_1_max), .Y(max_2_max), .X_num(max_1_max_num), .Y_num(max_2_max_num), .MAX(max_5_max),
    .MAX_num(max_5_max_num));
  MAX max_6 (
    .X(max_3_max), .Y(max_4_max), .X_num(max_3_max_num), .Y_num(max_4_max_num), .MAX(max_6_max),
    .MAX_num(max_6_max_num));
  MAX max_7 (
    .X(max_5_max), .Y(max_6_max), .X_num(max_5_max_num), .Y_num(max_6_max_num), .MAX_num(max_7_max_num));  // open: MAX
  Decoder #(.select(3), .tristate("false"), .disabled(0), .enable("true")) decoder_1 (
    .out0(decoder_1_out0), .out1(decoder_1_out1), .out2(decoder_1_out2), .out3(decoder_1_out3),
    .out4(decoder_1_out4), .out5(decoder_1_out5), .out6(decoder_1_out6), .out7(decoder_1_out7),
    .sel(priority_encoder_1_out), .en(priority_encoder_1_gs));
  Decoder #(.select(3), .tristate("false"), .disabled(0), .enable("true")) decoder_2 (
    .out0(decoder_2_out0), .out1(decoder_2_out1), .out2(decoder_2_out2), .out3(decoder_2_out3),
    .out4(decoder_2_out4), .out5(decoder_2_out5), .out6(decoder_2_out6), .out7(decoder_2_out7),
    .sel(max_7_max_num), .en(and_25_out));
  or or_10 (or_10_out, decoder_1_out0, decoder_2_out0);
  or or_11 (or_11_out, decoder_1_out1, decoder_2_out1);
  or or_12 (or_12_out, decoder_1_out2, decoder_2_out2);
  or or_13 (or_13_out, decoder_1_out3, decoder_2_out3);
  or or_14 (or_14_out, decoder_1_out4, decoder_2_out4);
  or or_15 (or_15_out, decoder_1_out5, decoder_2_out5);
  or or_16 (or_16_out, decoder_1_out6, decoder_2_out6);
  or or_17 (or_17_out, decoder_1_out7, decoder_2_out7);
  and and_26 (w0, EX_Branch, or_10_out, miss);
  and and_27 (w1, EX_Branch, or_11_out, miss);
  and and_28 (w2, EX_Branch, or_12_out, miss);
  and and_29 (w3, EX_Branch, or_13_out, miss);
  and and_30 (w4, EX_Branch, or_14_out, miss);
  and and_31 (w5, EX_Branch, or_15_out, miss);
  and and_32 (w6, EX_Branch, or_16_out, miss);
  and and_33 (w7, EX_Branch, or_17_out, miss);
endmodule

module \状态机  (
  input  [1:0] \现态 ,
  input  BranchTaken,
  output [1:0] \次态 
);

  wire and_1_out, and_2_out, and_3_out, and_4_out, not_1_out, not_2_out, not_3_out, not_4_out, not_5_out;

  not not_1 (not_1_out, \现态 [0]);
  not not_2 (not_2_out, \现态 [1]);
  not not_3 (not_3_out, \现态 [0]);
  not not_4 (not_4_out, BranchTaken);
  not not_5 (not_5_out, \现态 [0]);
  and and_1 (and_1_out, not_1_out, not_2_out, BranchTaken);
  and and_2 (and_2_out, \现态 [1], not_3_out, not_4_out);
  and and_3 (and_3_out, \现态 [1], not_5_out);
  and and_4 (and_4_out, \现态 [0], BranchTaken);
  or or_1 (\次态 [0], and_1_out, and_2_out);
  or or_2 (\次态 [1], and_3_out, and_4_out);
endmodule
