// Logisim project lab5.circ as structural Verilog: 14 circuits, main circuit 四位二进制可逆计数器
module \四位二进制可逆计数器  (
  input  D,
  input  CPu,
  input  CPd,
  input  C,
  input  B,
  input  A,
  input  \LD非 ,
  input  CLR,
  output out_9,
  output out_10,
  output out_11,
  output out_12
);

  wire and_1_out, and_2_out, and_3_out, and_4_out, and_5_out, and_6_out, and_7_out, and_8_out, and_9_out,
       and_10_out, and_11_out, and_12_out, and_13_out, and_14_out, d_ff_1_qn, d_ff_2_qn, d_ff_3_qn,
       d_ff_4_qn, or_1_out, or_2_out, or_3_out, or_4_out, or_5_out, or_6_out, or_7_out, or_8_out;

  and and_1 (and_1_out, CPu, out_12, out_11, out_10);
  and and_2 (and_2_out, CPd, ~out_12, ~out_11, ~out_10);  // AND_Gate
  and and_3 (and_3_out, CPu, out_12, out_11);
  and and_4 (and_4_out, CPd, ~out_12, ~out_11);  // AND_Gate
  and and_5 (and_5_out, CPu, out_12);
  and and_6 (and_6_out, CPd, ~out_12);  // AND_Gate
  or or_1 (or_1_out, and_1_out, and_2_out);
  and and_7 (and_7_out, D, ~\LD非 );  // AND_Gate
  or or_2 (or_2_out, and_3_out, and_4_out);
  and and_8 (and_8_out, C, ~\LD非 );  // AND_Gate
  or or_3 (or_3_out, and_5_out, and_6_out);
  and and_9 (and_9_out, B, ~\LD非 );  // AND_Gate
  or or_4 (or_4_out, CPu, CPd);
  and and_10 (and_10_out, A, ~\LD非 );  // AND_Gate
  D_Flip_Flop #(.trigger("falling"), .Pre_Clr_Positions("LEGACY"), .NegatePresetClear("false"), .enable("true"), .NewFFLayout("false")) d_ff_1 (
    .clk(or_1_out), .D(d_ff_1_qn), .Q(out_9), .Qn(d_ff_1_qn), .preset(and_7_out), .reset(or_5_out));  // open: en
  D_Flip_Flop #(.trigger("falling"), .Pre_Clr_Positions("LEGACY"), .NegatePresetClear("false"), .enable("true"), .NewFFLayout("false")) d_ff_2 (
    .clk(or_2_out), .D(d_ff_2_qn), .Q(out_10), .Qn(d_ff_2_qn), .preset(and_8_out), .reset(or_6_out));  // open: en
  D_Flip_Flop #(.trigger("falling"), .Pre_Clr_Positions("LEGACY"), .NegatePresetClear("false"), .enable("true"), .NewFFLayout("false")) d_ff_3 (
    .clk(or_3_out), .D(d_ff_3_qn), .Q(out_11), .Qn(d_ff_3_qn), .preset(and_9_out), .reset(or_7_out));  // open: en
  D_Flip_Flop #(.trigger("falling"), .Pre_Clr_Positions("LEGACY"), .NegatePresetClear("false"), .enable("true"), .NewFFLayout("false")) d_ff_4 (
    .clk(or_4_out), .D(d_ff_4_qn), .Q(out_12), .Qn(d_ff_4_qn), .preset(and_10_out), .reset(or_8_out));  // open: en
  and and_11 (and_11_out, ~D, ~\LD非 );  // AND_Gate
  and and_12 (and_12_out, ~C, ~\LD非 );  // AND_Gate
  and and_13 (and_13_out, ~B, ~\LD非 );  // AND_Gate
  and and_14 (and_14_out, ~A, ~\LD非 );  // AND_Gate
  or or_5 (or_5_out, and_11_out, CLR);
  or or_6 (or_6_out, and_12_out, CLR);
  or or_7 (or_7_out, and_13_out, CLR);
  or or_8 (or_8_out, and_14_out, CLR);
endmodule

module \六十进制计数器  (
  input  CPu,
  input  CPd,
  input  Adj,
  input  CLR,
  output out_5,
  output out_6,
  output out_7,
  output out_8,
  output out_9,
  output out_10,
  output out_11,
  output out_12,
  output out_13
);

  wire and_1_out, and_2_out, and_3_out, and_4_out, and_5_out, and_6_out, and_7_out, and_8_out, nand_1_out,
       or_1_out, or_2_out, or_3_out;

  and and_1 (and_1_out, CPd, ~and_8_out, Adj);  // AND_Gate
  or or_1 (or_1_out, and_2_out, CLR);
  and and_2 (and_2_out, out_5, ~out_7, out_9, ~out_11);  // AND_Gate
  and and_3 (and_3_out, out_5, ~out_7, ~out_9, out_11);  // AND_Gate
  and and_4 (and_4_out, ~out_5, ~out_7, ~out_9, ~out_11);  // AND_Gate
  \四位二进制可逆计数器  \u_四位二进制可逆计数器_1  (
    .D(1'b1), .CPu(CPu), .CPd(and_1_out), .C(1'b0), .B(1'b0), .A(1'b1), .\LD非 (nand_1_out), .CLR(or_1_out),
    .out_9(out_5), .out_10(out_7), .out_11(out_9), .out_12(out_11));
  and and_5 (and_5_out, and_3_out, CPu);
  nand nand_1 (nand_1_out, out_5, out_7, out_11);
  or or_2 (or_2_out, and_7_out, CLR);
  and and_6 (and_6_out, and_4_out, and_1_out);
  nand nand_2 (out_13, out_8, out_5, CPu, out_11, out_12);
  \四位二进制可逆计数器  \u_四位二进制可逆计数器_2  (
    .CPu(and_5_out), .CPd(and_6_out), .CLR(or_2_out), .out_9(out_6), .out_10(out_8), .out_11(out_10),
    .out_12(out_12));  // open: D, C, B, A, LD非
  or or_3 (or_3_out, out_6, out_8, out_10, out_12);
  and and_7 (and_7_out, out_8, out_10);
  and and_8 (and_8_out, ~or_3_out, and_4_out);  // AND_Gate
endmodule

module \六十进制计数器测试电路  (
  input  in_1,
  input  in_2
);

  wire button_1_out, button_2_out;
  wire [3:0] \六十进制计数器_1_out_11 , \六十进制计数器_1_out_12 ;

  Button button_1 (.out(button_1_out));
  Button button_2 (.out(button_2_out));
  Hex_Digit_Display hex_digit_display_1 (.value(\六十进制计数器_1_out_12 ));  // open: dp
  Hex_Digit_Display hex_digit_display_2 (.value(\六十进制计数器_1_out_11 ));  // open: dp
  \六十进制计数器  \u_六十进制计数器_1  (
    .CPu(button_1_out), .CPd(button_2_out), .Adj(in_2), .CLR(in_1), .out_5(\六十进制计数器_1_out_11 [3]),
    .out_7(\六十进制计数器_1_out_11 [2]), .out_9(\六十进制计数器_1_out_11 [1]), .out_11(\六十进制计数器_1_out_11 [0]),
    .out_6(\六十进制计数器_1_out_12 [3]), .out_8(\六十进制计数器_1_out_12 [2]), .out_10(\六十进制计数器_1_out_12 [1]),
    .out_12(\六十进制计数器_1_out_12 [0]));  // open: out_13
endmodule

module \十二进制计数器或二十四进制的计数器电路  (
  input  Set,
  input  in_2,
  input  CLR,
  input  in_4,
  input  in_5,
  output out_6,
  output AM_FM,
  output out_8,
  output out_9,
  output out_10,
  output out_11,
  output out_12,
  output out_13,
  output out_14,
  output out_15
);

  wire and_1_out, and_2_out, and_3_out, and_4_out, and_5_out, and_6_out, and_7_out, and_8_out, and_9_out,
       and_10_out, and_11_out, and_12_out, and_13_out, and_14_out, and_15_out, and_16_out, and_17_out,
       and_18_out, and_19_out, and_20_out, comparator_4_eq, nor_1_out, not_1_out, or_1_out, or_2_out,
       or_3_out;
  wire [1:0] comparator_2_gt, comparator_2_lt;
  wire [2:2] comparator_3_lt;
  wire [3:0] subtractor_1_out, subtractor_2_out, subtractor_3_out, \六十进制计数器_1_out_11 , \六十进制计数器_1_out_12 ;

  and and_1 (and_1_out, in_4, in_5);
  or or_1 (or_1_out, CLR, and_2_out);
  \六十进制计数器  \u_六十进制计数器_1  (
    .CPu(in_2), .CPd(and_1_out), .Adj(in_5), .CLR(or_1_out), .out_13(out_15), .out_5(\六十进制计数器_1_out_11 [3]),
    .out_7(\六十进制计数器_1_out_11 [2]), .out_9(\六十进制计数器_1_out_11 [1]), .out_11(\六十进制计数器_1_out_11 [0]),
    .out_6(\六十进制计数器_1_out_12 [3]), .out_8(\六十进制计数器_1_out_12 [2]), .out_10(\六十进制计数器_1_out_12 [1]),
    .out_12(\六十进制计数器_1_out_12 [0]));
  Comparator #(.width(5), .mode("twosComplement")) comparator_1 (
    .a(5'b00001), .b({1'b0, \六十进制计数器_1_out_12 }), .gt(comparator_2_gt[1]), .lt(comparator_2_lt[1]));  // open: eq
  Comparator #(.width(5), .mode("twosComplement")) comparator_2 (
    .a(5'b00010), .b({1'b0, \六十进制计数器_1_out_11 }), .gt(comparator_2_gt[0]), .lt(comparator_2_lt[0]));  // open: eq
  Subtractor #(.width(4)) subtractor_1 (
    .a(\六十进制计数器_1_out_11 ), .b(4'b0010), .out(subtractor_1_out));  // open: bin, bout
  and and_2 (and_2_out, ~\六十进制计数器_1_out_11 [0], ~\六十进制计数器_1_out_11 [1], ~\六十进制计数器_1_out_12 [0], \六十进制计数器_1_out_12 [1], \六十进制计数器_1_out_11 [2]);  // AND_Gate
  Comparator #(.width(4), .mode("twosComplement")) comparator_3 (
    .a(subtractor_1_out), .b(4'b0000), .lt(comparator_3_lt[2]));  // open: gt, eq
  Subtractor #(.width(4)) subtractor_2 (
    .a(\六十进制计数器_1_out_12 ), .b(4'b0001), .out(subtractor_2_out), .bin(comparator_3_lt[2]));  // open: bout
  Comparator #(.width(3), .mode("twosComplement")) comparator_4 (
    .a({1'b0, comparator_2_lt}), .b({1'b0, comparator_2_gt}), .eq(comparator_4_eq), .lt(AM_FM));  // open: gt
  or or_2 (or_2_out, comparator_4_eq, AM_FM);
  Subtractor #(.width(4)) subtractor_3 (
    .a(subtractor_1_out), .b({1'b0, {2{comparator_3_lt[2]}}, 1'b0}), .out(subtractor_3_out));  // open: bin, bout
  nor nor_1 (nor_1_out, \六十进制计数器_1_out_12 [3], \六十进制计数器_1_out_12 [2], \六十进制计数器_1_out_12 [1], \六十进制计数器_1_out_12 [0], \六十进制计数器_1_out_11 [3], \六十进制计数器_1_out_11 [2], \六十进制计数器_1_out_11 [1], \六十进制计数器_1_out_11 [0]);
  or or_3 (or_3_out, or_2_out, Set);
  not not_1 (not_1_out, or_3_out);
  and and_3 (and_3_out, \六十进制计数器_1_out_12 [3], or_3_out);
  and and_4 (and_4_out, \六十进制计数器_1_out_12 [2], or_3_out);
  and and_5 (and_5_out, \六十进制计数器_1_out_12 [1], or_3_out);
  and and_6 (and_6_out, \六十进制计数器_1_out_12 [0], or_3_out);
  and and_7 (and_7_out, \六十进制计数器_1_out_11 [3], or_3_out);
  and and_8 (and_8_out, or_3_out, \六十进制计数器_1_out_11 [2]);
  and and_9 (and_9_out, \六十进制计数器_1_out_11 [1], or_3_out);
  and and_10 (and_10_out, \六十进制计数器_1_out_11 [0], or_3_out);
  and and_11 (and_11_out, not_1_out, subtractor_2_out[3]);
  and and_12 (and_12_out, subtractor_2_out[2], not_1_out);
  and and_13 (and_13_out, not_1_out, subtractor_2_out[1]);
  and and_14 (and_14_out, subtractor_2_out[0], not_1_out);
  and and_15 (and_15_out, ~Set, nor_1_out);  // AND_Gate
  and and_16 (and_16_out, not_1_out, subtractor_3_out[3]);
  and and_17 (and_17_out, not_1_out, subtractor_3_out[2]);
  and and_18 (and_18_out, not_1_out, subtractor_3_out[1]);
  and and_19 (and_19_out, not_1_out, subtractor_3_out[0]);
  and and_20 (and_20_out, ~Set, nor_1_out);  // AND_Gate
  or or_4 (out_6, and_3_out, and_11_out);
  or or_5 (out_8, and_4_out, and_12_out);
  or or_6 (out_9, and_5_out, and_13_out);
  or or_7 (out_10, and_6_out, and_15_out, and_14_out);
  or or_8 (out_11, and_7_out, and_16_out);
  or or_9 (out_12, and_8_out, and_17_out);
  or or_10 (out_13, and_9_out, and_20_out, and_18_out);
  or or_11 (out_14, and_10_out, and_19_out);
endmodule

module \十二进制计数器或二十四进制的计数器测试电路  (
  input  in_1,
  input  in_2,
  input  in_3
);

  wire button_1_out, button_2_out;
  wire [3:0] \十二进制计数器或二十四进制的计数器电路_1_out_10 , \十二进制计数器或二十四进制的计数器电路_1_out_14 ;

  Hex_Digit_Display hex_digit_display_1 (.value(\十二进制计数器或二十四进制的计数器电路_1_out_10 ));  // open: dp
  Button button_1 (.out(button_1_out));
  Button button_2 (.out(button_2_out));
  Hex_Digit_Display hex_digit_display_2 (.value(\十二进制计数器或二十四进制的计数器电路_1_out_14 ));  // open: dp
  \十二进制计数器或二十四进制的计数器电路  \u_十二进制计数器或二十四进制的计数器电路_1  (
    .in_2(button_1_out), .in_4(button_2_out), .in_5(in_2), .CLR(in_1), .Set(in_3),
    .out_6(\十二进制计数器或二十四进制的计数器电路_1_out_10 [3]), .out_8(\十二进制计数器或二十四进制的计数器电路_1_out_10 [2]),
    .out_9(\十二进制计数器或二十四进制的计数器电路_1_out_10 [1]), .out_10(\十二进制计数器或二十四进制的计数器电路_1_out_10 [0]),
    .out_11(\十二进制计数器或二十四进制的计数器电路_1_out_14 [3]), .out_12(\十二进制计数器或二十四进制的计数器电路_1_out_14 [2]),
    .out_13(\十二进制计数器或二十四进制的计数器电路_1_out_14 [1]), .out_14(\十二进制计数器或二十四进制的计数器电路_1_out_14 [0]));  // open: out_15, AM_FM
endmodule

module \上下午文字显示的电路  (
  input  AM_FM,
  input  TT,
  output [4:0] out_3,
  output [4:0] out_4,
  output [4:0] out_5,
  output [4:0] out_6
);

  wire not_1_out;

  not not_1 (not_1_out, AM_FM);
  and and_1 (out_3[4], AM_FM, TT);
  and and_2 (out_3[0], not_1_out, TT);
  and and_3 (out_4[4], 1'b1, TT);

  assign out_3[3:1] = 3'b000;
  assign out_4[3:0] = {4{out_4[4]}};
  assign out_5 = {out_3[4], 1'b0, out_4[4], 1'b0, out_3[0]};
  assign out_6 = {out_3[4], 3'b000, out_3[0]};
endmodule

module \上下午文字显示测试电路  (
  input  in_1,
  input  in_2
);

  wire [4:0] \上下午文字显示的电路_1_out_3 , \上下午文字显示的电路_1_out_4 , \上下午文字显示的电路_1_out_5 , \上下午文字显示的电路_1_out_6 ;

  DotMatrix #(.inputtype("column"), .matrixcols(4), .matrixrows(5), .persist(0), .dotshape("square")) dotmatrix_1 (
    .col0(\上下午文字显示的电路_1_out_3 ), .col1(\上下午文字显示的电路_1_out_4 ), .col2(\上下午文字显示的电路_1_out_5 ),
    .col3(\上下午文字显示的电路_1_out_6 ));
  \上下午文字显示的电路  \u_上下午文字显示的电路_1  (
    .AM_FM(in_1), .TT(in_2), .out_3(\上下午文字显示的电路_1_out_3 ), .out_4(\上下午文字显示的电路_1_out_4 ),
    .out_5(\上下午文字显示的电路_1_out_5 ), .out_6(\上下午文字显示的电路_1_out_6 ));
endmodule

module \电子钟整点报时电路  (
  input  in_1,
  input  in_2,
  input  in_3,
  input  in_4,
  input  in_5,
  input  in_6,
  input  in_7,
  input  in_8,
  input  in_9,
  input  in_10,
  input  in_11,
  input  in_12,
  output out_13
);

  wire and_1_out, and_2_out, and_3_out;

  and and_1 (and_1_out, ~in_1, in_2, ~in_3, in_4);  // AND_Gate
  and and_2 (and_2_out, in_5, ~in_6, ~in_7, in_8);  // AND_Gate
  and and_3 (and_3_out, ~in_9, in_10, ~in_11, in_12);  // AND_Gate
  and and_4 (out_13, and_1_out, and_2_out, and_3_out);
endmodule

module \电子钟整点报时电路测试电路  (
  input  [3:0] in_1,
  input  [3:0] in_2,
  input  [3:0] in_3,
  output out_4
);

  \电子钟整点报时电路  \u_电子钟整点报时电路_1  (
    .in_1(in_1[3]), .in_2(in_1[2]), .in_3(in_1[1]), .in_4(in_1[0]), .in_5(in_2[3]), .in_6(in_2[2]),
    .in_7(in_2[1]), .in_8(in_2[0]), .in_9(in_3[3]), .in_10(in_3[2]), .in_11(in_3[1]), .in_12(in_3[0]),
    .out_13(out_4));
endmodule

module \秒脉冲产生电路  (
  input  in_1,
  output out_2
);

  wire and_1_out, and_2_out, d_ff_1_q, d_ff_1_qn, d_ff_2_q, d_ff_2_qn, d_ff_3_q, d_ff_3_qn;

  D_Flip_Flop #(.trigger("falling"), .Pre_Clr_Positions("LEGACY"), .NegatePresetClear("false"), .enable("true"), .NewFFLayout("false")) d_ff_1 (
    .clk(in_1), .D(d_ff_1_qn), .Q(d_ff_1_q), .Qn(d_ff_1_qn));  // open: preset, en, reset
  and and_1 (and_1_out, in_1, d_ff_1_q);
  D_Flip_Flop #(.trigger("falling"), .Pre_Clr_Positions("LEGACY"), .NegatePresetClear("false"), .enable("true"), .NewFFLayout("false")) d_ff_2 (
    .clk(and_1_out), .D(d_ff_2_qn), .Q(d_ff_2_q), .Qn(d_ff_2_qn));  // open: preset, en, reset
  and and_2 (and_2_out, and_1_out, d_ff_2_q);
  D_Flip_Flop #(.trigger("falling"), .Pre_Clr_Positions("LEGACY"), .NegatePresetClear("false"), .enable("true"), .NewFFLayout("false")) d_ff_3 (
    .clk(and_2_out), .D(d_ff_3_qn), .Q(d_ff_3_q), .Qn(d_ff_3_qn));  // open: preset, en, reset
  and and_3 (out_2, d_ff_3_q, d_ff_2_q, d_ff_1_q, in_1);
endmodule

module \多功能数字钟  (
  input  in_1,
  input  \闹钟开关 ,
  input  CPu,
  input  CPd,
  input  Clr,
  input  Adj0,
  input  Adj1,
  input  Set,
  input  \设置闹钟 ,
  output out_10,
  output [3:0] out_11,
  output [3:0] out_12,
  output out_13,
  output [3:0] out_14,
  output [3:0] out_15,
  output [3:0] out_16,
  output [3:0] out_17,
  output [4:0] out_18,
  output [4:0] out_19,
  output [4:0] out_20,
  output [4:0] out_21
);

  wire and_1_out, and_2_out, and_3_out, and_4_out, and_5_out, and_6_out, and_7_out, and_8_out, and_9_out,
       clock_1_out, comparator_1_eq, comparator_2_eq, comparator_3_eq, comparator_4_eq, comparator_5_eq,
       d_ff_1_qn, d_ff_2_qn, multiplexer_1_out, not_1_out, not_2_out, or_1_out, or_2_out, or_3_out,
       \六十进制计数器_1_out_13 , \六十进制计数器_2_out_13 , \十二进制计数器或二十四进制的计数器电路_1_am_fm , \电子钟整点报时电路_1_out_13 ,
       \秒脉冲产生电路_1_out_2 , \闹钟_1_out_10 ;
  wire [3:0] \六十进制计数器_2_out_11 , \六十进制计数器_2_out_12 , \十二进制计数器或二十四进制的计数器电路_1_out_10 ,
       \十二进制计数器或二十四进制的计数器电路_1_out_14 , \闹钟_1_out_6 , \闹钟_1_out_7 , \闹钟_1_out_8 , \闹钟_1_out_9 ;

  Clock #(.highDuration(1), .lowDuration(1)) clock_1 (.out(clock_1_out));
  or or_1 (or_1_out, clock_1_out, in_1);
  \秒脉冲产生电路  \u_秒脉冲产生电路_1  (.in_1(or_1_out), .out_2(\秒脉冲产生电路_1_out_2 ));
  and and_1 (and_1_out, Adj0, Adj1);
  and and_2 (and_2_out, Adj0, ~Adj1);  // AND_Gate
  \六十进制计数器  \u_六十进制计数器_1  (
    .CPu(\秒脉冲产生电路_1_out_2 ), .Adj(1'b0), .CLR(Clr), .out_13(\六十进制计数器_1_out_13 ), .out_5(out_12[3]),
    .out_7(out_12[2]), .out_9(out_12[1]), .out_11(out_12[0]), .out_6(out_11[3]), .out_8(out_11[2]),
    .out_10(out_11[1]), .out_12(out_11[0]));  // open: CPd
  and and_3 (and_3_out, ~\六十进制计数器_1_out_13 , ~Adj0);  // AND_Gate
  and and_4 (and_4_out, CPu, and_1_out);
  or or_2 (or_2_out, and_3_out, and_4_out);
  \闹钟  \u_闹钟_1  (
    .CPu(CPu), .CPd(CPd), .Adj0(\设置闹钟 ), .Adj1(Adj1), .out_6(\闹钟_1_out_6 ), .out_7(\闹钟_1_out_7 ),
    .out_8(\闹钟_1_out_8 ), .out_9(\闹钟_1_out_9 ), .Set(Set), .out_10(\闹钟_1_out_10 ));
  \六十进制计数器  \u_六十进制计数器_2  (
    .CPu(or_2_out), .CPd(CPd), .Adj(and_1_out), .CLR(Clr), .out_13(\六十进制计数器_2_out_13 ),
    .out_5(\六十进制计数器_2_out_11 [3]), .out_7(\六十进制计数器_2_out_11 [2]), .out_9(\六十进制计数器_2_out_11 [1]),
    .out_11(\六十进制计数器_2_out_11 [0]), .out_6(\六十进制计数器_2_out_12 [3]), .out_8(\六十进制计数器_2_out_12 [2]),
    .out_10(\六十进制计数器_2_out_12 [1]), .out_12(\六十进制计数器_2_out_12 [0]));
  and and_5 (and_5_out, CPu, and_2_out);
  and and_6 (and_6_out, ~\六十进制计数器_2_out_13 , ~Adj0);  // AND_Gate
  \电子钟整点报时电路  \u_电子钟整点报时电路_1  (
    .in_1(\六十进制计数器_2_out_12 [3]), .in_2(\六十进制计数器_2_out_12 [2]), .in_3(\六十进制计数器_2_out_12 [1]),
    .in_4(\六十进制计数器_2_out_12 [0]), .in_5(\六十进制计数器_2_out_11 [3]), .in_6(\六十进制计数器_2_out_11 [2]),
    .in_7(\六十进制计数器_2_out_11 [1]), .in_8(\六十进制计数器_2_out_11 [0]), .in_9(out_11[3]), .in_10(out_11[2]),
    .in_11(out_11[1]), .in_12(out_11[0]), .out_13(\电子钟整点报时电路_1_out_13 ));
  or or_3 (or_3_out, and_6_out, and_5_out);
  Multiplexer #(.select(1), .width(1), .disabled("Z"), .enable("true")) multiplexer_1 (
    .in0(\十二进制计数器或二十四进制的计数器电路_1_am_fm ), .in1(\闹钟_1_out_10 ), .out(multiplexer_1_out), .sel(\设置闹钟 ));  // open: en
  and and_7 (and_7_out, \秒脉冲产生电路_1_out_2 , \电子钟整点报时电路_1_out_13 );
  D_Flip_Flop #(.trigger("falling"), .Pre_Clr_Positions("LEGACY"), .NegatePresetClear("false"), .enable("true"), .NewFFLayout("false")) d_ff_1 (
    .clk(and_7_out), .D(d_ff_1_qn), .Q(out_10), .Qn(d_ff_1_qn));  // open: preset, en, reset
  \十二进制计数器或二十四进制的计数器电路  \u_十二进制计数器或二十四进制的计数器电路_1  (
    .in_2(or_3_out), .in_4(CPd), .in_5(and_2_out), .CLR(Clr), .Set(Set),
    .out_6(\十二进制计数器或二十四进制的计数器电路_1_out_10 [3]), .out_8(\十二进制计数器或二十四进制的计数器电路_1_out_10 [2]),
    .out_9(\十二进制计数器或二十四进制的计数器电路_1_out_10 [1]), .out_10(\十二进制计数器或二十四进制的计数器电路_1_out_10 [0]),
    .out_11(\十二进制计数器或二十四进制的计数器电路_1_out_14 [3]), .out_12(\十二进制计数器或二十四进制的计数器电路_1_out_14 [2]),
    .out_13(\十二进制计数器或二十四进制的计数器电路_1_out_14 [1]), .out_14(\十二进制计数器或二十四进制的计数器电路_1_out_14 [0]),
    .AM_FM(\十二进制计数器或二十四进制的计数器电路_1_am_fm ));  // open: out_15
  not not_1 (not_1_out, multiplexer_1_out);
  Comparator #(.width(1), .mode("twosComplement")) comparator_1 (
    .a(\十二进制计数器或二十四进制的计数器电路_1_am_fm ), .b(\闹钟_1_out_10 ), .eq(comparator_1_eq));  // open: gt, lt
  \上下午文字显示的电路  \u_上下午文字显示的电路_1  (
    .AM_FM(not_1_out), .TT(not_2_out), .out_3(out_21), .out_4(out_20), .out_5(out_19), .out_6(out_18));
  not not_2 (not_2_out, Set);
  Comparator #(.width(4), .mode("twosComplement")) comparator_2 (
    .a(\六十进制计数器_2_out_11 ), .b(\闹钟_1_out_7 ), .eq(comparator_2_eq));  // open: gt, lt
  Comparator #(.width(4), .mode("twosComplement")) comparator_3 (
    .a(\十二进制计数器或二十四进制的计数器电路_1_out_10 ), .b(\闹钟_1_out_8 ), .eq(comparator_3_eq));  // open: gt, lt
  Comparator #(.width(4), .mode("twosComplement")) comparator_4 (
    .a(\十二进制计数器或二十四进制的计数器电路_1_out_14 ), .b(\闹钟_1_out_9 ), .eq(comparator_4_eq));  // open: gt, lt
  Multiplexer #(.select(1), .width(4), .disabled("Z"), .enable("true")) multiplexer_2 (
    .in0(\十二进制计数器或二十四进制的计数器电路_1_out_10 ), .in1(\闹钟_1_out_8 ), .out(out_14), .sel(\设置闹钟 ));  // open: en
  Multiplexer #(.select(1), .width(4), .disabled("Z"), .enable("true")) multiplexer_3 (
    .in0(\十二进制计数器或二十四进制的计数器电路_1_out_14 ), .in1(\闹钟_1_out_9 ), .out(out_15), .sel(\设置闹钟 ));  // open: en
  Multiplexer #(.select(1), .width(4), .disabled("Z"), .enable("true")) multiplexer_4 (
    .in0(\六十进制计数器_2_out_12 ), .in1(\闹钟_1_out_6 ), .out(out_16), .sel(\设置闹钟 ));  // open: en
  Multiplexer #(.select(1), .width(4), .disabled("Z"), .enable("true")) multiplexer_5 (
    .in0(\六十进制计数器_2_out_11 ), .in1(\闹钟_1_out_7 ), .out(out_17), .sel(\设置闹钟 ));  // open: en
  Comparator #(.width(4), .mode("twosComplement")) comparator_5 (
    .a(\六十进制计数器_2_out_12 ), .b(\闹钟_1_out_6 ), .eq(comparator_5_eq));  // open: gt, lt
  and and_8 (and_8_out, comparator_5_eq, comparator_2_eq, comparator_3_eq, comparator_4_eq, \闹钟开关 , ~\设置闹钟 , comparator_1_eq);  // AND_Gate
  D_Flip_Flop #(.trigger("falling"), .Pre_Clr_Positions("LEGACY"), .NegatePresetClear("false"), .enable("true"), .NewFFLayout("false")) d_ff_2 (
    .clk(and_9_out), .D(d_ff_2_qn), .Q(out_13), .Qn(d_ff_2_qn));  // open: preset, en, reset
  and and_9 (and_9_out, and_8_out, \秒脉冲产生电路_1_out_2 );
endmodule

module \多功能数字钟测试电路  (
  input  in_1,
  input  in_2,
  input  in_3,
  input  in_4,
  input  in_5,
  input  in_6
);

  wire button_1_out, button_2_out, clock_1_out, \多功能数字钟_1_out_10 , \多功能数字钟_1_out_13 ;
  wire [3:0] \多功能数字钟_1_out_11 , \多功能数字钟_1_out_12 , \多功能数字钟_1_out_14 , \多功能数字钟_1_out_15 , \多功能数字钟_1_out_16 ,
       \多功能数字钟_1_out_17 ;
  wire [4:0] \多功能数字钟_1_out_18 , \多功能数字钟_1_out_19 , \多功能数字钟_1_out_20 , \多功能数字钟_1_out_21 ;

  DotMatrix #(.inputtype("column"), .matrixcols(4), .matrixrows(5), .persist(0), .dotshape("square")) dotmatrix_1 (
    .col0(\多功能数字钟_1_out_21 ), .col1(\多功能数字钟_1_out_20 ), .col2(\多功能数字钟_1_out_19 ), .col3(\多功能数字钟_1_out_18 ));
  Hex_Digit_Display hex_digit_display_1 (.value(\多功能数字钟_1_out_14 ));  // open: dp
  Clock #(.highDuration(1), .lowDuration(1)) clock_1 (.out(clock_1_out));
  Hex_Digit_Display hex_digit_display_2 (.value(\多功能数字钟_1_out_16 ));  // open: dp
  Hex_Digit_Display hex_digit_display_3 (.value(\多功能数字钟_1_out_15 ));  // open: dp
  Button button_1 (.out(button_1_out));
  Button button_2 (.out(button_2_out));
  Hex_Digit_Display hex_digit_display_4 (.value(\多功能数字钟_1_out_17 ));  // open: dp
  Hex_Digit_Display hex_digit_display_5 (.value(\多功能数字钟_1_out_12 ));  // open: dp
  Hex_Digit_Display hex_digit_display_6 (.value(\多功能数字钟_1_out_11 ));  // open: dp
  \多功能数字钟  \u_多功能数字钟_1  (
    .CPu(button_2_out), .CPd(button_1_out), .Clr(in_6), .Adj0(in_1), .Adj1(in_2), .out_11(\多功能数字钟_1_out_11 ),
    .out_12(\多功能数字钟_1_out_12 ), .out_10(\多功能数字钟_1_out_10 ), .out_16(\多功能数字钟_1_out_16 ),
    .out_17(\多功能数字钟_1_out_17 ), .out_14(\多功能数字钟_1_out_14 ), .out_15(\多功能数字钟_1_out_15 ),
    .out_21(\多功能数字钟_1_out_21 ), .out_20(\多功能数字钟_1_out_20 ), .out_19(\多功能数字钟_1_out_19 ),
    .out_18(\多功能数字钟_1_out_18 ), .Set(in_5), .in_1(clock_1_out), .\设置闹钟 (in_3), .\闹钟开关 (in_4),
    .out_13(\多功能数字钟_1_out_13 ));
  LED #(.active("true")) led_1 (.in(\多功能数字钟_1_out_13 ));
  LED #(.active("true")) led_2 (.in(\多功能数字钟_1_out_10 ));
endmodule

module \闹钟  (
  input  CPu,
  input  CPd,
  input  Set,
  input  Adj0,
  input  Adj1,
  output [3:0] out_6,
  output [3:0] out_7,
  output [3:0] out_8,
  output [3:0] out_9,
  output out_10
);

  wire and_1_out, and_2_out, and_3_out, and_4_out, comparator_3_lt;
  wire [1:0] comparator_2_gt, comparator_2_lt;

  and and_1 (and_1_out, CPu, and_2_out);
  and and_2 (and_2_out, Adj0, Adj1);
  and and_3 (and_3_out, Adj0, ~Adj1);  // AND_Gate
  \六十进制计数器  \u_六十进制计数器_1  (
    .CPu(and_1_out), .CPd(CPd), .Adj(and_2_out), .out_5(out_7[3]), .out_7(out_7[2]), .out_9(out_7[1]),
    .out_11(out_7[0]), .out_6(out_6[3]), .out_8(out_6[2]), .out_10(out_6[1]), .out_12(out_6[0]));  // open: CLR, out_13
  and and_4 (and_4_out, and_3_out, CPu);
  \十二进制计数器或二十四进制的计数器电路  \u_十二进制计数器或二十四进制的计数器电路_1  (
    .in_2(and_4_out), .in_4(CPd), .in_5(and_3_out), .Set(Set), .out_6(out_8[3]), .out_8(out_8[2]),
    .out_9(out_8[1]), .out_10(out_8[0]), .out_11(out_9[3]), .out_12(out_9[2]), .out_13(out_9[1]),
    .out_14(out_9[0]), .AM_FM(out_10));  // open: CLR, out_15
  Comparator #(.width(5), .mode("twosComplement")) comparator_1 (
    .a(5'b00001), .b({1'b0, out_8}), .gt(comparator_2_gt[1]), .lt(comparator_2_lt[1]));  // open: eq
  Comparator #(.width(5), .mode("twosComplement")) comparator_2 (
    .a(5'b00010), .b({1'b0, out_9}), .gt(comparator_2_gt[0]), .lt(comparator_2_lt[0]));  // open: eq
  Comparator #(.width(3), .mode("twosComplement")) comparator_3 (
    .a({1'b0, comparator_2_lt}), .b({1'b0, comparator_2_gt}), .lt(comparator_3_lt));  // open: gt, eq
endmodule

module \闹钟测试  (
  input  in_1,
  input  in_2,
  input  in_3,
  output out_4
);

  wire button_1_out, button_2_out;
  wire [3:0] \闹钟_1_out_6 , \闹钟_1_out_7 , \闹钟_1_out_8 , \闹钟_1_out_9 ;

  Button button_1 (.out(button_1_out));
  Button button_2 (.out(button_2_out));
  Hex_Digit_Display hex_digit_display_1 (.value(\闹钟_1_out_8 ));  // open: dp
  Hex_Digit_Display hex_digit_display_2 (.value(\闹钟_1_out_9 ));  // open: dp
  Hex_Digit_Display hex_digit_display_3 (.value(\闹钟_1_out_6 ));  // open: dp
  Hex_Digit_Display hex_digit_display_4 (.value(\闹钟_1_out_7 ));  // open: dp
  \闹钟  \u_闹钟_1  (
    .CPu(button_1_out), .CPd(button_2_out), .Adj0(in_1), .Adj1(in_2), .out_6(\闹钟_1_out_6 ),
    .out_7(\闹钟_1_out_7 ), .out_8(\闹钟_1_out_8 ), .out_9(\闹钟_1_out_9 ), .Set(in_3), .out_10(out_4));
endmodule
